// Digital circuit alu-16b-final.dig as structural Verilog
module alu_16b_final (
  input  CLK,
  input  [15:0] A,
  input  [15:0] B,
  input  [15:0] C,
  input  [15:0] Test,
  input  RST,
  input  hold,
  input  zin,
  input  FLAG_WE,
  input  [2:0] cin_sel,
  output [7:0] lutB,
  output [7:0] lutA,
  output [15:0] Out,
  output Z_out,
  output [7:0] CSR_FLAG
);

  wire _7400_1_pin3, _7400_3_pin3, aeff15, beff15, C_out, cin, count_en, cout0, cout1, cout2, e0, en, found,
       GT_sign, GTE_sign, LT_sign, N_out, nhold, not_1_out, nZout, ovf, rc0, rc1, rc2, reg_en, V_out, xA, xB,
       xC, xor_1_out, xor_2_out;
  wire [7:0] lutAin, lutBin;

  _74161 _74161_1 (
    .pin1(RST), .pin2(CLK), .pin3(1'b0), .pin4(1'b0), .pin5(1'b0), .pin6(1'b0), .pin7(count_en), .pin8(1'b0),
    .pin9(1'b1), .pin10(1'b1), .pin11(lutAin[3]), .pin12(lutAin[2]), .pin13(lutAin[1]), .pin14(lutAin[0]),
    .pin15(rc0), .pin16(1'b1));
  _7400 _7400_1 (
    .pin1(ovf), .pin2(ovf), .pin3(_7400_1_pin3), .pin4(_7400_1_pin3), .pin5(found), .pin6(e0), .pin7(1'b0),
    .pin8(en), .pin9(e0), .pin10(RST), .pin11(nhold), .pin12(hold), .pin13(hold), .pin14(1'b1));
  _74688 _74688_1 (
    .pin1(1'b0), .pin2(Out[0]), .pin3(Test[0]), .pin4(Out[1]), .pin5(Test[1]), .pin6(Out[2]), .pin7(Test[2]),
    .pin8(Out[3]), .pin9(Test[3]), .pin10(1'b0), .pin11(Out[4]), .pin12(Test[4]), .pin13(Out[5]),
    .pin14(Test[5]), .pin15(Out[6]), .pin16(Test[6]), .pin17(Out[7]), .pin18(Test[7]), .pin19(xA),
    .pin20(1'b1));
  _74161 _74161_2 (
    .pin1(RST), .pin2(CLK), .pin3(1'b0), .pin4(1'b0), .pin5(1'b0), .pin6(1'b0), .pin7(count_en), .pin8(1'b0),
    .pin9(1'b1), .pin10(rc0), .pin11(lutAin[7]), .pin12(lutAin[6]), .pin13(lutAin[5]), .pin14(lutAin[4]),
    .pin15(rc1), .pin16(1'b1));
  _74688 _74688_2 (
    .pin1(xA), .pin2(Out[8]), .pin3(Test[8]), .pin4(Out[9]), .pin5(Test[9]), .pin6(Out[10]), .pin7(Test[10]),
    .pin8(Out[11]), .pin9(Test[11]), .pin10(1'b0), .pin11(Out[12]), .pin12(Test[12]), .pin13(Out[13]),
    .pin14(Test[13]), .pin15(Out[14]), .pin16(Test[14]), .pin17(Out[15]), .pin18(Test[15]), .pin19(found),
    .pin20(1'b1));
  _7400 _7400_2 (
    .pin1(nhold), .pin2(en), .pin3(reg_en), .pin4(reg_en), .pin5(reg_en), .pin6(count_en), .pin7(1'b0),
    .pin9(1'b0), .pin10(1'b0), .pin12(1'b0), .pin13(1'b0), .pin14(1'b1));  // open: pin8, pin11
  _74161 _74161_3 (
    .pin1(RST), .pin2(CLK), .pin3(1'b0), .pin4(1'b0), .pin5(1'b0), .pin6(1'b0), .pin7(count_en), .pin8(1'b0),
    .pin9(1'b1), .pin10(rc1), .pin11(lutBin[3]), .pin12(lutBin[2]), .pin13(lutBin[1]), .pin14(lutBin[0]),
    .pin15(rc2), .pin16(1'b1));
  _74377 _74377_1 (
    .pin1(reg_en), .pin2(lutA[0]), .pin3(lutAin[0]), .pin4(lutAin[1]), .pin5(lutA[1]), .pin6(lutA[2]),
    .pin7(lutAin[2]), .pin8(lutAin[3]), .pin9(lutA[3]), .pin10(1'b0), .pin11(CLK), .pin12(lutA[4]),
    .pin13(lutAin[4]), .pin14(lutAin[5]), .pin15(lutA[5]), .pin16(lutA[6]), .pin17(lutAin[6]),
    .pin18(lutAin[7]), .pin19(lutA[7]), .pin20(1'b1));
  _74161 _74161_4 (
    .pin1(RST), .pin2(CLK), .pin3(1'b0), .pin4(1'b0), .pin5(1'b0), .pin6(1'b0), .pin7(count_en), .pin8(1'b0),
    .pin9(1'b1), .pin10(rc2), .pin11(lutBin[7]), .pin12(lutBin[6]), .pin13(lutBin[5]), .pin14(lutBin[4]),
    .pin15(ovf), .pin16(1'b1));
  _74377 _74377_2 (
    .pin1(reg_en), .pin2(lutB[0]), .pin3(lutBin[0]), .pin4(lutBin[1]), .pin5(lutB[1]), .pin6(lutB[2]),
    .pin7(lutBin[2]), .pin8(lutBin[3]), .pin9(lutB[3]), .pin10(1'b0), .pin11(CLK), .pin12(lutB[4]),
    .pin13(lutBin[4]), .pin14(lutBin[5]), .pin15(lutB[5]), .pin16(lutB[6]), .pin17(lutBin[6]),
    .pin18(lutBin[7]), .pin19(lutB[7]), .pin20(1'b1));
  alu_4b_final alu_4b_final_1 (
    .A(A[3:0]), .B(B[3:0]), .lutA(lutA), .C(C[3:0]), .cin(cin), .lutB(lutB), .Out(Out[3:0]), .cout(cout0));  // open: aeff3, beff3
  alu_4b_final alu_4b_final_2 (
    .A(A[11:8]), .B(B[11:8]), .lutA(lutA), .C(C[11:8]), .cin(cout1), .lutB(lutB), .Out(Out[11:8]),
    .cout(cout2));  // open: aeff3, beff3
  _74688 _74688_3 (
    .pin1(1'b0), .pin2(Out[0]), .pin3(1'b0), .pin4(Out[1]), .pin5(1'b0), .pin6(Out[2]), .pin7(1'b0),
    .pin8(Out[3]), .pin9(1'b0), .pin10(1'b0), .pin11(Out[4]), .pin12(1'b0), .pin13(Out[5]), .pin14(1'b0),
    .pin15(Out[6]), .pin16(1'b0), .pin17(Out[7]), .pin18(1'b0), .pin19(xB), .pin20(1'b1));
  _74688 _74688_4 (
    .pin1(xB), .pin2(Out[8]), .pin3(1'b0), .pin4(Out[9]), .pin5(1'b0), .pin6(Out[10]), .pin7(1'b0),
    .pin8(Out[11]), .pin9(1'b0), .pin10(1'b0), .pin11(Out[12]), .pin12(1'b0), .pin13(Out[13]), .pin14(1'b0),
    .pin15(Out[14]), .pin16(1'b0), .pin17(Out[15]), .pin18(1'b0), .pin19(nZout), .pin20(1'b1));
  alu_4b_final alu_4b_final_3 (
    .A(A[7:4]), .B(B[7:4]), .lutA(lutA), .C(C[7:4]), .cin(cout0), .lutB(lutB), .Out(Out[7:4]), .cout(cout1));  // open: aeff3, beff3
  alu_4b_final alu_4b_final_4 (
    .A(A[15:12]), .B(B[15:12]), .lutA(lutA), .C(C[15:12]), .cin(cout2), .lutB(lutB), .Out(Out[15:12]),
    .cout(C_out), .sum3(N_out), .aeff3(aeff15), .beff3(beff15));
  _7400 _7400_3 (
    .pin1(nZout), .pin2(nZout), .pin3(_7400_3_pin3), .pin4(_7400_3_pin3), .pin5(zin), .pin6(xC), .pin7(1'b0),
    .pin8(Z_out), .pin9(xC), .pin10(xC), .pin12(1'b0), .pin13(1'b0), .pin14(1'b1));  // open: pin11
  _74151 _74151_1 (
    .pin1(CSR_FLAG[0]), .pin2(CSR_FLAG[3]), .pin3(1'b1), .pin4(1'b0), .pin5(cin), .pin7(1'b0), .pin8(1'b0),
    .pin9(cin_sel[2]), .pin10(cin_sel[1]), .pin11(cin_sel[0]), .pin12(CSR_FLAG[6]), .pin13(CSR_FLAG[5]),
    .pin14(CSR_FLAG[4]), .pin15(CSR_FLAG[2]), .pin16(1'b1));  // open: pin6
  not not_1 (not_1_out, FLAG_WE);
  _74377 _74377_3 (
    .pin1(not_1_out), .pin2(CSR_FLAG[0]), .pin3(Z_out), .pin4(nZout), .pin5(CSR_FLAG[1]), .pin6(CSR_FLAG[2]),
    .pin7(N_out), .pin8(C_out), .pin9(CSR_FLAG[3]), .pin10(1'b0), .pin11(CLK), .pin12(CSR_FLAG[4]),
    .pin13(V_out), .pin14(LT_sign), .pin15(CSR_FLAG[5]), .pin16(CSR_FLAG[6]), .pin17(GT_sign),
    .pin18(GTE_sign), .pin19(CSR_FLAG[7]), .pin20(1'b1));
  and and_1 (V_out, xor_2_out, xor_1_out);
  and and_2 (GT_sign, nZout, GTE_sign);
  xor xor_1 (xor_1_out, N_out, aeff15);
  xor xor_2 (xor_2_out, beff15, N_out);
  not not_2 (GTE_sign, LT_sign);
  xor xor_3 (LT_sign, V_out, N_out);

  // Other names for the same wires on the sheet: a4[3:0] = A[3:0]; a8[3:0] = A[7:4]; a12[3:0] = A[11:8];
  //   a16[3:0] = A[15:12]; b4[3:0] = B[3:0]; b8[3:0] = B[7:4]; b12[3:0] = B[11:8]; b16[3:0] = B[15:12];
  //   c4[3:0] = C[3:0]; c8[3:0] = C[7:4]; c12[3:0] = C[11:8]; c16[3:0] = C[15:12]; COUT = C_out;
  //   cin_SEL_0 = cin_sel[0]; cin_SEL_1 = cin_sel[1]; cin_SEL_2 = cin_sel[2]; flag_c = CSR_FLAG[3];
  //   flag_gt = CSR_FLAG[6]; flag_gte = CSR_FLAG[7]; flag_lt = CSR_FLAG[5]; flag_n = CSR_FLAG[2];
  //   flag_v = CSR_FLAG[4]; flag_z = CSR_FLAG[0]; flag_z_b = CSR_FLAG[1]; OUT4[3:0] = Out[3:0]; out4_t = Out[4];
  //   OUT8[3:0] = Out[7:4]; out8_t = Out[8]; OUT12[3:0] = Out[11:8]; out12_t = Out[12]; OUT16[3:0] = Out[15:12];
  //   q0 = lutAin[0]; q1 = lutAin[1]; q2 = lutAin[2]; q3 = lutAin[3]; q4 = lutAin[4]; q5 = lutAin[5]; q6 = lutAin[6];
  //   q7 = lutAin[7]; q8 = lutBin[0]; q9 = lutBin[1]; q10 = lutBin[2]; q11 = lutBin[3]; q12 = lutBin[4];
  //   q13 = lutBin[5]; q14 = lutBin[6]; q15 = lutBin[7]; sum15 = N_out

  // Notes on the sheet:
  //   CLK: Hz: 100000
  //   A: default 10811
  //   B: default 7245
  //   C: default 20318
  //   Test: default 4112
  //   RST: default 1
  //   Overflow Logic
endmodule
