// Digital circuit alu-1b-final.dig as structural Verilog
module alu_1b_final (
  input  [7:0] OPCODE,
  input  A,
  input  B,
  input  C,
  input  Asel,
  input  Bsel,
  input  A_inv,
  input  B_inv,
  output MUX_OUT,
  output G,
  output P
);

  wire A_eff, and_1_out, and_2_out, B_eff, multiplexer_1_out, multiplexer_2_out;

  and and_1 (and_1_out, Asel, A);
  and and_2 (and_2_out, Bsel, B);
  xor xor_1 (A_eff, and_1_out, A_inv);
  xor xor_2 (B_eff, and_2_out, B_inv);
  Multiplexer #(.Selector_Bits(2)) multiplexer_1 (
    .sel({B_eff, A_eff}), .in_0(OPCODE[0]), .in_1(OPCODE[1]), .in_2(OPCODE[2]), .in_3(OPCODE[3]),
    .out(multiplexer_1_out));
  Multiplexer #(.Selector_Bits(2)) multiplexer_2 (
    .sel({B_eff, A_eff}), .in_0(OPCODE[4]), .in_1(OPCODE[5]), .in_2(OPCODE[6]), .in_3(OPCODE[7]),
    .out(multiplexer_2_out));
  Multiplexer multiplexer_3 (.sel(C), .in_0(multiplexer_1_out), .in_1(multiplexer_2_out), .out(MUX_OUT));
  and and_3 (G, A_eff, B_eff);
  xor xor_3 (P, A_eff, B_eff);
endmodule

/* Test case Arithmetic Tests:
# Arithmetic Tests (OPCODE 0x96)
OPCODE Asel A_inv Bsel B_inv A B C MUX_OUT P G
150 0 0 0 0 0 0 0 0 0 0
150 0 0 0 0 0 1 0 0 0 0
150 0 0 0 0 1 0 0 0 0 0
150 0 0 0 0 1 1 0 0 0 0
150 0 0 0 0 0 0 1 1 0 0
150 0 0 0 0 0 1 1 1 0 0
150 0 0 0 0 1 0 1 1 0 0
150 0 0 0 0 1 1 1 1 0 0
150 0 0 0 1 0 0 0 1 1 0
150 0 0 0 1 0 1 0 1 1 0
150 0 0 0 1 1 0 0 1 1 0
150 0 0 0 1 1 1 0 1 1 0
150 0 0 0 1 0 0 1 0 1 0
150 0 0 0 1 0 1 1 0 1 0
150 0 0 0 1 1 0 1 0 1 0
150 0 0 0 1 1 1 1 0 1 0
150 0 0 1 0 0 0 0 0 0 0
150 0 0 1 0 0 1 0 1 1 0
150 0 0 1 0 1 0 0 0 0 0
150 0 0 1 0 1 1 0 1 1 0
150 0 0 1 0 0 0 1 1 0 0
150 0 0 1 0 0 1 1 0 1 0
150 0 0 1 0 1 0 1 1 0 0
150 0 0 1 0 1 1 1 0 1 0
150 0 0 1 1 0 0 0 1 1 0
150 0 0 1 1 0 1 0 0 0 0
150 0 0 1 1 1 0 0 1 1 0
150 0 0 1 1 1 1 0 0 0 0
150 0 0 1 1 0 0 1 0 1 0
150 0 0 1 1 0 1 1 1 0 0
150 0 0 1 1 1 0 1 0 1 0
150 0 0 1 1 1 1 1 1 0 0
150 0 1 0 0 0 0 0 1 1 0
150 0 1 0 0 0 1 0 1 1 0
150 0 1 0 0 1 0 0 1 1 0
150 0 1 0 0 1 1 0 1 1 0
150 0 1 0 0 0 0 1 0 1 0
150 0 1 0 0 0 1 1 0 1 0
150 0 1 0 0 1 0 1 0 1 0
150 0 1 0 0 1 1 1 0 1 0
150 0 1 0 1 0 0 0 0 0 1
150 0 1 0 1 0 1 0 0 0 1
150 0 1 0 1 1 0 0 0 0 1
150 0 1 0 1 1 1 0 0 0 1
150 0 1 0 1 0 0 1 1 0 1
150 0 1 0 1 0 1 1 1 0 1
150 0 1 0 1 1 0 1 1 0 1
150 0 1 0 1 1 1 1 1 0 1
150 0 1 1 0 0 0 0 1 1 0
150 0 1 1 0 0 1 0 0 0 1
150 0 1 1 0 1 0 0 1 1 0
150 0 1 1 0 1 1 0 0 0 1
150 0 1 1 0 0 0 1 0 1 0
150 0 1 1 0 0 1 1 1 0 1
150 0 1 1 0 1 0 1 0 1 0
150 0 1 1 0 1 1 1 1 0 1
150 0 1 1 1 0 0 0 0 0 1
150 0 1 1 1 0 1 0 1 1 0
150 0 1 1 1 1 0 0 0 0 1
150 0 1 1 1 1 1 0 1 1 0
150 0 1 1 1 0 0 1 1 0 1
150 0 1 1 1 0 1 1 0 1 0
150 0 1 1 1 1 0 1 1 0 1
150 0 1 1 1 1 1 1 0 1 0
150 1 0 0 0 0 0 0 0 0 0
150 1 0 0 0 0 1 0 0 0 0
150 1 0 0 0 1 0 0 1 1 0
150 1 0 0 0 1 1 0 1 1 0
150 1 0 0 0 0 0 1 1 0 0
150 1 0 0 0 0 1 1 1 0 0
150 1 0 0 0 1 0 1 0 1 0
150 1 0 0 0 1 1 1 0 1 0
150 1 0 0 1 0 0 0 1 1 0
150 1 0 0 1 0 1 0 1 1 0
150 1 0 0 1 1 0 0 0 0 1
150 1 0 0 1 1 1 0 0 0 1
150 1 0 0 1 0 0 1 0 1 0
150 1 0 0 1 0 1 1 0 1 0
150 1 0 0 1 1 0 1 1 0 1
150 1 0 0 1 1 1 1 1 0 1
150 1 0 1 0 0 0 0 0 0 0
150 1 0 1 0 0 1 0 1 1 0
150 1 0 1 0 1 0 0 1 1 0
150 1 0 1 0 1 1 0 0 0 1
150 1 0 1 0 0 0 1 1 0 0
150 1 0 1 0 0 1 1 0 1 0
150 1 0 1 0 1 0 1 0 1 0
150 1 0 1 0 1 1 1 1 0 1
150 1 0 1 1 0 0 0 1 1 0
150 1 0 1 1 0 1 0 0 0 0
150 1 0 1 1 1 0 0 0 0 1
150 1 0 1 1 1 1 0 1 1 0
150 1 0 1 1 0 0 1 0 1 0
150 1 0 1 1 0 1 1 1 0 0
150 1 0 1 1 1 0 1 1 0 1
150 1 0 1 1 1 1 1 0 1 0
150 1 1 0 0 0 0 0 1 1 0
150 1 1 0 0 0 1 0 1 1 0
150 1 1 0 0 1 0 0 0 0 0
150 1 1 0 0 1 1 0 0 0 0
150 1 1 0 0 0 0 1 0 1 0
150 1 1 0 0 0 1 1 0 1 0
150 1 1 0 0 1 0 1 1 0 0
150 1 1 0 0 1 1 1 1 0 0
150 1 1 0 1 0 0 0 0 0 1
150 1 1 0 1 0 1 0 0 0 1
150 1 1 0 1 1 0 0 1 1 0
150 1 1 0 1 1 1 0 1 1 0
150 1 1 0 1 0 0 1 1 0 1
150 1 1 0 1 0 1 1 1 0 1
150 1 1 0 1 1 0 1 0 1 0
150 1 1 0 1 1 1 1 0 1 0
150 1 1 1 0 0 0 0 1 1 0
150 1 1 1 0 0 1 0 0 0 1
150 1 1 1 0 1 0 0 0 0 0
150 1 1 1 0 1 1 0 1 1 0
150 1 1 1 0 0 0 1 0 1 0
150 1 1 1 0 0 1 1 1 0 1
150 1 1 1 0 1 0 1 1 0 0
150 1 1 1 0 1 1 1 0 1 0
150 1 1 1 1 0 0 0 0 0 1
150 1 1 1 1 0 1 0 1 1 0
150 1 1 1 1 1 0 0 1 1 0
150 1 1 1 1 1 1 0 0 0 0
150 1 1 1 1 0 0 1 1 0 1
150 1 1 1 1 0 1 1 0 1 0
150 1 1 1 1 1 0 1 0 1 0
150 1 1 1 1 1 1 1 1 0 0
            
*/

/* Test case Logic Tests:
# Logic Tests (All 256 OpCodes)
OPCODE Asel A_inv Bsel B_inv A B C MUX_OUT P G
0 1 0 1 0 0 0 0 0 0 0
0 1 0 1 0 0 0 1 0 0 0
0 1 0 1 0 0 1 0 0 0 0
0 1 0 1 0 0 1 1 0 0 0
0 1 0 1 0 1 0 0 0 0 0
0 1 0 1 0 1 0 1 0 0 0
0 1 0 1 0 1 1 0 0 0 1
0 1 0 1 0 1 1 1 0 0 1
1 1 0 1 0 0 0 0 1 1 0
1 1 0 1 0 0 0 1 0 1 0
1 1 0 1 0 0 1 0 0 0 0
1 1 0 1 0 0 1 1 0 0 0
1 1 0 1 0 1 0 0 0 0 0
1 1 0 1 0 1 0 1 0 0 0
1 1 0 1 0 1 1 0 0 0 1
1 1 0 1 0 1 1 1 0 0 1
2 1 0 1 0 0 0 0 0 0 0
2 1 0 1 0 0 0 1 0 0 0
2 1 0 1 0 0 1 0 0 0 0
2 1 0 1 0 0 1 1 0 0 0
2 1 0 1 0 1 0 0 1 1 0
2 1 0 1 0 1 0 1 0 1 0
2 1 0 1 0 1 1 0 0 0 1
2 1 0 1 0 1 1 1 0 0 1
3 1 0 1 0 0 0 0 1 1 0
3 1 0 1 0 0 0 1 0 1 0
3 1 0 1 0 0 1 0 0 0 0
3 1 0 1 0 0 1 1 0 0 0
3 1 0 1 0 1 0 0 1 1 0
3 1 0 1 0 1 0 1 0 1 0
3 1 0 1 0 1 1 0 0 0 1
3 1 0 1 0 1 1 1 0 0 1
4 1 0 1 0 0 0 0 0 0 0
4 1 0 1 0 0 0 1 0 0 0
4 1 0 1 0 0 1 0 1 1 0
4 1 0 1 0 0 1 1 0 1 0
4 1 0 1 0 1 0 0 0 0 0
4 1 0 1 0 1 0 1 0 0 0
4 1 0 1 0 1 1 0 0 0 1
4 1 0 1 0 1 1 1 0 0 1
5 1 0 1 0 0 0 0 1 1 0
5 1 0 1 0 0 0 1 0 1 0
5 1 0 1 0 0 1 0 1 1 0
5 1 0 1 0 0 1 1 0 1 0
5 1 0 1 0 1 0 0 0 0 0
5 1 0 1 0 1 0 1 0 0 0
5 1 0 1 0 1 1 0 0 0 1
5 1 0 1 0 1 1 1 0 0 1
6 1 0 1 0 0 0 0 0 0 0
6 1 0 1 0 0 0 1 0 0 0
6 1 0 1 0 0 1 0 1 1 0
6 1 0 1 0 0 1 1 0 1 0
6 1 0 1 0 1 0 0 1 1 0
6 1 0 1 0 1 0 1 0 1 0
6 1 0 1 0 1 1 0 0 0 1
6 1 0 1 0 1 1 1 0 0 1
7 1 0 1 0 0 0 0 1 1 0
7 1 0 1 0 0 0 1 0 1 0
7 1 0 1 0 0 1 0 1 1 0
7 1 0 1 0 0 1 1 0 1 0
7 1 0 1 0 1 0 0 1 1 0
7 1 0 1 0 1 0 1 0 1 0
7 1 0 1 0 1 1 0 0 0 1
7 1 0 1 0 1 1 1 0 0 1
8 1 0 1 0 0 0 0 0 0 0
8 1 0 1 0 0 0 1 0 0 0
8 1 0 1 0 0 1 0 0 0 0
8 1 0 1 0 0 1 1 0 0 0
8 1 0 1 0 1 0 0 0 0 0
8 1 0 1 0 1 0 1 0 0 0
8 1 0 1 0 1 1 0 1 1 1
8 1 0 1 0 1 1 1 0 1 1
9 1 0 1 0 0 0 0 1 1 0
9 1 0 1 0 0 0 1 0 1 0
9 1 0 1 0 0 1 0 0 0 0
9 1 0 1 0 0 1 1 0 0 0
9 1 0 1 0 1 0 0 0 0 0
9 1 0 1 0 1 0 1 0 0 0
9 1 0 1 0 1 1 0 1 1 1
9 1 0 1 0 1 1 1 0 1 1
10 1 0 1 0 0 0 0 0 0 0
10 1 0 1 0 0 0 1 0 0 0
10 1 0 1 0 0 1 0 0 0 0
10 1 0 1 0 0 1 1 0 0 0
10 1 0 1 0 1 0 0 1 1 0
10 1 0 1 0 1 0 1 0 1 0
10 1 0 1 0 1 1 0 1 1 1
10 1 0 1 0 1 1 1 0 1 1
11 1 0 1 0 0 0 0 1 1 0
11 1 0 1 0 0 0 1 0 1 0
11 1 0 1 0 0 1 0 0 0 0
11 1 0 1 0 0 1 1 0 0 0
11 1 0 1 0 1 0 0 1 1 0
11 1 0 1 0 1 0 1 0 1 0
11 1 0 1 0 1 1 0 1 1 1
11 1 0 1 0 1 1 1 0 1 1
12 1 0 1 0 0 0 0 0 0 0
12 1 0 1 0 0 0 1 0 0 0
12 1 0 1 0 0 1 0 1 1 0
12 1 0 1 0 0 1 1 0 1 0
12 1 0 1 0 1 0 0 0 0 0
12 1 0 1 0 1 0 1 0 0 0
12 1 0 1 0 1 1 0 1 1 1
12 1 0 1 0 1 1 1 0 1 1
13 1 0 1 0 0 0 0 1 1 0
13 1 0 1 0 0 0 1 0 1 0
13 1 0 1 0 0 1 0 1 1 0
13 1 0 1 0 0 1 1 0 1 0
13 1 0 1 0 1 0 0 0 0 0
13 1 0 1 0 1 0 1 0 0 0
13 1 0 1 0 1 1 0 1 1 1
13 1 0 1 0 1 1 1 0 1 1
14 1 0 1 0 0 0 0 0 0 0
14 1 0 1 0 0 0 1 0 0 0
14 1 0 1 0 0 1 0 1 1 0
14 1 0 1 0 0 1 1 0 1 0
14 1 0 1 0 1 0 0 1 1 0
14 1 0 1 0 1 0 1 0 1 0
14 1 0 1 0 1 1 0 1 1 1
14 1 0 1 0 1 1 1 0 1 1
15 1 0 1 0 0 0 0 1 1 0
15 1 0 1 0 0 0 1 0 1 0
15 1 0 1 0 0 1 0 1 1 0
15 1 0 1 0 0 1 1 0 1 0
15 1 0 1 0 1 0 0 1 1 0
15 1 0 1 0 1 0 1 0 1 0
15 1 0 1 0 1 1 0 1 1 1
15 1 0 1 0 1 1 1 0 1 1
16 1 0 1 0 0 0 0 0 0 0
16 1 0 1 0 0 0 1 1 0 0
16 1 0 1 0 0 1 0 0 0 0
16 1 0 1 0 0 1 1 0 0 0
16 1 0 1 0 1 0 0 0 0 0
16 1 0 1 0 1 0 1 0 0 0
16 1 0 1 0 1 1 0 0 0 1
16 1 0 1 0 1 1 1 0 0 1
17 1 0 1 0 0 0 0 1 1 0
17 1 0 1 0 0 0 1 1 1 0
17 1 0 1 0 0 1 0 0 0 0
17 1 0 1 0 0 1 1 0 0 0
17 1 0 1 0 1 0 0 0 0 0
17 1 0 1 0 1 0 1 0 0 0
17 1 0 1 0 1 1 0 0 0 1
17 1 0 1 0 1 1 1 0 0 1
18 1 0 1 0 0 0 0 0 0 0
18 1 0 1 0 0 0 1 1 0 0
18 1 0 1 0 0 1 0 0 0 0
18 1 0 1 0 0 1 1 0 0 0
18 1 0 1 0 1 0 0 1 1 0
18 1 0 1 0 1 0 1 0 1 0
18 1 0 1 0 1 1 0 0 0 1
18 1 0 1 0 1 1 1 0 0 1
19 1 0 1 0 0 0 0 1 1 0
19 1 0 1 0 0 0 1 1 1 0
19 1 0 1 0 0 1 0 0 0 0
19 1 0 1 0 0 1 1 0 0 0
19 1 0 1 0 1 0 0 1 1 0
19 1 0 1 0 1 0 1 0 1 0
19 1 0 1 0 1 1 0 0 0 1
19 1 0 1 0 1 1 1 0 0 1
20 1 0 1 0 0 0 0 0 0 0
20 1 0 1 0 0 0 1 1 0 0
20 1 0 1 0 0 1 0 1 1 0
20 1 0 1 0 0 1 1 0 1 0
20 1 0 1 0 1 0 0 0 0 0
20 1 0 1 0 1 0 1 0 0 0
20 1 0 1 0 1 1 0 0 0 1
20 1 0 1 0 1 1 1 0 0 1
21 1 0 1 0 0 0 0 1 1 0
21 1 0 1 0 0 0 1 1 1 0
21 1 0 1 0 0 1 0 1 1 0
21 1 0 1 0 0 1 1 0 1 0
21 1 0 1 0 1 0 0 0 0 0
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*/

/* Test case Prefix Accelerators:
# Prefix-Logic Accelerators
OPCODE Asel A_inv Bsel B_inv A B C MUX_OUT P G
80 1 0 0 1 0 0 0 0 0 0
80 1 0 0 1 0 1 0 0 0 0
80 1 0 0 1 1 0 0 0 0 1
80 1 0 0 1 1 1 0 0 0 1
10 1 0 0 0 0 0 1 0 0 0
10 1 0 0 0 0 1 1 0 0 0
10 1 0 0 0 1 0 1 0 1 0
10 1 0 0 0 1 1 1 0 1 0
250 1 0 0 1 0 0 0 0 0 0
250 1 0 0 1 0 1 0 0 0 0
250 1 0 0 1 1 0 0 1 1 1
250 1 0 0 1 1 1 0 1 1 1
170 1 0 1 0 0 0 0 0 0 0
170 1 0 1 0 0 1 0 0 0 0
170 1 0 1 0 1 0 0 1 1 0
170 1 0 1 0 1 1 0 1 1 1
            
*/
