// Digital circuit alu-40b-final.dig as structural Verilog
module alu_40b_final (
  input  [7:0] lutA,
  input  [7:0] lutB,
  input  [39:0] A,
  input  [39:0] B,
  input  [39:0] C,
  input  [2:0] csel,
  input  FLAG_WE,
  input  CLK,
  output [39:0] OUT,
  output [7:0] csr
);

  wire zout_7__0, zout_15__8, zout_23__16, zout_31__24;
  wire [0:0] cin1, cin2, cin3, cin4;

  // alu_8b_final alu_8b_final_1: pin names not known; wires that end beside it: lutA, A[7:0], B[7:0], C[7:0], lutB, 1'b0, 1'b0, csel, CLK, OUT[7:0], zout_7__0, cin1[0]
  // alu_8b_final alu_8b_final_2: pin names not known; wires that end beside it: lutA, A[15:8], B[15:8], C[15:8], lutB, zout_7__0, 1'b0, {2'b00, cin1[0]}, CLK, OUT[15:8], zout_15__8, cin2[0]
  // alu_8b_final alu_8b_final_3: pin names not known; wires that end beside it: lutA, A[23:16], B[23:16], C[23:16], lutB, zout_15__8, 1'b0, {2'b00, cin2[0]}, CLK, OUT[23:16], zout_23__16, cin3[0]
  // alu_8b_final alu_8b_final_4: pin names not known; wires that end beside it: lutA, A[31:24], B[31:24], C[31:24], lutB, zout_23__16, 1'b0, {2'b00, cin3[0]}, CLK, OUT[31:24], zout_31__24, cin4[0]
  // alu_8b_final alu_8b_final_5: pin names not known; wires that end beside it: lutA, A[39:32], B[39:32], C[39:32], lutB, zout_31__24, FLAG_WE, {2'b00, cin4[0]}, CLK, OUT[39:32], csr

  // Other names for the same wires on the sheet: A_7__0[7:0] = A[7:0]; A_15__8[7:0] = A[15:8];
  //   A_23__16[7:0] = A[23:16]; A_31__24[7:0] = A[31:24]; A_39__32[7:0] = A[39:32]; B_7__0[7:0] = B[7:0];
  //   B_15__8[7:0] = B[15:8]; B_23__16[7:0] = B[23:16]; B_31__24[7:0] = B[31:24]; B_39__32[7:0] = B[39:32];
  //   C_7__0[7:0] = C[7:0]; C_15__8[7:0] = C[15:8]; C_23__16[7:0] = C[23:16]; C_31__24[7:0] = C[31:24];
  //   C_39__32[7:0] = C[39:32]; cout0 = cin1[0]; cout1 = cin2[0]; cout2 = cin3[0]; cout3 = cin4[0];
  //   csr_flg[7:0] = csr; OUT_7__0[7:0] = OUT[7:0]; OUT_15__8[7:0] = OUT[15:8]; OUT_23__16[7:0] = OUT[23:16];
  //   OUT_31__24[7:0] = OUT[31:24]; OUT_39__32[7:0] = OUT[39:32]

  // Notes on the sheet:
  //   A: default 2
  //   B: default 7
  //   C: default 341177945
  //   FLAG_WE: default 1
  //   CLK: Hz: 100000
endmodule
