// Digital circuit alu-4b-final.dig as structural Verilog
module alu_4b_final (
  input  [3:0] A,
  input  [3:0] B,
  input  [7:0] OPCODE,
  input  [3:0] C,
  input  [4:0] alu_ctrl,
  input  cin,
  output [3:0] Out,
  output cout,
  output sum3,
  output aeff3,
  output beff3
);

  wire aeff0, aeff1, aeff2, beff0, beff1, beff2, log0, log1, log2, log3, nand_1_out, nand_2_out, nand_3_out,
       nand_4_out, nand_5_out, nand_6_out, nand_7_out, nand_8_out, s0, s1, s2;

  nand nand_1 (nand_1_out, A[0], alu_ctrl[2]);
  nand nand_2 (nand_2_out, A[1], alu_ctrl[2]);
  nand nand_3 (nand_3_out, A[2], alu_ctrl[2]);
  nand nand_4 (nand_4_out, A[3], alu_ctrl[2]);
  xor xor_1 (aeff0, nand_1_out, alu_ctrl[1]);
  xor xor_2 (aeff1, nand_2_out, alu_ctrl[1]);
  xor xor_3 (aeff2, nand_3_out, alu_ctrl[1]);
  xor xor_4 (aeff3, nand_4_out, alu_ctrl[1]);
  nand nand_5 (nand_5_out, B[0], alu_ctrl[4]);
  nand nand_6 (nand_6_out, B[1], alu_ctrl[4]);
  nand nand_7 (nand_7_out, B[2], alu_ctrl[4]);
  nand nand_8 (nand_8_out, B[3], alu_ctrl[4]);
  xor xor_5 (beff0, nand_5_out, alu_ctrl[3]);
  xor xor_6 (beff1, nand_6_out, alu_ctrl[3]);
  xor xor_7 (beff2, nand_7_out, alu_ctrl[3]);
  xor xor_8 (beff3, nand_8_out, alu_ctrl[3]);
  alu_1b_final alu_1b_final_1 (.OPCODE(OPCODE), .A(A[0]), .B(B[0]), .C(C[0]), .MUX_OUT(log0));
  alu_1b_final alu_1b_final_2 (.OPCODE(OPCODE), .A(A[1]), .B(B[1]), .C(C[1]), .MUX_OUT(log1));
  alu_1b_final alu_1b_final_3 (.OPCODE(OPCODE), .A(A[2]), .B(B[2]), .C(C[2]), .MUX_OUT(log2));
  alu_1b_final alu_1b_final_4 (.OPCODE(OPCODE), .A(A[3]), .B(B[3]), .C(C[3]), .MUX_OUT(log3));
  _74283 _74283_1 (
    .pin1(s1), .pin2(beff1), .pin3(aeff1), .pin4(s0), .pin5(aeff0), .pin6(beff0), .pin7(cin), .pin8(1'b0),
    .pin9(cout), .pin10(sum3), .pin11(beff3), .pin12(aeff3), .pin13(s2), .pin14(aeff2), .pin15(beff2),
    .pin16(1'b1));
  _74257 _74257_1 (
    .pin1(alu_ctrl[0]), .pin2(log0), .pin3(s0), .pin4(Out[0]), .pin5(log1), .pin6(s1), .pin7(Out[1]),
    .pin8(1'b0), .pin9(Out[2]), .pin10(s2), .pin11(log2), .pin12(Out[3]), .pin13(sum3), .pin14(log3),
    .pin15(1'b0), .pin16(1'b1));

  // Other names for the same wires on the sheet: mode = alu_ctrl[0]; ainv = alu_ctrl[1]; asel = alu_ctrl[2];
  //   binv = alu_ctrl[3]; bsel = alu_ctrl[4]; s3 = sum3

  // Notes on the sheet:
  //   A: default 5
  //   B: default 3
endmodule
