// Digital circuit alu-8b-final.dig as structural Verilog
module alu_8b_final (
  input  [7:0] opcode,
  input  [4:0] control,
  input  [7:0] A,
  input  [7:0] B,
  input  [7:0] C,
  input  nz_in,
  input  cin,
  output [7:0] out,
  output vout,
  output zout,
  output nz_out,
  output n,
  output cout
);

  wire _7432_1_pin2, _7432_1_pin5, c0xp0, c4xp1, ceff0, ceff1, ceff2, ceff3, ceff4, ceff5, ceff6, ceff7,
       cin1, cin2, cin3, cin4, cin5, cin6, cin7, g0, g0_b, g1, g1_b, g2, g2_b, g3, g3_b, g4, g4_b, g5, g5_b,
       g6, g6_b, g7, g7_b, g_out_0, g_out_1, nor_1_out, nor_2_out, not_1_out, not_2_out, not_3_out, p0, p0_b,
       p1, p1_b, p2, p2_b, p3, p3_b, p4, p4_b, p5, p5_b, p6, p6_b, p7, p7_b, p_out_0, p_out_1;

  xor xor_1 (vout, cin7, cout);
  nor nor_1 (nor_1_out, out[0], out[1], out[2], out[3]);
  nor nor_2 (nor_2_out, out[4], out[5], out[6], n);
  and and_1 (zout, nor_1_out, nor_2_out);
  not not_1 (not_1_out, zout);
  or or_1 (nz_out, not_1_out, nz_in);
  alu_1b_final alu_1b_final_1 (
    .OPCODE(opcode), .A(A[0]), .B(B[0]), .C(ceff0), .Asel(control[0]), .Bsel(control[2]), .A_inv(control[1]),
    .B_inv(control[3]), .MUX_OUT(out[0]), .G(g0), .P(p0));
  alu_1b_final alu_1b_final_2 (
    .OPCODE(opcode), .A(A[1]), .B(B[1]), .C(ceff1), .Asel(control[0]), .Bsel(control[2]), .A_inv(control[1]),
    .B_inv(control[3]), .MUX_OUT(out[1]), .G(g1), .P(p1));
  alu_1b_final alu_1b_final_3 (
    .OPCODE(opcode), .A(A[2]), .B(B[2]), .C(ceff2), .Asel(control[0]), .Bsel(control[2]), .A_inv(control[1]),
    .B_inv(control[3]), .MUX_OUT(out[2]), .G(g2), .P(p2));
  alu_1b_final alu_1b_final_4 (
    .OPCODE(opcode), .A(A[3]), .B(B[3]), .C(ceff3), .Asel(control[0]), .Bsel(control[2]), .A_inv(control[1]),
    .B_inv(control[3]), .MUX_OUT(out[3]), .G(g3), .P(p3));
  alu_1b_final alu_1b_final_5 (
    .OPCODE(opcode), .A(A[4]), .B(B[4]), .C(ceff4), .Asel(control[0]), .Bsel(control[2]), .A_inv(control[1]),
    .B_inv(control[3]), .MUX_OUT(out[4]), .G(g4), .P(p4));
  alu_1b_final alu_1b_final_6 (
    .OPCODE(opcode), .A(A[5]), .B(B[5]), .C(ceff5), .Asel(control[0]), .Bsel(control[2]), .A_inv(control[1]),
    .B_inv(control[3]), .MUX_OUT(out[5]), .G(g5), .P(p5));
  alu_1b_final alu_1b_final_7 (
    .OPCODE(opcode), .A(A[6]), .B(B[6]), .C(ceff6), .Asel(control[0]), .Bsel(control[2]), .A_inv(control[1]),
    .B_inv(control[3]), .MUX_OUT(out[6]), .G(g6), .P(p6));
  alu_1b_final alu_1b_final_8 (
    .OPCODE(opcode), .A(A[7]), .B(B[7]), .C(ceff7), .Asel(control[0]), .Bsel(control[2]), .A_inv(control[1]),
    .B_inv(control[3]), .MUX_OUT(n), .G(g7), .P(p7));
  _74540 _74540_1 (
    .pin1(1'b0), .pin2(p0), .pin3(p1), .pin4(p2), .pin5(p3), .pin6(g0), .pin7(g1), .pin8(g2), .pin9(g3),
    .pin10(1'b0), .pin11(g3_b), .pin12(g2_b), .pin13(g1_b), .pin14(g0_b), .pin15(p3_b), .pin16(p2_b),
    .pin17(p1_b), .pin18(p0_b), .pin19(1'b0), .pin20(1'b1));
  _74182 _74182_1 (
    .pin1(g1_b), .pin2(p1_b), .pin3(g0_b), .pin4(p0_b), .pin5(g3_b), .pin6(p3_b), .pin7(p_out_0),
    .pin8(1'b0), .pin9(cin3), .pin10(g_out_0), .pin11(cin2), .pin12(cin1), .pin13(cin), .pin14(g2_b),
    .pin15(p2_b), .pin16(1'b1));
  _74157 _74157_1 (
    .pin1(control[4]), .pin2(cin), .pin3(C[0]), .pin4(ceff0), .pin5(cin1), .pin6(C[1]), .pin7(ceff1),
    .pin8(1'b0), .pin9(ceff2), .pin10(C[2]), .pin11(cin2), .pin12(ceff3), .pin13(C[3]), .pin14(cin3),
    .pin15(1'b0), .pin16(1'b1));
  _74157 _74157_2 (
    .pin1(control[4]), .pin2(cin4), .pin3(C[4]), .pin4(ceff4), .pin5(cin5), .pin6(C[5]), .pin7(ceff5),
    .pin8(1'b0), .pin9(ceff6), .pin10(C[6]), .pin11(cin6), .pin12(ceff7), .pin13(C[7]), .pin14(cin7),
    .pin15(1'b0), .pin16(1'b1));
  _74540 _74540_2 (
    .pin1(1'b0), .pin2(p4), .pin3(p5), .pin4(p6), .pin5(p7), .pin6(g4), .pin7(g5), .pin8(g6), .pin9(g7),
    .pin10(1'b0), .pin11(g7_b), .pin12(g6_b), .pin13(g5_b), .pin14(g4_b), .pin15(p7_b), .pin16(p6_b),
    .pin17(p5_b), .pin18(p4_b), .pin19(1'b0), .pin20(1'b1));
  _74182 _74182_2 (
    .pin1(g5_b), .pin2(p5_b), .pin3(g4_b), .pin4(p4_b), .pin5(g7_b), .pin6(p7_b), .pin7(p_out_1),
    .pin8(1'b0), .pin9(cin7), .pin10(g_out_1), .pin11(cin6), .pin12(cin5), .pin13(cin4), .pin14(g6_b),
    .pin15(p6_b), .pin16(1'b1));
  not not_2 (not_2_out, p_out_0);
  not not_3 (not_3_out, p_out_1);
  _7408 _7408_1 (
    .pin1(not_2_out), .pin2(cin), .pin3(c0xp0), .pin4(not_3_out), .pin5(cin4), .pin6(c4xp1), .pin7(1'b0),
    .pin9(1'b0), .pin10(1'b0), .pin12(1'b0), .pin13(1'b0), .pin14(1'b1));  // open: pin8, pin11
  _7432 _7432_1 (
    .pin1(c0xp0), .pin2(_7432_1_pin2), .pin3(cin4), .pin4(c4xp1), .pin5(_7432_1_pin5), .pin6(cout),
    .pin7(1'b0), .pin9(1'b0), .pin10(1'b0), .pin12(1'b0), .pin13(1'b0), .pin14(1'b1));  // open: pin8, pin11
  not not_4 (_7432_1_pin2, g_out_0);
  not not_5 (_7432_1_pin5, g_out_1);

  assign out[7] = n;

  // Other names for the same wires on the sheet: cin0 = cin; cin8 = cout; asel = control[0]; ainv = control[1];
  //   bsel = control[2]; binv = control[3]; csel = control[4]; out7 = n

  // Notes on the sheet:
  //   opcode: default 105
  //   control: default 17
  //   A: default 6
  //   B: default 1
  //   C: default 1
endmodule

/* Test case All 91 Operations Test:
opcode control A B C nz-in cin out vout zout nz-out n cout
150 5 149 10 49 1 0 159 x x x x x
150 5 138 146 234 0 1 29 x x x x x
150 1 133 234 150 0 1 134 x x x x x
150 4 71 92 68 1 1 93 x x x x x
150 9 203 42 29 0 0 202 x x x x x
150 6 144 190 232 0 0 189 x x x x x
150 3 99 142 180 1 1 157 x x x x x
150 12 194 174 181 1 1 82 x x x x x
150 3 150 158 14 1 0 105 x x x x x
150 12 32 43 182 1 0 212 x x x x x
150 1 62 249 113 0 0 62 x x x x x
150 4 248 52 207 1 0 52 x x x x x
150 0 23 143 191 1 0 0 x x x x x
150 0 18 194 216 1 1 1 x x x x x
150 10 1 2 25 0 1 255 x x x x x
150 10 195 44 204 0 0 254 x x x x x
150 5 120 253 211 0 0 117 x x x x x
105 12 189 17 179 1 0 17 x x x x x
105 12 115 45 219 0 1 46 x x x x x
105 20 7 45 219 0 1 9 x x x x x
105 5 22 73 7 0 1 161 x x x x x
105 5 22 73 7 1 0 160 x x x x x
150 15 84 32 49 0 1 139 x x x x x
150 15 226 95 77 1 0 189 x x x x x
150 1 170 0 0 0 1 171 x x x x x
150 9 170 0 0 0 0 169 x x x x x
150 1 170 0 0 0 0 170 x x x x x
150 3 10 0 0 0 1 246 x x x x x
150 3 170 0 0 0 0 85 x x x x x
0 21 68 135 121 0 1 0 x x x x x
255 21 111 107 86 0 1 255 x x x x x
170 21 19 55 33 1 0 19 x x x x x
85 21 92 73 181 1 0 163 x x x x x
204 21 75 238 241 0 1 238 x x x x x
51 21 140 223 194 1 0 32 x x x x x
240 21 20 169 110 1 0 110 x x x x x
15 21 211 250 125 0 1 130 x x x x x
136 21 190 14 211 0 0 14 x x x x x
238 21 42 160 237 1 1 170 x x x x x
119 21 217 91 228 0 1 166 x x x x x
17 21 252 179 221 1 0 0 x x x x x
102 21 120 89 213 0 1 33 x x x x x
153 21 213 76 167 0 0 102 x x x x x
160 21 205 116 146 0 1 128 x x x x x
250 21 28 164 108 0 1 124 x x x x x
95 21 219 243 92 1 0 167 x x x x x
5 21 16 148 189 0 0 66 x x x x x
90 21 191 123 252 0 1 67 x x x x x
165 21 63 201 40 1 0 232 x x x x x
192 21 56 68 20 1 0 4 x x x x x
252 21 216 32 156 1 1 188 x x x x x
63 21 87 204 11 1 1 247 x x x x x
3 21 118 17 126 0 0 128 x x x x x
60 21 86 211 162 1 1 113 x x x x x
195 21 164 103 26 1 1 130 x x x x x
34 21 70 26 130 0 0 68 x x x x x
68 21 76 225 191 0 1 161 x x x x x
187 21 156 12 130 1 0 255 x x x x x
221 21 200 167 64 0 1 183 x x x x x
10 21 184 59 170 1 1 16 x x x x x
80 21 216 210 40 1 1 32 x x x x x
175 21 190 232 174 1 0 255 x x x x x
245 21 1 7 72 1 0 254 x x x x x
12 21 120 138 70 1 0 136 x x x x x
48 21 83 70 91 0 0 25 x x x x x
207 21 209 0 164 1 0 91 x x x x x
243 21 137 205 29 0 0 63 x x x x x
128 21 34 215 143 0 0 2 x x x x x
254 21 175 148 12 0 1 191 x x x x x
127 21 122 150 93 1 1 239 x x x x x
1 21 16 253 221 1 1 2 x x x x x
150 21 83 60 255 1 1 144 x x x x x
105 21 244 241 246 0 1 12 x x x x x
232 21 180 163 87 0 1 183 x x x x x
23 21 89 50 163 0 0 204 x x x x x
202 21 173 217 171 1 0 141 x x x x x
226 21 167 154 121 1 0 61 x x x x x
228 21 160 28 173 0 1 188 x x x x x
234 21 153 36 57 1 0 185 x x x x x
236 21 98 41 237 1 1 105 x x x x x
248 21 134 199 26 1 0 158 x x x x x
168 21 42 88 116 1 1 40 x x x x x
200 21 40 204 55 0 0 12 x x x x x
224 21 115 69 15 0 0 7 x x x x x
21 21 197 9 216 1 0 50 x x x x x
19 21 195 28 75 1 0 160 x x x x x
7 21 56 43 190 0 0 65 x x x x x
87 21 105 155 34 0 0 214 x x x x x
55 21 225 221 104 0 0 54 x x x x x
31 21 68 248 134 0 0 123 x x x x x
*/
