// Digital circuit alu-display-control.dig as structural Verilog
module alu_display_control (
  input  [31:0] Data_A,
  input  [31:0] Data_B,
  input  [31:0] Data_C,
  input  [31:0] Data_W,
  input  clk,
  output [7:0] out_5
);

  wire _74154_2_pin19, a0, a1, a2, a3, a4, a5, a6, a7, d0, d1, d2, d3, d4, d5, d6, d7, not_2_out, not_3_out,
       not_4_out, not_5_out, not_6_out, not_7_out, not_8_out, not_9_out, not_10_out, not_11_out, not_12_out,
       not_13_out, not_14_out, not_15_out, not_16_out, not_17_out, not_18_out, not_19_out, not_20_out,
       not_21_out, not_22_out, not_23_out, not_24_out, not_25_out, not_26_out, not_27_out, not_28_out,
       not_29_out, not_30_out, not_31_out, not_32_out, regA0, regA1, regA2, regA3, regA4, regA5, regA6,
       regA7, regB0, regB1, regB2, regB3, regB4, regB5, regB6, regB7, regC0, regC1, regC2, regC3, regC4,
       regC5, regC6, regC7, regW0, regW1, regW2, regW3, regW4, regW5, regW6, regW7, tc0;
  wire [3:0] multiplexer_1_out, multiplexer_2_out, multiplexer_3_out, multiplexer_4_out, mux, register_1_q,
       register_2_q, register_3_q, register_4_q, register_5_q, register_6_q, register_7_q, register_8_q,
       register_9_q, register_10_q, register_11_q, register_12_q, register_13_q, register_14_q,
       register_15_q, register_16_q, register_17_q, register_18_q, register_19_q, register_20_q,
       register_21_q, register_22_q, register_23_q, register_24_q, register_25_q, register_26_q,
       register_27_q, register_28_q, register_29_q, register_30_q, register_31_q;
  wire [7:4] register_1_q_2, register_2_q_2, register_3_q_2, register_4_q_2, register_5_q_2, register_6_q_2,
       register_7_q_2, register_8_q_2, register_9_q_2, register_10_q_2, register_11_q_2, register_12_q_2,
       register_13_q_2, register_14_q_2, register_15_q_2, register_16_q_2, register_17_q_2, register_18_q_2,
       register_19_q_2, register_20_q_2, register_21_q_2, register_22_q_2, register_23_q_2, register_24_q_2,
       register_25_q_2, register_26_q_2, register_27_q_2, register_28_q_2, register_29_q_2, register_30_q_2,
       register_31_q_2;

  Multiplexer #(.Selector_Bits(3), .Bits(4)) multiplexer_1 (
    .sel(out_5[2:0]), .in_0(Data_A[3:0]), .in_1(Data_A[7:4]), .in_2(Data_A[11:8]), .in_3(Data_A[15:12]),
    .in_4(Data_A[19:16]), .in_5(Data_A[23:20]), .in_6(Data_A[27:24]), .in_7(Data_A[31:28]),
    .out(multiplexer_1_out));
  Multiplexer #(.Selector_Bits(3), .Bits(4)) multiplexer_2 (
    .sel(out_5[2:0]), .in_0(Data_B[3:0]), .in_1(Data_B[7:4]), .in_2(Data_B[11:8]), .in_3(Data_B[15:12]),
    .in_4(Data_B[19:16]), .in_5(Data_B[23:20]), .in_6(Data_B[27:24]), .in_7(Data_B[31:28]),
    .out(multiplexer_2_out));
  Multiplexer #(.Selector_Bits(3), .Bits(4)) multiplexer_3 (
    .sel(out_5[2:0]), .in_0(Data_C[3:0]), .in_1(Data_C[7:4]), .in_2(Data_C[11:8]), .in_3(Data_C[15:12]),
    .in_4(Data_C[19:16]), .in_5(Data_C[23:20]), .in_6(Data_C[27:24]), .in_7(Data_C[31:28]),
    .out(multiplexer_3_out));
  Multiplexer #(.Selector_Bits(3), .Bits(4)) multiplexer_4 (
    .sel(out_5[2:0]), .in_0(Data_W[3:0]), .in_1(Data_W[7:4]), .in_2(Data_W[11:8]), .in_3(Data_W[15:12]),
    .in_4(Data_W[19:16]), .in_5(Data_W[23:20]), .in_6(Data_W[27:24]), .in_7(Data_W[31:28]),
    .out(multiplexer_4_out));
  Multiplexer #(.Selector_Bits(2), .Bits(4)) multiplexer_5 (
    .sel(out_5[4:3]), .in_0(multiplexer_1_out), .in_1(multiplexer_2_out), .in_2(multiplexer_3_out),
    .in_3(multiplexer_4_out), .out(mux));
  _74154 _74154_1 (
    .pin1(regA0), .pin2(regA1), .pin3(regA2), .pin4(regA3), .pin5(regA4), .pin6(regA5), .pin7(regA6),
    .pin8(regA7), .pin9(regB0), .pin10(regB1), .pin11(regB2), .pin12(1'b0), .pin13(regB3), .pin14(regB4),
    .pin15(regB5), .pin16(regB6), .pin17(regB7), .pin18(1'b0), .pin19(out_5[4]), .pin20(out_5[3]),
    .pin21(out_5[2]), .pin22(out_5[1]), .pin23(out_5[0]), .pin24(1'b1));
  _74154 _74154_2 (
    .pin1(regC0), .pin2(regC1), .pin3(regC2), .pin4(regC3), .pin5(regC4), .pin6(regC5), .pin7(regC6),
    .pin8(regC7), .pin9(regW0), .pin10(regW1), .pin11(regW2), .pin12(1'b0), .pin13(regW3), .pin14(regW4),
    .pin15(regW5), .pin16(regW6), .pin17(regW7), .pin18(1'b0), .pin19(_74154_2_pin19), .pin20(out_5[3]),
    .pin21(out_5[2]), .pin22(out_5[1]), .pin23(out_5[0]), .pin24(1'b1));
  not not_1 (_74154_2_pin19, out_5[4]);
  _74163 _74163_1 (
    .pin1(1'b1), .pin2(clk), .pin3(1'b0), .pin4(1'b0), .pin5(1'b0), .pin6(1'b0), .pin7(1'b1), .pin8(1'b0),
    .pin9(1'b1), .pin10(1'b1), .pin11(out_5[3]), .pin12(out_5[2]), .pin13(out_5[1]), .pin14(out_5[0]),
    .pin15(tc0), .pin16(1'b1));
  _74163 _74163_2 (
    .pin1(1'b1), .pin2(clk), .pin3(1'b0), .pin4(1'b0), .pin5(1'b0), .pin6(1'b0), .pin7(tc0), .pin8(1'b0),
    .pin9(1'b1), .pin10(tc0), .pin11(out_5[7]), .pin12(out_5[6]), .pin13(out_5[5]), .pin14(out_5[4]),
    .pin16(1'b1));  // open: pin15
  Register #(.Bits(8)) register_1 (
    .D({d7, d6, d5, d4, d3, d2, d1, d0}), .C(clk), .en(not_3_out), .Q({register_1_q_2, register_1_q}));
  Seven_Seg seven_seg_1 (
    .a(register_2_q[0]), .b(register_2_q[1]), .c(register_2_q[2]), .d(register_2_q[3]),
    .e(register_2_q_2[4]), .f(register_2_q_2[5]), .g(register_2_q_2[6]), .dp(register_2_q_2[7]));
  Register #(.Bits(8)) register_2 (
    .D({d7, d6, d5, d4, d3, d2, d1, d0}), .C(clk), .en(not_2_out), .Q({register_2_q_2, register_2_q}));
  not not_2 (not_2_out, regB7);
  Seven_Seg seven_seg_2 (
    .a(register_1_q[0]), .b(register_1_q[1]), .c(register_1_q[2]), .d(register_1_q[3]),
    .e(register_1_q_2[4]), .f(register_1_q_2[5]), .g(register_1_q_2[6]), .dp(register_1_q_2[7]));
  not not_3 (not_3_out, regA7);
  Register #(.Bits(8)) register_3 (
    .D({d7, d6, d5, d4, d3, d2, d1, d0}), .C(clk), .en(not_5_out), .Q({register_3_q_2, register_3_q}));
  Seven_Seg seven_seg_3 (
    .a(register_4_q[0]), .b(register_4_q[1]), .c(register_4_q[2]), .d(register_4_q[3]),
    .e(register_4_q_2[4]), .f(register_4_q_2[5]), .g(register_4_q_2[6]), .dp(register_4_q_2[7]));
  Register #(.Bits(8)) register_4 (
    .D({d7, d6, d5, d4, d3, d2, d1, d0}), .C(clk), .en(not_4_out), .Q({register_4_q_2, register_4_q}));
  not not_4 (not_4_out, regA6);
  Seven_Seg seven_seg_4 (
    .a(register_3_q[0]), .b(register_3_q[1]), .c(register_3_q[2]), .d(register_3_q[3]),
    .e(register_3_q_2[4]), .f(register_3_q_2[5]), .g(register_3_q_2[6]), .dp(register_3_q_2[7]));
  not not_5 (not_5_out, regB6);
  ROM #(.bigEndian("true"), .AddrBits(13), .Bits(8)) display_rom_1 (
    .A({{9{1'b0}}, mux}), .sel(1'b1), .D({d7, d6, d5, d4, d3, d2, d1, d0}));
  Register #(.Bits(8)) register_5 (
    .D({d7, d6, d5, d4, d3, d2, d1, d0}), .C(clk), .en(not_7_out), .Q({register_5_q_2, register_5_q}));
  Seven_Seg seven_seg_5 (
    .a(register_6_q[0]), .b(register_6_q[1]), .c(register_6_q[2]), .d(register_6_q[3]),
    .e(register_6_q_2[4]), .f(register_6_q_2[5]), .g(register_6_q_2[6]), .dp(register_6_q_2[7]));
  Register #(.Bits(8)) register_6 (
    .D({d7, d6, d5, d4, d3, d2, d1, d0}), .C(clk), .en(not_6_out), .Q({register_6_q_2, register_6_q}));
  not not_6 (not_6_out, regB5);
  Seven_Seg seven_seg_6 (
    .a(register_5_q[0]), .b(register_5_q[1]), .c(register_5_q[2]), .d(register_5_q[3]),
    .e(register_5_q_2[4]), .f(register_5_q_2[5]), .g(register_5_q_2[6]), .dp(register_5_q_2[7]));
  not not_7 (not_7_out, regA5);
  Register #(.Bits(8)) register_7 (
    .D({d7, d6, d5, d4, d3, d2, d1, d0}), .C(clk), .en(not_9_out), .Q({register_7_q_2, register_7_q}));
  Seven_Seg seven_seg_7 (
    .a(register_8_q[0]), .b(register_8_q[1]), .c(register_8_q[2]), .d(register_8_q[3]),
    .e(register_8_q_2[4]), .f(register_8_q_2[5]), .g(register_8_q_2[6]), .dp(register_8_q_2[7]));
  Register #(.Bits(8)) register_8 (
    .D({d7, d6, d5, d4, d3, d2, d1, d0}), .C(clk), .en(not_8_out), .Q({register_8_q_2, register_8_q}));
  not not_8 (not_8_out, regA4);
  Seven_Seg seven_seg_8 (
    .a(register_7_q[0]), .b(register_7_q[1]), .c(register_7_q[2]), .d(register_7_q[3]),
    .e(register_7_q_2[4]), .f(register_7_q_2[5]), .g(register_7_q_2[6]), .dp(register_7_q_2[7]));
  not not_9 (not_9_out, regB4);
  Register #(.Bits(8)) register_9 (
    .D({d7, d6, d5, d4, d3, d2, d1, d0}), .C(clk), .en(not_11_out), .Q({register_9_q_2, register_9_q}));
  Seven_Seg seven_seg_9 (
    .a(register_10_q[0]), .b(register_10_q[1]), .c(register_10_q[2]), .d(register_10_q[3]),
    .e(register_10_q_2[4]), .f(register_10_q_2[5]), .g(register_10_q_2[6]), .dp(register_10_q_2[7]));
  Register #(.Bits(8)) register_10 (
    .D({d7, d6, d5, d4, d3, d2, d1, d0}), .C(clk), .en(not_10_out), .Q({register_10_q_2, register_10_q}));
  not not_10 (not_10_out, regB3);
  Seven_Seg seven_seg_10 (
    .a(register_9_q[0]), .b(register_9_q[1]), .c(register_9_q[2]), .d(register_9_q[3]),
    .e(register_9_q_2[4]), .f(register_9_q_2[5]), .g(register_9_q_2[6]), .dp(register_9_q_2[7]));
  not not_11 (not_11_out, regA3);
  Register #(.Bits(8)) register_11 (
    .D({d7, d6, d5, d4, d3, d2, d1, d0}), .C(clk), .en(not_13_out), .Q({register_11_q_2, register_11_q}));
  Seven_Seg seven_seg_11 (
    .a(register_12_q[0]), .b(register_12_q[1]), .c(register_12_q[2]), .d(register_12_q[3]),
    .e(register_12_q_2[4]), .f(register_12_q_2[5]), .g(register_12_q_2[6]), .dp(register_12_q_2[7]));
  Register #(.Bits(8)) register_12 (
    .D({d7, d6, d5, d4, d3, d2, d1, d0}), .C(clk), .en(not_12_out), .Q({register_12_q_2, register_12_q}));
  not not_12 (not_12_out, regA2);
  Seven_Seg seven_seg_12 (
    .a(register_11_q[0]), .b(register_11_q[1]), .c(register_11_q[2]), .d(register_11_q[3]),
    .e(register_11_q_2[4]), .f(register_11_q_2[5]), .g(register_11_q_2[6]), .dp(register_11_q_2[7]));
  not not_13 (not_13_out, regB2);
  Register #(.Bits(8)) register_13 (
    .D({d7, d6, d5, d4, d3, d2, d1, d0}), .C(clk), .en(not_15_out), .Q({register_13_q_2, register_13_q}));
  Seven_Seg seven_seg_13 (
    .a(register_14_q[0]), .b(register_14_q[1]), .c(register_14_q[2]), .d(register_14_q[3]),
    .e(register_14_q_2[4]), .f(register_14_q_2[5]), .g(register_14_q_2[6]), .dp(register_14_q_2[7]));
  Register #(.Bits(8)) register_14 (
    .D({d7, d6, d5, d4, d3, d2, d1, d0}), .C(clk), .en(not_14_out), .Q({register_14_q_2, register_14_q}));
  not not_14 (not_14_out, regB1);
  Seven_Seg seven_seg_14 (
    .a(register_13_q[0]), .b(register_13_q[1]), .c(register_13_q[2]), .d(register_13_q[3]),
    .e(register_13_q_2[4]), .f(register_13_q_2[5]), .g(register_13_q_2[6]), .dp(register_13_q_2[7]));
  not not_15 (not_15_out, regA1);
  Seven_Seg seven_seg_15 (
    .a(register_15_q[0]), .b(register_15_q[1]), .c(register_15_q[2]), .d(register_15_q[3]),
    .e(register_15_q_2[4]), .f(register_15_q_2[5]), .g(register_15_q_2[6]), .dp(register_15_q_2[7]));
  Register #(.Bits(8)) register_15 (
    .D({d7, d6, d5, d4, d3, d2, d1, d0}), .C(clk), .en(not_16_out), .Q({register_15_q_2, register_15_q}));
  not not_16 (not_16_out, regA0);
  Seven_Seg seven_seg_16 (.a(a0), .b(a1), .c(a2), .d(a3), .e(a4), .f(a5), .g(a6), .dp(a7));
  Register #(.Bits(8)) register_16 (
    .D({d7, d6, d5, d4, d3, d2, d1, d0}), .C(clk), .en(not_18_out), .Q({register_16_q_2, register_16_q}));
  Seven_Seg seven_seg_17 (
    .a(register_17_q[0]), .b(register_17_q[1]), .c(register_17_q[2]), .d(register_17_q[3]),
    .e(register_17_q_2[4]), .f(register_17_q_2[5]), .g(register_17_q_2[6]), .dp(register_17_q_2[7]));
  Register #(.Bits(8)) register_17 (
    .D({d7, d6, d5, d4, d3, d2, d1, d0}), .C(clk), .en(not_17_out), .Q({register_17_q_2, register_17_q}));
  not not_17 (not_17_out, regW7);
  Seven_Seg seven_seg_18 (
    .a(register_16_q[0]), .b(register_16_q[1]), .c(register_16_q[2]), .d(register_16_q[3]),
    .e(register_16_q_2[4]), .f(register_16_q_2[5]), .g(register_16_q_2[6]), .dp(register_16_q_2[7]));
  not not_18 (not_18_out, regC7);
  Register #(.Bits(8)) register_18 (
    .D({d7, d6, d5, d4, d3, d2, d1, d0}), .C(clk), .en(not_20_out), .Q({register_18_q_2, register_18_q}));
  _74377 _74377_1 (
    .pin1(regB0), .pin2(a0), .pin3(d0), .pin4(d1), .pin5(a1), .pin6(a2), .pin7(d2), .pin8(d3), .pin9(a3),
    .pin10(1'b0), .pin11(clk), .pin12(a4), .pin13(d4), .pin14(d5), .pin15(a5), .pin16(a6), .pin17(d6),
    .pin18(d7), .pin19(a7), .pin20(1'b1));
  Seven_Seg seven_seg_19 (
    .a(register_19_q[0]), .b(register_19_q[1]), .c(register_19_q[2]), .d(register_19_q[3]),
    .e(register_19_q_2[4]), .f(register_19_q_2[5]), .g(register_19_q_2[6]), .dp(register_19_q_2[7]));
  Register #(.Bits(8)) register_19 (
    .D({d7, d6, d5, d4, d3, d2, d1, d0}), .C(clk), .en(not_19_out), .Q({register_19_q_2, register_19_q}));
  not not_19 (not_19_out, regC6);
  Seven_Seg seven_seg_20 (
    .a(register_18_q[0]), .b(register_18_q[1]), .c(register_18_q[2]), .d(register_18_q[3]),
    .e(register_18_q_2[4]), .f(register_18_q_2[5]), .g(register_18_q_2[6]), .dp(register_18_q_2[7]));
  not not_20 (not_20_out, regW6);
  Register #(.Bits(8)) register_20 (
    .D({d7, d6, d5, d4, d3, d2, d1, d0}), .C(clk), .en(not_22_out), .Q({register_20_q_2, register_20_q}));
  Seven_Seg seven_seg_21 (
    .a(register_21_q[0]), .b(register_21_q[1]), .c(register_21_q[2]), .d(register_21_q[3]),
    .e(register_21_q_2[4]), .f(register_21_q_2[5]), .g(register_21_q_2[6]), .dp(register_21_q_2[7]));
  Register #(.Bits(8)) register_21 (
    .D({d7, d6, d5, d4, d3, d2, d1, d0}), .C(clk), .en(not_21_out), .Q({register_21_q_2, register_21_q}));
  not not_21 (not_21_out, regW5);
  Seven_Seg seven_seg_22 (
    .a(register_20_q[0]), .b(register_20_q[1]), .c(register_20_q[2]), .d(register_20_q[3]),
    .e(register_20_q_2[4]), .f(register_20_q_2[5]), .g(register_20_q_2[6]), .dp(register_20_q_2[7]));
  not not_22 (not_22_out, regC5);
  Register #(.Bits(8)) register_22 (
    .D({d7, d6, d5, d4, d3, d2, d1, d0}), .C(clk), .en(not_24_out), .Q({register_22_q_2, register_22_q}));
  Seven_Seg seven_seg_23 (
    .a(register_23_q[0]), .b(register_23_q[1]), .c(register_23_q[2]), .d(register_23_q[3]),
    .e(register_23_q_2[4]), .f(register_23_q_2[5]), .g(register_23_q_2[6]), .dp(register_23_q_2[7]));
  Register #(.Bits(8)) register_23 (
    .D({d7, d6, d5, d4, d3, d2, d1, d0}), .C(clk), .en(not_23_out), .Q({register_23_q_2, register_23_q}));
  not not_23 (not_23_out, regC4);
  Seven_Seg seven_seg_24 (
    .a(register_22_q[0]), .b(register_22_q[1]), .c(register_22_q[2]), .d(register_22_q[3]),
    .e(register_22_q_2[4]), .f(register_22_q_2[5]), .g(register_22_q_2[6]), .dp(register_22_q_2[7]));
  not not_24 (not_24_out, regW4);
  Register #(.Bits(8)) register_24 (
    .D({d7, d6, d5, d4, d3, d2, d1, d0}), .C(clk), .en(not_26_out), .Q({register_24_q_2, register_24_q}));
  Seven_Seg seven_seg_25 (
    .a(register_25_q[0]), .b(register_25_q[1]), .c(register_25_q[2]), .d(register_25_q[3]),
    .e(register_25_q_2[4]), .f(register_25_q_2[5]), .g(register_25_q_2[6]), .dp(register_25_q_2[7]));
  Register #(.Bits(8)) register_25 (
    .D({d7, d6, d5, d4, d3, d2, d1, d0}), .C(clk), .en(not_25_out), .Q({register_25_q_2, register_25_q}));
  not not_25 (not_25_out, regW3);
  Seven_Seg seven_seg_26 (
    .a(register_24_q[0]), .b(register_24_q[1]), .c(register_24_q[2]), .d(register_24_q[3]),
    .e(register_24_q_2[4]), .f(register_24_q_2[5]), .g(register_24_q_2[6]), .dp(register_24_q_2[7]));
  not not_26 (not_26_out, regC3);
  Register #(.Bits(8)) register_26 (
    .D({d7, d6, d5, d4, d3, d2, d1, d0}), .C(clk), .en(not_28_out), .Q({register_26_q_2, register_26_q}));
  Seven_Seg seven_seg_27 (
    .a(register_27_q[0]), .b(register_27_q[1]), .c(register_27_q[2]), .d(register_27_q[3]),
    .e(register_27_q_2[4]), .f(register_27_q_2[5]), .g(register_27_q_2[6]), .dp(register_27_q_2[7]));
  Register #(.Bits(8)) register_27 (
    .D({d7, d6, d5, d4, d3, d2, d1, d0}), .C(clk), .en(not_27_out), .Q({register_27_q_2, register_27_q}));
  not not_27 (not_27_out, regC2);
  Seven_Seg seven_seg_28 (
    .a(register_26_q[0]), .b(register_26_q[1]), .c(register_26_q[2]), .d(register_26_q[3]),
    .e(register_26_q_2[4]), .f(register_26_q_2[5]), .g(register_26_q_2[6]), .dp(register_26_q_2[7]));
  not not_28 (not_28_out, regW2);
  Register #(.Bits(8)) register_28 (
    .D({d7, d6, d5, d4, d3, d2, d1, d0}), .C(clk), .en(not_30_out), .Q({register_28_q_2, register_28_q}));
  Seven_Seg seven_seg_29 (
    .a(register_29_q[0]), .b(register_29_q[1]), .c(register_29_q[2]), .d(register_29_q[3]),
    .e(register_29_q_2[4]), .f(register_29_q_2[5]), .g(register_29_q_2[6]), .dp(register_29_q_2[7]));
  Register #(.Bits(8)) register_29 (
    .D({d7, d6, d5, d4, d3, d2, d1, d0}), .C(clk), .en(not_29_out), .Q({register_29_q_2, register_29_q}));
  not not_29 (not_29_out, regW1);
  Seven_Seg seven_seg_30 (
    .a(register_28_q[0]), .b(register_28_q[1]), .c(register_28_q[2]), .d(register_28_q[3]),
    .e(register_28_q_2[4]), .f(register_28_q_2[5]), .g(register_28_q_2[6]), .dp(register_28_q_2[7]));
  not not_30 (not_30_out, regC1);
  Register #(.Bits(8)) register_30 (
    .D({d7, d6, d5, d4, d3, d2, d1, d0}), .C(clk), .en(not_32_out), .Q({register_30_q_2, register_30_q}));
  Seven_Seg seven_seg_31 (
    .a(register_31_q[0]), .b(register_31_q[1]), .c(register_31_q[2]), .d(register_31_q[3]),
    .e(register_31_q_2[4]), .f(register_31_q_2[5]), .g(register_31_q_2[6]), .dp(register_31_q_2[7]));
  Register #(.Bits(8)) register_31 (
    .D({d7, d6, d5, d4, d3, d2, d1, d0}), .C(clk), .en(not_31_out), .Q({register_31_q_2, register_31_q}));
  not not_31 (not_31_out, regC0);
  Seven_Seg seven_seg_32 (
    .a(register_30_q[0]), .b(register_30_q[1]), .c(register_30_q[2]), .d(register_30_q[3]),
    .e(register_30_q_2[4]), .f(register_30_q_2[5]), .g(register_30_q_2[6]), .dp(register_30_q_2[7]));
  not not_32 (not_32_out, regW0);

  // Other names for the same wires on the sheet: din[7:0] = {d7, d6, d5, d4, d3, d2, d1, d0}; count0 = out_5[0];
  //   count_n[4:0] = out_5[4:0]; q0 = out_5[0]; sel0[2:0] = out_5[2:0]; sel1[2:0] = out_5[2:0];
  //   sel2[2:0] = out_5[2:0]; sel3[2:0] = out_5[2:0]; count1 = out_5[1]; q1 = out_5[1]; count2 = out_5[2];
  //   q2 = out_5[2]; count3 = out_5[3]; q3 = out_5[3]; count4 = out_5[4]; q4 = out_5[4]; q5 = out_5[5]; q6 = out_5[6];
  //   q7 = out_5[7]

  // Notes on the sheet:
  //   Data_A: default 3735928559
  //   Data_B: default 3134268229
  //   Data_C: default 305419896
  //   Data_W: default 2554539437
  //   clk: Hz: 10
  //   contents of display_rom_1 (hex, n*v repeats v):
  //   11
endmodule
