// Digital circuit alu-display-text.dig as structural Verilog
module alu_display_text (
  input  [9:0] ir_opcode,
  input  clk,
  output [7:0] out_2,
  output [15:0] out_3
);

  wire count0, count1, count2, count3, gnd, reg_textA0, reg_textA1, reg_textB0, reg_textB1, reg_textC0,
       reg_textC1, reg_textD0, reg_textD1, reg_textE0, reg_textE1, reg_textF0, reg_textF1, reg_textG0,
       reg_textG1, reg_textH0, reg_textH1, text_en;
  wire [15:0] text_seg1, text_seg2, text_seg3, text_seg4, text_seg5, text_seg6, text_seg7;

  SixteenSeg sixteenseg_1 (.led(out_3), .dp(gnd));
  SixteenSeg sixteenseg_2 (.led(text_seg1), .dp(gnd));
  SixteenSeg sixteenseg_3 (.led(text_seg2), .dp(gnd));
  Counter #(.Bits(4)) counter_1 (
    .en(text_en), .C(clk), .clr(1'b0), .out({count3, count2, count1, count0}));  // open: ovf
  SixteenSeg sixteenseg_4 (.led(text_seg3), .dp(gnd));
  SixteenSeg sixteenseg_5 (.led(text_seg4), .dp(gnd));
  ROM #(.bigEndian("true"), .AddrBits(13), .Bits(8)) display_rom_2 (
    .A({ir_opcode, count2, count1, count0}), .sel(text_en), .D(out_2));
  ROM #(.bigEndian("true"), .AddrBits(13), .Bits(8)) display_rom_3 (
    .A({ir_opcode, count3, count1, count0}), .sel(text_en), .D(out_2));
  SixteenSeg sixteenseg_6 (.led(text_seg5), .dp(gnd));
  SixteenSeg sixteenseg_7 (.led(text_seg6), .dp(gnd));
  SixteenSeg sixteenseg_8 (.led(text_seg7), .dp(gnd));
  Register #(.Bits(8)) register_1 (.D(out_2), .C(clk), .en(reg_textA0), .Q(out_3[7:0]));
  Register #(.Bits(8)) register_2 (.D(out_2), .C(clk), .en(reg_textA1), .Q(out_3[15:8]));
  Register #(.Bits(8)) register_3 (.D(out_2), .C(clk), .en(reg_textE0), .Q(text_seg4[7:0]));
  Register #(.Bits(8)) register_4 (.D(out_2), .C(clk), .en(reg_textE1), .Q(text_seg4[15:8]));
  Register #(.Bits(8)) register_5 (.D(out_2), .C(clk), .en(reg_textB0), .Q(text_seg1[7:0]));
  Register #(.Bits(8)) register_6 (.D(out_2), .C(clk), .en(reg_textB1), .Q(text_seg1[15:8]));
  Register #(.Bits(8)) register_7 (.D(out_2), .C(clk), .en(reg_textF0), .Q(text_seg5[7:0]));
  Register #(.Bits(8)) register_8 (.D(out_2), .C(clk), .en(reg_textF1), .Q(text_seg5[15:8]));
  Register #(.Bits(8)) register_9 (.D(out_2), .C(clk), .en(reg_textC0), .Q(text_seg2[7:0]));
  Register #(.Bits(8)) register_10 (.D(out_2), .C(clk), .en(reg_textC1), .Q(text_seg2[15:8]));
  Register #(.Bits(8)) register_11 (.D(out_2), .C(clk), .en(reg_textG0), .Q(text_seg6[7:0]));
  Register #(.Bits(8)) register_12 (.D(out_2), .C(clk), .en(reg_textG1), .Q(text_seg6[15:8]));
  Register #(.Bits(8)) register_13 (.D(out_2), .C(clk), .en(reg_textD0), .Q(text_seg3[7:0]));
  Register #(.Bits(8)) register_14 (.D(out_2), .C(clk), .en(reg_textD1), .Q(text_seg3[15:8]));
  Register #(.Bits(8)) register_15 (.D(out_2), .C(clk), .en(reg_textH0), .Q(text_seg7[7:0]));
  Register #(.Bits(8)) register_16 (.D(out_2), .C(clk), .en(reg_textH1), .Q(text_seg7[15:8]));
  Decoder #(.Selector_Bits(4)) decoder_1 (
    .out_0(reg_textA0), .out_1(reg_textA1), .out_2(reg_textB0), .out_3(reg_textB1), .out_4(reg_textC0),
    .out_5(reg_textC1), .out_6(reg_textD0), .out_7(reg_textD1), .out_8(reg_textE0), .out_9(reg_textE1),
    .out_10(reg_textF0), .out_11(reg_textF1), .out_12(reg_textG0), .out_13(reg_textG1), .out_14(reg_textH0),
    .out_15(reg_textH1));  // open: sel

  // Other names for the same wires on the sheet: text_seg0[15:0] = out_3; din_text[7:0] = out_2

  // Notes on the sheet:
  //   contents of display_rom_2 (hex, n*v repeats v):
  //   11
  //   contents of display_rom_3 (hex, n*v repeats v):
  //   11
endmodule
