// Digital circuit alu-test.dig as structural Verilog
module alu_test (
  input  [3:0] A,
  input  [3:0] B,
  input  [3:0] C,
  input  cin,
  input  clk,
  output [3:0] Out,
  output cout,
  output sum3,
  output aeff3,
  output beff3,
  output [7:0] lutA,
  output [7:0] lutB
);

  wire beff0, beff1, beff2, clk_t, counter_1_ovf, found, log0, log1, log2, not_1_out;
  wire [3:0] sub_1_s;

  Counter #(.Bits(8)) counter_1 (.en(1'b1), .C(clk_t), .clr(1'b0), .out(lutA), .ovf(counter_1_ovf));
  Counter #(.Bits(8)) counter_2 (.en(counter_1_ovf), .C(clk_t), .clr(1'b0), .out(lutB));  // open: ovf
  Sub #(.Bits(4)) sub_1 (.a(Out), .b(4'b0110), .c_i(1'b0), .s(sub_1_s));  // open: c_o
  and and_1 (clk_t, clk, not_1_out);
  not not_1 (not_1_out, found);
  nor nor_1 (found, sub_1_s[0], sub_1_s[1], sub_1_s[2], sub_1_s[3]);
  alu_1b_final alu_1b_final_1 (.OPCODE(lutB), .A(A[0]), .B(B[0]), .C(C[0]), .MUX_OUT(log0));
  alu_1b_final alu_1b_final_2 (.OPCODE(lutB), .A(A[1]), .B(B[1]), .C(C[1]), .MUX_OUT(log1));
  alu_1b_final alu_1b_final_3 (.OPCODE(lutB), .A(A[2]), .B(B[2]), .C(C[2]), .MUX_OUT(log2));
  alu_1b_final alu_1b_final_4 (.OPCODE(lutB), .A(A[3]), .B(B[3]), .C(C[3]), .MUX_OUT(aeff3));
  _74283 _74283_1 (
    .pin1(Out[1]), .pin2(beff1), .pin3(log1), .pin4(Out[0]), .pin5(log0), .pin6(beff0), .pin7(cin),
    .pin8(1'b0), .pin9(cout), .pin10(Out[3]), .pin11(beff3), .pin12(aeff3), .pin13(Out[2]), .pin14(log2),
    .pin15(beff2), .pin16(1'b1));
  alu_1b_final alu_1b_final_5 (.OPCODE(lutA), .A(A[0]), .B(B[0]), .C(C[0]), .MUX_OUT(beff0));
  alu_1b_final alu_1b_final_6 (.OPCODE(lutA), .A(A[1]), .B(B[1]), .C(C[1]), .MUX_OUT(beff1));
  alu_1b_final alu_1b_final_7 (.OPCODE(lutA), .A(A[2]), .B(B[2]), .C(C[2]), .MUX_OUT(beff2));
  alu_1b_final alu_1b_final_8 (.OPCODE(lutA), .A(A[3]), .B(B[3]), .C(C[3]), .MUX_OUT(beff3));

  assign sum3 = Out[3];

  // Other names for the same wires on the sheet: log3 = aeff3

  // Notes on the sheet:
  //   A: default 7
  //   B: default 14
  //   clk: Hz: 200000
endmodule
