// Digital circuit b-mux.dig as structural Verilog
module b_mux (
  input  [31:0] ir,
  input  [31:0] reg_b,
  input  [2:0] sel,
  output [31:0] alu_b
);

  Multiplexer #(.Selector_Bits(3), .Bits(32)) multiplexer_1 (
    .sel(sel), .in_0(reg_b), .in_1({{16{1'b0}}, ir[23:8]}), .in_2({{17{ir[23]}}, ir[22:8]}),
    .in_3({ir[23:8], {16{1'b0}}}), .in_4({ir[23:4], {12{1'b0}}}), .in_5({{25{ir[7]}}, ir[6:0]}),
    .in_6({{10{ir[23]}}, ir[22:1]}), .in_7({32{1'b0}}), .out(alu_b));

  // Other names for the same wires on the sheet: ir4[31:0] = {{25{ir[7]}}, ir[6:0]};
  //   ir5[31:0] = {{10{ir[23]}}, ir[22:1]}; ir3[31:12] = ir[23:4]; ir4_out[23:0] = {24{ir[7]}}; ir_7 = ir[7];
  //   ir0[15:0] = ir[23:8]; ir1[31:0] = {{17{ir[23]}}, ir[22:8]}; ir2[31:16] = ir[23:8]; ir1_out[15:0] = {16{ir[23]}};
  //   ir_23 = ir[23]
endmodule
