// Digital circuit bus-arbitration.dig as structural Verilog
module bus_arbitration (
  input  FETCH,
  input  [23:0] PC_OUT,
  input  [23:0] IR_ADDR,
  input  [31:0] Reg_A,
  input  MEM_RD_IN,
  input  [2:0] addr_sel,
  input  [31:0] Reg_b,
  input  [31:0] Reg_A_off,
  input  [31:0] Reg_B_off,
  input  [31:0] Reg_AB,
  input  [31:0] PC_offset,
  input  [31:0] SP_out,
  input  [31:0] Alu_in,
  output [23:0] ADDR_BUS,
  output MEM_RD_OUT
);

  or or_1 (MEM_RD_OUT, MEM_RD_IN, FETCH);
  Multiplexer #(.Selector_Bits(3), .Bits(24)) multiplexer_1 (
    .sel(addr_sel), .in_0(IR_ADDR), .in_1(Reg_A[23:0]), .in_2(Reg_b[23:0]), .in_3(Reg_A_off[23:0]),
    .in_4(Reg_B_off[23:0]), .in_5(PC_offset[23:0]), .in_6(Reg_AB[23:0]), .in_7(SP_out[23:0]), .out(ADDR_BUS));

  // Other names for the same wires on the sheet: alu_out[23:0] = Alu_in[23:0]; pc_offset_t[23:0] = PC_offset[23:0];
  //   reg_a_t[23:0] = Reg_A[23:0]; reg_a_offset[23:0] = Reg_A_off[23:0]; reg_a_b[23:0] = Reg_AB[23:0];
  //   reg_b_t[23:0] = Reg_b[23:0]; reg_b_offset[23:0] = Reg_B_off[23:0]; sp_out_t[23:0] = SP_out[23:0]
endmodule

/* Test case bus-arbitration-exhaustive:
FETCH MEM_RD_IN PC_OUT IR_ADDR reg_a addr_sel ADDR_BUS MEM_RD_OUT

# bus-arbitration.v: sel={FETCH,addr_sel}  MEM_RD_OUT = MEM_RD_IN | FETCH

# A. All 8 control corners (tagged PC/IR/reg_a)
0 0 0x00AA01 0x00BB02 0x00CC03 0 0x00AA01 0
0 1 0x00AA01 0x00BB02 0x00CC03 0 0x00AA01 1
0 0 0x00AA01 0x00BB02 0x00CC03 1 0x00BB02 0
0 1 0x00AA01 0x00BB02 0x00CC03 1 0x00BB02 1
1 0 0x00AA01 0x00BB02 0x00CC03 0 0x00AA01 1
1 1 0x00AA01 0x00BB02 0x00CC03 0 0x00AA01 1
1 0 0x00AA01 0x00BB02 0x00CC03 1 0x00CC03 1
1 1 0x00AA01 0x00BB02 0x00CC03 1 0x00CC03 1

# B. Four address modes (smoke)
0 0 0x000001 0x000002 0x000003 0 0x000001 0
0 0 0x000001 0x000002 0x000003 1 0x000002 0
1 0 0x000001 0x000002 0x000003 0 0x000001 1
1 0 0x000001 0x000002 0x000003 1 0x000003 1

# C. MEM_RD_OUT truth (FETCH OR MEM_RD_IN)
0 0 0x00AA01 0x00BB02 0x00CC03 0 0x00AA01 0
0 1 0x00AA01 0x00BB02 0x00CC03 0 0x00AA01 1
1 0 0x00AA01 0x00BB02 0x00CC03 0 0x00AA01 1
1 1 0x00AA01 0x00BB02 0x00CC03 0 0x00AA01 1

# D. Walking-one PC (modes 0x0 and 0x2)
0 0 0x000001 0x000000 0x000000 0 0x000001 0
1 0 0x000001 0x000000 0x000000 0 0x000001 1
0 0 0x000002 0x000000 0x000000 0 0x000002 0
1 0 0x000002 0x000000 0x000000 0 0x000002 1
0 0 0x000004 0x000000 0x000000 0 0x000004 0
1 0 0x000004 0x000000 0x000000 0 0x000004 1
0 0 0x000008 0x000000 0x000000 0 0x000008 0
1 0 0x000008 0x000000 0x000000 0 0x000008 1
0 0 0x000010 0x000000 0x000000 0 0x000010 0
1 0 0x000010 0x000000 0x000000 0 0x000010 1
0 0 0x000020 0x000000 0x000000 0 0x000020 0
1 0 0x000020 0x000000 0x000000 0 0x000020 1
0 0 0x000040 0x000000 0x000000 0 0x000040 0
1 0 0x000040 0x000000 0x000000 0 0x000040 1
0 0 0x000080 0x000000 0x000000 0 0x000080 0
1 0 0x000080 0x000000 0x000000 0 0x000080 1
0 0 0x000100 0x000000 0x000000 0 0x000100 0
1 0 0x000100 0x000000 0x000000 0 0x000100 1
0 0 0x000200 0x000000 0x000000 0 0x000200 0
1 0 0x000200 0x000000 0x000000 0 0x000200 1
0 0 0x000400 0x000000 0x000000 0 0x000400 0
1 0 0x000400 0x000000 0x000000 0 0x000400 1
0 0 0x000800 0x000000 0x000000 0 0x000800 0
1 0 0x000800 0x000000 0x000000 0 0x000800 1
0 0 0x001000 0x000000 0x000000 0 0x001000 0
1 0 0x001000 0x000000 0x000000 0 0x001000 1
0 0 0x002000 0x000000 0x000000 0 0x002000 0
1 0 0x002000 0x000000 0x000000 0 0x002000 1
0 0 0x004000 0x000000 0x000000 0 0x004000 0
1 0 0x004000 0x000000 0x000000 0 0x004000 1
0 0 0x008000 0x000000 0x000000 0 0x008000 0
1 0 0x008000 0x000000 0x000000 0 0x008000 1
0 0 0x010000 0x000000 0x000000 0 0x010000 0
1 0 0x010000 0x000000 0x000000 0 0x010000 1
0 0 0x020000 0x000000 0x000000 0 0x020000 0
1 0 0x020000 0x000000 0x000000 0 0x020000 1
0 0 0x040000 0x000000 0x000000 0 0x040000 0
1 0 0x040000 0x000000 0x000000 0 0x040000 1
0 0 0x080000 0x000000 0x000000 0 0x080000 0
1 0 0x080000 0x000000 0x000000 0 0x080000 1
0 0 0x100000 0x000000 0x000000 0 0x100000 0
1 0 0x100000 0x000000 0x000000 0 0x100000 1
0 0 0x200000 0x000000 0x000000 0 0x200000 0
1 0 0x200000 0x000000 0x000000 0 0x200000 1
0 0 0x400000 0x000000 0x000000 0 0x400000 0
1 0 0x400000 0x000000 0x000000 0 0x400000 1
0 0 0x800000 0x000000 0x000000 0 0x800000 0
1 0 0x800000 0x000000 0x000000 0 0x800000 1

# E. Walking-one IR (mode 0x1)
0 0 0x000000 0x000001 0x000000 1 0x000001 0
0 0 0x000000 0x000002 0x000000 1 0x000002 0
0 0 0x000000 0x000004 0x000000 1 0x000004 0
0 0 0x000000 0x000008 0x000000 1 0x000008 0
0 0 0x000000 0x000010 0x000000 1 0x000010 0
0 0 0x000000 0x000020 0x000000 1 0x000020 0
0 0 0x000000 0x000040 0x000000 1 0x000040 0
0 0 0x000000 0x000080 0x000000 1 0x000080 0
0 0 0x000000 0x000100 0x000000 1 0x000100 0
0 0 0x000000 0x000200 0x000000 1 0x000200 0
0 0 0x000000 0x000400 0x000000 1 0x000400 0
0 0 0x000000 0x000800 0x000000 1 0x000800 0
0 0 0x000000 0x001000 0x000000 1 0x001000 0
0 0 0x000000 0x002000 0x000000 1 0x002000 0
0 0 0x000000 0x004000 0x000000 1 0x004000 0
0 0 0x000000 0x008000 0x000000 1 0x008000 0
0 0 0x000000 0x010000 0x000000 1 0x010000 0
0 0 0x000000 0x020000 0x000000 1 0x020000 0
0 0 0x000000 0x040000 0x000000 1 0x040000 0
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*/
