// Digital circuit bus-arbitration2.dig as structural Verilog
module bus_arbitration2 (
  input  FETCH,
  input  [23:0] PC_OUT,
  input  [23:0] IR_ADDR,
  input  MEM_RD_IN,
  input  addr_sel,
  input  [31:0] ALU_IN,
  output MEM_RD_OUT,
  output [23:0] Addr_Out
);

  wire a0, a1, a2, a3, b0, b1, b2, b3, pc_en0, pc_en1;

  or or_1 (MEM_RD_OUT, MEM_RD_IN, FETCH);
  _74139 _74139_1 (
    .pin1(1'b0), .pin2(addr_sel), .pin3(FETCH), .pin4(a0), .pin5(a1), .pin6(a2), .pin7(a3), .pin8(1'b0),
    .pin9(b3), .pin10(b2), .pin11(b1), .pin12(b0), .pin13(FETCH), .pin14(addr_sel), .pin15(1'b0), .pin16(1'b1));
  // _74541 _74541_1: pin names not known; wires that end beside it: a0, 1'b0, 1'b1, b0
  // _74541 _74541_2: pin names not known; wires that end beside it: a1, 1'b0, 1'b1, b1
  // _74541 _74541_3: pin names not known; wires that end beside it: pc_en0, 1'b0, 1'b1, pc_en1
  // _74541 _74541_4: pin names not known; wires that end beside it: a0, 1'b0, 1'b1, b0
  // _74541 _74541_5: pin names not known; wires that end beside it: a1, 1'b0, 1'b1, b1
  // _74541 _74541_6: pin names not known; wires that end beside it: pc_en0, 1'b0, 1'b1, pc_en1
  // _74541 _74541_7: pin names not known; wires that end beside it: a0, 1'b0, 1'b1, b0
  // _74541 _74541_8: pin names not known; wires that end beside it: a1, 1'b0, 1'b1, b1
  // _74541 _74541_9: pin names not known; wires that end beside it: pc_en0, 1'b0, 1'b1, pc_en1
  not not_1 (pc_en0, FETCH);
  not not_2 (pc_en1, FETCH);

  // Other names for the same wires on the sheet: alu_in_8[7:0] = ALU_IN[7:0]; alu_in_16[7:0] = ALU_IN[15:8];
  //   alu_in_24[7:0] = ALU_IN[23:16]; ir_in_8[7:0] = IR_ADDR[7:0]; ir_in_16[7:0] = IR_ADDR[15:8];
  //   ir_in_24[7:0] = IR_ADDR[23:16]; pc_in_8[7:0] = PC_OUT[7:0]; pc_in_16[7:0] = PC_OUT[15:8];
  //   pc_in_24[7:0] = PC_OUT[23:16]; alu_out_8[7:0] = Addr_Out[7:0]; ir_out_8[7:0] = Addr_Out[7:0];
  //   pc_out_8[7:0] = Addr_Out[7:0]; alu_out_16[7:0] = Addr_Out[15:8]; ir_out_16[7:0] = Addr_Out[15:8];
  //   pc_out_16[7:0] = Addr_Out[15:8]; alu_out_24[7:0] = Addr_Out[23:16]; ir_out_24[7:0] = Addr_Out[23:16];
  //   pc_out_24[7:0] = Addr_Out[23:16]

  // Notes on the sheet:
  //   PC_OUT: default 59404
  //   IR_ADDR: default 248179
  //   ALU_IN: default 33284
endmodule

/* Test case bus-arbitration:
FETCH MEM_RD_IN PC_OUT IR_ADDR reg_a addr_sel ADDR_BUS MEM_RD_OUT

# bus-arbitration.v: sel={FETCH,addr_sel}  MEM_RD_OUT = MEM_RD_IN | FETCH

# A. All 8 control corners (tagged PC/IR/reg_a)
0 0 0x00AA01 0x00BB02 0x00CC03 0 0x00AA01 0
0 1 0x00AA01 0x00BB02 0x00CC03 0 0x00AA01 1
0 0 0x00AA01 0x00BB02 0x00CC03 1 0x00BB02 0
0 1 0x00AA01 0x00BB02 0x00CC03 1 0x00BB02 1
1 0 0x00AA01 0x00BB02 0x00CC03 0 0x00AA01 1
1 1 0x00AA01 0x00BB02 0x00CC03 0 0x00AA01 1
1 0 0x00AA01 0x00BB02 0x00CC03 1 0x00CC03 1
1 1 0x00AA01 0x00BB02 0x00CC03 1 0x00CC03 1

# B. Four address modes (smoke)
0 0 0x000001 0x000002 0x000003 0 0x000001 0
0 0 0x000001 0x000002 0x000003 1 0x000002 0
1 0 0x000001 0x000002 0x000003 0 0x000001 1
1 0 0x000001 0x000002 0x000003 1 0x000003 1

# C. MEM_RD_OUT truth (FETCH OR MEM_RD_IN)
0 0 0x00AA01 0x00BB02 0x00CC03 0 0x00AA01 0
0 1 0x00AA01 0x00BB02 0x00CC03 0 0x00AA01 1
1 0 0x00AA01 0x00BB02 0x00CC03 0 0x00AA01 1
1 1 0x00AA01 0x00BB02 0x00CC03 0 0x00AA01 1

# D. Walking-one PC (modes 0x0 and 0x2)
0 0 0x000001 0x000000 0x000000 0 0x000001 0
1 0 0x000001 0x000000 0x000000 0 0x000001 1
0 0 0x000002 0x000000 0x000000 0 0x000002 0
1 0 0x000002 0x000000 0x000000 0 0x000002 1
0 0 0x000004 0x000000 0x000000 0 0x000004 0
1 0 0x000004 0x000000 0x000000 0 0x000004 1
0 0 0x000008 0x000000 0x000000 0 0x000008 0
1 0 0x000008 0x000000 0x000000 0 0x000008 1
0 0 0x000010 0x000000 0x000000 0 0x000010 0
1 0 0x000010 0x000000 0x000000 0 0x000010 1
0 0 0x000020 0x000000 0x000000 0 0x000020 0
1 0 0x000020 0x000000 0x000000 0 0x000020 1
0 0 0x000040 0x000000 0x000000 0 0x000040 0
1 0 0x000040 0x000000 0x000000 0 0x000040 1
0 0 0x000080 0x000000 0x000000 0 0x000080 0
1 0 0x000080 0x000000 0x000000 0 0x000080 1
0 0 0x000100 0x000000 0x000000 0 0x000100 0
1 0 0x000100 0x000000 0x000000 0 0x000100 1
0 0 0x000200 0x000000 0x000000 0 0x000200 0
1 0 0x000200 0x000000 0x000000 0 0x000200 1
0 0 0x000400 0x000000 0x000000 0 0x000400 0
1 0 0x000400 0x000000 0x000000 0 0x000400 1
0 0 0x000800 0x000000 0x000000 0 0x000800 0
1 0 0x000800 0x000000 0x000000 0 0x000800 1
0 0 0x001000 0x000000 0x000000 0 0x001000 0
1 0 0x001000 0x000000 0x000000 0 0x001000 1
0 0 0x002000 0x000000 0x000000 0 0x002000 0
1 0 0x002000 0x000000 0x000000 0 0x002000 1
0 0 0x004000 0x000000 0x000000 0 0x004000 0
1 0 0x004000 0x000000 0x000000 0 0x004000 1
0 0 0x008000 0x000000 0x000000 0 0x008000 0
1 0 0x008000 0x000000 0x000000 0 0x008000 1
0 0 0x010000 0x000000 0x000000 0 0x010000 0
1 0 0x010000 0x000000 0x000000 0 0x010000 1
0 0 0x020000 0x000000 0x000000 0 0x020000 0
1 0 0x020000 0x000000 0x000000 0 0x020000 1
0 0 0x040000 0x000000 0x000000 0 0x040000 0
1 0 0x040000 0x000000 0x000000 0 0x040000 1
0 0 0x080000 0x000000 0x000000 0 0x080000 0
1 0 0x080000 0x000000 0x000000 0 0x080000 1
0 0 0x100000 0x000000 0x000000 0 0x100000 0
1 0 0x100000 0x000000 0x000000 0 0x100000 1
0 0 0x200000 0x000000 0x000000 0 0x200000 0
1 0 0x200000 0x000000 0x000000 0 0x200000 1
0 0 0x400000 0x000000 0x000000 0 0x400000 0
1 0 0x400000 0x000000 0x000000 0 0x400000 1
0 0 0x800000 0x000000 0x000000 0 0x800000 0
1 0 0x800000 0x000000 0x000000 0 0x800000 1

# E. Walking-one IR (mode 0x1)
0 0 0x000000 0x000001 0x000000 1 0x000001 0
0 0 0x000000 0x000002 0x000000 1 0x000002 0
0 0 0x000000 0x000004 0x000000 1 0x000004 0
0 0 0x000000 0x000008 0x000000 1 0x000008 0
0 0 0x000000 0x000010 0x000000 1 0x000010 0
0 0 0x000000 0x000020 0x000000 1 0x000020 0
0 0 0x000000 0x000040 0x000000 1 0x000040 0
0 0 0x000000 0x000080 0x000000 1 0x000080 0
0 0 0x000000 0x000100 0x000000 1 0x000100 0
0 0 0x000000 0x000200 0x000000 1 0x000200 0
0 0 0x000000 0x000400 0x000000 1 0x000400 0
0 0 0x000000 0x000800 0x000000 1 0x000800 0
0 0 0x000000 0x001000 0x000000 1 0x001000 0
0 0 0x000000 0x002000 0x000000 1 0x002000 0
0 0 0x000000 0x004000 0x000000 1 0x004000 0
0 0 0x000000 0x008000 0x000000 1 0x008000 0
0 0 0x000000 0x010000 0x000000 1 0x010000 0
0 0 0x000000 0x020000 0x000000 1 0x020000 0
0 0 0x000000 0x040000 0x000000 1 0x040000 0
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*/
