// Digital circuit byte-lane-decoder.dig as structural Verilog
module byte_lane_decoder (
  input  [39:0] mem_in,
  input  [3:0] sel_in,
  input  [7:0] io_data_in,
  output [39:0] mem_out
);

  wire [23:0] d15__gt_24, d31__gt_24;
  wire [31:0] d7__gt_32, d15__gt_32, d23__gt_32, d31__gt_32;

  Multiplexer #(.Selector_Bits(4), .Bits(40)) multiplexer_1 (
    .sel(sel_in), .in_0(mem_in),
    .in_1({mem_in[7:0], mem_in[15:8], mem_in[23:16], mem_in[31:24], mem_in[39:32]}),
    .in_2({{32{1'b0}}, io_data_in}), .in_3({{32{1'b0}}, mem_in[7:0]}), .in_4({d7__gt_32, mem_in[7:0]}),
    .in_5({d15__gt_32, mem_in[15:8]}), .in_6({d23__gt_32, mem_in[23:16]}),
    .in_7({d31__gt_32, mem_in[31:24]}), .in_8({{32{1'b0}}, mem_in[15:8]}),
    .in_9({{32{1'b0}}, mem_in[23:16]}), .in_10({{32{1'b0}}, mem_in[31:24]}),
    .in_11({{32{1'b0}}, mem_in[39:32]}), .in_12({d15__gt_24, mem_in[15:0]}),
    .in_13({d31__gt_24, mem_in[31:16]}), .in_14({{24{1'b0}}, mem_in[15:0]}),
    .in_15({{24{1'b0}}, mem_in[31:16]}), .out(mem_out));
  BitExtender #(.inputBits(1), .outputBits(32)) bitextender_1 (.in(mem_in[7]), .out(d7__gt_32));
  BitExtender #(.inputBits(1), .outputBits(32)) bitextender_2 (.in(mem_in[15]), .out(d15__gt_32));
  BitExtender #(.inputBits(1), .outputBits(32)) bitextender_3 (.in(mem_in[23]), .out(d23__gt_32));
  BitExtender #(.inputBits(1), .outputBits(32)) bitextender_4 (.in(mem_in[31]), .out(d31__gt_32));
  BitExtender #(.inputBits(1), .outputBits(24)) bitextender_5 (.in(mem_in[15]), .out(d15__gt_24));
  BitExtender #(.inputBits(1), .outputBits(24)) bitextender_6 (.in(mem_in[31]), .out(d31__gt_24));

  // Other names for the same wires on the sheet: in0[39:0] = {d7__gt_32, mem_in[7:0]};
  //   in8[39:0] = {d15__gt_24, mem_in[15:0]}; in1[39:0] = {d15__gt_32, mem_in[15:8]};
  //   in2[39:0] = {d23__gt_32, mem_in[23:16]}; in9[39:0] = {d31__gt_24, mem_in[31:16]};
  //   in3[39:0] = {d31__gt_32, mem_in[31:24]}; io_in[7:0] = io_data_in; byte0[7:0] = mem_in[7:0];
  //   byte01[15:0] = mem_in[15:0]; in10[15:0] = mem_in[15:0];
  //   in12[39:0] = {mem_in[7:0], mem_in[15:8], mem_in[23:16], mem_in[31:24], mem_in[39:32]}; in13[7:0] = mem_in[7:0];
  //   byte1[7:0] = mem_in[15:8]; in4[7:0] = mem_in[15:8]; byte2[7:0] = mem_in[23:16]; byte23[15:0] = mem_in[31:16];
  //   in5[7:0] = mem_in[23:16]; in11[15:0] = mem_in[31:16]; byte3[7:0] = mem_in[31:24]; in6[7:0] = mem_in[31:24];
  //   byte4[7:0] = mem_in[39:32]; in7[7:0] = mem_in[39:32]; sel[3:0] = sel_in

  // Notes on the sheet:
  //   mem_in: default 738175336175
  //   io_data_in: default 4660
  //   BYTE-EXTRACT
  //   S-BYTE
  //   S-HALF-LOW-HIGH
  //   Z-BYTE
  //   Z-HALF-LOW-HIGH
endmodule

/* Test case byte-lane spot-check:
mem-in sel-in io-data-in c-addr-msb2 mem-out

# A — word pass-through (sel=0: mem_sel=0, c-addr-msb2=0)
0xAABBCCDD 0 0 0 0xAABBCCDD
0x01020304 0 0 0 0x01020304

# B — byte swap for stores (sel=1)
0xAABBCCDD 1 0 0 0xDDCCBBAA

# C — IO read path (sel=2)
0x00000000 2 0xDEADBEEF 0 0xDEADBEEF

# D — sign-extend byte0 (sel=4: mem_sel=0, c-addr-msb2=1)
0xAABBCC80 0 0 1 0xFFFFFF80
0x000000FF 0 0 1 0xFFFFFFFF

# E — zero-extend byte0 (sel=8: mem_sel=0, c-addr-msb2=2)
0xAABBCCDD 0 0 2 0x000000DD

# F — sign-extend byte1 (sel=5: mem_sel=1, c-addr-msb2=1)
0x0000807F 1 0 1 0xFFFFFF80

# G — sign-extend half (sel=12: mem_sel=0, c-addr-msb2=3)
0xAABB8000 0 0 3 0xFFFF8000

# H — zero-extend half (sel=14: mem_sel=2, c-addr-msb2=3)
0xAABBCCDD 2 0 3 0x0000CCDD
*/
