// Digital circuit flag-reg.dig as structural Verilog
module flag_reg (
  input  ZERO_IN,
  input  CARRY_IN,
  input  NEGATIVE_IN,
  input  OVERFLOW_IN,
  input  FLAG_WE,
  input  CLK,
  input  EXEC,
  output FLAG_Z,
  output FLAG_C,
  output FLAG_N,
  output FLAG_O
);

  wire CLK_GATED, FLAG_C_N, FLAG_NN, FLAG_O_N, FLAG_Z_N;

  _7474 _7474_1 (
    .pin1(1'b1), .pin2(ZERO_IN), .pin3(CLK_GATED), .pin4(1'b1), .pin5(FLAG_Z), .pin6(FLAG_Z_N), .pin7(1'b0),
    .pin8(FLAG_C_N), .pin9(FLAG_C), .pin10(1'b1), .pin11(CLK_GATED), .pin12(CARRY_IN), .pin13(1'b1),
    .pin14(1'b1));
  and and_1 (CLK_GATED, CLK, EXEC, FLAG_WE);
  _7474 _7474_2 (
    .pin1(1'b1), .pin2(NEGATIVE_IN), .pin3(CLK_GATED), .pin4(1'b1), .pin5(FLAG_N), .pin6(FLAG_NN),
    .pin7(1'b0), .pin8(FLAG_O_N), .pin9(FLAG_O), .pin10(1'b1), .pin11(CLK_GATED), .pin12(OVERFLOW_IN),
    .pin13(1'b1), .pin14(1'b1));
endmodule

/* Test case flag-reg tests:
ZERO_IN CARRY_IN NEGATIVE_IN OVERFLOW_IN FLAG_WE CLK FLAG_Z FLAG_C FLAG_N FLAG_O

# -------------------------------------------------------
# SECTION 1: Power-on / reset baseline
# After reset (no clock edge delivered yet) outputs are X (unknown).
# We first write 0000 to establish a known state.
# -------------------------------------------------------

# Write all-zeros: WE=1, CLK rising edge -> capture 0000
0 0 0 0 1 C 0 0 0 0
0 0 0 0 1 0 0 0 0 0

# -------------------------------------------------------
# SECTION 2: WE=0 gating - clock edges must NOT change outputs
# -------------------------------------------------------

# Try to write all-ones with WE=0; outputs must stay 0000
1 1 1 1 0 C 0 0 0 0
1 1 1 1 0 0 0 0 0 0
# Multiple clock cycles with WE=0 - still no capture
1 1 1 1 0 C 0 0 0 0
1 1 1 1 0 C 0 0 0 0
1 1 1 1 0 C 0 0 0 0
# Clear inputs while WE still low - outputs still 0000
0 0 0 0 0 C 0 0 0 0
0 0 0 0 0 0 0 0 0 0

# -------------------------------------------------------
# SECTION 3: Write all-ones (1111) with WE=1
# -------------------------------------------------------
1 1 1 1 1 C 1 1 1 1
1 1 1 1 1 0 1 1 1 1

# -------------------------------------------------------
# SECTION 4: WE=0 gating - outputs stay at 1111 even with 0-inputs on CLK
# -------------------------------------------------------
0 0 0 0 0 C 1 1 1 1
0 0 0 0 0 C 1 1 1 1
0 0 0 0 0 C 1 1 1 1

# -------------------------------------------------------
# SECTION 5: All 16 input combinations captured correctly (WE=1)
# We sequence through every 4-bit combination {ZERO,CARRY,NEG,OVF}
# 0000
0 0 0 0 1 C 0 0 0 0
# 0001
0 0 0 1 1 C 0 0 0 1
# 0010
0 0 1 0 1 C 0 0 1 0
# 0011
0 0 1 1 1 C 0 0 1 1
# 0100
0 1 0 0 1 C 0 1 0 0
# 0101
0 1 0 1 1 C 0 1 0 1
# 0110
0 1 1 0 1 C 0 1 1 0
# 0111
0 1 1 1 1 C 0 1 1 1
# 1000
1 0 0 0 1 C 1 0 0 0
# 1001
1 0 0 1 1 C 1 0 0 1
# 1010
1 0 1 0 1 C 1 0 1 0
# 1011
1 0 1 1 1 C 1 0 1 1
# 1100
1 1 0 0 1 C 1 1 0 0
# 1101
1 1 0 1 1 C 1 1 0 1
# 1110
1 1 1 0 1 C 1 1 1 0
# 1111
1 1 1 1 1 C 1 1 1 1

# -------------------------------------------------------
# SECTION 6: Individual flag isolation - only ZERO_IN active
# -------------------------------------------------------
# Start from 0000
0 0 0 0 1 C 0 0 0 0
# Set only ZERO
1 0 0 0 1 C 1 0 0 0
# Clear only ZERO
0 0 0 0 1 C 0 0 0 0

# -------------------------------------------------------
# SECTION 7: Individual flag isolation - only CARRY_IN active
# -------------------------------------------------------
0 1 0 0 1 C 0 1 0 0
0 0 0 0 1 C 0 0 0 0

# -------------------------------------------------------
# SECTION 8: Individual flag isolation - only NEGATIVE_IN active
# -------------------------------------------------------
0 0 1 0 1 C 0 0 1 0
0 0 0 0 1 C 0 0 0 0

# -------------------------------------------------------
# SECTION 9: Individual flag isolation - only OVERFLOW_IN active
# -------------------------------------------------------
0 0 0 1 1 C 0 0 0 1
0 0 0 0 1 C 0 0 0 0

# -------------------------------------------------------
# SECTION 10: Toggle each flag high then low (1->0) - verifies no latching
# -------------------------------------------------------
# Load 1111
1 1 1 1 1 C 1 1 1 1
# Clear ZERO only
0 1 1 1 1 C 0 1 1 1
# Clear CARRY only (from 1111)
1 1 1 1 1 C 1 1 1 1
1 0 1 1 1 C 1 0 1 1
# Clear NEGATIVE only (from 1111)
1 1 1 1 1 C 1 1 1 1
1 1 0 1 1 C 1 1 0 1
# Clear OVERFLOW only (from 1111)
1 1 1 1 1 C 1 1 1 1
1 1 1 0 1 C 1 1 1 0

# -------------------------------------------------------
# SECTION 11: Rapid alternating WE toggling
# Each line: same data inputs, alternating WE, check output sticky
# -------------------------------------------------------
# Write 1010
1 0 1 0 1 C 1 0 1 0
# WE=0, try to overwrite with 0101 - must stay 1010
0 1 0 1 0 C 1 0 1 0
0 1 0 1 0 C 1 0 1 0
# WE=1 - now overwrite with 0101
0 1 0 1 1 C 0 1 0 1
# WE=0 - try to overwrite with 1010 - must stay 0101
1 0 1 0 0 C 0 1 0 1
1 0 1 0 0 C 0 1 0 1
# WE=1 now write 1111
1 1 1 1 1 C 1 1 1 1

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*/
