// Digital circuit fsm.dig as structural Verilog
module fsm (
  input  RST,
  input  hold,
  input  [2:0] csel,
  input  CLK,
  output [31:0] out
);

  wire _7400_1_pin3, count_en, e0, en, found, nhold, out32, out33, out34, out35, out36, out37, out38, out39,
       out40, out41, out42, out43, out44, out45, out46, out47, out48, out49, out50, out51, out52, out53,
       out54, out55, out56, out57, out58, out59, out60, out61, out62, out63, ovf, r0, r1, r2, r3, r4, r5, r6,
       rc0, rc1, rc2, reg_en, zout_7__0, zout_15__8, zout_23__16, zout_31__24, zout_39__32, zout_47__40,
       zout_55__48;
  wire [0:0] cin1, cin2, cin3, cin4, cin5, cin6, cin7;
  wire [7:0] csr_flg, lutA, lutAin, lutB, lutBin;
  wire [63:0] Test;

  _7400 _7400_1 (
    .pin1(ovf), .pin2(ovf), .pin3(_7400_1_pin3), .pin4(_7400_1_pin3), .pin5(found), .pin6(e0), .pin7(1'b0),
    .pin8(en), .pin9(e0), .pin10(RST), .pin11(nhold), .pin12(hold), .pin13(hold), .pin14(1'b1));
  _74161 _74161_1 (
    .pin1(RST), .pin2(CLK), .pin3(1'b0), .pin4(1'b0), .pin5(1'b0), .pin6(1'b0), .pin7(count_en), .pin8(1'b0),
    .pin9(1'b1), .pin10(1'b1), .pin11(lutAin[3]), .pin12(lutAin[2]), .pin13(lutAin[1]), .pin14(lutAin[0]),
    .pin15(rc0), .pin16(1'b1));
  _74688 _74688_1 (
    .pin1(1'b0), .pin2(out[0]), .pin3(Test[0]), .pin4(out[1]), .pin5(Test[1]), .pin6(out[2]), .pin7(Test[2]),
    .pin8(out[3]), .pin9(Test[3]), .pin10(1'b0), .pin11(out[4]), .pin12(Test[4]), .pin13(out[5]),
    .pin14(Test[5]), .pin15(out[6]), .pin16(Test[6]), .pin17(out[7]), .pin18(Test[7]), .pin19(r0),
    .pin20(1'b1));
  _74688 _74688_2 (
    .pin1(r3), .pin2(out32), .pin3(Test[32]), .pin4(out33), .pin5(Test[33]), .pin6(out34), .pin7(Test[34]),
    .pin8(out35), .pin9(Test[35]), .pin10(1'b0), .pin11(out36), .pin12(Test[36]), .pin13(out37),
    .pin14(Test[37]), .pin15(out38), .pin16(Test[38]), .pin17(out39), .pin18(Test[39]), .pin19(r4),
    .pin20(1'b1));
  _74161 _74161_2 (
    .pin1(RST), .pin2(CLK), .pin3(1'b0), .pin4(1'b0), .pin5(1'b0), .pin6(1'b0), .pin7(count_en), .pin8(1'b0),
    .pin9(1'b1), .pin10(rc0), .pin11(lutAin[7]), .pin12(lutAin[6]), .pin13(lutAin[5]), .pin14(lutAin[4]),
    .pin15(rc1), .pin16(1'b1));
  _7400 _7400_2 (
    .pin1(nhold), .pin2(en), .pin3(reg_en), .pin4(reg_en), .pin5(reg_en), .pin6(count_en), .pin7(1'b0),
    .pin9(1'b0), .pin10(1'b0), .pin12(1'b0), .pin13(1'b0), .pin14(1'b1));  // open: pin8, pin11
  _74688 _74688_3 (
    .pin1(r0), .pin2(out[8]), .pin3(Test[8]), .pin4(out[9]), .pin5(Test[9]), .pin6(out[10]), .pin7(Test[10]),
    .pin8(out[11]), .pin9(Test[11]), .pin10(1'b0), .pin11(out[12]), .pin12(Test[12]), .pin13(out[13]),
    .pin14(Test[13]), .pin15(out[14]), .pin16(Test[14]), .pin17(out[15]), .pin18(Test[15]), .pin19(r1),
    .pin20(1'b1));
  _74688 _74688_4 (
    .pin1(r4), .pin2(out40), .pin3(Test[40]), .pin4(out41), .pin5(Test[41]), .pin6(out42), .pin7(Test[42]),
    .pin8(out43), .pin9(Test[43]), .pin10(1'b0), .pin11(out44), .pin12(Test[44]), .pin13(out45),
    .pin14(Test[45]), .pin15(out46), .pin16(Test[46]), .pin17(out47), .pin18(Test[47]), .pin19(r5),
    .pin20(1'b1));
  _74377 _74377_1 (
    .pin1(reg_en), .pin2(lutA[0]), .pin3(lutAin[0]), .pin4(lutAin[1]), .pin5(lutA[1]), .pin6(lutA[2]),
    .pin7(lutAin[2]), .pin8(lutAin[3]), .pin9(lutA[3]), .pin10(1'b0), .pin11(CLK), .pin12(lutA[4]),
    .pin13(lutAin[4]), .pin14(lutAin[5]), .pin15(lutA[5]), .pin16(lutA[6]), .pin17(lutAin[6]),
    .pin18(lutAin[7]), .pin19(lutA[7]), .pin20(1'b1));
  _74161 _74161_3 (
    .pin1(RST), .pin2(CLK), .pin3(1'b0), .pin4(1'b0), .pin5(1'b0), .pin6(1'b0), .pin7(count_en), .pin8(1'b0),
    .pin9(1'b1), .pin10(rc1), .pin11(lutBin[3]), .pin12(lutBin[2]), .pin13(lutBin[1]), .pin14(lutBin[0]),
    .pin15(rc2), .pin16(1'b1));
  _74688 _74688_5 (
    .pin1(r1), .pin2(out[16]), .pin3(Test[16]), .pin4(out[17]), .pin5(Test[17]), .pin6(out[18]),
    .pin7(Test[18]), .pin8(out[19]), .pin9(Test[19]), .pin10(1'b0), .pin11(out[20]), .pin12(Test[20]),
    .pin13(out[21]), .pin14(Test[21]), .pin15(out[22]), .pin16(Test[22]), .pin17(out[23]), .pin18(Test[23]),
    .pin19(r2), .pin20(1'b1));
  _74688 _74688_6 (
    .pin1(r5), .pin2(out48), .pin3(Test[48]), .pin4(out49), .pin5(Test[49]), .pin6(out50), .pin7(Test[50]),
    .pin8(out51), .pin9(Test[51]), .pin10(1'b0), .pin11(out52), .pin12(Test[52]), .pin13(out53),
    .pin14(Test[53]), .pin15(out54), .pin16(Test[54]), .pin17(out55), .pin18(Test[55]), .pin19(r6),
    .pin20(1'b1));
  _74161 _74161_4 (
    .pin1(RST), .pin2(CLK), .pin3(1'b0), .pin4(1'b0), .pin5(1'b0), .pin6(1'b0), .pin7(count_en), .pin8(1'b0),
    .pin9(1'b1), .pin10(rc2), .pin11(lutBin[7]), .pin12(lutBin[6]), .pin13(lutBin[5]), .pin14(lutBin[4]),
    .pin15(ovf), .pin16(1'b1));
  _74377 _74377_2 (
    .pin1(reg_en), .pin2(lutB[0]), .pin3(lutBin[0]), .pin4(lutBin[1]), .pin5(lutB[1]), .pin6(lutB[2]),
    .pin7(lutBin[2]), .pin8(lutBin[3]), .pin9(lutB[3]), .pin10(1'b0), .pin11(CLK), .pin12(lutB[4]),
    .pin13(lutBin[4]), .pin14(lutBin[5]), .pin15(lutB[5]), .pin16(lutB[6]), .pin17(lutBin[6]),
    .pin18(lutBin[7]), .pin19(lutB[7]), .pin20(1'b1));
  _74688 _74688_7 (
    .pin1(r2), .pin2(out[24]), .pin3(Test[24]), .pin4(out[25]), .pin5(Test[25]), .pin6(out[26]),
    .pin7(Test[26]), .pin8(out[27]), .pin9(Test[27]), .pin10(1'b0), .pin11(out[28]), .pin12(Test[28]),
    .pin13(out[29]), .pin14(Test[29]), .pin15(out[30]), .pin16(Test[30]), .pin17(out[31]), .pin18(Test[31]),
    .pin19(r3), .pin20(1'b1));
  _74688 _74688_8 (
    .pin1(r6), .pin2(out56), .pin3(Test[56]), .pin4(out57), .pin5(Test[57]), .pin6(out58), .pin7(Test[58]),
    .pin8(out59), .pin9(Test[59]), .pin10(1'b0), .pin11(out60), .pin12(Test[60]), .pin13(out61),
    .pin14(Test[61]), .pin15(out62), .pin16(Test[62]), .pin17(out63), .pin18(Test[63]), .pin19(found),
    .pin20(1'b1));
  alu_8b_final alu_8b_final_1 (
    .lutA(lutA), .A(8'hbb), .B(8'hcd), .C(8'h59), .lutB(lutB), .zin(1'b0), .FLAG_WE(1'b1), .csel(csel),
    .CLK(CLK), .out(out[7:0]), .zout(zout_7__0), .cout(cin1[0]));  // open: csr_flg
  alu_8b_final alu_8b_final_2 (
    .lutA(lutA), .A({8{1'b0}}), .B({8{1'b0}}), .C({8{1'b0}}), .lutB(lutB), .zin(zout_31__24), .FLAG_WE(1'b1),
    .csel({2'b00, cin4[0]}), .CLK(CLK), .out({out39, out38, out37, out36, out35, out34, out33, out32}),
    .zout(zout_39__32), .cout(cin5[0]));  // open: csr_flg
  alu_8b_final alu_8b_final_3 (
    .lutA(lutA), .A(8'h3a), .B(8'h45), .C(8'hf6), .lutB(lutB), .zin(zout_7__0), .FLAG_WE(1'b1),
    .csel({2'b00, cin1[0]}), .CLK(CLK), .out(out[15:8]), .zout(zout_15__8), .cout(cin2[0]));  // open: csr_flg
  alu_8b_final alu_8b_final_4 (
    .lutA(lutA), .A({8{1'b0}}), .B({8{1'b0}}), .C({8{1'b0}}), .lutB(lutB), .zin(zout_47__40), .FLAG_WE(1'b1),
    .csel({2'b00, cin5[0]}), .CLK(CLK), .out({out47, out46, out45, out44, out43, out42, out41, out40}),
    .zout(zout_47__40), .cout(cin6[0]));  // open: csr_flg
  alu_8b_final alu_8b_final_5 (
    .lutA(lutA), .A(8'h65), .B(8'h1), .C(8'h55), .lutB(lutB), .zin(zout_15__8), .FLAG_WE(1'b1),
    .csel({2'b00, cin2[0]}), .CLK(CLK), .out(out[23:16]), .zout(zout_23__16), .cout(cin3[0]));  // open: csr_flg
  alu_8b_final alu_8b_final_6 (
    .lutA(lutA), .A({8{1'b0}}), .B({8{1'b0}}), .C({8{1'b0}}), .lutB(lutB), .zin(zout_55__48), .FLAG_WE(1'b1),
    .csel({2'b00, cin6[0]}), .CLK(CLK), .out({out55, out54, out53, out52, out51, out50, out49, out48}),
    .zout(zout_55__48), .cout(cin7[0]));  // open: csr_flg
  alu_8b_final alu_8b_final_7 (
    .lutA(lutA), .A(8'h2e), .B(8'h7d), .C(8'h14), .lutB(lutB), .zin(zout_23__16), .FLAG_WE(1'b1),
    .csel({2'b00, cin3[0]}), .CLK(CLK), .out(out[31:24]), .zout(zout_31__24), .cout(cin4[0]));  // open: csr_flg
  alu_8b_final alu_8b_final_8 (
    .lutA(lutA), .A({8{1'b0}}), .B({8{1'b0}}), .C({8{1'b0}}), .lutB(lutB), .zin(zout_55__48), .FLAG_WE(1'b1),
    .csel({2'b00, cin7[0]}), .CLK(CLK), .out({out63, out62, out61, out60, out59, out58, out57, out56}),
    .csr_flg(csr_flg));  // open: zout, cout
  // also tied to GND on the sheet: {Test[0], Test[2], Test[3], Test[5], Test[6], Test[7], Test[8], Test[9], Test[10], Test[11], Test[12], Test[13], Test[14], Test[15], Test[16], Test[18], Test[19], Test[20], Test[21], Test[22], Test[23], Test[24], Test[25], Test[26], Test[28], Test[29], Test[30], Test[31], Test[32], Test[33], Test[34], Test[35], Test[36], Test[37], Test[38], Test[39], Test[40], Test[41], Test[42], Test[43], Test[44], Test[45], Test[46], Test[47], Test[48], Test[49], Test[50], Test[51], Test[52], Test[53], Test[54], Test[55], Test[56], Test[57], Test[58], Test[59], Test[60], Test[61], Test[62], Test[63]}
  // also tied to VCC on the sheet: {Test[1], Test[4], Test[17], Test[27]}

  // Other names for the same wires on the sheet: cout0 = cin1[0]; cout1 = cin2[0]; cout2 = cin3[0]; cout3 = cin4[0];
  //   cout4 = cin5[0]; cout5 = cin6[0]; cout6 = cin7[0]; OUT_7__0[7:0] = out[7:0];
  //   OUT_t[63:0] = {out63, out62, out61, out60, out59, out58, out57, out56, out55, out54, out53, out52, out51, out50, out49, out48, out47, out46, out45, out44, out43, out42, out41, out40, out39, out38, out37, out36, out35, out34, out33, out32, out};
  //   OUT_15__8[7:0] = out[15:8]; OUT_23__16[7:0] = out[23:16]; OUT_31__24[7:0] = out[31:24];
  //   OUT_39__32[7:0] = {out39, out38, out37, out36, out35, out34, out33, out32};
  //   OUT_47__40[7:0] = {out47, out46, out45, out44, out43, out42, out41, out40};
  //   OUT_55__48[7:0] = {out55, out54, out53, out52, out51, out50, out49, out48};
  //   OUT_63__56[7:0] = {out63, out62, out61, out60, out59, out58, out57, out56}; q0 = lutAin[0]; q1 = lutAin[1];
  //   q2 = lutAin[2]; q3 = lutAin[3]; q4 = lutAin[4]; q5 = lutAin[5]; q6 = lutAin[6]; q7 = lutAin[7]; q8 = lutBin[0];
  //   q9 = lutBin[1]; q10 = lutBin[2]; q11 = lutBin[3]; q12 = lutBin[4]; q13 = lutBin[5]; q14 = lutBin[6];
  //   q15 = lutBin[7]

  // Notes on the sheet:
  //   RST: default 1
  //   CLK: Hz: 1000000
endmodule
