// Digital circuit hex_seg.dig as structural Verilog
module hex_seg (
  input  clk,
  input  data_tog,
  input  en_tog,
  output [6:0] data_out,
  output [7:0] en_out,
  output dp
);

  wire [3:0] multiplexer_1_out;
  wire [6:0] bitextender_2_out, hex_d;
  wire [7:0] bitextender_1_out, counter_1_out;

  BitExtender #(.inputBits(1), .outputBits(8)) bitextender_1 (.in(en_tog), .out(bitextender_1_out));
  Counter #(.Bits(8)) counter_1 (.en(1'b1), .C(clk), .clr(1'b0), .out(counter_1_out));  // open: ovf
  Multiplexer #(.Bits(4), .Selector_Bits(3)) multiplexer_1 (
    .sel(counter_1_out[2:0]), .in_0(4'b1110), .in_1(4'b0100), .in_2(4'b0011), .in_3(4'b1101), .in_4(4'b1111),
    .in_5(4'b0111), .in_6(4'b0110), .in_7(4'b0101), .out(multiplexer_1_out));
  assign en_out = counter_1_out ^ bitextender_1_out;  // XOr xor_1, 8 bits wide
  ROM #(.AddrBits(4), .Bits(7)) hex (.A(multiplexer_1_out), .sel(1'b1), .D(hex_d));
  assign data_out = hex_d ^ bitextender_2_out;  // XOr xor_2, 7 bits wide
  BitExtender #(.inputBits(1), .outputBits(7)) bitextender_2 (.in(data_tog), .out(bitextender_2_out));

  assign dp = 1'b1;

  // Notes on the sheet:
  //   contents of hex (hex, n*v repeats v):
  //   40,79,24,30,19,12,2,78,0,10,8,3,46,21,6,e
endmodule
