// Digital circuit io_controller.dig as structural Verilog
module io_controller (
  input  [23:0] mem_addr,
  input  c_wr,
  input  [15:0] kb_data,
  input  [31:0] mem_data_out,
  output [31:0] io_data_in,
  output ram_cs,
  output vram_we,
  output [15:0] vram_addr,
  output [15:0] vram_data,
  output term_we,
  output [15:0] term_data
);

  wire comp2_eq, comp3__gt, comp3_eq, comp4__lt, comp4_eq, or_1_out;

  Comparator #(.Bits(24)) comparator_1 (.a(mem_addr), .b(24'h800000), .lt(ram_cs));  // open: gt, eq
  Comparator #(.Bits(24)) comparator_2 (.a(mem_addr), .b(24'h800010), .eq(comp2_eq));  // open: gt, lt
  Comparator #(.Bits(24)) comparator_3 (.a(mem_addr), .b(24'hf00000), .gt(comp3__gt), .eq(comp3_eq));  // open: lt
  or or_1 (or_1_out, comp3__gt, comp3_eq);
  Comparator #(.Bits(24)) comparator_4 (.a(mem_addr), .b(24'h800014), .eq(comp4_eq), .lt(comp4__lt));  // open: gt
  Multiplexer #(.Bits(32)) multiplexer_1 (
    .sel(comp4_eq), .in_0({32{1'b0}}), .in_1({{16{1'b0}}, kb_data}), .out(io_data_in));
  and and_1 (vram_we, or_1_out, c_wr);
  and and_2 (term_we, comp2_eq, c_wr);

  assign term_data = mem_data_out[15:0];
  assign vram_addr = mem_addr[15:0];
  assign vram_data = mem_data_out[15:0];

  // Other names for the same wires on the sheet: c_dout[31:0] = mem_data_out; c_term_data[15:0] = mem_data_out[15:0];
  //   c_vram_data[15:0] = mem_data_out[15:0]; c_io_in[31:0] = io_data_in; c_ram_cs = ram_cs; c_term_we = term_we;
  //   c_vram_we = vram_we; c_kb_in[15:0] = kb_data; c_vram_addr[15:0] = mem_addr[15:0]
endmodule

/* Test case:
mem_addr c_wr mem_rd kb_data mem_data_out kb_avail io_data_in ram_cs vram_we vram_addr vram_data term_we term_data
0x000000 0 1 0x0000 0x00000000 0 0x00000000 1 0 0x0000 0x0000 0 0x0000
0x7FFFFF 0 1 0x0000 0x00000000 0 0x00000000 1 0 0xFFFF 0x0000 0 0x0000
0x800000 0 1 0x0000 0x00000000 0 0x00000000 0 0 0x0000 0x0000 0 0x0000
0x800001 0 1 0x0000 0x00000000 0 0x00000000 0 0 0x0001 0x0000 0 0x0000
0x800010 1 0 0x0000 0x12345678 0 0x00000000 0 0 0x0010 0x5678 1 0x5678
0x800010 0 1 0x0000 0x12345678 0 0x00000000 0 0 0x0010 0x5678 0 0x5678
0x800014 0 1 0xABCD 0x00000000 1 0x0000ABCD 0 0 0x0014 0x0000 0 0x0000
0x800014 1 0 0x1234 0x00000000 1 0x00001234 0 0 0x0014 0x0000 0 0x0000
0xEFFFFF 0 1 0x0000 0x00000000 0 0x00000000 0 0 0xFFFF 0x0000 0 0x0000
0xF00000 1 0 0x0000 0xDEADBEEF 0 0x00000000 0 1 0x0000 0xBEEF 0 0xBEEF
0xF00000 0 1 0x0000 0xDEADBEEF 0 0x00000000 0 0 0x0000 0xBEEF 0 0xBEEF
0xFFFFFF 1 0 0x0000 0x00001111 0 0x00000000 0 1 0xFFFF 0x1111 0 0x1111
*/
