// Digital circuit ir-reg-control.dig as structural Verilog
module ir_reg_control (
  input  [8:0] op,
  output [3:0] ir_imm_sel,
  output [2:0] wb_sel,
  output reg_we
);

  ROM #(.bigEndian("true"), .AddrBits(9), .Bits(8)) ir_reg_control (
    .A(op), .sel(1'b1), .D({reg_we, wb_sel, ir_imm_sel}));

  // Other names for the same wires on the sheet: ir_opcode[8:0] = op

  // Notes on the sheet:
  //   op: default 48
  //   contents of ir_reg_control (hex, n*v repeats v):
  //   0,80,80,80,80,80,80,0,0,0,0,0,0,0,0,0,0,0,0,0,0,0,0,0,0,0,0,0,0,0,0,0,83,87,87,87,eb,0,0,0,
  //   0,0,0,0,0,0,0,0,0,0,0,0,0,0,0,0,0,0,0,0,0,0,0,0,90,90,90,0,0,0,0,0,0,0,0,0,0,0,0,0,0,0,0,0,
  //   0,0,0,0,0,0,0,0,0,0,0,0,b3,b3,0,0,0,0,0,0,3,3,0,0,0,0,0,0,0,0,0,0,0,0,0,0,0,0,0,0,0,0,0,0,c,
  //   c,c,0,0,0,0,0,0,0,0,0,0,0,0,0,0,0,0,0,0,0,0,0,0,0,0,0,0,0,0,0,d,a9,0,0,0,0,0,0,0,0,0,0,0,0,
  //   0,0,0,0,0,0,0,0,0,0,0,0,0,0,0,0,0,0,0,0,0,0,0,0,0,0,0,0,0,0,0,0,0,0,0,0,0,0,0,0,0,0,0,0,0,0,
  //   0,0,0,0,0,0,0,0,0,0,0,0,0,0,0,0,0,0,0,0,0,0,0,0,0,0,0,0,0,0,0,0,0,0,0,0,0,0,0,0,0,0,0,0,0,0,
  //   0,0,0,0,0,0,0,0,0,0,0,0,0,0,0,0,0,0,0,0,0,0,0,0,0,0,0,0,0,0,0,0,0,0,0,0,0,0,0,0,0,0,0,0,0,0,
  //   0,0,0,0,0,0,0,0,0,0,0,0,0,0,0,0,0,0,0,0,0,0,0,0,0,0,0,0,0,0,0,0,0,0,0,0,0,0,0,0,0,0,0,0,0,0,
  //   0,0,0,0,0,0,0,0,0,0,0,0,0,0,0,0,0,0,0,0,0,0,0,0,0,0,0,0,0,0,0,0,0,0,0,0,0,0,0,0,0,0,0,0,0,0,
  //   0,0,0,0,0,0,0,0,0,0,0,0,0,0,0,0,0,0,0,0,0,0,0,0,0,0,0,0,0,0,0,0,0,0,0,0,0,0,0,0,0,0,0,0,0,0,
  //   0,0,0,0,0,0,0,0,0,0,0,0,0,0,0,0,0,0,0,0,0,0,0,0,0,0,0,0,0,0,0,0,0,0,0,0,0,0,0,0,0,0,0,0,0,0,
  //   0,0,0,0,0,0,0,0,0,0,0,0,0,0,0,0
endmodule

/* Test case tomato-v1-burn:
op ir-imm-sel wb-sel reg-we
# NOP
0 0 0 0
# ADD
1 0 0 1
# SUB
2 0 0 1
# AND
3 0 0 1
# OR
4 0 0 1
# XOR
5 0 0 1
# MOV
6 0 0 1
# CMP
7 0 0 0
# ADDI
32 3 0 1
# ANDI
33 7 0 1
# ORI
34 7 0 1
# XORI
35 7 0 1
# LUI
36 11 6 1
# LSL
64 0 1 1
# LSR
65 0 1 1
# ASR
66 0 1 1
# LW
96 3 3 1
# LB
97 3 3 1
# SW
104 3 0 0
# SB
105 3 0 0
# BEQ
128 12 0 0
# BNE
129 12 0 0
# BLT
130 12 0 0
# JMP
160 13 0 0
# JAL
161 9 2 1
# RET
162 0 0 0
# JR
163 0 0 0
# HALT
255 0 0 0
*/
