// Digital circuit ir.dig as structural Verilog
module ir (
  input  [31:0] DATA_IN,
  input  LOAD,
  input  CLK,
  input  [3:0] ir_sel,
  input  [31:0] RegB,
  output [8:0] OPCODE,
  output [4:0] ADDR_A,
  output [4:0] ADDR_B,
  output [4:0] ADDR_W,
  output [21:0] ADDR_ABS,
  output [21:0] OFFSET,
  output [31:0] ir_imm_out,
  output [2:0] BANK_SEL,
  output [4:0] ADDR_C
);

  wire [25:0] ir14__gt_26;
  wire [31:8] ir2;
  wire [31:12] ir3;
  wire [31:16] ir8;
  wire [31:18] ir12;
  wire [31:23] ir9;
  wire [31:25] ir13;

  Register #(.Bits(32)) register_1 (
    .D(DATA_IN), .C(CLK), .en(LOAD), .Q({OPCODE, ADDR_W[4], ADDR_ABS[21:18], ADDR_A, ADDR_ABS[12:0]}));
  Multiplexer #(.Selector_Bits(4), .Bits(32)) multiplexer_1 (
    .sel(ir_sel), .in_0({{24{1'b0}}, ADDR_ABS[7:0]}), .in_1(RegB), .in_2({ir2, ADDR_ABS[7:0]}),
    .in_3({ir3, ADDR_ABS[21:18], ADDR_A, ADDR_ABS[12:10]}), .in_4({{20{1'b0}}, ADDR_ABS[11:0]}),
    .in_5({{27{1'b0}}, ADDR_W[4], ADDR_ABS[21:18]}), .in_6({{27{1'b0}}, ADDR_ABS[20:18], ADDR_A[4:3]}),
    .in_7({{16{1'b0}}, ADDR_A[2:0], ADDR_ABS[12:0]}), .in_8({ir8, ADDR_A[2:0], ADDR_ABS[12:0]}),
    .in_9({ir9, ADDR_W[4], ADDR_ABS[21:18], ADDR_A, ADDR_ABS[12:0]}),
    .in_10({ADDR_W[4], ADDR_ABS[21:18], ADDR_A, ADDR_ABS[12:7], {16{1'b0}}}),
    .in_11({ADDR_W[4], ADDR_ABS[21:18], ADDR_A, ADDR_ABS[12:3], {12{1'b0}}}),
    .in_12({ir12, ADDR_A[2:0], ADDR_ABS[12:0], 2'b00}),
    .in_13({ir13, ADDR_W[4], ADDR_ABS[21:18], ADDR_A, ADDR_ABS[12:0], 2'b00}),
    .in_14({{9{1'b0}}, ADDR_W[4], ADDR_ABS[21:18], ADDR_A, ADDR_ABS[12:0]}),
    .in_15({ir14__gt_26, ADDR_A[1:0], ADDR_ABS[12:9]}), .out(ir_imm_out));
  BitExtender #(.inputBits(1), .outputBits(24)) bitextender_1 (.in(ADDR_ABS[7]), .out(ir2));
  BitExtender #(.inputBits(1), .outputBits(20)) bitextender_2 (.in(ADDR_ABS[21]), .out(ir3));
  BitExtender #(.inputBits(1)) bitextender_3 (.in(ADDR_A[2]), .out(ir8));
  BitExtender #(.inputBits(1), .outputBits(9)) bitextender_4 (.in(ADDR_W[4]), .out(ir9));
  BitExtender #(.inputBits(1), .outputBits(14)) bitextender_5 (.in(ADDR_A[2]), .out(ir12));
  BitExtender #(.inputBits(1), .outputBits(7)) bitextender_6 (.in(ADDR_W[4]), .out(ir13));
  BitExtender #(.inputBits(1), .outputBits(26)) bitextender_7 (.in(ADDR_A[1]), .out(ir14__gt_26));

  assign ADDR_ABS[17:13] = ADDR_A;
  assign ADDR_B = ADDR_ABS[12:8];
  assign ADDR_C = ADDR_ABS[12:8];
  assign ADDR_W[3:0] = ADDR_ABS[21:18];
  assign BANK_SEL = ADDR_ABS[2:0];
  assign OFFSET = {ADDR_ABS[21:18], ADDR_A, ADDR_ABS[12:0]};

  // Other names for the same wires on the sheet: imm_out[31:0] = ir_imm_out; ir7__gt_22[23:0] = ir2;
  //   ir15[31:0] = {ir14__gt_26, ADDR_A[1:0], ADDR_ABS[12:9]}; ir15__gt_14[13:0] = ir12; ir15__gt_16[15:0] = ir8;
  //   ir21__gt_7[6:0] = ir13; ir21__gt_9[8:0] = ir9; ir21__gt_18[19:0] = ir3; ir1[7:0] = ADDR_ABS[7:0];
  //   ir2[7:0] = ADDR_ABS[7:0]; ir4[11:0] = ADDR_ABS[11:0]; ir7[15:0] = {ADDR_A[2:0], ADDR_ABS[12:0]};
  //   ir8[15:0] = {ADDR_A[2:0], ADDR_ABS[12:0]}; ir9[22:0] = {ADDR_W[4], ADDR_ABS[21:18], ADDR_A, ADDR_ABS[12:0]};
  //   ir12[17:2] = {ADDR_A[2:0], ADDR_ABS[12:0]}; ir13[24:2] = {ADDR_W[4], ADDR_ABS[21:18], ADDR_A, ADDR_ABS[12:0]};
  //   ir14[22:0] = {ADDR_W[4], ADDR_ABS[21:18], ADDR_A, ADDR_ABS[12:0]};
  //   ir_bus[22:0] = {ADDR_W[4], ADDR_ABS[21:18], ADDR_A, ADDR_ABS[12:0]};
  //   ir_bus_main[31:0] = {OPCODE, ADDR_W[4], ADDR_ABS[21:18], ADDR_A, ADDR_ABS[12:0]}; ADDR_C_t[4:0] = ADDR_ABS[7:3];
  //   ir11[31:12] = {ADDR_W[4], ADDR_ABS[21:18], ADDR_A, ADDR_ABS[12:3]};
  //   ir10[31:16] = {ADDR_W[4], ADDR_ABS[21:18], ADDR_A, ADDR_ABS[12:7]};
  //   ir3[11:0] = {ADDR_ABS[21:18], ADDR_A, ADDR_ABS[12:10]}; ir6[4:0] = {ADDR_ABS[20:18], ADDR_A[4:3]};
  //   ir5[4:0] = {ADDR_W[4], ADDR_ABS[21:18]}; reg_b[31:0] = RegB

  // Notes on the sheet:
  //   DATA_IN: default 3735928559
  //   RegB: default 2882356583
endmodule

/* Test case ir-layout-decode:
CLK LOAD DATA_IN ir-sel RegB OPCODE ADDR_A ADDR_B ADDR_W BANK_SEL ADDR_ABS OFFSET COND MUX1_SEL MUX2_SEL ir-imm-out

# 10|6|6|6|4 field split (opcode[31:22] ra rb rd bank[3:0]) — latch then read
# enc: op=0x2AF ra=0x0D rb=0x04 rd=0x23 bank=4
0 0 0xABCD1234 0 0 x x x x x x x x x x x
0 1 0xABCD1234 0 0 x x x x x x x x x x x
C 1 0xABCD1234 0 0 x x x x x x x x x x x
0 0 0xABCD1234 0 0 0x2AF 0x0D 0x04 0x23 4 0xD1234 0xD1234 4 0 0 x

# NOP opcode all-zero operand zone
0 0 0x00000000 0 0 x x x x x x x x x x x
0 1 0x00000000 0 0 x x x x x x x x x x x
C 1 0x00000000 0 0 x x x x x x x x x x x
0 0 0x00000000 0 0 0x000 0x00 0x00 0x00 0 0x000000 0x000000 0 0 0 x

# reg-reg word: ADD ra=1 rb=2 rd=3 bank=11 (op=0x001)
0 0 0x0041083B 0 0 x x x x x x x x x x x
0 1 0x0041083B 0 0 x x x x x x x x x x x
C 1 0x0041083B 0 0 x x x x x x x x x x x
0 0 0x0041083B 0 0 0x001 0x01 0x02 0x03 11 0x1083B 0x1083B 3 1 1 x
*/

/* Test case ir-addr-ctrl:
CLK LOAD DATA_IN ir-sel RegB OPCODE ADDR_A ADDR_B ADDR_W BANK_SEL ADDR_ABS OFFSET COND MUX1_SEL MUX2_SEL ir-imm-out

# ADDR_ABS/OFFSET = IR[21:0]; COND=IR[2:0]; BANK_SEL=IR[3:0] (low nibble)
0 0 0x003FFFFF 0 0 x x x x x x x x x x x
0 1 0x003FFFFF 0 0 x x x x x x x x x x x
C 1 0x003FFFFF 0 0 x x x x x x x x x x x
0 0 0x003FFFFF 0 0 0x000 0x3F 0x3F 0x3F 15 0x3FFFFF 0x3FFFFF 7 1 1 x

# jump-style: bank=1 operand payload 0x155000
0 0 0x00155001 0 0 x x x x x x x x x x x
0 1 0x00155001 0 0 x x x x x x x x x x x
C 1 0x00155001 0 0 x x x x x x x x x x x
0 0 0x00155001 0 0 0x000 0x15 0x14 0x00 1 0x155001 0x155001 1 1 0 x
*/

/* Test case ir-imm-decode:
CLK LOAD DATA_IN ir-sel RegB OPCODE ADDR_A ADDR_B ADDR_W BANK_SEL ADDR_ABS OFFSET COND MUX1_SEL MUX2_SEL ir-imm-out

# sel=0 pass-through RegB
0 0 0x00000000 0 0xABCD0000 x x x x x x x x x x x
0 1 0x00000000 0 0xABCD0000 x x x x x x x x x x x
C 1 0x00000000 0 0xABCD0000 x x x x x x x x x x x
0 0 0x00000000 0 0xABCD0000 0x000 0x00 0x00 0x00 0 0x000000 0x000000 0 0 0 0xABCD0000

# sel=2 8b_sign IR[7:0]=0xFB (-5)
0 0 0x000000FB 2 0 x x x x x x x x x x x
0 1 0x000000FB 2 0 x x x x x x x x x x x
C 1 0x000000FB 2 0 x x x x x x x x x x x
0 0 0x000000FB 2 0 x x x x x x x x x x 0xFFFFFFFB

# sel=3 12b_sign from ir-bus[11:0] (word 0x400 yields 1 with current taps)
0 0 0x00000400 3 0 x x x x x x x x x x x
0 1 0x00000400 3 0 x x x x x x x x x x x
C 1 0x00000400 3 0 x x x x x x x x x x x
0 0 0x00000400 3 0 x x x x x x x x x x 0x00000001

# sel=5 SHAMT — ir-bus[12:8] tap (0x500: shamt field overlaps rd; imm=0 today)
0 0 0x00000500 5 0 x x x x x x x x x x x
0 1 0x00000500 5 0 x x x x x x x x x x x
C 1 0x00000500 5 0 x x x x x x x x x x x
0 0 0x00000500 5 0 x x x x x x x x x x 0x00000000

# sel=7 16b_zero IR[15:0]=0x1234
0 0 0x00001234 7 0 x x x x x x x x x x x
0 1 0x00001234 7 0 x x x x x x x x x x x
C 1 0x00001234 7 0 x x x x x x x x x x x
0 0 0x00001234 7 0 x x x x x x x x x x 0x00001234

# sel=11 LUI20 (ir-bus[21:4] shifted — word 0x1234500)
0 0 0x01234500 11 0 x x x x x x x x x x x
0 1 0x01234500 11 0 x x x x x x x x x x x
C 1 0x01234500 11 0 x x x x x x x x x x x
0 0 0x01234500 11 0 x x x x x x x x x x 0x8D140000

# sel=14 imm22z zero_ext(IR[21:0]) — word 0x00054321
0 0 0x00054321 14 0 x x x x x x x x x x x
0 1 0x00054321 14 0 x x x x x x x x x x x
C 1 0x00054321 14 0 x x x x x x x x x x x
0 0 0x00054321 14 0 x x x x x x x x x x 0x00054321

# sel=15 imm6s sign_ext(IR[14:9]) — IR[14:9]=6'b111111 (-1)
0 0 0x00007FC0 15 0 x x x x x x x x x x x
0 1 0x00007FC0 15 0 x x x x x x x x x x x
C 1 0x00007FC0 15 0 x x x x x x x x x x x
0 0 0x00007FC0 15 0 x x x x x x x x x x 0xFFFFFFFF
*/
