// Digital circuit led_matrix.dig as structural Verilog
module led_matrix (
  input  clk,
  output out_2,
  output out_3,
  output out_4,
  output out_5,
  output out_6,
  output out_7,
  output out_8,
  output out_9,
  output out_10,
  output out_11,
  output out_12,
  output out_13,
  output out_14,
  output out_15,
  output out_16,
  output out_17,
  output out_18,
  output out_19,
  output out_20,
  output out_21,
  output out_22,
  output out_23,
  output out_24,
  output out_25,
  output out_26,
  output out_27,
  output out_28,
  output out_29,
  output out_30,
  output out_31,
  output out_32,
  output out_33,
  output out_34,
  output out_35,
  output out_36,
  output out_37,
  output out_38,
  output out_39,
  output out_40,
  output out_41,
  output out_42,
  output out_43,
  output out_44,
  output out_45,
  output out_46,
  output out_47,
  output out_48,
  output out_49,
  output out_50,
  output out_51,
  output out_52,
  output out_53,
  output out_54,
  output out_55,
  output out_56,
  output out_57,
  output out_58,
  output out_59,
  output out_60,
  output out_61,
  output out_62,
  output out_63,
  output out_64,
  output out_65
);

  wire [5:0] addr;
  wire [63:0] A, B, C;

  Counter #(.Bits(64)) counter_1 (.en(1'b1), .C(clk), .clr(1'b0), .out(A));  // open: ovf
  Counter #(.Bits(64)) counter_2 (.en(1'b1), .C(clk), .clr(1'b0), .out(B));  // open: ovf
  Counter #(.Bits(64)) counter_3 (.en(1'b1), .C(clk), .clr(1'b0), .out(C));  // open: ovf
  Counter #(.Bits(6)) counter_4 (.en(1'b1), .C(clk), .clr(1'b0), .out(addr));  // open: ovf
  // fsm fsm_1: pin names not known; wires that end beside it: A, B, C, A, 1'b1, 1'b0, 1'b0, 3'b000, 1'b0, clk, {out_65, out_64, out_63, out_62, out_61, out_60, out_59, out_58, out_57, out_56, out_55, out_54, out_53, out_52, out_51, out_50, out_49, out_48, out_47, out_46, out_45, out_44, out_43, out_42, out_41, out_40, out_39, out_38, out_37, out_36, out_35, out_34, out_33, out_32, out_31, out_30, out_29, out_28, out_27, out_26, out_25, out_24, out_23, out_22, out_21, out_20, out_19, out_18, out_17, out_16, out_15, out_14, out_13, out_12, out_11, out_10, out_9, out_8, out_7, out_6, out_5, out_4, out_3, out_2}

  // Other names for the same wires on the sheet: data[63:0] = {out_65, out_64, out_63, out_62, out_61, out_60, out_59, out_58, out_57, out_56, out_55, out_54, out_53, out_52, out_51, out_50, out_49, out_48, out_47, out_46, out_45, out_44, out_43, out_42, out_41, out_40, out_39, out_38, out_37, out_36, out_35, out_34, out_33, out_32, out_31, out_30, out_29, out_28, out_27, out_26, out_25, out_24, out_23, out_22, out_21, out_20, out_19, out_18, out_17, out_16, out_15, out_14, out_13, out_12, out_11, out_10, out_9, out_8, out_7, out_6, out_5, out_4, out_3, out_2}

  // Notes on the sheet:
  //   clk: Hz: 2
endmodule
