// Digital circuit mem-bus-control.dig as structural Verilog
module mem_bus_control (
  input  [8:0] op,
  output [2:0] ctrl_bussel
);

  wire [7:3] mem_bus_control_d;

  ROM #(.bigEndian("true"), .AddrBits(9), .isProgramMemory("true"), .Bits(8)) mem_bus_control (
    .A(op), .sel(1'b1), .D({mem_bus_control_d, ctrl_bussel}));

  // Other names for the same wires on the sheet: ir_opcode[8:0] = op

  // Notes on the sheet:
  //   op: default 48
  //   contents of mem_bus_control (hex, n*v repeats v):
  //   0,0,0,0,0,0,0,0,0,0,0,0,0,0,0,0,0,0,0,0,0,0,0,0,0,0,0,0,0,0,0,0,0,0,0,0,0,0,0,0,0,0,0,0,0,0,
  //   0,0,0,0,0,0,0,0,0,0,0,0,0,0,0,0,0,0,0,0,0,0,0,0,0,0,0,0,0,0,0,0,0,0,0,0,0,0,0,0,0,0,0,0,0,0,
  //   0,0,0,0,1,1,0,0,0,0,0,0,1,1,0,0,0,0,0,0,0,0,0,0,0,0,0,0,0,0,0,0,0,0,0,0,0,0,0,0,0,0,0,0,0,0,
  //   0,0,0,0,0,0,0,0,0,0,0,0,0,0,0,0,0,0,0,0,0,0,0,0,2,2,0,0,0,0,0,0,0,0,0,0,0,0,0,0,0,0,0,0,0,0,
  //   0,0,0,0,0,0,0,0,0,0,0,0,0,0,0,0,0,0,0,0,0,0,0,0,0,0,0,0,0,0,0,0,0,0,0,0,0,0,0,0,0,0,0,0,0,0,
  //   0,0,0,0,0,0,0,0,0,0,0,0,0,0,0,0,0,0,0,0,0,0,0,0,0,0,0,0,0,0,0,0,0,0,0,0,0,0,0,0,0,0,0,0,0,0,
  //   0,0,0,0,0,0,0,0,0,0,0,0,0,0,0,0,0,0,0,0,0,0,0,0,0,0,0,0,0,0,0,0,0,0,0,0,0,0,0,0,0,0,0,0,0,0,
  //   0,0,0,0,0,0,0,0,0,0,0,0,0,0,0,0,0,0,0,0,0,0,0,0,0,0,0,0,0,0,0,0,0,0,0,0,0,0,0,0,0,0,0,0,0,0,
  //   0,0,0,0,0,0,0,0,0,0,0,0,0,0,0,0,0,0,0,0,0,0,0,0,0,0,0,0,0,0,0,0,0,0,0,0,0,0,0,0,0,0,0,0,0,0,
  //   0,0,0,0,0,0,0,0,0,0,0,0,0,0,0,0,0,0,0,0,0,0,0,0,0,0,0,0,0,0,0,0,0,0,0,0,0,0,0,0,0,0,0,0,0,0,
  //   0,0,0,0,0,0,0,0,0,0,0,0,0,0,0,0,0,0,0,0,0,0,0,0,0,0,0,0,0,0,0,0,0,0,0,0,0,0,0,0,0,0,0,0,0,0,
  //   0,0,0,0,0,0
endmodule

/* Test case tomato-v1-burn:
op ctrl-bussel
# NOP
0 0
# ADD
1 0
# SUB
2 0
# AND
3 0
# OR
4 0
# XOR
5 0
# MOV
6 0
# CMP
7 0
# ADDI
32 0
# ANDI
33 0
# ORI
34 0
# XORI
35 0
# LUI
36 0
# LSL
64 0
# LSR
65 0
# ASR
66 0
# LW
96 1
# LB
97 1
# SW
104 1
# SB
105 1
# BEQ
128 0
# BNE
129 0
# BLT
130 0
# JMP
160 0
# JAL
161 0
# RET
162 2
# JR
163 2
# HALT
255 0
*/
