// Digital circuit mem-control.dig as structural Verilog
module mem_control (
  input  [9:0] op,
  input  exec,
  output [7:0] alu_op,
  output [3:0] alu_pre,
  output [1:0] cin_sel,
  output [1:0] shift_op,
  output [3:0] ir_imm_sel,
  output bank_en,
  output [2:0] wb_sel,
  output reg_we,
  output flags_we,
  output mem_rd,
  output mem_wr,
  output [3:0] byte_sel,
  output branch_en,
  output jump_type,
  output [2:0] pc_src,
  output [1:0] sp_out,
  output [1:0] cycles,
  output [2:0] ctrl_bussel,
  output mul_en,
  output pc_link_we,
  output [1:0] mem_sel,
  output [3:0] pc_cond,
  output p_enc,
  output HALT_IN
);

  wire comparator_1_eq;
  wire [63:53] microcode_eeprom_d;

  ROM #(.bigEndian("true"), .AddrBits(10), .Bits(64)) microcode_eeprom (
    .A(op), .sel(1'b1),
    .D({microcode_eeprom_d, p_enc, mul_en, ctrl_bussel, cycles, pc_cond, pc_link_we, pc_src, sp_out, jump_type, branch_en, mem_sel, byte_sel, mem_wr, mem_rd, flags_we, bank_en, reg_we, wb_sel, ir_imm_sel, shift_op, cin_sel, alu_pre, alu_op}));
  and and_1 (HALT_IN, comparator_1_eq, exec);
  Comparator #(.Bits(10)) comparator_1 (.a(10'hff), .b(op), .eq(comparator_1_eq));  // open: gt, lt

  // Other names for the same wires on the sheet: ir_opcode[9:0] = op; seq_exec = exec

  // Notes on the sheet:
  //   op: default 48
  //   contents of microcode_eeprom (hex, n*v repeats v):
  //   80000000000,80003800596,80003802d96,80003801588,800038015ee,80003801566
  //   ,80003801133,80003802796,80003802596,80003803769,800038015c0,800038012ee
  //   ,80003802596,80003800f96,800018004cc,80002001769,80003830596,80003831769
  //   ,80003871588,800038715ee,80003871566,80003880596,80003820596,80002071588
  //   ,80002031769,80001eb0000,6810018b0596,80001ea0000,80001e20000
  //   ,80001e80000,80003c01769,80003c01769,80001900000,80001904000,80001908000
  //   ,8000190c000,80001950000,80001954000,80001958000,8000195c000,8*0
  //   ,300005b30796,300035b30796,300025b30796,300015b30796,300005b30796
  //   ,480005b00000,300005b015aa,9*0,300008030796,300038030796,300018030796
  //   ,480008000000,12*0,801000c0000,c01000c0000,a01000c0000,e01000c0000
  //   ,d01000c0000,901000c0000,e01000c0000,f01000c0000,8*0,88201a90000
  //   ,308201a30596,802000d0000,482200000000,482200000000,11*0,f00008000000
  //   ,f00005b00000,88201a90000,f00204300000,f00004b00000,e80000000000
  //   ,f00008000000,f00004b00000,80000a00000,800008015f0,800008015aa
  //   ,f00004b00000,f00008000000,3000480015aa,3000880015aa,0,4*1080001f00000
  //   ,80001d00000,1080001f80000,10*0,4*2080001f00000,12*0,80001c00000
  //   ,80002000000,80001800000,5*80000000000,80001830596,3000c8030796
  //   ,f00088000000,80001000000,80000000000,800008015e4,80000000000
  //   ,1800000b0000,80002802796,80002802796,80002000596,80002001566
  //   ,80000801433,800008015ca,800008015e4,80000800096,80000801577,80000801511
  //   ,80000801599,80000801266,800008015e8,80000801517,80000000000,80000000000
  //   ,80002c01769,5*80003c01769,8*80000000000,0,0,10*80000000000,80002800796
  //   ,80000000000,800000c0000,800000c0000,33*0,80000000000,8*0,80003830596
  //   ,80003831769,8*0,80003841588,800038415ee,80003841566,80003830596
  //   ,80003840596,80002031588,80002031769,80001ea0000,0,80001e70000
  //   ,80001e10000,80001e70000,80003c81769,80003c71769,80001910000,80001914000
  //   ,80001918000,8000191c000,17*0,80000000000,10*0,800038e0596,80003820596
  //   ,80003880596,800038e1769,800020e1769,80001e10000,80001e70000,80001ea0000
  //   ,800038f0596,80003881769,80003841588,80003831588,800038415ee,80003841566
  //   ,80002081769,6810018f0596,1080001f30000,80002041588,300005b00000
  //   ,802000c0000,88201ad0000,308201af0596,80001910000,80003800596
  //   ,80003810596,80003840596,80003850596,80003860596,80003870596,80003890596
  //   ,800038a0596,800038b0596,800038c0596,800038d0596,80003801769,80003811769
  //   ,80003821769,80003841769,80003851769,80003861769,80003871769,80003891769
  //   ,800038a1769,800038b1769,800038c1769,800038d1769,800038f1769,80003801588
  //   ,80003811588,80003821588,80003851588,80003861588,80003881588,80003891588
  //   ,800038a1588,800038b1588,800038c1588,800038d1588,800038e1588,800038f1588
  //   ,800038015ee,800038115ee,800038215ee,800038315ee,800038515ee,800038615ee
  //   ,800038815ee,800038915ee,800038a15ee,800038b15ee,800038c15ee,800038d15ee
  //   ,800038e15ee,800038f15ee,80003801566,80003811566,80003821566,80003831566
  //   ,80003851566,80003861566,80003881566,80003891566,800038a1566,800038b1566
  //   ,800038c1566,800038d1566,800038e1566,800038f1566,80002001769,80002011769
  //   ,80002021769,80002041769,80002051769,80002061769,80002071769,80002091769
  //   ,800020a1769,800020b1769,800020c1769,800020d1769,800020f1769,80001e00000
  //   ,80001e30000,80001e40000,80001e50000,80001e60000,80001e70000,80001e80000
  //   ,80001e90000,80001ea0000,80001eb0000,80001ec0000,80001ed0000,80001ee0000
  //   ,80001ef0000,80001e00000,80001e10000,80001e20000,80001e30000,80001e40000
  //   ,80001e50000,80001e60000,80001e90000,80001ea0000,80001eb0000,80001ec0000
  //   ,80001ed0000,80001ee0000,80001ef0000,80001e00000,80001e10000,80001e20000
  //   ,80001e30000,80001e40000,80001e50000,80001e60000,80001e70000,80001e80000
  //   ,80001e90000,80001ec0000,80001ed0000,80001ee0000,80001ef0000,681001800596
  //   ,681001810596,681001820596,681001830596,681001840596,681001850596
  //   ,681001860596,681001870596,681001880596,681001890596,6810018a0596
  //   ,6810018c0596,6810018d0596,6810018e0596,80001e00000,80001e10000
  //   ,80001e20000,80001e30000,80001e40000,80001e50000,80001e60000,80001e70000
  //   ,80001e80000,80001e90000,80001eb0000,80001ec0000,80001ed0000,80001ee0000
  //   ,80001ef0000,1080001f00000,1080001f10000,1080001f20000,1080001f40000
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endmodule

/* Test case microcode exhaustive:
op alu-op alu-pre cin-sel shift-op ir-imm-sel wb-sel reg-we bank-en flags-we mem-rd mem-wr byte-sel mem-sel branch-en jump-type sp-out pc-src pc-link-we pc-cond cycles ctrl-bussel mul_en div_en
# TOMATO32 native microcode smoke set (synced from catalog rom_hex)
# Format: op alu-op alu-pre ... (22 fields)
# NOP (0x00)
0x00 0x00 0x00 0 0 0 0 0 0 0 0 0 0 0 0 0 0 0 0 0 1 0 0 0
# ADD (0x01)
0x01 0x96 0x05 0 0 0 0 1 1 1 0 0 0 0 0 0 0 0 0 0 1 0 0 0
# SUB (0x02)
0x02 0x96 0x0D 1 0 0 0 1 1 1 0 0 0 0 0 0 0 0 0 0 1 0 0 0
# AND (0x03)
0x03 0x88 0x15 0 0 0 0 1 1 1 0 0 0 0 0 0 0 0 0 0 1 0 0 0
# OR (0x04)
0x04 0xEE 0x15 0 0 0 0 1 1 1 0 0 0 0 0 0 0 0 0 0 1 0 0 0
# XOR (0x05)
0x05 0x66 0x15 0 0 0 0 1 1 1 0 0 0 0 0 0 0 0 0 0 1 0 0 0
# NOT (0x06)
0x06 0x33 0x11 0 0 0 0 1 1 1 0 0 0 0 0 0 0 0 0 0 1 0 0 0
# NEG (0x07)
0x07 0x96 0x07 1 0 0 0 1 1 1 0 0 0 0 0 0 0 0 0 0 1 0 0 0
# ADC (0x08)
0x08 0x96 0x05 1 0 0 0 1 1 1 0 0 0 0 0 0 0 0 0 0 1 0 0 0
# SBC (0x09)
0x09 0x69 0x17 1 0 0 0 1 1 1 0 0 0 0 0 0 0 0 0 0 1 0 0 0
# ANDN (0x0A)
0x0A 0xC0 0x15 0 0 0 0 1 1 1 0 0 0 0 0 0 0 0 0 0 1 0 0 0
# ORN (0x0B)
0x0B 0xEE 0x12 0 0 0 0 1 1 1 0 0 0 0 0 0 0 0 0 0 1 0 0 0
# INC (0x0C)
0x0C 0x96 0x05 1 0 0 0 1 1 1 0 0 0 0 0 0 0 0 0 0 1 0 0 0
# DEC (0x0D)
0x0D 0x96 0x0F 0 0 0 0 1 1 1 0 0 0 0 0 0 0 0 0 0 1 0 0 0
# MOV (0x0E)
0x0E 0xCC 0x04 0 0 0 0 1 1 0 0 0 0 0 0 0 0 0 0 0 1 0 0 0
# CMP (0x0F)
0x0F 0x69 0x17 0 0 0 0 0 0 1 0 0 0 0 0 0 0 0 0 0 1 0 0 0
# ADDI (0x10)
0x10 0x96 0x05 0 0 3 0 1 1 1 0 0 0 0 0 0 0 0 0 0 1 0 0 0
# SUBI (0x11)
0x11 0x69 0x17 0 0 3 0 1 1 1 0 0 0 0 0 0 0 0 0 0 1 0 0 0
# ANDI (0x12)
0x12 0x88 0x15 0 0 7 0 1 1 1 0 0 0 0 0 0 0 0 0 0 1 0 0 0
# ORI (0x13)
0x13 0xEE 0x15 0 0 7 0 1 1 1 0 0 0 0 0 0 0 0 0 0 1 0 0 0
# XORI (0x14)
0x14 0x66 0x15 0 0 7 0 1 1 1 0 0 0 0 0 0 0 0 0 0 1 0 0 0
# ADDI16 (0x15)
0x15 0x96 0x05 0 0 8 0 1 1 1 0 0 0 0 0 0 0 0 0 0 1 0 0 0
# ADDI8 (0x16)
0x16 0x96 0x05 0 0 2 0 1 1 1 0 0 0 0 0 0 0 0 0 0 1 0 0 0
# TST (0x17)
0x17 0x88 0x15 0 0 7 0 0 0 1 0 0 0 0 0 0 0 0 0 0 1 0 0 0
# CMPI (0x18)
0x18 0x69 0x17 0 0 3 0 0 0 1 0 0 0 0 0 0 0 0 0 0 1 0 0 0
# LUI (0x19)
0x19 0x00 0x00 0 0 11 6 1 1 0 0 0 0 0 0 0 0 0 0 0 1 0 0 0
# AUIPC (0x1A)
0x1A 0x96 0x05 0 0 11 0 1 1 0 0 0 0 0 0 0 0 1 0 0 1 3 0 0
# MOVT (0x1B)
0x1B 0x00 0x00 0 0 10 6 1 1 0 0 0 0 0 0 0 0 0 0 0 1 0 0 0
# MOVI8 (0x1C)
0x1C 0x00 0x00 0 0 2 6 1 1 0 0 0 0 0 0 0 0 0 0 0 1 0 0 0
# MOVI16 (0x1D)
0x1D 0x00 0x00 0 0 8 6 1 1 0 0 0 0 0 0 0 0 0 0 0 1 0 0 0
# SLT (0x1E)
0x1E 0x69 0x17 0 0 0 4 1 1 1 0 0 0 0 0 0 0 0 0 0 1 0 0 0
# SLTU (0x1F)
0x1F 0x69 0x17 0 0 0 4 1 1 1 0 0 0 0 0 0 0 0 0 0 1 0 0 0
# LSL (0x20)
0x20 0x00 0x00 0 0 0 1 1 1 0 0 0 0 0 0 0 0 0 0 0 1 0 0 0
# LSR (0x21)
0x21 0x00 0x00 0 1 0 1 1 1 0 0 0 0 0 0 0 0 0 0 0 1 0 0 0
# ASR (0x22)
0x22 0x00 0x00 0 2 0 1 1 1 0 0 0 0 0 0 0 0 0 0 0 1 0 0 0
# ROR (0x23)
0x23 0x00 0x00 0 3 0 1 1 1 0 0 0 0 0 0 0 0 0 0 0 1 0 0 0
# LSLI (0x24)
0x24 0x00 0x00 0 0 5 1 1 1 0 0 0 0 0 0 0 0 0 0 0 1 0 0 0
# LSRI (0x25)
0x25 0x00 0x00 0 1 5 1 1 1 0 0 0 0 0 0 0 0 0 0 0 1 0 0 0
# ASRI (0x26)
0x26 0x00 0x00 0 2 5 1 1 1 0 0 0 0 0 0 0 0 0 0 0 1 0 0 0
# RORI (0x27)
0x27 0x00 0x00 0 3 5 1 1 1 0 0 0 0 0 0 0 0 0 0 0 1 0 0 0
# LW (0x30)
0x30 0x96 0x07 0 0 3 3 1 1 0 1 0 0 0 0 0 0 0 0 0 2 1 0 0
# LH (0x31)
0x31 0x96 0x07 0 0 3 3 1 1 0 1 0 3 0 0 0 0 0 0 0 2 1 0 0
# LHU (0x32)
0x32 0x96 0x07 0 0 3 3 1 1 0 1 0 2 0 0 0 0 0 0 0 2 1 0 0
# LB (0x33)
0x33 0x96 0x07 0 0 3 3 1 1 0 1 0 1 0 0 0 0 0 0 0 2 1 0 0
# LBU (0x34)
0x34 0x96 0x07 0 0 3 3 1 1 0 1 0 0 0 0 0 0 0 0 0 2 1 0 0
# LW0 (0x35)
0x35 0x00 0x00 0 0 0 3 1 1 0 1 0 0 0 0 0 0 0 0 0 1 2 0 0
# SW (0x40)
0x40 0x96 0x07 0 0 3 0 0 0 0 0 1 0 0 0 0 0 0 0 0 2 1 0 0
# SH (0x41)
0x41 0x96 0x07 0 0 3 0 0 0 0 0 1 3 0 0 0 0 0 0 0 2 1 0 0
# SB (0x42)
0x42 0x96 0x07 0 0 3 0 0 0 0 0 1 1 0 0 0 0 0 0 0 2 1 0 0
# SW0 (0x43)
0x43 0x00 0x00 0 0 0 0 0 0 0 0 1 0 0 0 0 0 0 0 0 1 2 0 0
# BEQ (0x50)
0x50 0x00 0x00 0 0 12 0 0 0 0 0 0 0 0 1 0 0 0 0 0 1 0 0 0
# BNE (0x51)
0x51 0x00 0x00 0 0 12 0 0 0 0 0 0 0 0 1 0 0 0 0 4 1 0 0 0
# BLT (0x52)
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*/

/* Test case microcode-first-20:
op alu-op alu-pre cin-sel shift-op ir-imm-sel wb-sel reg-we bank-en flags-we mem-rd mem-wr byte-sel mem-sel branch-en jump-type sp-out pc-src pc-link-we pc-cond cycles ctrl-bussel mul_en div_en
# auto-sync from docs/catalog/tomato-opcode-map.csv (0x00..0x13)
# NOP (0x00)
0x00 0x00 0x00 0 0 0 0 0 0 0 0 0 0 0 0 0 0 0 0 0 1 0 0 0
# ADD (0x01)
0x01 0x96 0x05 0 0 0 0 1 1 1 0 0 0 0 0 0 0 0 0 0 1 0 0 0
# SUB (0x02)
0x02 0x96 0x0D 1 0 0 0 1 1 1 0 0 0 0 0 0 0 0 0 0 1 0 0 0
# AND (0x03)
0x03 0x88 0x15 0 0 0 0 1 1 1 0 0 0 0 0 0 0 0 0 0 1 0 0 0
# OR (0x04)
0x04 0xEE 0x15 0 0 0 0 1 1 1 0 0 0 0 0 0 0 0 0 0 1 0 0 0
# XOR (0x05)
0x05 0x66 0x15 0 0 0 0 1 1 1 0 0 0 0 0 0 0 0 0 0 1 0 0 0
# NOT (0x06)
0x06 0x33 0x11 0 0 0 0 1 1 1 0 0 0 0 0 0 0 0 0 0 1 0 0 0
# NEG (0x07)
0x07 0x96 0x07 1 0 0 0 1 1 1 0 0 0 0 0 0 0 0 0 0 1 0 0 0
# ADC (0x08)
0x08 0x96 0x05 1 0 0 0 1 1 1 0 0 0 0 0 0 0 0 0 0 1 0 0 0
# SBC (0x09)
0x09 0x69 0x17 1 0 0 0 1 1 1 0 0 0 0 0 0 0 0 0 0 1 0 0 0
# ANDN (0x0A)
0x0A 0xC0 0x15 0 0 0 0 1 1 1 0 0 0 0 0 0 0 0 0 0 1 0 0 0
# ORN (0x0B)
0x0B 0xEE 0x12 0 0 0 0 1 1 1 0 0 0 0 0 0 0 0 0 0 1 0 0 0
# INC (0x0C)
0x0C 0x96 0x05 1 0 0 0 1 1 1 0 0 0 0 0 0 0 0 0 0 1 0 0 0
# DEC (0x0D)
0x0D 0x96 0x0F 0 0 0 0 1 1 1 0 0 0 0 0 0 0 0 0 0 1 0 0 0
# MOV (0x0E)
0x0E 0xCC 0x04 0 0 0 0 1 1 0 0 0 0 0 0 0 0 0 0 0 1 0 0 0
# CMP (0x0F)
0x0F 0x69 0x17 0 0 0 0 0 0 1 0 0 0 0 0 0 0 0 0 0 1 0 0 0
# ADDI (0x10)
0x10 0x96 0x05 0 0 3 0 1 1 1 0 0 0 0 0 0 0 0 0 0 1 0 0 0
# SUBI (0x11)
0x11 0x69 0x17 0 0 3 0 1 1 1 0 0 0 0 0 0 0 0 0 0 1 0 0 0
# ANDI (0x12)
0x12 0x88 0x15 0 0 7 0 1 1 1 0 0 0 0 0 0 0 0 0 0 1 0 0 0
# ORI (0x13)
0x13 0xEE 0x15 0 0 7 0 1 1 1 0 0 0 0 0 0 0 0 0 0 1 0 0 0
*/

/* Test case microcode-cat-09:
op alu-op alu-pre cin-sel shift-op ir-imm-sel wb-sel reg-we bank-en flags-we mem-rd mem-wr byte-sel mem-sel branch-en jump-type sp-out pc-src pc-link-we pc-cond cycles ctrl-bussel mul_en div_en
# catalog block 09: 35 unique opcodes (0x318..0x3FF)
# golden = unpack(docs/catalog/tomato-opcode-map.csv rom_hex)
# STW (0x318) tier=native rom=0000300008080000
0x318 0x00 0x00 0 0 8 0 0 0 0 0 1 0 0 0 0 0 0 0 0 2 1 0 0
# STH (0x319) tier=native rom=0000300038080000
0x319 0x00 0x00 0 0 8 0 0 0 0 0 1 3 0 0 0 0 0 0 0 2 1 0 0
# STB (0x31A) tier=native rom=0000300018080000
0x31A 0x00 0x00 0 0 8 0 0 0 0 0 1 1 0 0 0 0 0 0 0 2 1 0 0
# STMW (0x31B) tier=native rom=0000080000080000
0x31B 0x00 0x00 0 0 8 0 0 0 0 0 0 0 0 0 0 0 0 0 0 1 0 0 0
# LDI (0x320) tier=native rom=0000080001E80000
0x320 0x00 0x00 0 0 8 6 1 1 0 0 0 0 0 0 0 0 0 0 0 1 0 0 0
# LEA (0x321) tier=native rom=0000080003830596
0x321 0x96 0x05 0 0 3 0 1 1 1 0 0 0 0 0 0 0 0 0 0 1 0 0 0
# MOVZX (0x322) tier=native rom=0000300005B00000
0x322 0x00 0x00 0 0 0 3 1 1 0 1 0 0 0 0 0 0 0 0 0 2 1 0 0
# MOVSX (0x323) tier=native rom=0000300015B00000
0x323 0x00 0x00 0 0 0 3 1 1 0 1 0 1 0 0 0 0 0 0 0 2 1 0 0
# LW (0x330) tier=native rom=0000300005B10000
0x330 0x00 0x00 0 0 1 3 1 1 0 1 0 0 0 0 0 0 0 0 0 2 1 0 0
# SW (0x331) tier=native rom=0000300008010000
0x331 0x00 0x00 0 0 1 0 0 0 0 0 1 0 0 0 0 0 0 0 0 2 1 0 0
# ADD (0x332) tier=native rom=0000080003810596
0x332 0x96 0x05 0 0 1 0 1 1 1 0 0 0 0 0 0 0 0 0 0 1 0 0 0
# SUB (0x333) tier=native rom=0000080003812D96
0x333 0x96 0x0D 1 0 1 0 1 1 1 0 0 0 0 0 0 0 0 0 0 1 0 0 0
# MIPS (0x340) tier=native rom=0000080000070000
0x340 0x00 0x00 0 0 7 0 0 0 0 0 0 0 0 0 0 0 0 0 0 1 0 0 0
# MIPS (0x341) tier=native rom=00000800000D0000
0x341 0x00 0x00 0 0 13 0 0 0 0 0 0 0 0 0 0 0 0 0 0 1 0 0 0
# MIPS (0x342) tier=native rom=00000800000D0000
0x342 0x00 0x00 0 0 13 0 0 0 0 0 0 0 0 0 0 0 0 0 0 1 0 0 0
# BGEZAL (0x343) tier=native rom=00000800000C0000
0x343 0x00 0x00 0 0 12 0 0 0 0 0 0 0 0 0 0 0 0 0 0 1 0 0 0
# BLTZAL (0x344) tier=native rom=00000800000C0000
0x344 0x00 0x00 0 0 12 0 0 0 0 0 0 0 0 0 0 0 0 0 0 1 0 0 0
# MOVCC (0x350) tier=native rom=0000080000000000
0x350 0x00 0x00 0 0 0 0 0 0 0 0 0 0 0 0 0 0 0 0 0 1 0 0 0
# MOVZ (0x351) tier=native rom=0000080000000000
0x351 0x00 0x00 0 0 0 0 0 0 0 0 0 0 0 0 0 0 0 0 0 1 0 0 0
# MOVN (0x352) tier=native rom=0000080000000000
0x352 0x00 0x00 0 0 0 0 0 0 0 0 0 0 0 0 0 0 0 0 0 1 0 0 0
# TRAP (0x360) tier=native rom=0000080000010000
0x360 0x00 0x00 0 0 1 0 0 0 0 0 0 0 0 0 0 0 0 0 0 1 0 0 0
# ERET (0x361) tier=sequence rom=0000080000000000
0x361 0x00 0x00 0 0 0 0 0 0 0 0 0 0 0 0 0 0 0 0 0 1 0 0 0
# MFC0 (0x362) tier=native rom=0000080000000000
0x362 0x00 0x00 0 0 0 0 0 0 0 0 0 0 0 0 0 0 0 0 0 1 0 0 0
# MTC0 (0x363) tier=native rom=0000080000000000
0x363 0x00 0x00 0 0 0 0 0 0 0 0 0 0 0 0 0 0 0 0 0 1 0 0 0
# MRS (0x364) tier=native rom=0000080000000000
0x364 0x00 0x00 0 0 0 0 0 0 0 0 0 0 0 0 0 0 0 0 0 1 0 0 0
# MSR (0x365) tier=native rom=0000080000000000
0x365 0x00 0x00 0 0 0 0 0 0 0 0 0 0 0 0 0 0 0 0 0 1 0 0 0
# FMOV (0x370) tier=hook rom=0000080000000000
0x370 0x00 0x00 0 0 0 0 0 0 0 0 0 0 0 0 0 0 0 0 0 1 0 0 0
# FADD (0x371) tier=hook rom=0000080000000000
0x371 0x00 0x00 0 0 0 0 0 0 0 0 0 0 0 0 0 0 0 0 0 1 0 0 0
# FSUB (0x372) tier=hook rom=0000080000000000
0x372 0x00 0x00 0 0 0 0 0 0 0 0 0 0 0 0 0 0 0 0 0 1 0 0 0
# FMUL (0x373) tier=hook rom=0000080000000000
0x373 0x00 0x00 0 0 0 0 0 0 0 0 0 0 0 0 0 0 0 0 0 1 0 0 0
# FDIV (0x374) tier=hook rom=0000080000000000
0x374 0x00 0x00 0 0 0 0 0 0 0 0 0 0 0 0 0 0 0 0 0 1 0 0 0
# FCMP (0x375) tier=hook rom=0000080000000000
0x375 0x00 0x00 0 0 0 0 0 0 0 0 0 0 0 0 0 0 0 0 0 1 0 0 0
# FCVT (0x376) tier=hook rom=0000080000000000
0x376 0x00 0x00 0 0 0 0 0 0 0 0 0 0 0 0 0 0 0 0 0 1 0 0 0
# FSQRT (0x377) tier=hook rom=0000080000000000
0x377 0x00 0x00 0 0 0 0 0 0 0 0 0 0 0 0 0 0 0 0 0 1 0 0 0
# HALT (0x3FF) tier=native rom=0000080000000000
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*/

/* Test case microcode-cat-08:
op alu-op alu-pre cin-sel shift-op ir-imm-sel wb-sel reg-we bank-en flags-we mem-rd mem-wr byte-sel mem-sel branch-en jump-type sp-out pc-src pc-link-we pc-cond cycles ctrl-bussel mul_en div_en
# catalog block 08: 50 unique opcodes (0x227..0x314)
# golden = unpack(docs/catalog/tomato-opcode-map.csv rom_hex)
# XNOR_A (0x227) tier=native rom=00000800038035A5
0x227 0xA5 0x15 1 0 0 0 1 1 1 0 0 0 0 0 0 0 0 0 0 1 0 0 0
# AND_B (0x228) tier=native rom=00000800038035C0
0x228 0xC0 0x15 1 0 0 0 1 1 1 0 0 0 0 0 0 0 0 0 0 1 0 0 0
# OR_B (0x229) tier=native rom=00000800038035FC
0x229 0xFC 0x15 1 0 0 0 1 1 1 0 0 0 0 0 0 0 0 0 0 1 0 0 0
# NAND_B (0x22A) tier=native rom=000008000380353F
0x22A 0x3F 0x15 1 0 0 0 1 1 1 0 0 0 0 0 0 0 0 0 0 1 0 0 0
# NOR_B (0x22B) tier=native rom=0000080003803503
0x22B 0x03 0x15 1 0 0 0 1 1 1 0 0 0 0 0 0 0 0 0 0 1 0 0 0
# XOR_B (0x22C) tier=native rom=000008000380353C
0x22C 0x3C 0x15 1 0 0 0 1 1 1 0 0 0 0 0 0 0 0 0 0 1 0 0 0
# XNOR_B (0x22D) tier=native rom=00000800038035C3
0x22D 0xC3 0x15 1 0 0 0 1 1 1 0 0 0 0 0 0 0 0 0 0 1 0 0 0
# BIC_A (0x22E) tier=native rom=0000080003803522
0x22E 0x22 0x15 1 0 0 0 1 1 1 0 0 0 0 0 0 0 0 0 0 1 0 0 0
# BIC_B (0x22F) tier=native rom=0000080003803544
0x22F 0x44 0x15 1 0 0 0 1 1 1 0 0 0 0 0 0 0 0 0 0 1 0 0 0
# ORN_A (0x230) tier=native rom=00000800038035BB
0x230 0xBB 0x15 1 0 0 0 1 1 1 0 0 0 0 0 0 0 0 0 0 1 0 0 0
# BIC_A (0x231) tier=native rom=000008000380350A
0x231 0x0A 0x15 1 0 0 0 1 1 1 0 0 0 0 0 0 0 0 0 0 1 0 0 0
# BIC_C (0x232) tier=native rom=0000080003803550
0x232 0x50 0x15 1 0 0 0 1 1 1 0 0 0 0 0 0 0 0 0 0 1 0 0 0
# ORN_A (0x233) tier=native rom=00000800038035AF
0x233 0xAF 0x15 1 0 0 0 1 1 1 0 0 0 0 0 0 0 0 0 0 1 0 0 0
# BIC_B (0x234) tier=native rom=000008000380350C
0x234 0x0C 0x15 1 0 0 0 1 1 1 0 0 0 0 0 0 0 0 0 0 1 0 0 0
# BIC_C (0x235) tier=native rom=0000080003803530
0x235 0x30 0x15 1 0 0 0 1 1 1 0 0 0 0 0 0 0 0 0 0 1 0 0 0
# ORN_B (0x236) tier=native rom=00000800038035CF
0x236 0xCF 0x15 1 0 0 0 1 1 1 0 0 0 0 0 0 0 0 0 0 1 0 0 0
# AND3 (0x237) tier=native rom=0000080003803580
0x237 0x80 0x15 1 0 0 0 1 1 1 0 0 0 0 0 0 0 0 0 0 1 0 0 0
# OR3 (0x238) tier=native rom=00000800038035FE
0x238 0xFE 0x15 1 0 0 0 1 1 1 0 0 0 0 0 0 0 0 0 0 1 0 0 0
# NAND3 (0x239) tier=native rom=000008000380357F
0x239 0x7F 0x15 1 0 0 0 1 1 1 0 0 0 0 0 0 0 0 0 0 1 0 0 0
# NOR3 (0x23A) tier=native rom=0000080003803501
0x23A 0x01 0x15 1 0 0 0 1 1 1 0 0 0 0 0 0 0 0 0 0 1 0 0 0
# XOR3_/_SUM (0x23B) tier=native rom=0000080003803596
0x23B 0x96 0x15 1 0 0 0 1 1 1 0 0 0 0 0 0 0 0 0 0 1 0 0 0
# XNOR3 (0x23C) tier=native rom=0000080003803569
0x23C 0x69 0x15 1 0 0 0 1 1 1 0 0 0 0 0 0 0 0 0 0 1 0 0 0
# MAJ (0x23D) tier=native rom=00000800038035E8
0x23D 0xE8 0x15 1 0 0 0 1 1 1 0 0 0 0 0 0 0 0 0 0 1 0 0 0
# MIN (0x23E) tier=sequence rom=0000080003803517
0x23E 0x17 0x15 1 0 0 0 1 1 1 0 0 0 0 0 0 0 0 0 0 1 0 0 0
# MUX_C?B:A (0x23F) tier=native rom=00000800038035CA
0x23F 0xCA 0x15 1 0 0 0 1 1 1 0 0 0 0 0 0 0 0 0 0 1 0 0 0
# MUX_B?C:A (0x240) tier=native rom=00000800038035E2
0x240 0xE2 0x15 1 0 0 0 1 1 1 0 0 0 0 0 0 0 0 0 0 1 0 0 0
# MUX_A?C:B (0x241) tier=native rom=00000800038035E4
0x241 0xE4 0x15 1 0 0 0 1 1 1 0 0 0 0 0 0 0 0 0 0 1 0 0 0
# AO21 (0x242) tier=native rom=00000800038035EA
0x242 0xEA 0x15 1 0 0 0 1 1 1 0 0 0 0 0 0 0 0 0 0 1 0 0 0
# AO21 (0x243) tier=native rom=00000800038035EC
0x243 0xEC 0x15 1 0 0 0 1 1 1 0 0 0 0 0 0 0 0 0 0 1 0 0 0
# AO21 (0x244) tier=native rom=00000800038035F8
0x244 0xF8 0x15 1 0 0 0 1 1 1 0 0 0 0 0 0 0 0 0 0 1 0 0 0
# OA21 (0x245) tier=native rom=00000800038035A8
0x245 0xA8 0x15 1 0 0 0 1 1 1 0 0 0 0 0 0 0 0 0 0 1 0 0 0
# OA21 (0x246) tier=native rom=00000800038035C8
0x246 0xC8 0x15 1 0 0 0 1 1 1 0 0 0 0 0 0 0 0 0 0 1 0 0 0
# OA21 (0x247) tier=native rom=00000800038035E0
0x247 0xE0 0x15 1 0 0 0 1 1 1 0 0 0 0 0 0 0 0 0 0 1 0 0 0
# AOI21 (0x248) tier=native rom=0000080003803515
0x248 0x15 0x15 1 0 0 0 1 1 1 0 0 0 0 0 0 0 0 0 0 1 0 0 0
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*/

/* Test case microcode-cat-07:
op alu-op alu-pre cin-sel shift-op ir-imm-sel wb-sel reg-we bank-en flags-we mem-rd mem-wr byte-sel mem-sel branch-en jump-type sp-out pc-src pc-link-we pc-cond cycles ctrl-bussel mul_en div_en
# catalog block 07: 50 unique opcodes (0x1F5..0x226)
# golden = unpack(docs/catalog/tomato-opcode-map.csv rom_hex)
# MULI (0x1F5) tier=native rom=0001080001FB0000
0x1F5 0x00 0x00 0 0 11 7 1 1 0 0 0 0 0 0 0 0 0 0 0 1 0 1 0
# MULI (0x1F6) tier=native rom=0001080001FC0000
0x1F6 0x00 0x00 0 0 12 7 1 1 0 0 0 0 0 0 0 0 0 0 0 1 0 1 0
# MULI (0x1F7) tier=native rom=0001080001FD0000
0x1F7 0x00 0x00 0 0 13 7 1 1 0 0 0 0 0 0 0 0 0 0 0 1 0 1 0
# MULI (0x1F8) tier=native rom=0001080001FE0000
0x1F8 0x00 0x00 0 0 14 7 1 1 0 0 0 0 0 0 0 0 0 0 0 1 0 1 0
# MULI (0x1F9) tier=native rom=0001080001FF0000
0x1F9 0x00 0x00 0 0 15 7 1 1 0 0 0 0 0 0 0 0 0 0 0 1 0 1 0
# TST (0x1FA) tier=native rom=0000080002001588
0x1FA 0x88 0x15 0 0 0 0 0 0 1 0 0 0 0 0 0 0 0 0 0 1 0 0 0
# TST (0x1FB) tier=native rom=0000080002011588
0x1FB 0x88 0x15 0 0 1 0 0 0 1 0 0 0 0 0 0 0 0 0 0 1 0 0 0
# TST (0x1FC) tier=native rom=0000080002021588
0x1FC 0x88 0x15 0 0 2 0 0 0 1 0 0 0 0 0 0 0 0 0 0 1 0 0 0
# TST (0x1FD) tier=native rom=0000080002031588
0x1FD 0x88 0x15 0 0 3 0 0 0 1 0 0 0 0 0 0 0 0 0 0 1 0 0 0
# TST (0x1FE) tier=native rom=0000080002051588
0x1FE 0x88 0x15 0 0 5 0 0 0 1 0 0 0 0 0 0 0 0 0 0 1 0 0 0
# TST (0x1FF) tier=native rom=0000080002061588
0x1FF 0x88 0x15 0 0 6 0 0 0 1 0 0 0 0 0 0 0 0 0 0 1 0 0 0
# INC_A (0x200) tier=native rom=0000080003802196
0x200 0x96 0x01 1 0 0 0 1 1 1 0 0 0 0 0 0 0 0 0 0 1 0 0 0
# INC_B (0x201) tier=native rom=0000080003802496
0x201 0x96 0x04 1 0 0 0 1 1 1 0 0 0 0 0 0 0 0 0 0 1 0 0 0
# DEC_A (0x202) tier=native rom=0000080003800996
0x202 0x96 0x09 0 0 0 0 1 1 1 0 0 0 0 0 0 0 0 0 0 1 0 0 0
# DEC_B (0x203) tier=native rom=0000080003800696
0x203 0x96 0x06 0 0 0 0 1 1 1 0 0 0 0 0 0 0 0 0 0 1 0 0 0
# NEG_A (0x204) tier=native rom=0000080003802396
0x204 0x96 0x03 1 0 0 0 1 1 1 0 0 0 0 0 0 0 0 0 0 1 0 0 0
# NEG_B (0x205) tier=native rom=0000080003802C96
0x205 0x96 0x0C 1 0 0 0 1 1 1 0 0 0 0 0 0 0 0 0 0 1 0 0 0
# MOV_A (0x206) tier=native rom=0000080003800196
0x206 0x96 0x01 0 0 0 0 1 1 1 0 0 0 0 0 0 0 0 0 0 1 0 0 0
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*/

/* Test case microcode-cat-06:
op alu-op alu-pre cin-sel shift-op ir-imm-sel wb-sel reg-we bank-en flags-we mem-rd mem-wr byte-sel mem-sel branch-en jump-type sp-out pc-src pc-link-we pc-cond cycles ctrl-bussel mul_en div_en
# catalog block 06: 50 unique opcodes (0x1C3..0x1F4)
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*/

/* Test case microcode-cat-05:
op alu-op alu-pre cin-sel shift-op ir-imm-sel wb-sel reg-we bank-en flags-we mem-rd mem-wr byte-sel mem-sel branch-en jump-type sp-out pc-src pc-link-we pc-cond cycles ctrl-bussel mul_en div_en
# catalog block 05: 50 unique opcodes (0x191..0x1C2)
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*/

/* Test case microcode-cat-04:
op alu-op alu-pre cin-sel shift-op ir-imm-sel wb-sel reg-we bank-en flags-we mem-rd mem-wr byte-sel mem-sel branch-en jump-type sp-out pc-src pc-link-we pc-cond cycles ctrl-bussel mul_en div_en
# catalog block 04: 50 unique opcodes (0x15F..0x190)
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*/

/* Test case microcode-cat-03:
op alu-op alu-pre cin-sel shift-op ir-imm-sel wb-sel reg-we bank-en flags-we mem-rd mem-wr byte-sel mem-sel branch-en jump-type sp-out pc-src pc-link-we pc-cond cycles ctrl-bussel mul_en div_en
# catalog block 03: 50 unique opcodes (0x109..0x15E)
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*/

/* Test case microcode-cat-02:
op alu-op alu-pre cin-sel shift-op ir-imm-sel wb-sel reg-we bank-en flags-we mem-rd mem-wr byte-sel mem-sel branch-en jump-type sp-out pc-src pc-link-we pc-cond cycles ctrl-bussel mul_en div_en
# catalog block 02: 50 unique opcodes (0xAB..0x108)
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*/

/* Test case microcode-cat-01:
op alu-op alu-pre cin-sel shift-op ir-imm-sel wb-sel reg-we bank-en flags-we mem-rd mem-wr byte-sel mem-sel branch-en jump-type sp-out pc-src pc-link-we pc-cond cycles ctrl-bussel mul_en div_en
# catalog block 01: 50 unique opcodes (0x43..0xAA)
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*/

/* Test case microcode-cat-00:
op alu-op alu-pre cin-sel shift-op ir-imm-sel wb-sel reg-we bank-en flags-we mem-rd mem-wr byte-sel mem-sel branch-en jump-type sp-out pc-src pc-link-we pc-cond cycles ctrl-bussel mul_en div_en
# catalog block 00: 50 unique opcodes (0x00..0x42)
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*/
