// Digital circuit mem-io-control.dig as structural Verilog
module mem_io_control (
  input  [8:0] op,
  input  seq_fetch,
  output bank_en,
  output mem_rd,
  output mem_wr,
  output [3:0] byte_sel
);

  wire nand_1_out, nand_2_out;
  wire [7:2] mem_io_control_d;

  ROM #(.bigEndian("true"), .AddrBits(9), .isProgramMemory("true"), .Bits(8)) mem_io_control (
    .A(op), .sel(1'b1), .D({mem_io_control_d[7], byte_sel, mem_io_control_d[2], mem_rd, bank_en}));
  nand nand_1 (nand_1_out, seq_fetch, seq_fetch);
  nand nand_2 (nand_2_out, mem_io_control_d[2], nand_1_out);
  nand nand_3 (mem_wr, nand_2_out, nand_2_out);

  // Other names for the same wires on the sheet: ir_opcode[8:0] = op

  // Notes on the sheet:
  //   op: default 48
  //   contents of mem_io_control (hex, n*v repeats v):
  //   0,1,1,1,1,1,1,0,0,0,0,0,0,0,0,0,0,0,0,0,0,0,0,0,0,0,0,0,0,0,0,0,1,1,1,1,1,0,0,0,0,0,0,0,0,0,
  //   0,0,0,0,0,0,0,0,0,0,0,0,0,0,0,0,0,0,1,1,1,0,0,0,0,0,0,0,0,0,0,0,0,0,0,0,0,0,0,0,0,0,0,0,0,0,
  //   0,0,0,0,3,b,0,0,0,0,0,0,4,c,0,0,0,0,0,0,0,0,0,0,0,0,0,0,0,0,0,0,0,0,0,0,0,0,0,0,0,0,0,0,0,0,
  //   0,0,0,0,0,0,0,0,0,0,0,0,0,0,0,0,0,0,0,0,0,0,0,1,0,0,0,0,0,0,0,0,0,0,0,0,0,0,0,0,0,0,0,0,0,0,
  //   0,0,0,0,0,0,0,0,0,0,0,0,0,0,0,0,0,0,0,0,0,0,0,0,0,0,0,0,0,0,0,0,0,0,0,0,0,0,0,0,0,0,0,0,0,0,
  //   0,0,0,0,0,0,0,0,0,0,0,0,0,0,0,0,0,0,0,0,0,0,0,0,0,0,0,0,0,0,0,0,0,0,0,0,0,0,0,0,0,0,0,0,0,0,
  //   0,0,0,0,0,0,0,0,0,0,0,0,0,0,0,0,0,0,0,0,0,0,0,0,0,0,0,0,0,0,0,0,0,0,0,0,0,0,0,0,0,0,0,0,0,0,
  //   0,0,0,0,0,0,0,0,0,0,0,0,0,0,0,0,0,0,0,0,0,0,0,0,0,0,0,0,0,0,0,0,0,0,0,0,0,0,0,0,0,0,0,0,0,0,
  //   0,0,0,0,0,0,0,0,0,0,0,0,0,0,0,0,0,0,0,0,0,0,0,0,0,0,0,0,0,0,0,0,0,0,0,0,0,0,0,0,0,0,0,0,0,0,
  //   0,0,0,0,0,0,0,0,0,0,0,0,0,0,0,0,0,0,0,0,0,0,0,0,0,0,0,0,0,0,0,0,0,0,0,0,0,0,0,0,0,0,0,0,0,0,
  //   0,0,0,0,0,0,0,0,0,0,0,0,0,0,0,0,0,0,0,0,0,0,0,0,0,0,0,0,0,0,0,0,0,0,0,0,0,0,0,0,0,0,0,0,0,0,
  //   0,0,0,0,0,0
endmodule

/* Test case tomato-v1-burn:
op seq_fetch bank-en mem-rd mem-wr byte-sel
# NOP
0 0 0 0 0 0
# ADD
1 0 1 0 0 0
# SUB
2 0 1 0 0 0
# AND
3 0 1 0 0 0
# OR
4 0 1 0 0 0
# XOR
5 0 1 0 0 0
# MOV
6 0 1 0 0 0
# CMP
7 0 0 0 0 0
# ADDI
32 0 1 0 0 0
# ANDI
33 0 1 0 0 0
# ORI
34 0 1 0 0 0
# XORI
35 0 1 0 0 0
# LUI
36 0 1 0 0 0
# LSL
64 0 1 0 0 0
# LSR
65 0 1 0 0 0
# ASR
66 0 1 0 0 0
# LW
96 0 1 1 0 0
# LB
97 0 1 1 0 1
# SW
104 0 0 0 1 0
# SB
105 0 0 0 1 1
# BEQ
128 0 0 0 0 0
# BNE
129 0 0 0 0 0
# BLT
130 0 0 0 0 0
# JMP
160 0 0 0 0 0
# JAL
161 0 1 0 0 0
# RET
162 0 0 0 0 0
# JR
163 0 0 0 0 0
# HALT
255 0 0 0 0 0
*/
