// Digital circuit microcode.dig as structural Verilog
module microcode (
  input  [9:0] op,
  output [7:0] alu_op,
  output [4:0] alu_pre,
  output cin_sel,
  output [1:0] shift_op,
  output [3:0] ir_imm_sel,
  output bank_en,
  output [2:0] wb_sel,
  output reg_we,
  output flags_we,
  output mem_rd,
  output mem_wr,
  output [1:0] byte_sel,
  output branch_en,
  output jump_type,
  output [2:0] pc_src,
  output [1:0] sp_out,
  output [1:0] cycles,
  output [2:0] ctrl_bussel,
  output mul_en,
  output div_en,
  output pc_link_we,
  output [1:0] mem_sel,
  output [2:0] pc_cond
);

  wire [63:50] microcode_eeprom_d;

  ROM #(.bigEndian("true"), .AddrBits(10), .Bits(64)) microcode_eeprom (
    .A(op), .sel(1'b1),
    .D({microcode_eeprom_d, div_en, mul_en, ctrl_bussel, cycles, pc_cond, pc_link_we, pc_src, sp_out, jump_type, branch_en, mem_sel, byte_sel, mem_wr, mem_rd, flags_we, bank_en, reg_we, wb_sel, ir_imm_sel, shift_op, cin_sel, alu_pre, alu_op}));

  // Notes on the sheet:
  //   op: default 48
  //   contents of microcode_eeprom (hex, n*v repeats v):
  //   0000080000000000,0000080003800596,0000080003802D96,0000080003801588,00000800038015EE,0000080003801566,
  //   0000080003801133,0000080003802796,0000080003802596,0000080003803769,00000800038015C0,00000800038012EE,
  //   0000080003802596,0000080003800F96,00000800018004CC,0000080002001769,0000080003830596,0000080003831769,
  //   0000080003871588,00000800038715EE,0000080003871566,0000080003880596,0000080003820596,0000080002071588,
  //   0000080002031769,0000080001EB0000,00006810018B0596,0000080001EA0000,0000080001E20000,0000080001E80000,
  //   0000080003C01769,0000080003C01769,0000080001900000,0000080001904000,0000080001908000,000008000190C000,
  //   0000080001950000,0000080001954000,0000080001958000,000008000195C000,0000000000000000,0000000000000000,
  //   0000000000000000,0000000000000000,0000000000000000,0000000000000000,0000000000000000,0000000000000000,
  //   0000300005B30796,0000300035B30796,0000300025B30796,0000300015B30796,0000300005B30796,0000480005B00000,
  //   0000300005B015AA,0000000000000000,0000000000000000,0000000000000000,0000000000000000,0000000000000000,
  //   0000000000000000,0000000000000000,0000000000000000,0000000000000000,0000300008030796,0000300038030796,
  //   0000300018030796,0000480008000000,0000000000000000,0000000000000000,0000000000000000,0000000000000000,
  //   0000000000000000,0000000000000000,0000000000000000,0000000000000000,0000000000000000,0000000000000000,
  //   0000000000000000,0000000000000000,00000801000C0000,00000C01000C0000,00000A01000C0000,00000E01000C0000,
  //   00000D01000C0000,00000901000C0000,00000E01000C0000,00000F01000C0000,0000000000000000,0000000000000000,
  //   0000000000000000,0000000000000000,0000000000000000,0000000000000000,0000000000000000,0000000000000000,
  //   0000088201A90000,0000308201A30596,00000802000D0000,0000482200000000,0000482200000000,0000000000000000,
  //   0000000000000000,0000000000000000,0000000000000000,0000000000000000,0000000000000000,0000000000000000,
  //   0000000000000000,0000000000000000,0000000000000000,0000000000000000,0000F00008000000,0000F00005B00000,
  //   0000088201A90000,0000F00204300000,0000F00004B00000,0000E80000000000,0000F00008000000,0000F00004B00000,
  //   0000080000A00000,00000800008015F0,00000800008015AA,0000F00004B00000,0000F00008000000,00003000480015AA,
  //   00003000880015AA,0000000000000000,0001080001F00000,0001080001F00000,0001080001F00000,0001080001F00000,
  //   0000080001D00000,0001080001F80000,0000000000000000,0000000000000000,0000000000000000,0000000000000000,
  //   0000000000000000,0000000000000000,0000000000000000,0000000000000000,0000000000000000,0000000000000000,
  //   0002080001F00000,0002080001F00000,0002080001F00000,0002080001F00000,0000000000000000,0000000000000000,
  //   0000000000000000,0000000000000000,0000000000000000,0000000000000000,0000000000000000,0000000000000000,
  //   0000000000000000,0000000000000000,0000000000000000,0000000000000000,0000080001C00000,0000080002000000,
  //   0000080001800000,0000080000000000,0000080000000000,0000080000000000,0000080000000000,0000080000000000,
  //   0000080001830596,00003000C8030796,0000F00088000000,0000080001000000,0000080000000000,00000800008015E4,
  //   0000080000000000,00001800000B0000,0000080002802796,0000080002802796,0000080002000596,0000080002001566,
  //   0000080000801433,00000800008015CA,00000800008015E4,0000080000800096,0000080000801577,0000080000801511,
  //   0000080000801599,0000080000801266,00000800008015E8,0000080000801517,0000080000000000,0000080000000000,
  //   0000080002C01769,0000080003C01769,0000080003C01769,0000080003C01769,0000080003C01769,0000080003C01769,
  //   0000080000000000,0000080000000000,0000080000000000,0000080000000000,0000080000000000,0000080000000000,
  //   0000080000000000,0000080000000000,0000000000000000,0000000000000000,0000080000000000,0000080000000000,
  //   0000080000000000,0000080000000000,0000080000000000,0000080000000000,0000080000000000,0000080000000000,
  //   0000080000000000,0000080000000000,0000080002800796,0000080000000000,00000800000C0000,00000800000C0000,
  //   0000000000000000,0000000000000000,0000000000000000,0000000000000000,0000000000000000,0000000000000000,
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endmodule

/* Test case microcode exhaustive:
op alu-op alu-pre cin-sel shift-op ir-imm-sel wb-sel reg-we bank-en flags-we mem-rd mem-wr byte-sel mem-sel branch-en jump-type sp-out pc-src pc-link-we pc-cond cycles ctrl-bussel mul_en div_en
# TOMATO32 native microcode smoke set (synced from catalog rom_hex)
# Format: op alu-op alu-pre ... (22 fields)
# NOP (0x00)
0x00 0x00 0x00 0 0 0 0 0 0 0 0 0 0 0 0 0 0 0 0 0 1 0 0 0
# ADD (0x01)
0x01 0x96 0x05 0 0 0 0 1 1 1 0 0 0 0 0 0 0 0 0 0 1 0 0 0
# SUB (0x02)
0x02 0x96 0x0D 1 0 0 0 1 1 1 0 0 0 0 0 0 0 0 0 0 1 0 0 0
# AND (0x03)
0x03 0x88 0x15 0 0 0 0 1 1 1 0 0 0 0 0 0 0 0 0 0 1 0 0 0
# OR (0x04)
0x04 0xEE 0x15 0 0 0 0 1 1 1 0 0 0 0 0 0 0 0 0 0 1 0 0 0
# XOR (0x05)
0x05 0x66 0x15 0 0 0 0 1 1 1 0 0 0 0 0 0 0 0 0 0 1 0 0 0
# NOT (0x06)
0x06 0x33 0x11 0 0 0 0 1 1 1 0 0 0 0 0 0 0 0 0 0 1 0 0 0
# NEG (0x07)
0x07 0x96 0x07 1 0 0 0 1 1 1 0 0 0 0 0 0 0 0 0 0 1 0 0 0
# ADC (0x08)
0x08 0x96 0x05 1 0 0 0 1 1 1 0 0 0 0 0 0 0 0 0 0 1 0 0 0
# SBC (0x09)
0x09 0x69 0x17 1 0 0 0 1 1 1 0 0 0 0 0 0 0 0 0 0 1 0 0 0
# ANDN (0x0A)
0x0A 0xC0 0x15 0 0 0 0 1 1 1 0 0 0 0 0 0 0 0 0 0 1 0 0 0
# ORN (0x0B)
0x0B 0xEE 0x12 0 0 0 0 1 1 1 0 0 0 0 0 0 0 0 0 0 1 0 0 0
# INC (0x0C)
0x0C 0x96 0x05 1 0 0 0 1 1 1 0 0 0 0 0 0 0 0 0 0 1 0 0 0
# DEC (0x0D)
0x0D 0x96 0x0F 0 0 0 0 1 1 1 0 0 0 0 0 0 0 0 0 0 1 0 0 0
# MOV (0x0E)
0x0E 0xCC 0x04 0 0 0 0 1 1 0 0 0 0 0 0 0 0 0 0 0 1 0 0 0
# CMP (0x0F)
0x0F 0x69 0x17 0 0 0 0 0 0 1 0 0 0 0 0 0 0 0 0 0 1 0 0 0
# ADDI (0x10)
0x10 0x96 0x05 0 0 3 0 1 1 1 0 0 0 0 0 0 0 0 0 0 1 0 0 0
# SUBI (0x11)
0x11 0x69 0x17 0 0 3 0 1 1 1 0 0 0 0 0 0 0 0 0 0 1 0 0 0
# ANDI (0x12)
0x12 0x88 0x15 0 0 7 0 1 1 1 0 0 0 0 0 0 0 0 0 0 1 0 0 0
# ORI (0x13)
0x13 0xEE 0x15 0 0 7 0 1 1 1 0 0 0 0 0 0 0 0 0 0 1 0 0 0
# XORI (0x14)
0x14 0x66 0x15 0 0 7 0 1 1 1 0 0 0 0 0 0 0 0 0 0 1 0 0 0
# ADDI16 (0x15)
0x15 0x96 0x05 0 0 8 0 1 1 1 0 0 0 0 0 0 0 0 0 0 1 0 0 0
# ADDI8 (0x16)
0x16 0x96 0x05 0 0 2 0 1 1 1 0 0 0 0 0 0 0 0 0 0 1 0 0 0
# TST (0x17)
0x17 0x88 0x15 0 0 7 0 0 0 1 0 0 0 0 0 0 0 0 0 0 1 0 0 0
# CMPI (0x18)
0x18 0x69 0x17 0 0 3 0 0 0 1 0 0 0 0 0 0 0 0 0 0 1 0 0 0
# LUI (0x19)
0x19 0x00 0x00 0 0 11 6 1 1 0 0 0 0 0 0 0 0 0 0 0 1 0 0 0
# AUIPC (0x1A)
0x1A 0x96 0x05 0 0 11 0 1 1 0 0 0 0 0 0 0 0 1 0 0 1 3 0 0
# MOVT (0x1B)
0x1B 0x00 0x00 0 0 10 6 1 1 0 0 0 0 0 0 0 0 0 0 0 1 0 0 0
# MOVI8 (0x1C)
0x1C 0x00 0x00 0 0 2 6 1 1 0 0 0 0 0 0 0 0 0 0 0 1 0 0 0
# MOVI16 (0x1D)
0x1D 0x00 0x00 0 0 8 6 1 1 0 0 0 0 0 0 0 0 0 0 0 1 0 0 0
# SLT (0x1E)
0x1E 0x69 0x17 0 0 0 4 1 1 1 0 0 0 0 0 0 0 0 0 0 1 0 0 0
# SLTU (0x1F)
0x1F 0x69 0x17 0 0 0 4 1 1 1 0 0 0 0 0 0 0 0 0 0 1 0 0 0
# LSL (0x20)
0x20 0x00 0x00 0 0 0 1 1 1 0 0 0 0 0 0 0 0 0 0 0 1 0 0 0
# LSR (0x21)
0x21 0x00 0x00 0 1 0 1 1 1 0 0 0 0 0 0 0 0 0 0 0 1 0 0 0
# ASR (0x22)
0x22 0x00 0x00 0 2 0 1 1 1 0 0 0 0 0 0 0 0 0 0 0 1 0 0 0
# ROR (0x23)
0x23 0x00 0x00 0 3 0 1 1 1 0 0 0 0 0 0 0 0 0 0 0 1 0 0 0
# LSLI (0x24)
0x24 0x00 0x00 0 0 5 1 1 1 0 0 0 0 0 0 0 0 0 0 0 1 0 0 0
# LSRI (0x25)
0x25 0x00 0x00 0 1 5 1 1 1 0 0 0 0 0 0 0 0 0 0 0 1 0 0 0
# ASRI (0x26)
0x26 0x00 0x00 0 2 5 1 1 1 0 0 0 0 0 0 0 0 0 0 0 1 0 0 0
# RORI (0x27)
0x27 0x00 0x00 0 3 5 1 1 1 0 0 0 0 0 0 0 0 0 0 0 1 0 0 0
# LW (0x30)
0x30 0x96 0x07 0 0 3 3 1 1 0 1 0 0 0 0 0 0 0 0 0 2 1 0 0
# LH (0x31)
0x31 0x96 0x07 0 0 3 3 1 1 0 1 0 3 0 0 0 0 0 0 0 2 1 0 0
# LHU (0x32)
0x32 0x96 0x07 0 0 3 3 1 1 0 1 0 2 0 0 0 0 0 0 0 2 1 0 0
# LB (0x33)
0x33 0x96 0x07 0 0 3 3 1 1 0 1 0 1 0 0 0 0 0 0 0 2 1 0 0
# LBU (0x34)
0x34 0x96 0x07 0 0 3 3 1 1 0 1 0 0 0 0 0 0 0 0 0 2 1 0 0
# LW0 (0x35)
0x35 0x00 0x00 0 0 0 3 1 1 0 1 0 0 0 0 0 0 0 0 0 1 2 0 0
# SW (0x40)
0x40 0x96 0x07 0 0 3 0 0 0 0 0 1 0 0 0 0 0 0 0 0 2 1 0 0
# SH (0x41)
0x41 0x96 0x07 0 0 3 0 0 0 0 0 1 3 0 0 0 0 0 0 0 2 1 0 0
# SB (0x42)
0x42 0x96 0x07 0 0 3 0 0 0 0 0 1 1 0 0 0 0 0 0 0 2 1 0 0
# SW0 (0x43)
0x43 0x00 0x00 0 0 0 0 0 0 0 0 1 0 0 0 0 0 0 0 0 1 2 0 0
# BEQ (0x50)
0x50 0x00 0x00 0 0 12 0 0 0 0 0 0 0 0 1 0 0 0 0 0 1 0 0 0
# BNE (0x51)
0x51 0x00 0x00 0 0 12 0 0 0 0 0 0 0 0 1 0 0 0 0 4 1 0 0 0
# BLT (0x52)
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*/

/* Test case microcode-first-20:
op alu-op alu-pre cin-sel shift-op ir-imm-sel wb-sel reg-we bank-en flags-we mem-rd mem-wr byte-sel mem-sel branch-en jump-type sp-out pc-src pc-link-we pc-cond cycles ctrl-bussel mul_en div_en
# auto-sync from docs/catalog/tomato-opcode-map.csv (0x00..0x13)
# NOP (0x00)
0x00 0x00 0x00 0 0 0 0 0 0 0 0 0 0 0 0 0 0 0 0 0 1 0 0 0
# ADD (0x01)
0x01 0x96 0x05 0 0 0 0 1 1 1 0 0 0 0 0 0 0 0 0 0 1 0 0 0
# SUB (0x02)
0x02 0x96 0x0D 1 0 0 0 1 1 1 0 0 0 0 0 0 0 0 0 0 1 0 0 0
# AND (0x03)
0x03 0x88 0x15 0 0 0 0 1 1 1 0 0 0 0 0 0 0 0 0 0 1 0 0 0
# OR (0x04)
0x04 0xEE 0x15 0 0 0 0 1 1 1 0 0 0 0 0 0 0 0 0 0 1 0 0 0
# XOR (0x05)
0x05 0x66 0x15 0 0 0 0 1 1 1 0 0 0 0 0 0 0 0 0 0 1 0 0 0
# NOT (0x06)
0x06 0x33 0x11 0 0 0 0 1 1 1 0 0 0 0 0 0 0 0 0 0 1 0 0 0
# NEG (0x07)
0x07 0x96 0x07 1 0 0 0 1 1 1 0 0 0 0 0 0 0 0 0 0 1 0 0 0
# ADC (0x08)
0x08 0x96 0x05 1 0 0 0 1 1 1 0 0 0 0 0 0 0 0 0 0 1 0 0 0
# SBC (0x09)
0x09 0x69 0x17 1 0 0 0 1 1 1 0 0 0 0 0 0 0 0 0 0 1 0 0 0
# ANDN (0x0A)
0x0A 0xC0 0x15 0 0 0 0 1 1 1 0 0 0 0 0 0 0 0 0 0 1 0 0 0
# ORN (0x0B)
0x0B 0xEE 0x12 0 0 0 0 1 1 1 0 0 0 0 0 0 0 0 0 0 1 0 0 0
# INC (0x0C)
0x0C 0x96 0x05 1 0 0 0 1 1 1 0 0 0 0 0 0 0 0 0 0 1 0 0 0
# DEC (0x0D)
0x0D 0x96 0x0F 0 0 0 0 1 1 1 0 0 0 0 0 0 0 0 0 0 1 0 0 0
# MOV (0x0E)
0x0E 0xCC 0x04 0 0 0 0 1 1 0 0 0 0 0 0 0 0 0 0 0 1 0 0 0
# CMP (0x0F)
0x0F 0x69 0x17 0 0 0 0 0 0 1 0 0 0 0 0 0 0 0 0 0 1 0 0 0
# ADDI (0x10)
0x10 0x96 0x05 0 0 3 0 1 1 1 0 0 0 0 0 0 0 0 0 0 1 0 0 0
# SUBI (0x11)
0x11 0x69 0x17 0 0 3 0 1 1 1 0 0 0 0 0 0 0 0 0 0 1 0 0 0
# ANDI (0x12)
0x12 0x88 0x15 0 0 7 0 1 1 1 0 0 0 0 0 0 0 0 0 0 1 0 0 0
# ORI (0x13)
0x13 0xEE 0x15 0 0 7 0 1 1 1 0 0 0 0 0 0 0 0 0 0 1 0 0 0
*/

/* Test case microcode-cat-09:
op alu-op alu-pre cin-sel shift-op ir-imm-sel wb-sel reg-we bank-en flags-we mem-rd mem-wr byte-sel mem-sel branch-en jump-type sp-out pc-src pc-link-we pc-cond cycles ctrl-bussel mul_en div_en
# catalog block 09: 35 unique opcodes (0x318..0x3FF)
# golden = unpack(docs/catalog/tomato-opcode-map.csv rom_hex)
# STW (0x318) tier=native rom=0000300008080000
0x318 0x00 0x00 0 0 8 0 0 0 0 0 1 0 0 0 0 0 0 0 0 2 1 0 0
# STH (0x319) tier=native rom=0000300038080000
0x319 0x00 0x00 0 0 8 0 0 0 0 0 1 3 0 0 0 0 0 0 0 2 1 0 0
# STB (0x31A) tier=native rom=0000300018080000
0x31A 0x00 0x00 0 0 8 0 0 0 0 0 1 1 0 0 0 0 0 0 0 2 1 0 0
# STMW (0x31B) tier=native rom=0000080000080000
0x31B 0x00 0x00 0 0 8 0 0 0 0 0 0 0 0 0 0 0 0 0 0 1 0 0 0
# LDI (0x320) tier=native rom=0000080001E80000
0x320 0x00 0x00 0 0 8 6 1 1 0 0 0 0 0 0 0 0 0 0 0 1 0 0 0
# LEA (0x321) tier=native rom=0000080003830596
0x321 0x96 0x05 0 0 3 0 1 1 1 0 0 0 0 0 0 0 0 0 0 1 0 0 0
# MOVZX (0x322) tier=native rom=0000300005B00000
0x322 0x00 0x00 0 0 0 3 1 1 0 1 0 0 0 0 0 0 0 0 0 2 1 0 0
# MOVSX (0x323) tier=native rom=0000300015B00000
0x323 0x00 0x00 0 0 0 3 1 1 0 1 0 1 0 0 0 0 0 0 0 2 1 0 0
# LW (0x330) tier=native rom=0000300005B10000
0x330 0x00 0x00 0 0 1 3 1 1 0 1 0 0 0 0 0 0 0 0 0 2 1 0 0
# SW (0x331) tier=native rom=0000300008010000
0x331 0x00 0x00 0 0 1 0 0 0 0 0 1 0 0 0 0 0 0 0 0 2 1 0 0
# ADD (0x332) tier=native rom=0000080003810596
0x332 0x96 0x05 0 0 1 0 1 1 1 0 0 0 0 0 0 0 0 0 0 1 0 0 0
# SUB (0x333) tier=native rom=0000080003812D96
0x333 0x96 0x0D 1 0 1 0 1 1 1 0 0 0 0 0 0 0 0 0 0 1 0 0 0
# MIPS (0x340) tier=native rom=0000080000070000
0x340 0x00 0x00 0 0 7 0 0 0 0 0 0 0 0 0 0 0 0 0 0 1 0 0 0
# MIPS (0x341) tier=native rom=00000800000D0000
0x341 0x00 0x00 0 0 13 0 0 0 0 0 0 0 0 0 0 0 0 0 0 1 0 0 0
# MIPS (0x342) tier=native rom=00000800000D0000
0x342 0x00 0x00 0 0 13 0 0 0 0 0 0 0 0 0 0 0 0 0 0 1 0 0 0
# BGEZAL (0x343) tier=native rom=00000800000C0000
0x343 0x00 0x00 0 0 12 0 0 0 0 0 0 0 0 0 0 0 0 0 0 1 0 0 0
# BLTZAL (0x344) tier=native rom=00000800000C0000
0x344 0x00 0x00 0 0 12 0 0 0 0 0 0 0 0 0 0 0 0 0 0 1 0 0 0
# MOVCC (0x350) tier=native rom=0000080000000000
0x350 0x00 0x00 0 0 0 0 0 0 0 0 0 0 0 0 0 0 0 0 0 1 0 0 0
# MOVZ (0x351) tier=native rom=0000080000000000
0x351 0x00 0x00 0 0 0 0 0 0 0 0 0 0 0 0 0 0 0 0 0 1 0 0 0
# MOVN (0x352) tier=native rom=0000080000000000
0x352 0x00 0x00 0 0 0 0 0 0 0 0 0 0 0 0 0 0 0 0 0 1 0 0 0
# TRAP (0x360) tier=native rom=0000080000010000
0x360 0x00 0x00 0 0 1 0 0 0 0 0 0 0 0 0 0 0 0 0 0 1 0 0 0
# ERET (0x361) tier=sequence rom=0000080000000000
0x361 0x00 0x00 0 0 0 0 0 0 0 0 0 0 0 0 0 0 0 0 0 1 0 0 0
# MFC0 (0x362) tier=native rom=0000080000000000
0x362 0x00 0x00 0 0 0 0 0 0 0 0 0 0 0 0 0 0 0 0 0 1 0 0 0
# MTC0 (0x363) tier=native rom=0000080000000000
0x363 0x00 0x00 0 0 0 0 0 0 0 0 0 0 0 0 0 0 0 0 0 1 0 0 0
# MRS (0x364) tier=native rom=0000080000000000
0x364 0x00 0x00 0 0 0 0 0 0 0 0 0 0 0 0 0 0 0 0 0 1 0 0 0
# MSR (0x365) tier=native rom=0000080000000000
0x365 0x00 0x00 0 0 0 0 0 0 0 0 0 0 0 0 0 0 0 0 0 1 0 0 0
# FMOV (0x370) tier=hook rom=0000080000000000
0x370 0x00 0x00 0 0 0 0 0 0 0 0 0 0 0 0 0 0 0 0 0 1 0 0 0
# FADD (0x371) tier=hook rom=0000080000000000
0x371 0x00 0x00 0 0 0 0 0 0 0 0 0 0 0 0 0 0 0 0 0 1 0 0 0
# FSUB (0x372) tier=hook rom=0000080000000000
0x372 0x00 0x00 0 0 0 0 0 0 0 0 0 0 0 0 0 0 0 0 0 1 0 0 0
# FMUL (0x373) tier=hook rom=0000080000000000
0x373 0x00 0x00 0 0 0 0 0 0 0 0 0 0 0 0 0 0 0 0 0 1 0 0 0
# FDIV (0x374) tier=hook rom=0000080000000000
0x374 0x00 0x00 0 0 0 0 0 0 0 0 0 0 0 0 0 0 0 0 0 1 0 0 0
# FCMP (0x375) tier=hook rom=0000080000000000
0x375 0x00 0x00 0 0 0 0 0 0 0 0 0 0 0 0 0 0 0 0 0 1 0 0 0
# FCVT (0x376) tier=hook rom=0000080000000000
0x376 0x00 0x00 0 0 0 0 0 0 0 0 0 0 0 0 0 0 0 0 0 1 0 0 0
# FSQRT (0x377) tier=hook rom=0000080000000000
0x377 0x00 0x00 0 0 0 0 0 0 0 0 0 0 0 0 0 0 0 0 0 1 0 0 0
# HALT (0x3FF) tier=native rom=0000080000000000
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*/

/* Test case microcode-cat-08:
op alu-op alu-pre cin-sel shift-op ir-imm-sel wb-sel reg-we bank-en flags-we mem-rd mem-wr byte-sel mem-sel branch-en jump-type sp-out pc-src pc-link-we pc-cond cycles ctrl-bussel mul_en div_en
# catalog block 08: 50 unique opcodes (0x227..0x314)
# golden = unpack(docs/catalog/tomato-opcode-map.csv rom_hex)
# XNOR_A (0x227) tier=native rom=00000800038035A5
0x227 0xA5 0x15 1 0 0 0 1 1 1 0 0 0 0 0 0 0 0 0 0 1 0 0 0
# AND_B (0x228) tier=native rom=00000800038035C0
0x228 0xC0 0x15 1 0 0 0 1 1 1 0 0 0 0 0 0 0 0 0 0 1 0 0 0
# OR_B (0x229) tier=native rom=00000800038035FC
0x229 0xFC 0x15 1 0 0 0 1 1 1 0 0 0 0 0 0 0 0 0 0 1 0 0 0
# NAND_B (0x22A) tier=native rom=000008000380353F
0x22A 0x3F 0x15 1 0 0 0 1 1 1 0 0 0 0 0 0 0 0 0 0 1 0 0 0
# NOR_B (0x22B) tier=native rom=0000080003803503
0x22B 0x03 0x15 1 0 0 0 1 1 1 0 0 0 0 0 0 0 0 0 0 1 0 0 0
# XOR_B (0x22C) tier=native rom=000008000380353C
0x22C 0x3C 0x15 1 0 0 0 1 1 1 0 0 0 0 0 0 0 0 0 0 1 0 0 0
# XNOR_B (0x22D) tier=native rom=00000800038035C3
0x22D 0xC3 0x15 1 0 0 0 1 1 1 0 0 0 0 0 0 0 0 0 0 1 0 0 0
# BIC_A (0x22E) tier=native rom=0000080003803522
0x22E 0x22 0x15 1 0 0 0 1 1 1 0 0 0 0 0 0 0 0 0 0 1 0 0 0
# BIC_B (0x22F) tier=native rom=0000080003803544
0x22F 0x44 0x15 1 0 0 0 1 1 1 0 0 0 0 0 0 0 0 0 0 1 0 0 0
# ORN_A (0x230) tier=native rom=00000800038035BB
0x230 0xBB 0x15 1 0 0 0 1 1 1 0 0 0 0 0 0 0 0 0 0 1 0 0 0
# BIC_A (0x231) tier=native rom=000008000380350A
0x231 0x0A 0x15 1 0 0 0 1 1 1 0 0 0 0 0 0 0 0 0 0 1 0 0 0
# BIC_C (0x232) tier=native rom=0000080003803550
0x232 0x50 0x15 1 0 0 0 1 1 1 0 0 0 0 0 0 0 0 0 0 1 0 0 0
# ORN_A (0x233) tier=native rom=00000800038035AF
0x233 0xAF 0x15 1 0 0 0 1 1 1 0 0 0 0 0 0 0 0 0 0 1 0 0 0
# BIC_B (0x234) tier=native rom=000008000380350C
0x234 0x0C 0x15 1 0 0 0 1 1 1 0 0 0 0 0 0 0 0 0 0 1 0 0 0
# BIC_C (0x235) tier=native rom=0000080003803530
0x235 0x30 0x15 1 0 0 0 1 1 1 0 0 0 0 0 0 0 0 0 0 1 0 0 0
# ORN_B (0x236) tier=native rom=00000800038035CF
0x236 0xCF 0x15 1 0 0 0 1 1 1 0 0 0 0 0 0 0 0 0 0 1 0 0 0
# AND3 (0x237) tier=native rom=0000080003803580
0x237 0x80 0x15 1 0 0 0 1 1 1 0 0 0 0 0 0 0 0 0 0 1 0 0 0
# OR3 (0x238) tier=native rom=00000800038035FE
0x238 0xFE 0x15 1 0 0 0 1 1 1 0 0 0 0 0 0 0 0 0 0 1 0 0 0
# NAND3 (0x239) tier=native rom=000008000380357F
0x239 0x7F 0x15 1 0 0 0 1 1 1 0 0 0 0 0 0 0 0 0 0 1 0 0 0
# NOR3 (0x23A) tier=native rom=0000080003803501
0x23A 0x01 0x15 1 0 0 0 1 1 1 0 0 0 0 0 0 0 0 0 0 1 0 0 0
# XOR3_/_SUM (0x23B) tier=native rom=0000080003803596
0x23B 0x96 0x15 1 0 0 0 1 1 1 0 0 0 0 0 0 0 0 0 0 1 0 0 0
# XNOR3 (0x23C) tier=native rom=0000080003803569
0x23C 0x69 0x15 1 0 0 0 1 1 1 0 0 0 0 0 0 0 0 0 0 1 0 0 0
# MAJ (0x23D) tier=native rom=00000800038035E8
0x23D 0xE8 0x15 1 0 0 0 1 1 1 0 0 0 0 0 0 0 0 0 0 1 0 0 0
# MIN (0x23E) tier=sequence rom=0000080003803517
0x23E 0x17 0x15 1 0 0 0 1 1 1 0 0 0 0 0 0 0 0 0 0 1 0 0 0
# MUX_C?B:A (0x23F) tier=native rom=00000800038035CA
0x23F 0xCA 0x15 1 0 0 0 1 1 1 0 0 0 0 0 0 0 0 0 0 1 0 0 0
# MUX_B?C:A (0x240) tier=native rom=00000800038035E2
0x240 0xE2 0x15 1 0 0 0 1 1 1 0 0 0 0 0 0 0 0 0 0 1 0 0 0
# MUX_A?C:B (0x241) tier=native rom=00000800038035E4
0x241 0xE4 0x15 1 0 0 0 1 1 1 0 0 0 0 0 0 0 0 0 0 1 0 0 0
# AO21 (0x242) tier=native rom=00000800038035EA
0x242 0xEA 0x15 1 0 0 0 1 1 1 0 0 0 0 0 0 0 0 0 0 1 0 0 0
# AO21 (0x243) tier=native rom=00000800038035EC
0x243 0xEC 0x15 1 0 0 0 1 1 1 0 0 0 0 0 0 0 0 0 0 1 0 0 0
# AO21 (0x244) tier=native rom=00000800038035F8
0x244 0xF8 0x15 1 0 0 0 1 1 1 0 0 0 0 0 0 0 0 0 0 1 0 0 0
# OA21 (0x245) tier=native rom=00000800038035A8
0x245 0xA8 0x15 1 0 0 0 1 1 1 0 0 0 0 0 0 0 0 0 0 1 0 0 0
# OA21 (0x246) tier=native rom=00000800038035C8
0x246 0xC8 0x15 1 0 0 0 1 1 1 0 0 0 0 0 0 0 0 0 0 1 0 0 0
# OA21 (0x247) tier=native rom=00000800038035E0
0x247 0xE0 0x15 1 0 0 0 1 1 1 0 0 0 0 0 0 0 0 0 0 1 0 0 0
# AOI21 (0x248) tier=native rom=0000080003803515
0x248 0x15 0x15 1 0 0 0 1 1 1 0 0 0 0 0 0 0 0 0 0 1 0 0 0
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*/

/* Test case microcode-cat-07:
op alu-op alu-pre cin-sel shift-op ir-imm-sel wb-sel reg-we bank-en flags-we mem-rd mem-wr byte-sel mem-sel branch-en jump-type sp-out pc-src pc-link-we pc-cond cycles ctrl-bussel mul_en div_en
# catalog block 07: 50 unique opcodes (0x1F5..0x226)
# golden = unpack(docs/catalog/tomato-opcode-map.csv rom_hex)
# MULI (0x1F5) tier=native rom=0001080001FB0000
0x1F5 0x00 0x00 0 0 11 7 1 1 0 0 0 0 0 0 0 0 0 0 0 1 0 1 0
# MULI (0x1F6) tier=native rom=0001080001FC0000
0x1F6 0x00 0x00 0 0 12 7 1 1 0 0 0 0 0 0 0 0 0 0 0 1 0 1 0
# MULI (0x1F7) tier=native rom=0001080001FD0000
0x1F7 0x00 0x00 0 0 13 7 1 1 0 0 0 0 0 0 0 0 0 0 0 1 0 1 0
# MULI (0x1F8) tier=native rom=0001080001FE0000
0x1F8 0x00 0x00 0 0 14 7 1 1 0 0 0 0 0 0 0 0 0 0 0 1 0 1 0
# MULI (0x1F9) tier=native rom=0001080001FF0000
0x1F9 0x00 0x00 0 0 15 7 1 1 0 0 0 0 0 0 0 0 0 0 0 1 0 1 0
# TST (0x1FA) tier=native rom=0000080002001588
0x1FA 0x88 0x15 0 0 0 0 0 0 1 0 0 0 0 0 0 0 0 0 0 1 0 0 0
# TST (0x1FB) tier=native rom=0000080002011588
0x1FB 0x88 0x15 0 0 1 0 0 0 1 0 0 0 0 0 0 0 0 0 0 1 0 0 0
# TST (0x1FC) tier=native rom=0000080002021588
0x1FC 0x88 0x15 0 0 2 0 0 0 1 0 0 0 0 0 0 0 0 0 0 1 0 0 0
# TST (0x1FD) tier=native rom=0000080002031588
0x1FD 0x88 0x15 0 0 3 0 0 0 1 0 0 0 0 0 0 0 0 0 0 1 0 0 0
# TST (0x1FE) tier=native rom=0000080002051588
0x1FE 0x88 0x15 0 0 5 0 0 0 1 0 0 0 0 0 0 0 0 0 0 1 0 0 0
# TST (0x1FF) tier=native rom=0000080002061588
0x1FF 0x88 0x15 0 0 6 0 0 0 1 0 0 0 0 0 0 0 0 0 0 1 0 0 0
# INC_A (0x200) tier=native rom=0000080003802196
0x200 0x96 0x01 1 0 0 0 1 1 1 0 0 0 0 0 0 0 0 0 0 1 0 0 0
# INC_B (0x201) tier=native rom=0000080003802496
0x201 0x96 0x04 1 0 0 0 1 1 1 0 0 0 0 0 0 0 0 0 0 1 0 0 0
# DEC_A (0x202) tier=native rom=0000080003800996
0x202 0x96 0x09 0 0 0 0 1 1 1 0 0 0 0 0 0 0 0 0 0 1 0 0 0
# DEC_B (0x203) tier=native rom=0000080003800696
0x203 0x96 0x06 0 0 0 0 1 1 1 0 0 0 0 0 0 0 0 0 0 1 0 0 0
# NEG_A (0x204) tier=native rom=0000080003802396
0x204 0x96 0x03 1 0 0 0 1 1 1 0 0 0 0 0 0 0 0 0 0 1 0 0 0
# NEG_B (0x205) tier=native rom=0000080003802C96
0x205 0x96 0x0C 1 0 0 0 1 1 1 0 0 0 0 0 0 0 0 0 0 1 0 0 0
# MOV_A (0x206) tier=native rom=0000080003800196
0x206 0x96 0x01 0 0 0 0 1 1 1 0 0 0 0 0 0 0 0 0 0 1 0 0 0
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*/

/* Test case microcode-cat-06:
op alu-op alu-pre cin-sel shift-op ir-imm-sel wb-sel reg-we bank-en flags-we mem-rd mem-wr byte-sel mem-sel branch-en jump-type sp-out pc-src pc-link-we pc-cond cycles ctrl-bussel mul_en div_en
# catalog block 06: 50 unique opcodes (0x1C3..0x1F4)
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*/

/* Test case microcode-cat-05:
op alu-op alu-pre cin-sel shift-op ir-imm-sel wb-sel reg-we bank-en flags-we mem-rd mem-wr byte-sel mem-sel branch-en jump-type sp-out pc-src pc-link-we pc-cond cycles ctrl-bussel mul_en div_en
# catalog block 05: 50 unique opcodes (0x191..0x1C2)
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*/

/* Test case microcode-cat-04:
op alu-op alu-pre cin-sel shift-op ir-imm-sel wb-sel reg-we bank-en flags-we mem-rd mem-wr byte-sel mem-sel branch-en jump-type sp-out pc-src pc-link-we pc-cond cycles ctrl-bussel mul_en div_en
# catalog block 04: 50 unique opcodes (0x15F..0x190)
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*/

/* Test case microcode-cat-03:
op alu-op alu-pre cin-sel shift-op ir-imm-sel wb-sel reg-we bank-en flags-we mem-rd mem-wr byte-sel mem-sel branch-en jump-type sp-out pc-src pc-link-we pc-cond cycles ctrl-bussel mul_en div_en
# catalog block 03: 50 unique opcodes (0x109..0x15E)
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*/

/* Test case microcode-cat-02:
op alu-op alu-pre cin-sel shift-op ir-imm-sel wb-sel reg-we bank-en flags-we mem-rd mem-wr byte-sel mem-sel branch-en jump-type sp-out pc-src pc-link-we pc-cond cycles ctrl-bussel mul_en div_en
# catalog block 02: 50 unique opcodes (0xAB..0x108)
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*/

/* Test case microcode-cat-01:
op alu-op alu-pre cin-sel shift-op ir-imm-sel wb-sel reg-we bank-en flags-we mem-rd mem-wr byte-sel mem-sel branch-en jump-type sp-out pc-src pc-link-we pc-cond cycles ctrl-bussel mul_en div_en
# catalog block 01: 50 unique opcodes (0x43..0xAA)
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*/

/* Test case microcode-cat-00:
op alu-op alu-pre cin-sel shift-op ir-imm-sel wb-sel reg-we bank-en flags-we mem-rd mem-wr byte-sel mem-sel branch-en jump-type sp-out pc-src pc-link-we pc-cond cycles ctrl-bussel mul_en div_en
# catalog block 00: 50 unique opcodes (0x00..0x42)
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*/
