// Digital circuit mul-div.dig as structural Verilog
module mul_div (
  input  [31:0] B,
  input  [1:0] mode,
  input  [31:0] mul_div,
  input  p_enc_out,
  input  clk,
  input  [31:0] A,
  output [31:0] Shift_Out,
  output [15:0] nxt_enc,
  output nA_is_Zero
);

  wire decoder_1_out_0, decoder_1_out_1, decoder_1_out_2, decoder_1_out_3, decoder_1_out_4, decoder_1_out_5,
       decoder_1_out_6, decoder_1_out_7, decoder_1_out_8, decoder_1_out_9, decoder_1_out_10,
       decoder_1_out_11, decoder_1_out_12, decoder_1_out_13, decoder_1_out_14, decoder_1_out_15, out,
       shift_1_p6, shift_1_p7, shift_1_p12, shift_1_p13, shift_1_p15, shift_1_p16, shift_1_p17, shift_1_p18,
       shift_1_p24, shift_1_p26, shift_res, undriven;
  wire [3:0] enc_out;
  wire [15:0] d0, undriven_2;
  wire [26:0] p_enc_val;
  wire [31:27] undriven_3;

  PriorityEncoder #(.Selector_Bits(5)) priorityencoder_1 (
    .in0(p_enc_val[0]), .in3(p_enc_val[0]), .in5(p_enc_val[0]), .in6(p_enc_val[0]), .in8(p_enc_val[0]));  // open: in1, in2, in4, in7, in9, in10, in11, in12, in13, in14, in15, in16, in17, in18, in19, in20, in21, in22, in23, in24, in25, in26, in27, in28, in29, in30, in31, num, any
  or or_1 (mul_div[0], undriven, 1'b0, d0[0], nxt_enc[0]);  // open: In_2, In_3, In_4, In_5, In_6, In_7, In_8, In_9, In_10, In_11, In_13, In_14, In_15, In_16, In_17, In_18, In_20, In_22, In_23, In_24, In_25, In_26, In_27, In_28, In_29, In_30, In_31, In_32
  assign nxt_enc = nxt_enc & d0;  // And and_1, 16 bits wide
  not not_1 (nxt_enc[0], decoder_1_out_0);
  not not_2 (nxt_enc[1], decoder_1_out_1);
  Decoder #(.Selector_Bits(4)) decoder_1 (
    .sel(enc_out), .out_0(decoder_1_out_0), .out_1(decoder_1_out_1), .out_2(decoder_1_out_2),
    .out_3(decoder_1_out_3), .out_4(decoder_1_out_4), .out_5(decoder_1_out_5), .out_6(decoder_1_out_6),
    .out_7(decoder_1_out_7), .out_8(decoder_1_out_8), .out_9(decoder_1_out_9), .out_10(decoder_1_out_10),
    .out_11(decoder_1_out_11), .out_12(decoder_1_out_12), .out_13(decoder_1_out_13),
    .out_14(decoder_1_out_14), .out_15(decoder_1_out_15));
  PriorityEncoder #(.Selector_Bits(4)) priorityencoder_2 (
    .in0(undriven_2[0]), .in1(undriven_2[1]), .in2(undriven_2[2]), .in3(undriven_2[3]), .in4(undriven_2[4]),
    .in5(undriven_2[5]), .in6(undriven_2[6]), .in7(undriven_2[7]), .in8(undriven_2[8]), .in9(undriven_2[9]),
    .in10(undriven_2[10]), .in11(undriven_2[11]), .in12(undriven_2[12]), .in13(undriven_2[13]),
    .in14(undriven_2[14]), .in15(undriven_2[15]), .num(enc_out));  // open: any
  Multiplexer #(.Bits(32)) multiplexer_1 (.in_0(mul_div));  // open: sel, in_1, out
  not not_3 (nxt_enc[2], decoder_1_out_2);
  not not_4 (nxt_enc[3], decoder_1_out_3);
  not not_5 (nxt_enc[4], decoder_1_out_4);
  not not_6 (nxt_enc[5], decoder_1_out_5);
  // shift shift_1: pin names not known; wires that end beside it: B, {A[31:10], {2{A[10]}}, A[7:0]}, mul_div, {A[31:10], {2{A[10]}}, A[7:0]}, mode, shift_1_p6, shift_1_p7, shift_1_p6, out, shift_1_p7, shift_res, shift_1_p12, shift_1_p13, enc_out, shift_1_p15, shift_1_p16, shift_1_p17, shift_1_p18, shift_1_p12, shift_1_p13, shift_1_p15, shift_1_p16, shift_1_p17, shift_1_p24, shift_1_p24, shift_1_p26, out
  not not_7 (nxt_enc[6], decoder_1_out_6);
  not not_8 (nxt_enc[7], decoder_1_out_7);
  not not_9 (nxt_enc[8], decoder_1_out_8);
  not not_10 (nxt_enc[9], decoder_1_out_9);
  not not_11 (nxt_enc[10], decoder_1_out_10);
  not not_12 (nxt_enc[11], decoder_1_out_11);
  not not_13 (nxt_enc[12], decoder_1_out_12);
  not not_14 (nxt_enc[13], decoder_1_out_13);
  not not_15 (nxt_enc[14], decoder_1_out_14);
  not not_16 (nxt_enc[15], decoder_1_out_15);
  Multiplexer #(.Bits(32)) multiplexer_2 (.in_0(Shift_Out));  // open: sel, in_1, out
  // Pins of 1 and 27 bits meet at {{26{1'b0}}, A[10]}
  // Pins of 1 and 27 bits meet at p_enc_val
  // Pins of 1 and 32 bits meet at {undriven_3, p_enc_val}
  // Pins of 1 and 16 bits meet at {16{1'b0}}
  // Pins of 1 and 16 bits meet at d0
  // Pins of 1 and 16 bits meet at nxt_enc
  // Pins of 1 and 4 bits meet at mul_div[3:0]
  // Pins of 1 and 32 bits meet at mul_div

  assign A[9:8] = {2{A[10]}};
  // also tied to GND on the sheet: {mul_div[4], mul_div[5], mul_div[6], mul_div[7], mul_div[8], mul_div[9], mul_div[10], mul_div[11], mul_div[12], mul_div[13], mul_div[14], mul_div[15], mul_div[16], mul_div[17], mul_div[18], mul_div[19], mul_div[20], mul_div[21], mul_div[22], mul_div[23], mul_div[24], mul_div[25], mul_div[26], mul_div[27], mul_div[28], mul_div[29], mul_div[30], mul_div[31], A[10]}

  // Notes on the sheet:
  //   B: default 50000
  //   mode: default 1
  //   A: default 30000
endmodule

/* Test case:
A B mode mul-div p-enc-out clk Shift-Out nxt-enc ~A_is_Zero\n0xAAAAAAAA 0x0 0 0 0 0 0xAAAAAAAA 0x0 1\n0xAAAAAAAA 0x1 0 0 0 0 0x55555555 0x0 1\n0xAAAAAAAA 0x2 0 0 0 0 0x2AAAAAAA 0x0 1\n0xAAAAAAAA 0x3 0 0 0 0 0x15555555 0x0 1\n0xAAAAAAAA 0x4 0 0 0 0 0xAAAAAAA 0x0 1\n0xAAAAAAAA 0x5 0 0 0 0 0x5555555 0x0 1\n0xAAAAAAAA 0x6 0 0 0 0 0x2AAAAAA 0x0 1\n0xAAAAAAAA 0x7 0 0 0 0 0x1555555 0x0 1\n0xAAAAAAAA 0x8 0 0 0 0 0xAAAAAA 0x0 1\n0xAAAAAAAA 0x9 0 0 0 0 0x555555 0x0 1\n0xAAAAAAAA 0xA 0 0 0 0 0x2AAAAA 0x0 1\n0xAAAAAAAA 0xB 0 0 0 0 0x155555 0x0 1\n0xAAAAAAAA 0xC 0 0 0 0 0xAAAAA 0x0 1\n0xAAAAAAAA 0xD 0 0 0 0 0x55555 0x0 1\n0xAAAAAAAA 0xE 0 0 0 0 0x2AAAA 0x0 1\n0xAAAAAAAA 0xF 0 0 0 0 0x15555 0x0 1\n0xAAAAAAAA 0x10 0 0 0 0 0xAAAA 0x0 1\n0xAAAAAAAA 0x11 0 0 0 0 0x5555 0x0 1\n0xAAAAAAAA 0x12 0 0 0 0 0x2AAA 0x0 1\n0xAAAAAAAA 0x13 0 0 0 0 0x1555 0x0 1\n0xAAAAAAAA 0x14 0 0 0 0 0xAAA 0x0 1\n0xAAAAAAAA 0x15 0 0 0 0 0x555 0x0 1\n0xAAAAAAAA 0x16 0 0 0 0 0x2AA 0x0 1\n0xAAAAAAAA 0x17 0 0 0 0 0x155 0x0 1\n0xAAAAAAAA 0x18 0 0 0 0 0xAA 0x0 1\n0xAAAAAAAA 0x19 0 0 0 0 0x55 0x0 1\n0xAAAAAAAA 0x1A 0 0 0 0 0x2A 0x0 1\n0xAAAAAAAA 0x1B 0 0 0 0 0x15 0x0 1\n0xAAAAAAAA 0x1C 0 0 0 0 0xA 0x0 1\n0xAAAAAAAA 0x1D 0 0 0 0 0x5 0x0 1\n0xAAAAAAAA 0x1E 0 0 0 0 0x2 0x0 1\n0xAAAAAAAA 0x1F 0 0 0 0 0x1 0x0 1\n0x55555555 0x0 0 0 0 0 0x55555555 0x0 1\n0x55555555 0x1 0 0 0 0 0x2AAAAAAA 0x0 1\n0x55555555 0x2 0 0 0 0 0x15555555 0x0 1\n0x55555555 0x3 0 0 0 0 0xAAAAAAA 0x0 1\n0x55555555 0x4 0 0 0 0 0x5555555 0x0 1\n0x55555555 0x5 0 0 0 0 0x2AAAAAA 0x0 1\n0x55555555 0x6 0 0 0 0 0x1555555 0x0 1\n0x55555555 0x7 0 0 0 0 0xAAAAAA 0x0 1\n0x55555555 0x8 0 0 0 0 0x555555 0x0 1\n0x55555555 0x9 0 0 0 0 0x2AAAAA 0x0 1\n0x55555555 0xA 0 0 0 0 0x155555 0x0 1\n0x55555555 0xB 0 0 0 0 0xAAAAA 0x0 1\n0x55555555 0xC 0 0 0 0 0x55555 0x0 1\n0x55555555 0xD 0 0 0 0 0x2AAAA 0x0 1\n0x55555555 0xE 0 0 0 0 0x15555 0x0 1\n0x55555555 0xF 0 0 0 0 0xAAAA 0x0 1\n0x55555555 0x10 0 0 0 0 0x5555 0x0 1\n0x55555555 0x11 0 0 0 0 0x2AAA 0x0 1\n0x55555555 0x12 0 0 0 0 0x1555 0x0 1\n0x55555555 0x13 0 0 0 0 0xAAA 0x0 1\n0x55555555 0x14 0 0 0 0 0x555 0x0 1\n0x55555555 0x15 0 0 0 0 0x2AA 0x0 1\n0x55555555 0x16 0 0 0 0 0x155 0x0 1\n0x55555555 0x17 0 0 0 0 0xAA 0x0 1\n0x55555555 0x18 0 0 0 0 0x55 0x0 1\n0x55555555 0x19 0 0 0 0 0x2A 0x0 1\n0x55555555 0x1A 0 0 0 0 0x15 0x0 1\n0x55555555 0x1B 0 0 0 0 0xA 0x0 1\n0x55555555 0x1C 0 0 0 0 0x5 0x0 1\n0x55555555 0x1D 0 0 0 0 0x2 0x0 1\n0x55555555 0x1E 0 0 0 0 0x1 0x0 1\n0x55555555 0x1F 0 0 0 0 0x0 0x0 1\n0x12345678 0x0 0 0 0 0 0x12345678 0x0 1\n0x12345678 0x1 0 0 0 0 0x91A2B3C 0x0 1\n0x12345678 0x2 0 0 0 0 0x48D159E 0x0 1\n0x12345678 0x3 0 0 0 0 0x2468ACF 0x0 1\n0x12345678 0x4 0 0 0 0 0x1234567 0x0 1\n0x12345678 0x5 0 0 0 0 0x91A2B3 0x0 1\n0x12345678 0x6 0 0 0 0 0x48D159 0x0 1\n0x12345678 0x7 0 0 0 0 0x2468AC 0x0 1\n0x12345678 0x8 0 0 0 0 0x123456 0x0 1\n0x12345678 0x9 0 0 0 0 0x91A2B 0x0 1\n0x12345678 0xA 0 0 0 0 0x48D15 0x0 1\n0x12345678 0xB 0 0 0 0 0x2468A 0x0 1\n0x12345678 0xC 0 0 0 0 0x12345 0x0 1\n0x12345678 0xD 0 0 0 0 0x91A2 0x0 1\n0x12345678 0xE 0 0 0 0 0x48D1 0x0 1\n0x12345678 0xF 0 0 0 0 0x2468 0x0 1\n0x12345678 0x10 0 0 0 0 0x1234 0x0 1\n0x12345678 0x11 0 0 0 0 0x91A 0x0 1\n0x12345678 0x12 0 0 0 0 0x48D 0x0 1\n0x12345678 0x13 0 0 0 0 0x246 0x0 1\n0x12345678 0x14 0 0 0 0 0x123 0x0 1\n0x12345678 0x15 0 0 0 0 0x91 0x0 1\n0x12345678 0x16 0 0 0 0 0x48 0x0 1\n0x12345678 0x17 0 0 0 0 0x24 0x0 1\n0x12345678 0x18 0 0 0 0 0x12 0x0 1\n0x12345678 0x19 0 0 0 0 0x9 0x0 1\n0x12345678 0x1A 0 0 0 0 0x4 0x0 1\n0x12345678 0x1B 0 0 0 0 0x2 0x0 1\n0x12345678 0x1C 0 0 0 0 0x1 0x0 1\n0x12345678 0x1D 0 0 0 0 0x0 0x0 1\n0x12345678 0x1E 0 0 0 0 0x0 0x0 1\n0x12345678 0x1F 0 0 0 0 0x0 0x0 1\n0xAAAAAAAA 0x0 1 0 0 0 0xAAAAAAAA 0x0 1\n0xAAAAAAAA 0x1 1 0 0 0 0x55555554 0x0 1\n0xAAAAAAAA 0x2 1 0 0 0 0xAAAAAAA8 0x0 1\n0xAAAAAAAA 0x3 1 0 0 0 0x55555550 0x0 1\n0xAAAAAAAA 0x4 1 0 0 0 0xAAAAAAA0 0x0 1\n0xAAAAAAAA 0x5 1 0 0 0 0x55555540 0x0 1\n0xAAAAAAAA 0x6 1 0 0 0 0xAAAAAA80 0x0 1\n0xAAAAAAAA 0x7 1 0 0 0 0x5555550
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*/
