// Digital circuit mux24_4to1.dig as structural Verilog
module mux24_4to1 (
  input  [23:0] A,
  input  [23:0] B,
  input  [23:0] C,
  input  [23:0] D,
  input  [1:0] sel,
  output [23:0] y
);

  mux8_4to1 mux8_4to1_1 (.A(A[7:0]), .B(B[7:0]), .C(C[7:0]), .D(D[7:0]), .sel(sel), .Y(y[7:0]));
  mux8_4to1 mux8_4to1_2 (.A(A[15:8]), .B(B[15:8]), .C(C[15:8]), .D(D[15:8]), .sel(sel), .Y(y[15:8]));
  mux8_4to1 mux8_4to1_3 (.A(A[23:16]), .B(B[23:16]), .C(C[23:16]), .D(D[23:16]), .sel(sel), .Y(y[23:16]));

  // Other names for the same wires on the sheet: a8[7:0] = A[7:0]; a16[7:0] = A[15:8]; a24[7:0] = A[23:16];
  //   b8[7:0] = B[7:0]; b16[7:0] = B[15:8]; b24[7:0] = B[23:16]; c8[7:0] = C[7:0]; c16[7:0] = C[15:8];
  //   c24[7:0] = C[23:16]; d8[7:0] = D[7:0]; d16[7:0] = D[15:8]; d24[7:0] = D[23:16]; y8[7:0] = y[7:0];
  //   y16[7:0] = y[15:8]; y24[7:0] = y[23:16]

  // Notes on the sheet:
  //   A: default 23454334
  //   B: default 191
  //   C: default 7654567
  //   D: default 3367789
endmodule
