// Digital circuit mux8_4to1.dig as structural Verilog
module mux8_4to1 (
  input  [7:0] A,
  input  [7:0] B,
  input  [7:0] C,
  input  [7:0] D,
  input  [1:0] sel,
  output [7:0] Y
);

  wire a0, a1, a2, a3, b0, b1, b2, b3;

  // _74541 _74541_1: pin names not known; wires that end beside it: a0, 1'b0, 1'b1, b0
  // _74541 _74541_2: pin names not known; wires that end beside it: a1, 1'b0, 1'b1, b1
  // _74541 _74541_3: pin names not known; wires that end beside it: a2, 1'b0, 1'b1, b2
  // _74541 _74541_4: pin names not known; wires that end beside it: a3, 1'b0, 1'b1, b3
  _74139 _74139_1 (
    .pin1(1'b0), .pin2(sel[0]), .pin3(sel[1]), .pin4(a0), .pin5(a1), .pin6(a2), .pin7(a3), .pin8(1'b0),
    .pin9(b3), .pin10(b2), .pin11(b1), .pin12(b0), .pin13(sel[1]), .pin14(sel[0]), .pin15(1'b0), .pin16(1'b1));

  // Notes on the sheet:
  //   A: default 34
  //   B: default 22
  //   C: default 93
  //   D: default 77
endmodule
