// Digital circuit pc-control.dig as structural Verilog
module pc_control (
  input  [9:0] op,
  input  exec,
  output branch_en,
  output jump_type,
  output [2:0] pc_src,
  output pc_link_we,
  output [1:0] cycles,
  output [3:0] pc_cond,
  output [1:0] sp_out,
  output HALT_IN
);

  wire comparator_1_eq;
  wire [7:6] pc_sp_mul_control_d;

  and and_1 (HALT_IN, comparator_1_eq, exec);
  Comparator #(.Bits(10)) comparator_1 (.a(10'hff), .b(op), .eq(comparator_1_eq));  // open: gt, lt
  ROM #(.bigEndian("true"), .AddrBits(10), .Bits(8)) pc_control (
    .A(op), .sel(1'b1), .D({cycles, pc_link_we, pc_src, jump_type, branch_en}));
  ROM #(.bigEndian("true"), .AddrBits(10), .Bits(8)) pc_sp_mul_control (
    .A(op), .sel(1'b1), .D({pc_sp_mul_control_d, sp_out, pc_cond}));

  // Other names for the same wires on the sheet: ir_opcode[9:0] = op; seq_exec = exec

  // Notes on the sheet:
  //   op: default 48
  //   pc_control loads pc_control.hex
  //   pc_sp_mul_control loads pc_sp_mul_control.hex
endmodule

/* Test case:
op exec branch-en jump-type pc-src pc-link-we cycles pc-cond sp-out HALT_IN
0 0 0 0 0 0 1 0 0 0
0 1 0 0 0 0 1 0 0 0
1 0 0 0 0 0 1 0 0 0
1 1 0 0 0 0 1 0 0 0
2 0 0 0 0 0 1 0 0 0
2 1 0 0 0 0 1 0 0 0
3 0 0 0 0 0 1 0 0 0
3 1 0 0 0 0 1 0 0 0
4 0 0 0 0 0 1 0 0 0
4 1 0 0 0 0 1 0 0 0
5 0 0 0 0 0 1 0 0 0
5 1 0 0 0 0 1 0 0 0
6 0 0 0 0 0 1 0 0 0
6 1 0 0 0 0 1 0 0 0
7 0 0 0 0 0 1 0 0 0
7 1 0 0 0 0 1 0 0 0
8 0 0 0 0 0 1 0 0 0
8 1 0 0 0 0 1 0 0 0
9 0 0 0 0 0 1 0 0 0
9 1 0 0 0 0 1 0 0 0
10 0 0 0 0 0 1 0 0 0
10 1 0 0 0 0 1 0 0 0
11 0 0 0 0 0 1 0 0 0
11 1 0 0 0 0 1 0 0 0
12 0 0 0 0 0 1 0 0 0
12 1 0 0 0 0 1 0 0 0
13 0 0 0 0 0 1 0 0 0
13 1 0 0 0 0 1 0 0 0
14 0 0 0 0 0 1 0 0 0
14 1 0 0 0 0 1 0 0 0
15 0 0 0 0 0 1 0 0 0
15 1 0 0 0 0 1 0 0 0
16 0 0 0 0 0 1 0 0 0
16 1 0 0 0 0 1 0 0 0
17 0 0 0 0 0 1 0 0 0
17 1 0 0 0 0 1 0 0 0
18 0 0 0 0 0 1 0 0 0
18 1 0 0 0 0 1 0 0 0
19 0 0 0 0 0 1 0 0 0
19 1 0 0 0 0 1 0 0 0
20 0 0 0 0 0 1 0 0 0
20 1 0 0 0 0 1 0 0 0
21 0 0 0 0 0 1 0 0 0
21 1 0 0 0 0 1 0 0 0
22 0 0 0 0 0 1 0 0 0
22 1 0 0 0 0 1 0 0 0
23 0 0 0 0 0 1 0 0 0
23 1 0 0 0 0 1 0 0 0
24 0 0 0 0 0 1 0 0 0
24 1 0 0 0 0 1 0 0 0
25 0 0 0 0 0 1 0 0 0
25 1 0 0 0 0 1 0 0 0
26 0 0 0 1 0 1 0 0 0
26 1 0 0 1 0 1 0 0 0
27 0 0 0 0 0 1 0 0 0
27 1 0 0 0 0 1 0 0 0
28 0 0 0 0 0 1 0 0 0
28 1 0 0 0 0 1 0 0 0
29 0 0 0 0 0 1 0 0 0
29 1 0 0 0 0 1 0 0 0
30 0 0 0 0 0 1 0 0 0
30 1 0 0 0 0 1 0 0 0
31 0 0 0 0 0 1 0 0 0
31 1 0 0 0 0 1 0 0 0
32 0 0 0 0 0 1 0 0 0
32 1 0 0 0 0 1 0 0 0
33 0 0 0 0 0 1 0 0 0
33 1 0 0 0 0 1 0 0 0
34 0 0 0 0 0 1 0 0 0
34 1 0 0 0 0 1 0 0 0
35 0 0 0 0 0 1 0 0 0
35 1 0 0 0 0 1 0 0 0
36 0 0 0 0 0 1 0 0 0
36 1 0 0 0 0 1 0 0 0
37 0 0 0 0 0 1 0 0 0
37 1 0 0 0 0 1 0 0 0
38 0 0 0 0 0 1 0 0 0
38 1 0 0 0 0 1 0 0 0
39 0 0 0 0 0 1 0 0 0
39 1 0 0 0 0 1 0 0 0
48 0 0 0 0 0 2 0 0 0
48 1 0 0 0 0 2 0 0 0
49 0 0 0 0 0 2 0 0 0
49 1 0 0 0 0 2 0 0 0
50 0 0 0 0 0 2 0 0 0
50 1 0 0 0 0 2 0 0 0
51 0 0 0 0 0 2 0 0 0
51 1 0 0 0 0 2 0 0 0
52 0 0 0 0 0 2 0 0 0
52 1 0 0 0 0 2 0 0 0
53 0 0 0 0 0 1 0 0 0
53 1 0 0 0 0 1 0 0 0
54 0 0 0 0 0 2 0 0 0
54 1 0 0 0 0 2 0 0 0
64 0 0 0 0 0 2 0 0 0
64 1 0 0 0 0 2 0 0 0
65 0 0 0 0 0 2 0 0 0
65 1 0 0 0 0 2 0 0 0
66 0 0 0 0 0 2 0 0 0
66 1 0 0 0 0 2 0 0 0
67 0 0 0 0 0 1 0 0 0
67 1 0 0 0 0 1 0 0 0
80 0 1 0 0 0 1 0 0 0
80 1 1 0 0 0 1 0 0 0
81 0 1 0 0 0 1 4 0 0
81 1 1 0 0 0 1 4 0 0
82 0 1 0 0 0 1 2 0 0
82 1 1 0 0 0 1 2 0 0
83 0 1 0 0 0 1 6 0 0
83 1 1 0 0 0 1 6 0 0
84 0 1 0 0 0 1 5 0 0
84 1 1 0 0 0 1 5 0 0
85 0 1 0 0 0 1 1 0 0
85 1 1 0 0 0 1 1 0 0
86 0 1 0 0 0 1 6 0 0
86 1 1 0 0 0 1 6 0 0
87 0 1 0 0 0 1 7 0 0
87 1 1 0 0 0 1 7 0 0
96 0 0 1 0 1 1 0 0 0
96 1 0 1 0 1 1 0 0 0
97 0 0 1 0 1 2 0 0 0
97 1 0 1 0 1 2 0 0 0
98 0 0 1 0 0 1 0 0 0
98 1 0 1 0 0 1 0 0 0
99 0 0 1 2 0 1 0 0 0
99 1 0 1 2 0 1 0 0 0
100 0 0 1 2 0 1 0 0 0
100 1 0 1 2 0 1 0 0 0
112 0 0 0 0 0 2 0 0 0
112 1 0 0 0 0 2 0 0 0
113 0 0 0 0 0 2 0 0 0
113 1 0 0 0 0 2 0 0 0
114 0 0 1 0 1 1 0 0 0
114 1 0 1 0 1 1 0 0 0
115 0 0 1 0 0 2 0 0 0
115 1 0 1 0 0 2 0 0 0
116 0 0 0 0 0 2 0 0 0
116 1 0 0 0 0 2 0 0 0
117 0 0 0 0 0 1 0 0 0
117 1 0 0 0 0 1 0 0 0
118 0 0 0 0 0 2 0 0 0
118 1 0 0 0 0 2 0 0 0
119 0 0 0 0 0 2 0 0 0
119 1 0 0 0 0 2 0 0 0
120 0 0 0 0 0 1 0 0 0
120 1 0 0 0 0 1 0 0 0
121 0 0 0 0 0 1 0 0 0
121 1 0 0 0 0 1 0 0 0
122 0 0 0 0 0 1 0 0 0
122 1 0 0 0 0 1 0 0 0
123 0 0 0 0 0 2 0 0 0
123 1 0 0 0 0 2 0 0 0
124 0 0 0 0 0 2 0 0 0
124 1 0 0 0 0 2 0 0 0
125 0 0 0 0 0 2 0 0 0
125 1 0 0 0 0 2 0 0 0
126 0 0 0 0 0 2 0 0 0
126 1 0 0 0 0 2 0 0 0
128 0 0 0 0 0 1 0 0 0
128 1 0 0 0 0 1 0 0 0
129 0 0 0 0 0 1 0 0 0
129 1 0 0 0 0 1 0 0 0
130 0 0 0 0 0 1 0 0 0
130 1 0 0 0 0 1 0 0 0
131 0 0 0 0 0 1 0 0 0
131 1 0 0 0 0 1 0 0 0
132 0 0 0 0 0 1 0 0 0
132 1 0 0 0 0 1 0 0 0
133 0 0 0 0 0 1 0 0 0
133 1 0 0 0 0 1 0 0 0
144 0 0 0 0 0 1 0 0 0
144 1 0 0 0 0 1 0 0 0
145 0 0 0 0 0 1 0 0 0
145 1 0 0 0 0 1 0 0 0
146 0 0 0 0 0 1 0 0 0
146 1 0 0 0 0 1 0 0 0
147 0 0 0 0 0 1 0 0 0
147 1 0 0 0 0 1 0 0 0
160 0 0 0 0 0 1 0 0 0
160 1 0 0 0 0 1 0 0 0
161 0 0 0 0 0 1 0 0 0
161 1 0 0 0 0 1 0 0 0
162 0 0 0 0 0 1 0 0 0
162 1 0 0 0 0 1 0 0 0
163 0 0 0 0 0 1 0 0 0
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*/
