// Digital circuit pc2.dig as structural Verilog
module pc2 (
  input  CLK,
  input  nSR,
  input  [23:0] ADDR_ABS,
  input  [23:0] OFFSET,
  input  [23:0] ADDR_RET,
  input  MUX1_SEL,
  input  MUX2_SEL,
  input  FLAG_N,
  input  FLAG_C,
  input  FLAG_Z,
  input  FLAG_O,
  input  [2:0] COND,
  input  BRANCH_EN,
  input  INT_EN_IN,
  input  HALT_IN,
  input  INT_REQ,
  input  INT_VEC_0,
  input  INT_VEC_1,
  input  INT_VEC_2,
  input  [23:0] SP_DELTA,
  input  SP_LOAD_N,
  input  JUMP_UNCOND,
  input  PCEN,
  output INT_EN,
  output HALTED,
  output [23:0] PC_OUT,
  output [23:0] SP_OUT,
  output INT_ACK,
  output [3:0] FLAGS_SAVE,
  output [23:0] PC_SAVE
);

  wire and_1_out, CLK_GATED, COND_RESULT, not_1_out, PC_LOAD_N;
  wire [1:0] mux_sel;
  wire [23:0] INT_VECTOR, LOAD_ADDR, PC_REL, SP_D;

  not not_1 (not_1_out, MUX2_SEL);
  and and_1 (and_1_out, not_1_out, MUX1_SEL);
  or or_1 (mux_sel[1], MUX2_SEL, INT_ACK);
  or or_2 (mux_sel[0], INT_ACK, and_1_out);
  sc_pc_counter SC1_1 (.nSR(nSR), .clk(CLK_GATED), .nPE(PC_LOAD_N), .D(LOAD_ADDR), .pc_en(PCEN), .Q(PC_OUT));
  Multiplexer #(.Bits(24), .Selector_Bits(2)) multiplexer_1 (
    .sel(mux_sel), .in_0(ADDR_ABS), .in_1(PC_REL), .in_2(ADDR_RET), .in_3(INT_VECTOR), .out(LOAD_ADDR));
  sc_pc_counter SC1_2 (.nSR(nSR), .clk(CLK_GATED), .nPE(SP_LOAD_N), .D(SP_D), .pc_en(PCEN), .Q(SP_OUT));
  sc_adder24 SC2_1 (.B(OFFSET), .A(PC_OUT), .S(PC_REL));
  sc_branch SC4_1 (
    .FLAG_N(FLAG_N), .FLAG_C(FLAG_C), .FLAG_Z(FLAG_Z), .FLAG_O(FLAG_O), .COND(COND), .BRANCH_EN(BRANCH_EN),
    .COND_RESULT(COND_RESULT));
  sc_adder24 SC2_2 (.B(SP_DELTA), .A(SP_OUT), .S(SP_D));
  sc_flags_save SC6_1 (
    .INT_GATE(INT_ACK), .FLAG_N(FLAG_N), .FLAG_C(FLAG_C), .FLAG_Z(FLAG_Z), .FLAG_O(FLAG_O),
    .FLAGS_SAVE(FLAGS_SAVE));
  sc_control_flags SC5_1 (
    .INT_EN_IN(INT_EN_IN), .HALT_IN(HALT_IN), .INT_REQ(INT_REQ), .INT_VEC_0(INT_VEC_0),
    .INT_VEC_1(INT_VEC_1), .INT_VEC_2(INT_VEC_2), .CLK(CLK), .INT_VECTOR(INT_VECTOR), .INT_EN(INT_EN),
    .HALTED(HALTED), .INT_GATE(INT_ACK), .CLK_GATED(CLK_GATED));
  nor nor_1 (PC_LOAD_N, COND_RESULT, INT_ACK, JUMP_UNCOND);
  sc_adder24 SC2_3 (.B(24'h1), .A(PC_OUT), .S(PC_SAVE));

  // Other names for the same wires on the sheet: INT_GATE = INT_ACK; pc_en = PCEN
endmodule

/* Test case pc-unit-branch-exhaustive:
CLK ~SR ADDR_ABS OFFSET ADDR_RET MUX1_SEL MUX2_SEL FLAG_N FLAG_C FLAG_Z FLAG_O COND BRANCH_EN INT_EN_IN HALT_IN INT_REQ INT_VEC_0 INT_VEC_1 INT_VEC_2 SP_DELTA SP_LOAD_N JUMP_UNCOND INT_EN HALTED PC_OUT SP_OUT INT_ACK FLAGS_SAVE PC_SAVE

# COND 0..7, taken/not, abs/rel × 256 targets

0 0 0x000000 0x000000 0x000000 0 0 0 0 0 0 0 0 0 0 0 0 0 0 0x000000 1 0 x x x x x x x
C 0 0x000000 0x000000 0x000000 0 0 0 0 0 0 0 0 0 0 0 0 0 0 0x000000 1 0 x x x x x x x
0 1 0x000000 0x000000 0x000000 0 0 0 0 0 0 0 0 0 0 0 0 0 0 0x000000 1 0 x x x x x x x
C 1 0x000000 0x000000 0x000000 0 0 0 0 0 0 0 1 0 0 0 0 0 0 0x000000 1 0 x x x x x x x
0 1 0x000000 0x000000 0x000000 0 0 0 0 0 0 0 0 0 0 0 0 0 0 0x000000 1 0 0 0 0 0 0 0 1
0 0 0x000000 0x000000 0x000000 0 0 0 0 0 0 0 0 0 0 0 0 0 0 0x000000 1 0 x x x x x x x
C 0 0x000000 0x000000 0x000000 0 0 0 0 0 0 0 0 0 0 0 0 0 0 0x000000 1 0 x x x x x x x
0 1 0x000000 0x000000 0x000000 0 0 0 0 0 0 0 0 0 0 0 0 0 0 0x000000 1 0 x x x x x x x
C 1 0x000001 0x000000 0x000000 0 0 0 0 0 0 0 1 0 0 0 0 0 0 0x000000 1 0 x x x x x x x
0 1 0x000000 0x000000 0x000000 0 0 0 0 0 0 0 0 0 0 0 0 0 0 0x000000 1 0 0 0 0 0 0 0 1
0 0 0x000000 0x000000 0x000000 0 0 0 0 0 0 0 0 0 0 0 0 0 0 0x000000 1 0 x x x x x x x
C 0 0x000000 0x000000 0x000000 0 0 0 0 0 0 0 0 0 0 0 0 0 0 0x000000 1 0 x x x x x x x
0 1 0x000000 0x000000 0x000000 0 0 0 0 0 0 0 0 0 0 0 0 0 0 0x000000 1 0 x x x x x x x
C 1 0x000002 0x000000 0x000000 0 0 0 0 0 0 0 1 0 0 0 0 0 0 0x000000 1 0 x x x x x x x
0 1 0x000000 0x000000 0x000000 0 0 0 0 0 0 0 0 0 0 0 0 0 0 0x000000 1 0 0 0 0 0 0 0 1
0 0 0x000000 0x000000 0x000000 0 0 0 0 0 0 0 0 0 0 0 0 0 0 0x000000 1 0 x x x x x x x
C 0 0x000000 0x000000 0x000000 0 0 0 0 0 0 0 0 0 0 0 0 0 0 0x000000 1 0 x x x x x x x
0 1 0x000000 0x000000 0x000000 0 0 0 0 0 0 0 0 0 0 0 0 0 0 0x000000 1 0 x x x x x x x
C 1 0x000003 0x000000 0x000000 0 0 0 0 0 0 0 1 0 0 0 0 0 0 0x000000 1 0 x x x x x x x
0 1 0x000000 0x000000 0x000000 0 0 0 0 0 0 0 0 0 0 0 0 0 0 0x000000 1 0 0 0 0 0 0 0 1
0 0 0x000000 0x000000 0x000000 0 0 0 0 0 0 0 0 0 0 0 0 0 0 0x000000 1 0 x x x x x x x
C 0 0x000000 0x000000 0x000000 0 0 0 0 0 0 0 0 0 0 0 0 0 0 0x000000 1 0 x x x x x x x
0 1 0x000000 0x000000 0x000000 0 0 0 0 0 0 0 0 0 0 0 0 0 0 0x000000 1 0 x x x x x x x
C 1 0x000004 0x000000 0x000000 0 0 0 0 0 0 0 1 0 0 0 0 0 0 0x000000 1 0 x x x x x x x
0 1 0x000000 0x000000 0x000000 0 0 0 0 0 0 0 0 0 0 0 0 0 0 0x000000 1 0 0 0 0 0 0 0 1
0 0 0x000000 0x000000 0x000000 0 0 0 0 0 0 0 0 0 0 0 0 0 0 0x000000 1 0 x x x x x x x
C 0 0x000000 0x000000 0x000000 0 0 0 0 0 0 0 0 0 0 0 0 0 0 0x000000 1 0 x x x x x x x
0 1 0x000000 0x000000 0x000000 0 0 0 0 0 0 0 0 0 0 0 0 0 0 0x000000 1 0 x x x x x x x
C 1 0x000005 0x000000 0x000000 0 0 0 0 0 0 0 1 0 0 0 0 0 0 0x000000 1 0 x x x x x x x
0 1 0x000000 0x000000 0x000000 0 0 0 0 0 0 0 0 0 0 0 0 0 0 0x000000 1 0 0 0 0 0 0 0 1
0 0 0x000000 0x000000 0x000000 0 0 0 0 0 0 0 0 0 0 0 0 0 0 0x000000 1 0 x x x x x x x
C 0 0x000000 0x000000 0x000000 0 0 0 0 0 0 0 0 0 0 0 0 0 0 0x000000 1 0 x x x x x x x
0 1 0x000000 0x000000 0x000000 0 0 0 0 0 0 0 0 0 0 0 0 0 0 0x000000 1 0 x x x x x x x
C 1 0x000006 0x000000 0x000000 0 0 0 0 0 0 0 1 0 0 0 0 0 0 0x000000 1 0 x x x x x x x
0 1 0x000000 0x000000 0x000000 0 0 0 0 0 0 0 0 0 0 0 0 0 0 0x000000 1 0 0 0 0 0 0 0 1
0 0 0x000000 0x000000 0x000000 0 0 0 0 0 0 0 0 0 0 0 0 0 0 0x000000 1 0 x x x x x x x
C 0 0x000000 0x000000 0x000000 0 0 0 0 0 0 0 0 0 0 0 0 0 0 0x000000 1 0 x x x x x x x
0 1 0x000000 0x000000 0x000000 0 0 0 0 0 0 0 0 0 0 0 0 0 0 0x000000 1 0 x x x x x x x
C 1 0x000007 0x000000 0x000000 0 0 0 0 0 0 0 1 0 0 0 0 0 0 0x000000 1 0 x x x x x x x
0 1 0x000000 0x000000 0x000000 0 0 0 0 0 0 0 0 0 0 0 0 0 0 0x000000 1 0 0 0 0 0 0 0 1
0 0 0x000000 0x000000 0x000000 0 0 0 0 0 0 0 0 0 0 0 0 0 0 0x000000 1 0 x x x x x x x
C 0 0x000000 0x000000 0x000000 0 0 0 0 0 0 0 0 0 0 0 0 0 0 0x000000 1 0 x x x x x x x
0 1 0x000000 0x000000 0x000000 0 0 0 0 0 0 0 0 0 0 0 0 0 0 0x000000 1 0 x x x x x x x
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*/

/* Test case pc-unit-seq-inc:
CLK ~SR ADDR_ABS OFFSET ADDR_RET MUX1_SEL MUX2_SEL FLAG_N FLAG_C FLAG_Z FLAG_O COND BRANCH_EN INT_EN_IN HALT_IN INT_REQ INT_VEC_0 INT_VEC_1 INT_VEC_2 SP_DELTA SP_LOAD_N JUMP_UNCOND INT_EN HALTED PC_OUT SP_OUT INT_ACK FLAGS_SAVE PC_SAVE

# PC+1 via JUMP_UNCOND + MUX1_SEL + OFFSET=1 (same PC result as PCEN increment)

0 0 0x000000 0x000000 0x000000 0 0 0 0 0 0 0 0 0 0 0 0 0 0 0x000000 1 0 x x x x x x x
C 0 0x000000 0x000000 0x000000 0 0 0 0 0 0 0 0 0 0 0 0 0 0 0x000000 1 0 x x x x x x x
0 1 0x000000 0x000000 0x000000 0 0 0 0 0 0 0 0 0 0 0 0 0 0 0x000000 1 0 x x x x x x x
C 1 0x000000 0x000001 0x000000 1 0 0 0 0 0 0 0 0 0 0 0 0 0 0x000000 1 1 x x x x x x x
0 1 0x000000 0x000000 0x000000 0 0 0 0 0 0 0 0 0 0 0 0 0 0 0x000000 1 0 0 0 1 0 0 0 2
C 1 0x000000 0x000001 0x000000 1 0 0 0 0 0 0 0 0 0 0 0 0 0 0x000000 1 1 x x x x x x x
0 1 0x000000 0x000000 0x000000 0 0 0 0 0 0 0 0 0 0 0 0 0 0 0x000000 1 0 0 0 2 0 0 0 3
C 1 0x000000 0x000001 0x000000 1 0 0 0 0 0 0 0 0 0 0 0 0 0 0x000000 1 1 x x x x x x x
0 1 0x000000 0x000000 0x000000 0 0 0 0 0 0 0 0 0 0 0 0 0 0 0x000000 1 0 0 0 3 0 0 0 4
C 1 0x000000 0x000001 0x000000 1 0 0 0 0 0 0 0 0 0 0 0 0 0 0x000000 1 1 x x x x x x x
0 1 0x000000 0x000000 0x000000 0 0 0 0 0 0 0 0 0 0 0 0 0 0 0x000000 1 0 0 0 4 0 0 0 5
C 1 0x000000 0x000001 0x000000 1 0 0 0 0 0 0 0 0 0 0 0 0 0 0x000000 1 1 x x x x x x x
0 1 0x000000 0x000000 0x000000 0 0 0 0 0 0 0 0 0 0 0 0 0 0 0x000000 1 0 0 0 5 0 0 0 6
C 1 0x000000 0x000001 0x000000 1 0 0 0 0 0 0 0 0 0 0 0 0 0 0x000000 1 1 x x x x x x x
0 1 0x000000 0x000000 0x000000 0 0 0 0 0 0 0 0 0 0 0 0 0 0 0x000000 1 0 0 0 6 0 0 0 7
C 1 0x000000 0x000001 0x000000 1 0 0 0 0 0 0 0 0 0 0 0 0 0 0x000000 1 1 x x x x x x x
0 1 0x000000 0x000000 0x000000 0 0 0 0 0 0 0 0 0 0 0 0 0 0 0x000000 1 0 0 0 7 0 0 0 8
C 1 0x000000 0x000001 0x000000 1 0 0 0 0 0 0 0 0 0 0 0 0 0 0x000000 1 1 x x x x x x x
0 1 0x000000 0x000000 0x000000 0 0 0 0 0 0 0 0 0 0 0 0 0 0 0x000000 1 0 0 0 8 0 0 0 9
C 1 0x000000 0x000001 0x000000 1 0 0 0 0 0 0 0 0 0 0 0 0 0 0x000000 1 1 x x x x x x x
0 1 0x000000 0x000000 0x000000 0 0 0 0 0 0 0 0 0 0 0 0 0 0 0x000000 1 0 0 0 9 0 0 0 10
C 1 0x000000 0x000001 0x000000 1 0 0 0 0 0 0 0 0 0 0 0 0 0 0x000000 1 1 x x x x x x x
0 1 0x000000 0x000000 0x000000 0 0 0 0 0 0 0 0 0 0 0 0 0 0 0x000000 1 0 0 0 10 0 0 0 11
C 1 0x000000 0x000001 0x000000 1 0 0 0 0 0 0 0 0 0 0 0 0 0 0x000000 1 1 x x x x x x x
0 1 0x000000 0x000000 0x000000 0 0 0 0 0 0 0 0 0 0 0 0 0 0 0x000000 1 0 0 0 11 0 0 0 12
C 1 0x000000 0x000001 0x000000 1 0 0 0 0 0 0 0 0 0 0 0 0 0 0x000000 1 1 x x x x x x x
0 1 0x000000 0x000000 0x000000 0 0 0 0 0 0 0 0 0 0 0 0 0 0 0x000000 1 0 0 0 12 0 0 0 13
C 1 0x000000 0x000001 0x000000 1 0 0 0 0 0 0 0 0 0 0 0 0 0 0x000000 1 1 x x x x x x x
0 1 0x000000 0x000000 0x000000 0 0 0 0 0 0 0 0 0 0 0 0 0 0 0x000000 1 0 0 0 13 0 0 0 14
C 1 0x000000 0x000001 0x000000 1 0 0 0 0 0 0 0 0 0 0 0 0 0 0x000000 1 1 x x x x x x x
0 1 0x000000 0x000000 0x000000 0 0 0 0 0 0 0 0 0 0 0 0 0 0 0x000000 1 0 0 0 14 0 0 0 15
C 1 0x000000 0x000001 0x000000 1 0 0 0 0 0 0 0 0 0 0 0 0 0 0x000000 1 1 x x x x x x x
0 1 0x000000 0x000000 0x000000 0 0 0 0 0 0 0 0 0 0 0 0 0 0 0x000000 1 0 0 0 15 0 0 0 0x000010
C 1 0x000000 0x000001 0x000000 1 0 0 0 0 0 0 0 0 0 0 0 0 0 0x000000 1 1 x x x x x x x
0 1 0x000000 0x000000 0x000000 0 0 0 0 0 0 0 0 0 0 0 0 0 0 0x000000 1 0 0 0 0x000010 0 0 0 0x000011
C 1 0x000000 0x000001 0x000000 1 0 0 0 0 0 0 0 0 0 0 0 0 0 0x000000 1 1 x x x x x x x
0 1 0x000000 0x000000 0x000000 0 0 0 0 0 0 0 0 0 0 0 0 0 0 0x000000 1 0 0 0 0x000011 0 0 0 0x000012
C 1 0x000000 0x000001 0x000000 1 0 0 0 0 0 0 0 0 0 0 0 0 0 0x000000 1 1 x x x x x x x
0 1 0x000000 0x000000 0x000000 0 0 0 0 0 0 0 0 0 0 0 0 0 0 0x000000 1 0 0 0 0x000012 0 0 0 0x000013
C 1 0x000000 0x000001 0x000000 1 0 0 0 0 0 0 0 0 0 0 0 0 0 0x000000 1 1 x x x x x x x
0 1 0x000000 0x000000 0x000000 0 0 0 0 0 0 0 0 0 0 0 0 0 0 0x000000 1 0 0 0 0x000013 0 0 0 0x000014
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*/

/* Test case pc-unit-abs-jump:
CLK ~SR ADDR_ABS OFFSET ADDR_RET MUX1_SEL MUX2_SEL FLAG_N FLAG_C FLAG_Z FLAG_O COND BRANCH_EN INT_EN_IN HALT_IN INT_REQ INT_VEC_0 INT_VEC_1 INT_VEC_2 SP_DELTA SP_LOAD_N JUMP_UNCOND INT_EN HALTED PC_OUT SP_OUT INT_ACK FLAGS_SAVE PC_SAVE

# JUMP_UNCOND absolute (MUX1_SEL=0): corner targets + non-zero start PC

0 0 0x000000 0x000000 0x000000 0 0 0 0 0 0 0 0 0 0 0 0 0 0 0x000000 1 0 x x x x x x x
C 0 0x000000 0x000000 0x000000 0 0 0 0 0 0 0 0 0 0 0 0 0 0 0x000000 1 0 x x x x x x x
0 1 0x000000 0x000000 0x000000 0 0 0 0 0 0 0 0 0 0 0 0 0 0 0x000000 1 0 x x x x x x x
C 1 0x000000 0x000000 0x000000 0 0 0 0 0 0 0 0 0 0 0 0 0 0 0x000000 1 1 x x x x x x x
0 1 0x000000 0x000000 0x000000 0 0 0 0 0 0 0 0 0 0 0 0 0 0 0x000000 1 0 0 0 0 0 0 0 1
0 0 0x000000 0x000000 0x000000 0 0 0 0 0 0 0 0 0 0 0 0 0 0 0x000000 1 0 x x x x x x x
C 0 0x000000 0x000000 0x000000 0 0 0 0 0 0 0 0 0 0 0 0 0 0 0x000000 1 0 x x x x x x x
0 1 0x000000 0x000000 0x000000 0 0 0 0 0 0 0 0 0 0 0 0 0 0 0x000000 1 0 x x x x x x x
C 1 0x000001 0x000000 0x000000 0 0 0 0 0 0 0 0 0 0 0 0 0 0 0x000000 1 1 x x x x x x x
0 1 0x000000 0x000000 0x000000 0 0 0 0 0 0 0 0 0 0 0 0 0 0 0x000000 1 0 0 0 1 0 0 0 2
0 0 0x000000 0x000000 0x000000 0 0 0 0 0 0 0 0 0 0 0 0 0 0 0x000000 1 0 x x x x x x x
C 0 0x000000 0x000000 0x000000 0 0 0 0 0 0 0 0 0 0 0 0 0 0 0x000000 1 0 x x x x x x x
0 1 0x000000 0x000000 0x000000 0 0 0 0 0 0 0 0 0 0 0 0 0 0 0x000000 1 0 x x x x x x x
C 1 0x000010 0x000000 0x000000 0 0 0 0 0 0 0 0 0 0 0 0 0 0 0x000000 1 1 x x x x x x x
0 1 0x000000 0x000000 0x000000 0 0 0 0 0 0 0 0 0 0 0 0 0 0 0x000000 1 0 0 0 0x000010 0 0 0 0x000011
0 0 0x000000 0x000000 0x000000 0 0 0 0 0 0 0 0 0 0 0 0 0 0 0x000000 1 0 x x x x x x x
C 0 0x000000 0x000000 0x000000 0 0 0 0 0 0 0 0 0 0 0 0 0 0 0x000000 1 0 x x x x x x x
0 1 0x000000 0x000000 0x000000 0 0 0 0 0 0 0 0 0 0 0 0 0 0 0x000000 1 0 x x x x x x x
C 1 0x00FFFF 0x000000 0x000000 0 0 0 0 0 0 0 0 0 0 0 0 0 0 0x000000 1 1 x x x x x x x
0 1 0x000000 0x000000 0x000000 0 0 0 0 0 0 0 0 0 0 0 0 0 0 0x000000 1 0 0 0 0x00FFFF 0 0 0 0x010000
0 0 0x000000 0x000000 0x000000 0 0 0 0 0 0 0 0 0 0 0 0 0 0 0x000000 1 0 x x x x x x x
C 0 0x000000 0x000000 0x000000 0 0 0 0 0 0 0 0 0 0 0 0 0 0 0x000000 1 0 x x x x x x x
0 1 0x000000 0x000000 0x000000 0 0 0 0 0 0 0 0 0 0 0 0 0 0 0x000000 1 0 x x x x x x x
C 1 0xABCDEF 0x000000 0x000000 0 0 0 0 0 0 0 0 0 0 0 0 0 0 0x000000 1 1 x x x x x x x
0 1 0x000000 0x000000 0x000000 0 0 0 0 0 0 0 0 0 0 0 0 0 0 0x000000 1 0 0 0 0xABCDEF 0 0 0 0xABCDF0
0 0 0x000000 0x000000 0x000000 0 0 0 0 0 0 0 0 0 0 0 0 0 0 0x000000 1 0 x x x x x x x
C 0 0x000000 0x000000 0x000000 0 0 0 0 0 0 0 0 0 0 0 0 0 0 0x000000 1 0 x x x x x x x
0 1 0x000000 0x000000 0x000000 0 0 0 0 0 0 0 0 0 0 0 0 0 0 0x000000 1 0 x x x x x x x
C 1 0xFFFFFF 0x000000 0x000000 0 0 0 0 0 0 0 0 0 0 0 0 0 0 0x000000 1 1 x x x x x x x
0 1 0x000000 0x000000 0x000000 0 0 0 0 0 0 0 0 0 0 0 0 0 0 0x000000 1 0 0 0 0xFFFFFF 0 0 0 0
0 0 0x000000 0x000000 0x000000 0 0 0 0 0 0 0 0 0 0 0 0 0 0 0x000000 1 0 x x x x x x x
C 0 0x000000 0x000000 0x000000 0 0 0 0 0 0 0 0 0 0 0 0 0 0 0x000000 1 0 x x x x x x x
0 1 0x000000 0x000000 0x000000 0 0 0 0 0 0 0 0 0 0 0 0 0 0 0x000000 1 0 x x x x x x x
C 1 0x000100 0x000000 0x000000 0 0 0 0 0 0 0 0 0 0 0 0 0 0 0x000000 1 1 x x x x x x x
0 1 0x000000 0x000000 0x000000 0 0 0 0 0 0 0 0 0 0 0 0 0 0 0x000000 1 0 0 0 0x000100 0 0 0 0x000101
C 1 0x00ABCD 0x000000 0xDEADBE 0 1 0 0 0 0 0 0 0 0 0 0 0 0 0x000000 1 1 x x x x x x x
0 1 0x000000 0x000000 0x000000 0 0 0 0 0 0 0 0 0 0 0 0 0 0 0x000000 1 0 0 0 0xDEADBE 0 0 0 0xDEADBF
*/

/* Test case pc-unit-sp:
CLK ~SR ADDR_ABS OFFSET ADDR_RET MUX1_SEL MUX2_SEL FLAG_N FLAG_C FLAG_Z FLAG_O COND BRANCH_EN INT_EN_IN HALT_IN INT_REQ INT_VEC_0 INT_VEC_1 INT_VEC_2 SP_DELTA SP_LOAD_N JUMP_UNCOND INT_EN HALTED PC_OUT SP_OUT INT_ACK FLAGS_SAVE PC_SAVE

# SP_LOAD_N=0: SP <- SP + SP_DELTA

0 0 0x000000 0x000000 0x000000 0 0 0 0 0 0 0 0 0 0 0 0 0 0 0x000000 1 0 x x x x x x x
C 0 0x000000 0x000000 0x000000 0 0 0 0 0 0 0 0 0 0 0 0 0 0 0x000000 1 0 x x x x x x x
0 1 0x000000 0x000000 0x000000 0 0 0 0 0 0 0 0 0 0 0 0 0 0 0x000000 1 0 x x x x x x x
C 1 0x000000 0x000000 0x000000 0 0 0 0 0 0 0 0 0 0 0 0 0 0 0x000010 0 0 x x x x x x x
0 1 0x000000 0x000000 0x000000 0 0 0 0 0 0 0 0 0 0 0 0 0 0 0x000000 1 0 0 0 0 0x000010 0 0 1
C 1 0x000000 0x000000 0x000000 0 0 0 0 0 0 0 0 0 0 0 0 0 0 0x000001 0 0 x x x x x x x
0 1 0x000000 0x000000 0x000000 0 0 0 0 0 0 0 0 0 0 0 0 0 0 0x000000 1 0 0 0 0 0x000011 0 0 1
C 1 0x000000 0x000000 0x000000 0 0 0 0 0 0 0 0 0 0 0 0 0 0 0x000000 1 0 x x x x x x x
0 1 0x000000 0x000000 0x000000 0 0 0 0 0 0 0 0 0 0 0 0 0 0 0x000000 1 0 0 0 0 0x000011 0 0 1
*/

/* Test case pc-unit-jump-priority-exhaustive:
CLK ~SR ADDR_ABS OFFSET ADDR_RET MUX1_SEL MUX2_SEL FLAG_N FLAG_C FLAG_Z FLAG_O COND BRANCH_EN INT_EN_IN HALT_IN INT_REQ INT_VEC_0 INT_VEC_1 INT_VEC_2 SP_DELTA SP_LOAD_N JUMP_UNCOND INT_EN HALTED PC_OUT SP_OUT INT_ACK FLAGS_SAVE PC_SAVE

# Mux priority with competing ADDR_ABS/OFFSET/ADDR_RET (reset each case).
# INT vector path is in pc-unit-smoke (INT_EN is not cleared by ~SR).
# Load triggers: JUMP_UNCOND or taken BRANCH_EN (COND=JZ).

0 0 0x000000 0x000000 0x000000 0 0 0 0 0 0 0 0 0 0 0 0 0 0 0x000000 1 0 x x x x x x x
C 0 0x000000 0x000000 0x000000 0 0 0 0 0 0 0 0 0 0 0 0 0 0 0x000000 1 0 x x x x x x x
0 1 0x000000 0x000000 0x000000 0 0 0 0 0 0 0 0 0 0 0 0 0 0 0x000000 1 0 x x x x x x x
C 1 0x111111 0x222222 0x333333 0 0 0 0 0 0 0 0 0 0 0 0 0 0 0x000000 1 0 x x x x x x x
0 1 0x000000 0x000000 0x000000 0 0 0 0 0 0 0 0 0 0 0 0 0 0 0x000000 1 0 0 0 0 0 0 0 1
0 0 0x000000 0x000000 0x000000 0 0 0 0 0 0 0 0 0 0 0 0 0 0 0x000000 1 0 x x x x x x x
C 0 0x000000 0x000000 0x000000 0 0 0 0 0 0 0 0 0 0 0 0 0 0 0x000000 1 0 x x x x x x x
0 1 0x000000 0x000000 0x000000 0 0 0 0 0 0 0 0 0 0 0 0 0 0 0x000000 1 0 x x x x x x x
C 1 0x111111 0x222222 0x333333 0 1 0 0 0 0 0 0 0 0 0 0 0 0 0x000000 1 0 x x x x x x x
0 1 0x000000 0x000000 0x000000 0 0 0 0 0 0 0 0 0 0 0 0 0 0 0x000000 1 0 0 0 0 0 0 0 1
0 0 0x000000 0x000000 0x000000 0 0 0 0 0 0 0 0 0 0 0 0 0 0 0x000000 1 0 x x x x x x x
C 0 0x000000 0x000000 0x000000 0 0 0 0 0 0 0 0 0 0 0 0 0 0 0x000000 1 0 x x x x x x x
0 1 0x000000 0x000000 0x000000 0 0 0 0 0 0 0 0 0 0 0 0 0 0 0x000000 1 0 x x x x x x x
C 1 0x111111 0x222222 0x333333 1 0 0 0 0 0 0 0 0 0 0 0 0 0 0x000000 1 0 x x x x x x x
0 1 0x000000 0x000000 0x000000 0 0 0 0 0 0 0 0 0 0 0 0 0 0 0x000000 1 0 0 0 0 0 0 0 1
0 0 0x000000 0x000000 0x000000 0 0 0 0 0 0 0 0 0 0 0 0 0 0 0x000000 1 0 x x x x x x x
C 0 0x000000 0x000000 0x000000 0 0 0 0 0 0 0 0 0 0 0 0 0 0 0x000000 1 0 x x x x x x x
0 1 0x000000 0x000000 0x000000 0 0 0 0 0 0 0 0 0 0 0 0 0 0 0x000000 1 0 x x x x x x x
C 1 0x111111 0x222222 0x333333 1 1 0 0 0 0 0 0 0 0 0 0 0 0 0x000000 1 0 x x x x x x x
0 1 0x000000 0x000000 0x000000 0 0 0 0 0 0 0 0 0 0 0 0 0 0 0x000000 1 0 0 0 0 0 0 0 1
0 0 0x000000 0x000000 0x000000 0 0 0 0 0 0 0 0 0 0 0 0 0 0 0x000000 1 0 x x x x x x x
C 0 0x000000 0x000000 0x000000 0 0 0 0 0 0 0 0 0 0 0 0 0 0 0x000000 1 0 x x x x x x x
0 1 0x000000 0x000000 0x000000 0 0 0 0 0 0 0 0 0 0 0 0 0 0 0x000000 1 0 x x x x x x x
C 1 0x111111 0x222222 0x333333 0 0 0 0 1 0 0 0 0 0 0 0 0 0 0x000000 1 0 x x x x x x x
0 1 0x000000 0x000000 0x000000 0 0 0 0 0 0 0 0 0 0 0 0 0 0 0x000000 1 0 0 0 0 0 0 0 1
0 0 0x000000 0x000000 0x000000 0 0 0 0 0 0 0 0 0 0 0 0 0 0 0x000000 1 0 x x x x x x x
C 0 0x000000 0x000000 0x000000 0 0 0 0 0 0 0 0 0 0 0 0 0 0 0x000000 1 0 x x x x x x x
0 1 0x000000 0x000000 0x000000 0 0 0 0 0 0 0 0 0 0 0 0 0 0 0x000000 1 0 x x x x x x x
C 1 0x111111 0x222222 0x333333 0 1 0 0 1 0 0 0 0 0 0 0 0 0 0x000000 1 0 x x x x x x x
0 1 0x000000 0x000000 0x000000 0 0 0 0 0 0 0 0 0 0 0 0 0 0 0x000000 1 0 0 0 0 0 0 0 1
0 0 0x000000 0x000000 0x000000 0 0 0 0 0 0 0 0 0 0 0 0 0 0 0x000000 1 0 x x x x x x x
C 0 0x000000 0x000000 0x000000 0 0 0 0 0 0 0 0 0 0 0 0 0 0 0x000000 1 0 x x x x x x x
0 1 0x000000 0x000000 0x000000 0 0 0 0 0 0 0 0 0 0 0 0 0 0 0x000000 1 0 x x x x x x x
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*/

/* Test case pc-unit-jmp-exhaustive:
CLK ~SR ADDR_ABS OFFSET ADDR_RET MUX1_SEL MUX2_SEL FLAG_N FLAG_C FLAG_Z FLAG_O COND BRANCH_EN INT_EN_IN HALT_IN INT_REQ INT_VEC_0 INT_VEC_1 INT_VEC_2 SP_DELTA SP_LOAD_N JUMP_UNCOND INT_EN HALTED PC_OUT SP_OUT INT_ACK FLAGS_SAVE PC_SAVE

# JUMP_UNCOND abs/rel

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*/

/* Test case pc-unit-ret-exhaustive:
CLK ~SR ADDR_ABS OFFSET ADDR_RET MUX1_SEL MUX2_SEL FLAG_N FLAG_C FLAG_Z FLAG_O COND BRANCH_EN INT_EN_IN HALT_IN INT_REQ INT_VEC_0 INT_VEC_1 INT_VEC_2 SP_DELTA SP_LOAD_N JUMP_UNCOND INT_EN HALTED PC_OUT SP_OUT INT_ACK FLAGS_SAVE PC_SAVE

# JUMP_UNCOND + MUX2_SEL -> ADDR_RET

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*/

/* Test case pc-unit-smoke:
CLK ~SR ADDR_ABS OFFSET ADDR_RET MUX1_SEL MUX2_SEL FLAG_N FLAG_C FLAG_Z FLAG_O COND BRANCH_EN INT_EN_IN HALT_IN INT_REQ INT_VEC_0 INT_VEC_1 INT_VEC_2 SP_DELTA SP_LOAD_N JUMP_UNCOND INT_EN HALTED PC_OUT SP_OUT INT_ACK FLAGS_SAVE PC_SAVE

# One cycle each: reset, inc, JZ, JMP, RET, IRQ, HALT, SP

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*/
