// Digital circuit program-counter.dig as structural Verilog
module program_counter (
  input  [31:0] mem_din,
  input  [31:0] alu_in,
  input  [2:0] pc_src,
  input  [21:0] IR_ABS,
  input  RESET,
  input  [1:0] cycles,
  input  clk,
  input  FLAG_N,
  input  FLAG_C,
  input  FLAG_Z,
  input  FLAG_V,
  input  [2:0] COND,
  input  jump_type,
  input  branch_en,
  input  INT_EN_IN,
  input  HALT_IN,
  input  INT_REQ,
  input  INT_VEC_0,
  input  INT_VEC_1,
  input  INT_VEC_2,
  input  link_in,
  output [23:0] PC_OUT,
  output [23:0] PC_SAVE,
  output FETCH,
  output EXECUTE,
  output MEM_WAIT,
  output COND_RESULT,
  output INT_EN,
  output HALT,
  output INT_GATE,
  output CLK_GATED,
  output [23:0] PC_LINK
);

  wire and_1_out, and_4_out, and_5_out, link_reg_en, match, mux0, mux1, mux2, MUX_Y, nHALT, nor_4_out,
       not_1_out, not_2_out, not_3_out, not_4_out, not_5_out, not_7_out, not_8_out, not_9_out, nRESET,
       or_3_out, or_6_out, pc_load, pc_reg_en, seq0, seq1, seq_rst, xnor_1_out, xnor_2_out;
  wire [23:0] multiplexer_1_out, multiplexer_2_out, pc_mux, pc_rel;
  wire [23:22] ir_abs_x;

  BitExtender #(.inputBits(1), .outputBits(2)) bitextender_1 (.in(IR_ABS[21]), .out(ir_abs_x));
  Multiplexer #(.Bits(24)) multiplexer_1 (.sel(RESET), .in_0(PC_SAVE), .in_1({24{1'b0}}), .out(multiplexer_1_out));
  Register #(.Bits(24)) register_1 (.D(multiplexer_1_out), .C(CLK_GATED), .en(link_reg_en), .Q(PC_LINK));
  or or_1 (mux0, INT_GATE, pc_src[0], FETCH);
  or or_2 (mux1, FETCH, INT_GATE, pc_src[1]);
  Multiplexer #(.Bits(24)) multiplexer_2 (.sel(RESET), .in_0(pc_mux), .in_1({24{1'b0}}), .out(multiplexer_2_out));
  or or_3 (or_3_out, jump_type, COND_RESULT);
  and and_1 (and_1_out, EXECUTE, link_in, nRESET);
  Add #(.Bits(24)) add_1 (.a({ir_abs_x, IR_ABS}), .b(PC_OUT), .c_i(1'b0), .s(pc_rel));  // open: c_o
  Add #(.Bits(24)) add_2 (.a(24'h1), .b(PC_OUT), .c_i(1'b0), .s(PC_SAVE));  // open: c_o
  Register #(.Bits(24)) register_2 (.D(multiplexer_2_out), .C(CLK_GATED), .en(pc_reg_en), .Q(PC_OUT));
  Multiplexer #(.Selector_Bits(3), .Bits(24)) multiplexer_3 (
    .sel({mux2, mux1, mux0}), .in_0({2'b00, IR_ABS}), .in_1(pc_rel), .in_2(PC_LINK),
    .in_3({{18{1'b0}}, INT_VEC_2, INT_VEC_1, INT_VEC_0, 3'b000}), .in_4(alu_in[23:0]), .in_5(mem_din[23:0]),
    .in_6({24{1'b0}}), .in_7(PC_SAVE), .out(pc_mux));
  and and_2 (pc_load, EXECUTE, or_3_out);
  or or_4 (link_reg_en, and_1_out, RESET);
  or or_5 (pc_reg_en, FETCH, INT_GATE, pc_load);
  or or_6 (or_6_out, FETCH, pc_src[2]);
  and and_3 (mux2, or_6_out, not_1_out);
  not not_1 (not_1_out, INT_GATE);
  and and_4 (and_4_out, INT_EN_IN, nRESET);
  and and_5 (and_5_out, HALT_IN, nRESET);
  and and_6 (COND_RESULT, MUX_Y, branch_en);
  Multiplexer #(.Selector_Bits(3)) multiplexer_4 (
    .sel(COND), .in_0(FLAG_Z), .in_1(FLAG_C), .in_2(FLAG_N), .in_3(FLAG_V), .in_4(not_2_out),
    .in_5(not_3_out), .in_6(not_4_out), .in_7(not_5_out), .out(MUX_Y));
  not not_2 (not_2_out, FLAG_Z);
  not not_3 (not_3_out, FLAG_C);
  not not_4 (not_4_out, FLAG_N);
  not not_5 (not_5_out, FLAG_V);
  not not_6 (nRESET, RESET);
  D_FF d_ff_1 (.D(and_4_out), .C(clk), .Q(INT_EN));  // open: nQ
  D_FF d_ff_2 (.D(and_5_out), .C(clk), .Q(HALT));  // open: nQ
  Counter #(.Bits(2)) counter_1 (.en(1'b1), .C(not_7_out), .clr(seq_rst), .out({seq1, seq0}));  // open: ovf
  not not_7 (not_7_out, CLK_GATED);
  not not_8 (not_8_out, seq0);
  not not_9 (not_9_out, seq1);
  nor nor_1 (FETCH, seq0, seq1);
  nor nor_2 (EXECUTE, not_8_out, seq1);
  nor nor_3 (MEM_WAIT, seq0, not_9_out);
  xnor xnor_1 (xnor_1_out, cycles[0], seq0);
  xnor xnor_2 (xnor_2_out, cycles[1], seq1);
  nor nor_4 (nor_4_out, match, RESET);
  and and_7 (CLK_GATED, clk, nHALT);
  and and_8 (INT_GATE, INT_REQ, INT_EN);
  and and_9 (match, xnor_1_out, xnor_2_out);
  not not_10 (seq_rst, nor_4_out);
  not not_11 (nHALT, HALT);

  // Other names for the same wires on the sheet: alu[23:0] = alu_in[23:0]; brch_en = branch_en; cyc0 = cycles[0];
  //   cyc1 = cycles[1]; int_vec[5:3] = {INT_VEC_2, INT_VEC_1, INT_VEC_0}; ir_abs_t[21:0] = IR_ABS;
  //   ir_abs_x[21:0] = IR_ABS; jmp_type = jump_type; mem_in[23:0] = mem_din[23:0]; seq_out[1:0] = {seq1, seq0}

  // Notes on the sheet:
  //   IR_ABS: default 1
  //   INPUTS
  //   OUTPUTS
  //   BRANCH
  //   SEQUENCER
endmodule

/* Test case pc-irq-jump:
clk cycles jump-type branch-en RESET pc-src IR_ABS alu-in mem-din INT_EN_IN INT_REQ INT_VEC_0 INT_VEC_1 INT_VEC_2 PC-OUT PC-SAVE

# INT_GATE forces irq vector mux and pc-reg-en on FETCH

# RESET hold
0 0 0 0 1 0 0 0 0 0 0 0 0 0 x x
C 0 0 0 1 0 0 0 0 0 0 0 0 0 0 1
0 0 0 0 1 0 0 0 0 0 0 0 0 0 0 1

# Release RESET, first FETCH
0 0 0 0 0 0 0 0 0 0 0 0 0 0 x x
C 0 0 0 0 0 0 0 0 0 0 0 0 0 1 2
0 0 0 0 0 0 0 0 0 0 0 0 0 0 1 2

# Latch interrupt enable
0 0 0 0 0 0 0 0 0 1 0 0 0 0 x x
C 0 0 0 0 0 0 0 0 1 0 0 0 0 2 3
0 0 0 0 0 0 0 0 0 1 0 0 0 0 2 3

# IRQ on FETCH with encoded vector
0 0 0 0 0 0 0 0 0 1 1 1 0 1 x x
C 0 0 0 0 0 0 0 0 1 1 1 0 1 0x28 0x29
0 0 0 0 0 0 0 0 0 1 1 1 0 1 0x28 0x29

# FETCH with pc-src=0 IR_ABS=max - IRQ override still loads vector
0 0 1 0 0 0 0xFFFFFF 0 0 1 1 1 0 1 x x
C 0 1 0 0 0 0xFFFFFF 0 0 1 1 1 0 1 0x28 0x29
0 0 1 0 0 0 0xFFFFFF 0 0 1 1 1 0 1 0x28 0x29

# EXEC settle
0 1 0 0 0 0 0 0 0 1 0 0 0 0 x x
C 1 0 0 0 0 0 0 0 1 0 0 0 0 0x29 0x2A
0 1 0 0 0 0 0 0 0 1 0 0 0 0 0x29 0x2A

# Abs jump to target address
0 1 1 0 0 0 0x50 0 0 1 0 0 0 0 x x
C 1 1 0 0 0 0x50 0 0 1 0 0 0 0 0x50 0x51
0 1 1 0 0 0 0x50 0 0 1 0 0 0 0 0x50 0x51

# Clear INT_EN then INT_REQ ignored on FETCH
0 0 0 0 0 0 0 0 0 0 0 0 0 0 x x
C 0 0 0 0 0 0 0 0 0 0 0 0 0 0x51 0x52
0 0 0 0 0 0 0 0 0 0 0 0 0 0 0x51 0x52
0 0 0 0 0 0 0 0 0 0 1 1 0 1 x x
C 0 0 0 0 0 0 0 0 0 1 1 0 1 0x52 0x53
0 0 0 0 0 0 0 0 0 0 1 1 0 1 0x52 0x53
*/

/* Test case pc-fetch-override:
clk cycles jump-type branch-en RESET pc-src IR_ABS alu-in mem-din FLAG_Z FLAG_C FLAG_N FLAG_V COND PC-OUT PC-SAVE

# FETCH forces mux sel=7 (PC+1); jump-type/pc-src ignored in FETCH

# RESET hold
0 0 0 0 1 0 0 0 0 0 0 0 0 0 x x
C 0 0 0 1 0 0 0 0 0 0 0 0 0 0 1
0 0 0 0 1 0 0 0 0 0 0 0 0 0 0 1

# Release RESET, first FETCH
0 0 0 0 0 0 0 0 0 0 0 0 0 0 x x
C 0 0 0 0 0 0 0 0 0 0 0 0 0 1 2
0 0 0 0 0 0 0 0 0 0 0 0 0 0 1 2

# FETCH: pc-src=0 IR_ABS=max jump-type=1 ignored (increment only)
0 0 1 0 0 0 0xFFFFFF 0 0 0 0 0 0 0 x x
C 0 1 0 0 0 0xFFFFFF 0 0 0 0 0 0 0 2 3
0 0 1 0 0 0 0xFFFFFF 0 0 0 0 0 0 0 2 3

# FETCH: pc-src=1 negative offset (bit21=1) increment only
0 0 1 0 0 1 0x200000 0 0 0 0 0 0 0 x x
C 0 1 0 0 1 0x200000 0 0 0 0 0 0 0 3 4
0 0 1 0 0 1 0x200000 0 0 0 0 0 0 0 3 4

# EXEC settle
0 1 0 0 0 0 0 0 0 0 0 0 0 0 x x
C 1 0 0 0 0 0 0 0 0 0 0 0 0 4 5
0 1 0 0 0 0 0 0 0 0 0 0 0 0 4 5

# EXEC: same pc-src=1 offset -4 - rel jump PC=0
0 1 1 0 0 1 0x3FFFFC 0 0 0 0 0 0 0 x x
C 1 1 0 0 1 0x3FFFFC 0 0 0 0 0 0 0 0 1
0 1 1 0 0 1 0x3FFFFC 0 0 0 0 0 0 0 0 1

# FETCH after jump: increment from 0
0 0 0 0 0 0 0 0 0 0 0 0 0 0 x x
C 0 0 0 0 0 0 0 0 0 0 0 0 0 1 2
0 0 0 0 0 0 0 0 0 0 0 0 0 0 1 2
*/

/* Test case pc-link-gate:
clk cycles link-in jump-type RESET pc-src IR_ABS alu-in mem-din PC-OUT PC-SAVE PC-LINK

# Negative enable gating for link-in

# Setup: FETCH to PC=1
0 0 0 0 1 0 0 0 0 x x x
C 0 0 0 1 0 0 0 0 0 1 0
0 0 0 0 0 0 0 0 0 x x x
C 0 0 0 0 0 0 0 0 1 2 0
0 0 0 0 0 0 0 0 0 1 2 0

# FETCH only (cycles=0): link-in=1 must not latch
0 0 1 0 0 0 0 0 0 x x x
C 0 0 1 0 0 0 0 0 2 3 0
0 0 1 0 0 0 0 0 0 2 3 0

# EXEC, link-in=0: must not latch
0 1 0 0 0 0 0 0 0 x x x
C 1 0 0 0 0 0 0 0 3 4 0
0 1 0 0 0 0 0 0 0 3 4 0

# EXEC, link-in=1: sanity latch PC-SAVE=4
0 1 1 0 0 0 0 0 0 x x x
C 1 1 0 0 0 0 0 0 3 4 4
0 1 1 0 0 0 0 0 0 3 4 4
*/

/* Test case pc-sequencer-jump:
clk cycles jump-type branch-en RESET pc-src IR_ABS alu-in mem-din FLAG_Z FLAG_C FLAG_N FLAG_V COND PC-OUT PC-SAVE

# Jumps only in EXEC; MEM-WAIT negative

# RESET hold
0 0 0 0 1 0 0 0 0 0 0 0 0 0 x x
C 0 0 0 1 0 0 0 0 0 0 0 0 0 0 1
0 0 0 0 1 0 0 0 0 0 0 0 0 0 0 1

# Release RESET, FETCH
0 0 0 0 0 0 0 0 0 0 0 0 0 0 x x
C 0 0 0 0 0 0 0 0 0 0 0 0 0 1 2
0 0 0 0 0 0 0 0 0 0 0 0 0 0 1 2

# EXEC settle, abs jump to 0x60
0 1 0 0 0 0 0 0 0 0 0 0 0 0 x x
C 1 0 0 0 0 0 0 0 0 0 0 0 0 2 3
0 1 0 0 0 0 0 0 0 0 0 0 0 0 2 3
0 1 1 0 0 0 0x60 0 0 0 0 0 0 0 x x
C 1 1 0 0 0 0x60 0 0 0 0 0 0 0 0x60 0x61
0 1 1 0 0 0 0x60 0 0 0 0 0 0 0 0x60 0x61

# FETCH increment to 0x61, switch to cycles=2
0 0 0 0 0 0 0 0 0 0 0 0 0 0 x x
C 0 0 0 0 0 0 0 0 0 0 0 0 0 0x61 0x62
0 0 0 0 0 0 0 0 0 0 0 0 0 0 0x61 0x62
0 2 0 0 0 0 0 0 0 0 0 0 0 0 x x
C 2 0 0 0 0 0 0 0 0 0 0 0 0 0x62 0x63
0 2 0 0 0 0 0 0 0 0 0 0 0 0 0x62 0x63
0 2 0 0 0 0 0 0 0 0 0 0 0 0 x x
C 2 0 0 0 0 0 0 0 0 0 0 0 0 0x62 0x63
0 2 0 0 0 0 0 0 0 0 0 0 0 0 0x62 0x63

# jump-type=1 in MEM-WAIT (cycles=2): must not load
0 2 1 0 0 0 0x70 0 0 0 0 0 0 0 x x
C 2 1 0 0 0 0x70 0 0 0 0 0 0 0 0x62 0x63
0 2 1 0 0 0 0x70 0 0 0 0 0 0 0 0x62 0x63

# Branch taken in EXEC only (cycles=1)
0 1 0 0 0 0 0 0 0 0 0 0 0 0 x x
C 1 0 0 0 0 0 0 0 0 0 0 0 0 0x63 0x64
0 1 0 0 0 0 0 0 0 0 0 0 0 0 0x63 0x64
0 1 0 1 0 1 0x3FFFFC 0 0 1 0 0 0 0 x x
C 1 0 1 0 1 0x3FFFFC 0 0 1 0 0 0 0 0x5F 0x60
0 1 0 1 0 1 0x3FFFFC 0 0 1 0 0 0 0 0x5F 0x60
*/

/* Test case pc-halt-frozen:
clk cycles HALT_IN jump-type RESET pc-src IR_ABS alu-in mem-din PC-OUT PC-SAVE PC-LINK link-in

# HALT freezes PC and link via CLK_GATED=0

# RESET hold
0 0 0 0 1 0 0 0 0 x x x 0
C 0 0 0 1 0 0 0 0 0 1 0 0
0 0 0 0 1 0 0 0 0 0 1 0 0

# Release RESET, FETCH increments
0 0 0 0 0 0 0 0 0 x x x 0
C 0 0 0 0 0 0 0 0 1 2 0 0
0 0 0 0 0 0 0 0 0 1 2 0 0
0 0 0 0 0 0 0 0 0 x x x 0
C 0 0 0 0 0 0 0 0 2 3 0 0
0 0 0 0 0 0 0 0 0 2 3 0 0

# EXEC settle (PC=3)
0 1 0 0 0 0 0 0 0 x x x 0
C 1 0 0 0 0 0 0 0 3 4 0 0
0 1 0 0 0 0 0 0 0 3 4 0 0

# Latch HALT=1 on clock edge
0 1 1 0 0 0 0 0 0 x x x 0
C 1 1 0 0 0 0 0 0 3 4 0 0
0 1 1 0 0 0 0 0 0 3 4 0 0

# Halted: abs jump must not change PC
0 1 1 1 0 0 0x50 0 0 x x x 0
C 1 1 1 0 0 0x50 0 0 3 4 0 0
0 1 1 1 0 0 0x50 0 0 3 4 0 0

# Halted + link-in=1 in EXEC: PC-LINK unchanged
0 1 1 0 0 0 0 0 0 x x x 1
C 1 1 0 0 0 0 0 0 3 4 0 1
0 1 1 0 0 0 0 0 0 3 4 0 1

# RESET while halted clears PC and link
0 1 1 0 1 0 0 0 0 x x x 1
C 1 1 0 1 0 0 0 0 0 1 0 0
0 1 1 0 1 0 0 0 0 0 1 0 0

# Release RESET, clear HALT (two clocks)
0 1 0 0 0 0 0 0 0 x x x 0
C 1 0 0 0 0 0 0 0 1 2 0 0
0 1 0 0 0 0 0 0 0 1 2 0 0
C 1 0 0 0 0 0 0 0 1 2 0 0
0 1 0 0 0 0 0 0 0 1 2 0 0

# EXEC settle then jump works after de-halt
0 1 0 0 0 0 0 0 0 x x x 0
C 1 0 0 0 0 0 0 0 2 3 0 0
0 1 0 0 0 0 0 0 0 2 3 0 0
0 1 0 1 0 0 0x40 0 0 x x x 0
C 1 0 1 0 0 0x40 0 0 0x40 0x41 0 0
0 1 0 1 0 0 0x40 0 0 0x40 0x41 0 0
*/

/* Test case pc-mux-sources:
clk cycles jump-type branch-en RESET pc-src IR_ABS alu-in mem-din FLAG_Z FLAG_C FLAG_N FLAG_V COND INT_VEC_0 INT_VEC_1 INT_VEC_2 PC-OUT PC-SAVE PC-LINK

# Untested mux sources: pc-src 5 (mem), 6 (glue/0), 3 (int-vec), 2 (RET miss)

# RESET hold
0 0 0 0 1 0 0 0 0 0 0 0 0 0 0 0 0 x x x
C 0 0 0 1 0 0 0 0 0 0 0 0 0 0 0 0 0 1 0
0 0 0 0 1 0 0 0 0 0 0 0 0 0 0 0 0 0 1 0

# Release RESET, FETCH
0 0 0 0 0 0 0 0 0 0 0 0 0 0 0 0 0 x x x
C 0 0 0 0 0 0 0 0 0 0 0 0 0 0 0 0 1 2 0
0 0 0 0 0 0 0 0 0 0 0 0 0 0 0 0 0 1 2 0

# EXEC settle
0 1 0 0 0 0 0 0 0 0 0 0 0 0 0 0 0 x x x
C 1 0 0 0 0 0 0 0 0 0 0 0 0 0 0 0 2 3 0
0 1 0 0 0 0 0 0 0 0 0 0 0 0 0 0 0 2 3 0

# 1. mem jump (pc-src=5): mem-din lower 24b = 0xBBCCDD
0 1 1 0 0 5 0 0 0xBBCCDD 0 0 0 0 0 0 0 0 x x x
C 1 1 0 0 5 0 0 0xBBCCDD 0 0 0 0 0 0 0 0 0xBBCCDD 0xBBCCDE 0
0 1 1 0 0 5 0 0 0xBBCCDD 0 0 0 0 0 0 0 0 0xBBCCDD 0xBBCCDE 0

# FETCH->EXEC setup
0 1 0 0 0 0 0 0 0 0 0 0 0 0 0 0 0 x x x
C 1 0 0 0 0 0 0 0 0 0 0 0 0 0 0 0 0xBBCCDE 0xBBCCDF 0
0 1 0 0 0 0 0 0 0 0 0 0 0 0 0 0 0 0xBBCCDE 0xBBCCDF 0

# 2. glue jump (pc-src=6): loads 0
0 1 1 0 0 6 0 0 0 0 0 0 0 0 0 0 0 x x x
C 1 1 0 0 6 0 0 0 0 0 0 0 0 0 0 0 0 1 0
0 1 1 0 0 6 0 0 0 0 0 0 0 0 0 0 0 0 1 0

# FETCH->EXEC setup
0 1 0 0 0 0 0 0 0 0 0 0 0 0 0 0 0 x x x
C 1 0 0 0 0 0 0 0 0 0 0 0 0 0 0 0 1 2 0
0 1 0 0 0 0 0 0 0 0 0 0 0 0 0 0 0 1 2 0

# 3. int-vec jump (pc-src=3): vector 0x28 (VEC_0=1 VEC_1=0 VEC_2=1)
0 1 1 0 0 3 0 0 0 0 0 0 0 0 1 0 1 x x x
C 1 1 0 0 3 0 0 0 0 0 0 0 0 1 0 1 0x28 0x29 0
0 1 1 0 0 3 0 0 0 0 0 0 0 0 1 0 1 0x28 0x29 0

# FETCH->EXEC setup
0 1 0 0 0 0 0 0 0 0 0 0 0 0 0 0 0 x x x
C 1 0 0 0 0 0 0 0 0 0 0 0 0 0 0 0 0x29 0x2A 0
0 1 0 0 0 0 0 0 0 0 0 0 0 0 0 0 0 0x29 0x2A 0

# 4. RET miss (pc-src=2, PC-LINK=0)
0 1 1 0 0 2 0 0 0 0 0 0 0 0 0 0 0 x x x
C 1 1 0 0 2 0 0 0 0 0 0 0 0 0 0 0 0 1 0
0 1 1 0 0 2 0 0 0 0 0 0 0 0 0 0 0 0 1 0
*/

/* Test case pc-link-latch:
clk cycles link-in jump-type RESET pc-src IR_ABS alu-in mem-din PC-OUT PC-SAVE PC-LINK

# Latch PC-SAVE into pc_link on EXEC when link-in=1 (RESET=1 hold / RESET=0 run)

# 1. RESET hold
0 0 0 0 1 0 0 0 0 x x x
C 0 0 0 1 0 0 0 0 0 1 0

# 2. Release RESET, FETCH (PC 0->1)
0 0 0 0 0 0 0 0 0 x x x
C 0 0 0 0 0 0 0 0 1 2 0
0 0 0 0 0 0 0 0 0 1 2 0

# 3. EXEC (no link-in) — advance to PC=2
0 1 0 0 0 0 0 0 0 x x x
C 1 0 0 0 0 0 0 0 2 3 0
0 1 0 0 0 0 0 0 0 2 3 0

# 4. EXEC + link-in: latch PC-SAVE=3 into pc_link
0 1 1 0 0 0 0 0 0 x x x
C 1 1 0 0 0 0 0 0 2 3 3
0 1 1 0 0 0 0 0 0 2 3 3

# 5. Hold — pc_link unchanged
0 1 1 0 0 0 0 0 0 2 3 3
*/

/* Test case pc-link-ret:
clk cycles link-in jump-type RESET pc-src IR_ABS alu-in mem-din PC-OUT PC-SAVE PC-LINK

# RET via mux in_2 (pc-src=2)

# Latch PC-LINK=2
0 0 0 0 1 0 0 0 0 x x x
C 0 0 0 1 0 0 0 0 0 1 0
0 0 0 0 0 0 0 0 0 x x x
C 0 0 0 0 0 0 0 0 1 2 0
0 0 0 0 0 0 0 0 0 1 2 0
0 1 0 0 0 0 0 0 0 x x x
C 1 0 0 0 0 0 0 0 2 3 0
0 1 0 0 0 0 0 0 0 2 3 0
0 1 1 0 0 0 0 0 0 x x x
C 1 1 0 0 0 0 0 0 2 3 3
0 1 1 0 0 0 0 0 0 2 3 3

# EXEC settle before jump
0 1 0 0 0 0 0 0 0 x x x
C 1 0 0 0 0 0 0 0 3 4 3
0 1 0 0 0 0 0 0 0 3 4 3

# Jump away to 0x100
0 1 0 1 0 0 0x100 0 0 x x x
C 1 0 1 0 0 0x100 0 0 0x100 0x101 3
0 1 0 1 0 0 0x100 0 0 0x100 0x101 3

# FETCH — PC increments
0 0 0 0 0 0 0 0 0 x x x
C 0 0 0 0 0 0 0 0 0x101 0x102 3
0 0 0 0 0 0 0 0 0 0x101 0x102 3

# EXEC settle before RET (avoid FETCH mux override)
0 1 0 0 0 0 0 0 0 x x x
C 1 0 0 0 0 0 0 0 0x102 0x103 3
0 1 0 0 0 0 0 0 0 0x102 0x103 3

# RET: pc-src=2 restores PC-LINK
0 1 0 1 0 2 0 0 0 x x x
C 1 0 1 0 2 0 0 0 3 4 3
0 1 0 1 0 2 0 0 0 3 4 3
*/

/* Test case pc-link-reset:
clk cycles link-in jump-type RESET pc-src IR_ABS alu-in mem-din PC-OUT PC-SAVE PC-LINK

# RESET clears pc_link flop

# Latch PC-LINK=2
0 0 0 0 1 0 0 0 0 x x x
C 0 0 0 1 0 0 0 0 0 1 0
0 0 0 0 0 0 0 0 0 x x x
C 0 0 0 0 0 0 0 0 1 2 0
0 0 0 0 0 0 0 0 0 1 2 0
0 1 0 0 0 0 0 0 0 x x x
C 1 0 0 0 0 0 0 0 2 3 0
0 1 0 0 0 0 0 0 0 2 3 0
0 1 1 0 0 0 0 0 0 x x x
C 1 1 0 0 0 0 0 0 2 3 3
0 1 1 0 0 0 0 0 0 2 3 3

# RESET=1 clocks link to 0
0 1 1 0 1 0 0 0 0 2 3 3
C 1 1 0 1 0 0 0 0 0 1 0
0 1 1 0 1 0 0 0 0 0 1 0

# Release RESET — pc_link stays 0
0 1 1 0 0 0 0 0 0 0 1 0
*/

/* Test case pc-link-edge:
clk cycles link-in jump-type RESET HALT_IN pc-src IR_ABS alu-in mem-din PC-OUT PC-SAVE PC-LINK

# Link register edge cases: overwrite, RESET priority, halt block, post-RET latch

# RESET hold
0 0 0 0 1 0 0 0 0 0 x x x
C 0 0 0 1 0 0 0 0 0 0 1 0
0 0 0 0 1 0 0 0 0 0 0 1 0

# Release RESET, FETCH
0 0 0 0 0 0 0 0 0 0 x x x
C 0 0 0 0 0 0 0 0 0 1 2 0
0 0 0 0 0 0 0 0 0 0 1 2 0

# EXEC settle
0 1 0 0 0 0 0 0 0 0 x x x
C 1 0 0 0 0 0 0 0 0 2 3 0
0 1 0 0 0 0 0 0 0 0 2 3 0

# Jump to 0xAABB
0 1 0 1 0 0 0 0xAABB 0 0 x x x
C 1 0 1 0 0 0 0xAABB 0 0 0xAABB 0xAABC 0
0 1 0 1 0 0 0 0xAABB 0 0 0xAABB 0xAABC 0

# EXEC settle, latch PC-SAVE=0xAABC
0 1 0 0 0 0 0 0 0 0 x x x
C 1 0 0 0 0 0 0 0 0 0xAABC 0xAABD 0
0 1 0 0 0 0 0 0 0 0 0xAABC 0xAABD 0
0 1 1 0 0 0 0 0 0 0 x x x
C 1 1 0 0 0 0 0 0 0 0xAABC 0xAABD 0xAABD
0 1 1 0 0 0 0 0 0 0 0xAABC 0xAABD 0xAABD

# Second latch overwrites link
0 1 0 0 0 0 0 0 0 0 x x x
C 1 0 0 0 0 0 0 0 0 0xAABD 0xAABE 0xAABD
0 1 0 0 0 0 0 0 0 0 0xAABD 0xAABE 0xAABD
0 1 1 0 0 0 0 0 0 0 x x x
C 1 1 0 0 0 0 0 0 0 0xAABD 0xAABE 0xAABE
0 1 1 0 0 0 0 0 0 0 0xAABD 0xAABE 0xAABE

# RESET during EXEC with link-in=1 clears link
0 1 1 0 1 0 0 0 0 0 x x x
C 1 1 0 1 0 0 0 0 0 0 1 0
0 1 1 0 1 0 0 0 0 0 0 1 0
*/

/* Test case pc-boundary-arith:
clk cycles jump-type branch-en RESET pc-src IR_ABS alu-in mem-din FLAG_Z FLAG_C FLAG_N FLAG_V COND PC-OUT PC-SAVE

# 24-bit wrap and sign-ext relative adder edge cases

# RESET hold
0 0 0 0 1 0 0 0 0 0 0 0 0 0 x x
C 0 0 0 1 0 0 0 0 0 0 0 0 0 0 1
0 0 0 0 1 0 0 0 0 0 0 0 0 0 0 1

# Release RESET, FETCH
0 0 0 0 0 0 0 0 0 0 0 0 0 0 x x
C 0 0 0 0 0 0 0 0 0 0 0 0 0 1 2
0 0 0 0 0 0 0 0 0 0 0 0 0 0 1 2

# EXEC settle
0 1 0 0 0 0 0 0 0 0 0 0 0 0 x x
C 1 0 0 0 0 0 0 0 0 0 0 0 0 2 3
0 1 0 0 0 0 0 0 0 0 0 0 0 0 2 3

# Abs jump to 0x3FFFFE (22-bit ir-abs max-1)
0 1 1 0 0 0 0x3FFFFE 0 0 0 0 0 0 0 x x
C 1 1 0 0 0 0x3FFFFE 0 0 0 0 0 0 0 0x3FFFFE 0x3FFFFF
0 1 1 0 0 0 0x3FFFFE 0 0 0 0 0 0 0 0x3FFFFE 0x3FFFFF

# FETCH increment at 22-bit boundary
0 0 0 0 0 0 0 0 0 0 0 0 0 0 x x
C 0 0 0 0 0 0 0 0 0 0 0 0 0 0x3FFFFF 0x400000
0 0 0 0 0 0 0 0 0 0 0 0 0 0 0x3FFFFF 0x400000

# FETCH increment past 22-bit max
0 0 0 0 0 0 0 0 0 0 0 0 0 0 x x
C 0 0 0 0 0 0 0 0 0 0 0 0 0 0x400000 0x400001
0 0 0 0 0 0 0 0 0 0 0 0 0 0 0x400000 0x400001

# RESET then abs jump to 0x10 for sign-ext rel test
0 0 0 0 1 0 0 0 0 0 0 0 0 0 x x
C 0 0 0 1 0 0 0 0 0 0 0 0 0 0 1
0 0 0 0 1 0 0 0 0 0 0 0 0 0 0 1
0 0 0 0 0 0 0 0 0 0 0 0 0 0 x x
C 0 0 0 0 0 0 0 0 0 0 0 0 0 1 2
0 0 0 0 0 0 0 0 0 0 0 0 0 0 1 2
0 1 0 0 0 0 0 0 0 0 0 0 0 0 x x
C 1 0 0 0 0 0 0 0 0 0 0 0 0 2 3
0 1 0 0 0 0 0 0 0 0 0 0 0 0 2 3
0 1 1 0 0 0 0x10 0 0 0 0 0 0 0 x x
C 1 1 0 0 0 0x10 0 0 0 0 0 0 0 0x10 0x11
0 1 1 0 0 0 0x10 0 0 0 0 0 0 0 0x10 0x11

# EXEC settle
0 1 0 0 0 0 0 0 0 0 0 0 0 0 x x
C 1 0 0 0 0 0 0 0 0 0 0 0 0 0x11 0x12
0 1 0 0 0 0 0 0 0 0 0 0 0 0 0x11 0x12

# Sign-ext rel jump with negative offset
0 1 1 0 0 1 0x3FFFFC 0 0 0 0 0 0 0 x x
C 1 1 0 0 1 0x3FFFFC 0 0 0 0 0 0 0 0xD 0xE
0 1 1 0 0 1 0x3FFFFC 0 0 0 0 0 0 0 0xD 0xE
*/

/* Test case sc-control-flags-tests:
clk INT_EN_IN HALT_IN INT_REQ INT_VEC_0 INT_VEC_1 INT_VEC_2 INT_EN HALT INT_GATE CLK_GATED

# Interrupt enable + halt + INT_GATE + CLK_GATED + INT_VEC inputs
# C = rising clock edge on 7474; exhaustive sections use CLK=1 to verify FFs


# 1. Plan milestone — latch INT_EN

0 1 0 0 0 0 0 x x 0 0
C 1 0 0 0 0 0 1 0 0 0
0 1 0 0 0 0 0 1 0 0 0

# 2. INT_GATE = INT_REQ AND INT_EN

0 1 0 1 0 0 0 1 0 1 0
0 1 0 0 0 0 0 1 0 0 0
C 0 0 1 0 0 0 0 0 0 0
0 0 0 1 0 0 0 0 0 0 0
0 0 0 1 0 0 0 0 0 0 0

# 3. Halt — HALT=1, CLK_GATED=0 when CLK=1

C 1 1 0 0 0 0 1 1 0 0
0 1 1 0 0 0 0 1 1 0 0
1 1 1 0 0 0 0 1 1 0 0

# 4. Release halt — two clocks to clear HALT, then CLK_GATED=1

C 1 0 0 0 0 0 1 1 0 0
0 1 0 0 0 0 0 1 1 0 0
C 1 0 0 0 0 0 1 0 0 0
0 1 0 0 0 0 0 1 0 0 0
1 1 0 0 0 0 0 1 0 0 1

# 5. INT_VEC inputs encoding (bits 3–5 = vec × 8)

0 1 0 0 1 1 0 1 0 0 0
0 1 0 0 1 1 1 1 0 0 0
0 1 0 0 0 0 0 1 0 0 0
0 1 0 0 1 0 0 1 0 0 0
0 1 0 0 0 1 0 1 0 0 0
0 1 0 0 0 0 1 1 0 0 0

# 6. INT_EN clears on clock when INT_EN_IN=0

C 0 0 0 0 0 0 0 0 0 0
0 0 0 0 0 0 0 0 0 0 0
0 0 0 0 0 0 0 0 0 0 0

# 7. HALT_IN sequence — set then clear HALT

C 1 1 0 0 0 0 1 1 0 0
0 1 1 0 0 0 0 1 1 0 0
C 1 0 0 0 0 0 1 0 0 0
0 1 0 0 0 0 0 1 0 0 0
0 1 0 0 0 0 0 1 0 0 0

# 8. Re-latch INT_EN=1 for INT_GATE checks

C 1 0 0 0 0 0 1 0 0 0
0 1 0 0 0 0 0 1 0 0 0
0 1 0 0 0 0 0 1 0 0 0
0 1 0 1 0 0 0 1 0 1 0

# 9. All 8 INT_VEC inputs combinations (steady-state)

0 1 0 0 0 0 0 1 0 0 0
0 1 0 0 1 0 0 1 0 0 0
0 1 0 0 0 1 0 1 0 0 0
0 1 0 0 1 1 0 1 0 0 0
0 1 0 0 0 0 1 1 0 0 0
0 1 0 0 1 0 1 1 0 0 0
0 1 0 0 0 1 1 1 0 0 0
0 1 0 0 1 1 1 1 0 0 0

# 10. CLK_GATED low when CLK=0 (halt released)

C 1 0 0 0 0 0 1 0 0 0
0 1 0 0 0 0 0 1 0 0 0
0 1 0 0 0 0 0 1 0 0 0
1 1 0 0 0 0 0 1 0 0 1

# 11. Halt blocks gated clock even if CLK held high

C 1 1 0 0 0 0 1 x 0 0
0 1 1 0 0 0 0 1 x 0 0
1 1 1 0 0 0 0 1 1 0 0

# 12. HALT=1, INT_GATE and vector while halted

C 1 1 0 0 0 0 1 x 0 0
0 1 1 0 0 0 0 1 x 0 0
1 1 1 1 1 1 1 1 1 1 0

# 13. Release halt then hold INT_EN across extra clocks

C 1 0 0 0 0 0 1 1 0 0
0 1 0 0 0 0 0 1 1 0 0
C 1 0 0 0 0 0 1 x 0 0
0 1 0 0 0 0 0 1 x 0 0
C 1 0 0 0 0 0 1 0 0 0
0 1 0 0 0 0 0 1 0 0 0
C 1 0 0 0 0 0 1 0 0 0
0 1 0 0 0 0 0 1 0 0 0
1 1 0 0 0 0 0 1 0 0 1

# 14. Vector stable while toggling unrelated inputs

0 1 0 1 1 0 1 1 0 1 0
0 0 1 0 1 0 1 1 0 0 0

# 15. Exhaustive — all 4 latch input combinations (C pulse + CLK=1 verify)

C 0 0 0 0 0 0 x x 0 0
1 0 0 0 0 0 0 0 0 0 1
C 0 1 0 0 0 0 x x 0 0
1 0 1 0 0 0 0 0 1 0 0
C 1 0 0 0 0 0 x x 0 0
1 1 0 0 0 0 0 1 0 0 1
C 1 1 0 0 0 0 x x 0 0
1 1 1 0 0 0 0 1 1 0 0

# 16. Exhaustive — INT_GATE truth table at CLK=0

C 0 0 0 0 0 0 x x 0 0
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*/

/* Test case branch-pc:
clk cycles jump-type branch-en RESET pc-src IR_ABS alu-in mem-din FLAG_Z FLAG_C FLAG_N FLAG_V COND PC-OUT PC-SAVE

# Branch PC integration — BEQ/BNE in EXEC (cycles=1), pc-src=1 relative

# RESET hold
0 0 0 0 1 0 0 0 0 0 0 0 0 0 x x
C 0 0 0 1 0 0 0 0 0 0 0 0 0 0 1
0 0 0 0 1 0 0 0 0 0 0 0 0 0 0 1

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*/

/* Test case branch:
FLAG_Z FLAG_C FLAG_N FLAG_V COND branch-en COND_RESULT

# Branch condition mux (74151) + branch-en gate; combinational


# 1. Plan milestone cases

1 0 0 0 0 1 1
1 0 0 0 4 1 0
1 0 0 0 0 0 0
0 1 0 0 1 1 1
0 0 0 0 4 1 1

# 2. All eight conditions — taken, not-taken, BRANCH_EN gate

1 0 0 0 0 1 1
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*/

/* Test case program-counter:
clk cycles jump-type branch-en RESET pc-src IR_ABS alu-in mem-din FLAG_Z FLAG_C FLAG_N FLAG_V COND PC-OUT PC-SAVE

# PC smoke (cycles=0 FETCH / cycles=1 EXEC). RESET=1 hold / RESET=0 run.
# Jumps: jump-type=1 in EXEC. Branches: branch-en=1, jump-type=0, flags+COND.

# 1. Idle
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*/

/* Test case sequencer:
RESET cycles clk FETCH EXECUTE MEM-WAIT

# From sequencer.dig; RESET active-high hold (invert main reset)
# RESET=1 hold, RESET=0 run

# Sync after prog-count-2-smoke (phase may not be FETCH)
1 0 C x x x

# Hold (RESET=1): counter cleared — FETCH
1 0 0 1 0 0
1 0 C 1 0 0

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*/
