// Digital circuit sc_adder24.dig as structural Verilog
module sc_adder24 (
  input  [23:0] B,
  input  [23:0] A,
  output [23:0] S
);

  wire C_1, C_2, C_3, C_4, C_5;

  _74283 U1 (
    .pin1(S[1]), .pin2(B[1]), .pin3(A[1]), .pin4(S[0]), .pin5(A[0]), .pin6(B[0]), .pin7(1'b0), .pin8(1'b0),
    .pin9(C_1), .pin10(S[3]), .pin11(B[3]), .pin12(A[3]), .pin13(S[2]), .pin14(A[2]), .pin15(B[2]),
    .pin16(1'b1));
  _74283 U4 (
    .pin1(S[13]), .pin2(B[13]), .pin3(A[13]), .pin4(S[12]), .pin5(A[12]), .pin6(B[12]), .pin7(C_3),
    .pin8(1'b0), .pin9(C_4), .pin10(S[15]), .pin11(B[15]), .pin12(A[15]), .pin13(S[14]), .pin14(A[14]),
    .pin15(B[14]), .pin16(1'b1));
  _74283 U2 (
    .pin1(S[5]), .pin2(B[5]), .pin3(A[5]), .pin4(S[4]), .pin5(A[4]), .pin6(B[4]), .pin7(C_1), .pin8(1'b0),
    .pin9(C_2), .pin10(S[7]), .pin11(B[7]), .pin12(A[7]), .pin13(S[6]), .pin14(A[6]), .pin15(B[6]),
    .pin16(1'b1));
  _74283 U5 (
    .pin1(S[17]), .pin2(B[17]), .pin3(A[17]), .pin4(S[16]), .pin5(A[16]), .pin6(B[16]), .pin7(C_4),
    .pin8(1'b0), .pin9(C_5), .pin10(S[19]), .pin11(B[19]), .pin12(A[19]), .pin13(S[18]), .pin14(A[18]),
    .pin15(B[18]), .pin16(1'b1));
  _74283 U3 (
    .pin1(S[9]), .pin2(B[9]), .pin3(A[9]), .pin4(S[8]), .pin5(A[8]), .pin6(B[8]), .pin7(C_2), .pin8(1'b0),
    .pin9(C_3), .pin10(S[11]), .pin11(B[11]), .pin12(A[11]), .pin13(S[10]), .pin14(A[10]), .pin15(B[10]),
    .pin16(1'b1));
  _74283 U6 (
    .pin1(S[21]), .pin2(B[21]), .pin3(A[21]), .pin4(S[20]), .pin5(A[20]), .pin6(B[20]), .pin7(C_5),
    .pin8(1'b0), .pin10(S[23]), .pin11(B[23]), .pin12(A[23]), .pin13(S[22]), .pin14(A[22]), .pin15(B[22]),
    .pin16(1'b1));  // open: pin9

  // Other names for the same wires on the sheet: A_0 = A[0]; A_1 = A[1]; A_2 = A[2]; A_3 = A[3]; A_4 = A[4];
  //   A_5 = A[5]; A_6 = A[6]; A_7 = A[7]; A_8 = A[8]; A_9 = A[9]; A_10 = A[10]; A_11 = A[11]; A_12 = A[12];
  //   A_13 = A[13]; A_14 = A[14]; A_15 = A[15]; A_16 = A[16]; A_17 = A[17]; A_18 = A[18]; A_19 = A[19]; A_20 = A[20];
  //   A_21 = A[21]; A_22 = A[22]; A_23 = A[23]; B_0 = B[0]; B_1 = B[1]; B_2 = B[2]; B_3 = B[3]; B_4 = B[4];
  //   B_5 = B[5]; B_6 = B[6]; B_7 = B[7]; B_8 = B[8]; B_9 = B[9]; B_10 = B[10]; B_11 = B[11]; B_12 = B[12];
  //   B_13 = B[13]; B_14 = B[14]; B_15 = B[15]; B_16 = B[16]; B_17 = B[17]; B_18 = B[18]; B_19 = B[19]; B_20 = B[20];
  //   B_21 = B[21]; B_22 = B[22]; B_23 = B[23]; S_0 = S[0]; S_1 = S[1]; S_2 = S[2]; S_3 = S[3]; S_4 = S[4];
  //   S_5 = S[5]; S_6 = S[6]; S_7 = S[7]; S_8 = S[8]; S_9 = S[9]; S_10 = S[10]; S_11 = S[11]; S_12 = S[12];
  //   S_13 = S[13]; S_14 = S[14]; S_15 = S[15]; S_16 = S[16]; S_17 = S[17]; S_18 = S[18]; S_19 = S[19]; S_20 = S[20];
  //   S_21 = S[21]; S_22 = S[22]; S_23 = S[23]
endmodule

/* Test case sc-adder24-tests:
A B S

# 24-bit ripple-carry adder (6×74283), combinational


# 1. Plan milestone cases

0x000010 0x000008 0x000018
0x000010 0xffffff 0x00000f
0x0000ff 0x000001 0x000100
0xffffff 0x000001 0x000000

# 2. SP push/pop deltas

0x000010 0x000001 0x000011
0x000010 0xffffff 0x00000f
0x000100 0x000001 0x000101
0x000100 0xffffff 0x0000ff
0x00ff00 0x000001 0x00ff01
0x00ff00 0xffffff 0x00feff
0xabcdef 0x000001 0xabcdf0
0xabcdef 0xffffff 0xabcdee

# 3. Zero and identity

0x000000 0x000000 0x000000
0xabcdef 0x000000 0xabcdef
0x000000 0x123456 0x123456

# 4. Max and wrap

0xffffff 0x000000 0xffffff
0xffffff 0x000001 0x000000
0xffffff 0xffffff 0xfffffe

# 5. All nibble-boundary carries

0x000000 0x000001 0x000001
0x00000f 0x000001 0x000010
0x0000ff 0x000001 0x000100
0x000fff 0x000001 0x001000
0x00ffff 0x000001 0x010000
0x0fffff 0x000001 0x100000

# 6. Walking-one on A (B=0)

0x000001 0x000000 0x000001
0x000002 0x000000 0x000002
0x000004 0x000000 0x000004
0x000008 0x000000 0x000008
0x000010 0x000000 0x000010
0x000020 0x000000 0x000020
0x000040 0x000000 0x000040
0x000080 0x000000 0x000080
0x000100 0x000000 0x000100
0x000200 0x000000 0x000200
0x000400 0x000000 0x000400
0x000800 0x000000 0x000800
0x001000 0x000000 0x001000
0x002000 0x000000 0x002000
0x004000 0x000000 0x004000
0x008000 0x000000 0x008000
0x010000 0x000000 0x010000
0x020000 0x000000 0x020000
0x040000 0x000000 0x040000
0x080000 0x000000 0x080000
0x100000 0x000000 0x100000
0x200000 0x000000 0x200000
0x400000 0x000000 0x400000
0x800000 0x000000 0x800000

# 7. Walking-one on B (A=0)

0x000000 0x000001 0x000001
0x000000 0x000002 0x000002
0x000000 0x000004 0x000004
0x000000 0x000008 0x000008
0x000000 0x000010 0x000010
0x000000 0x000020 0x000020
0x000000 0x000040 0x000040
0x000000 0x000080 0x000080
0x000000 0x000100 0x000100
0x000000 0x000200 0x000200
0x000000 0x000400 0x000400
0x000000 0x000800 0x000800
0x000000 0x001000 0x001000
0x000000 0x002000 0x002000
0x000000 0x004000 0x004000
0x000000 0x008000 0x008000
0x000000 0x010000 0x010000
0x000000 0x020000 0x020000
0x000000 0x040000 0x040000
0x000000 0x080000 0x080000
0x000000 0x100000 0x100000
0x000000 0x200000 0x200000
0x000000 0x400000 0x400000
0x000000 0x800000 0x800000

# 8. Checkerboard / alternating patterns

0xaaaaaa 0x555555 0xffffff
0x555555 0xaaaaaa 0xffffff
0xf0f0f0 0x0f0f0f 0xffffff

# 9. PC-relative style offsets

0x001000 0x000010 0x001010
0x001000 0xffffff 0x000fff
0x000fff 0x000001 0x001000
0x800000 0x400000 0xc00000

# 10. Independent byte lanes (no cross-carry)

0x000055 0x0000aa 0x0000ff
0x005500 0x00aa00 0x00ff00
0x550000 0xaa0000 0xff0000
0x55000000 0xaa000000 0x000000
0x5500000000 0xaa00000000 0x000000
0x550000000000 0xaa0000000000 0x000000

# 11. Powers of two sums

0x000001 0x000001 0x000002
0x000001 0x000002 0x000003
0x000001 0x000004 0x000005
0x000001 0x000008 0x000009
0x000002 0x000002 0x000004
0x000002 0x000004 0x000006
0x000002 0x000008 0x00000a
0x000002 0x000010 0x000012
0x000004 0x000004 0x000008
0x000004 0x000008 0x00000c
0x000004 0x000010 0x000014
0x000004 0x000020 0x000024
0x000008 0x000008 0x000010
0x000008 0x000010 0x000018
0x000008 0x000020 0x000028
0x000008 0x000040 0x000048
0x000010 0x000010 0x000020
0x000010 0x000020 0x000030
0x000010 0x000040 0x000050
0x000010 0x000080 0x000090
0x000020 0x000020 0x000040
0x000020 0x000040 0x000060
0x000020 0x000080 0x0000a0
0x000020 0x000100 0x000120
0x000040 0x000040 0x000080
0x000040 0x000080 0x0000c0
0x000040 0x000100 0x000140
0x000040 0x000200 0x000240
0x000080 0x000080 0x000100
0x000080 0x000100 0x000180
0x000080 0x000200 0x000280
0x000080 0x000400 0x000480
0x000100 0x000100 0x000200
0x000100 0x000200 0x000300
0x000100 0x000400 0x000500
0x000100 0x000800 0x000900
0x000200 0x000200 0x000400
0x000200 0x000400 0x000600
0x000200 0x000800 0x000a00
0x000200 0x001000 0x001200
0x000400 0x000400 0x000800
0x000400 0x000800 0x000c00
0x000400 0x001000 0x001400
0x000400 0x002000 0x002400
0x000800 0x000800 0x001000
0x000800 0x001000 0x001800
0x000800 0x002000 0x002800
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*/
