// Digital circuit sc_branch.dig as structural Verilog
module sc_branch (
  input  FLAG_N,
  input  FLAG_C,
  input  FLAG_Z,
  input  FLAG_O,
  input  [2:0] COND,
  input  BRANCH_EN,
  output COND_RESULT
);

  wire _1Y, _2Y, _3Y, MUX_D7, MUX_Y;

  _74151 U1 (
    .pin1(FLAG_O), .pin2(FLAG_N), .pin3(FLAG_C), .pin4(FLAG_Z), .pin5(MUX_Y), .pin7(1'b0), .pin8(1'b0),
    .pin9(COND[2]), .pin10(COND[1]), .pin11(COND[0]), .pin12(MUX_D7), .pin13(_3Y), .pin14(_2Y), .pin15(_1Y),
    .pin16(1'b1));  // open: pin6
  and and_1 (COND_RESULT, MUX_Y, BRANCH_EN);
  _7404 _7404_1 (
    .pin1(FLAG_Z), .pin2(_1Y), .pin3(FLAG_C), .pin4(_2Y), .pin5(FLAG_N), .pin6(_3Y), .pin7(1'b0),
    .pin8(MUX_D7), .pin9(FLAG_O), .pin11(1'b0), .pin13(1'b0), .pin14(1'b1));  // open: pin10, pin12

  // Other names for the same wires on the sheet: COND_0 = COND[0]; COND_1 = COND[1]; COND_2 = COND[2]
endmodule

/* Test case sc-branch-tests:
FLAG_Z FLAG_C FLAG_N FLAG_O COND BRANCH_EN COND_RESULT

# Branch condition mux (74151) + BRANCH_EN gate; combinational


# 1. Plan milestone cases

1 0 0 0 0 1 1
1 0 0 0 4 1 0
1 0 0 0 0 0 0
0 1 0 0 1 1 1
0 0 0 0 4 1 1

# 2. All eight conditions — taken, not-taken, BRANCH_EN gate

1 0 0 0 0 1 1
1 0 0 0 0 0 0
0 1 0 0 1 1 1
0 1 0 0 1 0 0
0 0 1 0 2 1 1
0 0 1 0 2 0 0
0 0 0 1 3 1 1
0 0 0 1 3 0 0
0 0 0 0 4 1 1
0 0 0 0 4 0 0
0 0 0 0 5 1 1
0 0 0 0 5 0 0
0 0 0 0 6 1 1
0 0 0 0 6 0 0
0 0 0 0 7 1 1
0 0 0 0 7 0 0
0 0 0 0 0 1 0
0 0 0 0 1 1 0
0 0 0 0 2 1 0
0 0 0 0 3 1 0
1 0 0 0 4 1 0
0 1 0 0 5 1 0
0 0 1 0 6 1 0
0 0 0 1 7 1 0

# 3. Cross-condition — wrong flag for opcode

0 1 0 0 0 1 0
1 0 0 0 1 1 0

# 4. Inverted conditions vs direct (JZ vs JNZ)

1 0 0 0 0 1 1
1 0 0 0 4 1 0
0 0 0 0 4 1 1
0 0 0 0 0 1 0

# 5. Complete truth table — 2^8 inputs (all flags × cond × BRANCH_EN)

0 0 0 0 0 0 0
0 0 0 0 0 1 0
0 0 0 1 0 0 0
0 0 0 1 0 1 0
0 0 1 0 0 0 0
0 0 1 0 0 1 0
0 0 1 1 0 0 0
0 0 1 1 0 1 0
0 1 0 0 0 0 0
0 1 0 0 0 1 0
0 1 0 1 0 0 0
0 1 0 1 0 1 0
0 1 1 0 0 0 0
0 1 1 0 0 1 0
0 1 1 1 0 0 0
0 1 1 1 0 1 0
1 0 0 0 0 0 0
1 0 0 0 0 1 1
1 0 0 1 0 0 0
1 0 0 1 0 1 1
1 0 1 0 0 0 0
1 0 1 0 0 1 1
1 0 1 1 0 0 0
1 0 1 1 0 1 1
1 1 0 0 0 0 0
1 1 0 0 0 1 1
1 1 0 1 0 0 0
1 1 0 1 0 1 1
1 1 1 0 0 0 0
1 1 1 0 0 1 1
1 1 1 1 0 0 0
1 1 1 1 0 1 1
0 0 0 0 1 0 0
0 0 0 0 1 1 0
0 0 0 1 1 0 0
0 0 0 1 1 1 0
0 0 1 0 1 0 0
0 0 1 0 1 1 0
0 0 1 1 1 0 0
0 0 1 1 1 1 0
0 1 0 0 1 0 0
0 1 0 0 1 1 1
0 1 0 1 1 0 0
0 1 0 1 1 1 1
0 1 1 0 1 0 0
0 1 1 0 1 1 1
0 1 1 1 1 0 0
0 1 1 1 1 1 1
1 0 0 0 1 0 0
1 0 0 0 1 1 0
1 0 0 1 1 0 0
1 0 0 1 1 1 0
1 0 1 0 1 0 0
1 0 1 0 1 1 0
1 0 1 1 1 0 0
1 0 1 1 1 1 0
1 1 0 0 1 0 0
1 1 0 0 1 1 1
1 1 0 1 1 0 0
1 1 0 1 1 1 1
1 1 1 0 1 0 0
1 1 1 0 1 1 1
1 1 1 1 1 0 0
1 1 1 1 1 1 1
0 0 0 0 2 0 0
0 0 0 0 2 1 0
0 0 0 1 2 0 0
0 0 0 1 2 1 0
0 0 1 0 2 0 0
0 0 1 0 2 1 1
0 0 1 1 2 0 0
0 0 1 1 2 1 1
0 1 0 0 2 0 0
0 1 0 0 2 1 0
0 1 0 1 2 0 0
0 1 0 1 2 1 0
0 1 1 0 2 0 0
0 1 1 0 2 1 1
0 1 1 1 2 0 0
0 1 1 1 2 1 1
1 0 0 0 2 0 0
1 0 0 0 2 1 0
1 0 0 1 2 0 0
1 0 0 1 2 1 0
1 0 1 0 2 0 0
1 0 1 0 2 1 1
1 0 1 1 2 0 0
1 0 1 1 2 1 1
1 1 0 0 2 0 0
1 1 0 0 2 1 0
1 1 0 1 2 0 0
1 1 0 1 2 1 0
1 1 1 0 2 0 0
1 1 1 0 2 1 1
1 1 1 1 2 0 0
1 1 1 1 2 1 1
0 0 0 0 3 0 0
0 0 0 0 3 1 0
0 0 0 1 3 0 0
0 0 0 1 3 1 1
0 0 1 0 3 0 0
0 0 1 0 3 1 0
0 0 1 1 3 0 0
0 0 1 1 3 1 1
0 1 0 0 3 0 0
0 1 0 0 3 1 0
0 1 0 1 3 0 0
0 1 0 1 3 1 1
0 1 1 0 3 0 0
0 1 1 0 3 1 0
0 1 1 1 3 0 0
0 1 1 1 3 1 1
1 0 0 0 3 0 0
1 0 0 0 3 1 0
1 0 0 1 3 0 0
1 0 0 1 3 1 1
1 0 1 0 3 0 0
1 0 1 0 3 1 0
1 0 1 1 3 0 0
1 0 1 1 3 1 1
1 1 0 0 3 0 0
1 1 0 0 3 1 0
1 1 0 1 3 0 0
1 1 0 1 3 1 1
1 1 1 0 3 0 0
1 1 1 0 3 1 0
1 1 1 1 3 0 0
1 1 1 1 3 1 1
0 0 0 0 4 0 0
0 0 0 0 4 1 1
0 0 0 1 4 0 0
0 0 0 1 4 1 1
0 0 1 0 4 0 0
0 0 1 0 4 1 1
0 0 1 1 4 0 0
0 0 1 1 4 1 1
0 1 0 0 4 0 0
0 1 0 0 4 1 1
0 1 0 1 4 0 0
0 1 0 1 4 1 1
0 1 1 0 4 0 0
0 1 1 0 4 1 1
0 1 1 1 4 0 0
0 1 1 1 4 1 1
1 0 0 0 4 0 0
1 0 0 0 4 1 0
1 0 0 1 4 0 0
1 0 0 1 4 1 0
1 0 1 0 4 0 0
1 0 1 0 4 1 0
1 0 1 1 4 0 0
1 0 1 1 4 1 0
1 1 0 0 4 0 0
1 1 0 0 4 1 0
1 1 0 1 4 0 0
1 1 0 1 4 1 0
1 1 1 0 4 0 0
1 1 1 0 4 1 0
1 1 1 1 4 0 0
1 1 1 1 4 1 0
0 0 0 0 5 0 0
0 0 0 0 5 1 1
0 0 0 1 5 0 0
0 0 0 1 5 1 1
0 0 1 0 5 0 0
0 0 1 0 5 1 1
0 0 1 1 5 0 0
0 0 1 1 5 1 1
0 1 0 0 5 0 0
0 1 0 0 5 1 0
0 1 0 1 5 0 0
0 1 0 1 5 1 0
0 1 1 0 5 0 0
0 1 1 0 5 1 0
0 1 1 1 5 0 0
0 1 1 1 5 1 0
1 0 0 0 5 0 0
1 0 0 0 5 1 1
1 0 0 1 5 0 0
1 0 0 1 5 1 1
1 0 1 0 5 0 0
1 0 1 0 5 1 1
1 0 1 1 5 0 0
1 0 1 1 5 1 1
1 1 0 0 5 0 0
1 1 0 0 5 1 0
1 1 0 1 5 0 0
1 1 0 1 5 1 0
1 1 1 0 5 0 0
1 1 1 0 5 1 0
1 1 1 1 5 0 0
1 1 1 1 5 1 0
0 0 0 0 6 0 0
0 0 0 0 6 1 1
0 0 0 1 6 0 0
0 0 0 1 6 1 1
0 0 1 0 6 0 0
0 0 1 0 6 1 0
0 0 1 1 6 0 0
0 0 1 1 6 1 0
0 1 0 0 6 0 0
0 1 0 0 6 1 1
0 1 0 1 6 0 0
0 1 0 1 6 1 1
0 1 1 0 6 0 0
0 1 1 0 6 1 0
0 1 1 1 6 0 0
0 1 1 1 6 1 0
1 0 0 0 6 0 0
1 0 0 0 6 1 1
1 0 0 1 6 0 0
1 0 0 1 6 1 1
1 0 1 0 6 0 0
1 0 1 0 6 1 0
1 0 1 1 6 0 0
1 0 1 1 6 1 0
1 1 0 0 6 0 0
1 1 0 0 6 1 1
1 1 0 1 6 0 0
1 1 0 1 6 1 1
1 1 1 0 6 0 0
1 1 1 0 6 1 0
1 1 1 1 6 0 0
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*/
