// Digital circuit sc_control_flags.dig as structural Verilog
module sc_control_flags (
  input  INT_EN_IN,
  input  HALT_IN,
  input  INT_REQ,
  input  INT_VEC_0,
  input  INT_VEC_1,
  input  INT_VEC_2,
  input  CLK,
  output [23:0] INT_VECTOR,
  output INT_EN,
  output HALTED,
  output INT_GATE,
  output CLK_GATED
);

  wire _1Y;

  _7474 _7474_1 (
    .pin1(1'b1), .pin2(INT_EN_IN), .pin3(CLK), .pin4(1'b1), .pin5(INT_EN), .pin7(1'b0), .pin9(HALTED),
    .pin10(1'b1), .pin11(CLK), .pin12(HALT_IN), .pin13(1'b1), .pin14(1'b1));  // open: pin6, pin8
  and and_1 (INT_GATE, INT_REQ, INT_EN);
  not not_1 (_1Y, HALTED);
  and and_2 (CLK_GATED, CLK, _1Y);

  assign INT_VECTOR = {{18{1'b0}}, INT_VEC_2, INT_VEC_1, INT_VEC_0, 3'b000};
endmodule

/* Test case sc-control-flags-tests:
CLK INT_EN_IN HALT_IN INT_REQ INT_VEC_0 INT_VEC_1 INT_VEC_2 INT_EN HALTED INT_GATE CLK_GATED INT_VECTOR

# Interrupt enable + halt + INT_GATE + CLK_GATED + INT_VECTOR
# C = rising clock edge on 7474; exhaustive sections use CLK=1 to verify FFs


# 1. Plan milestone — latch INT_EN

0 1 0 0 0 0 0 x x 0 0 0x000000
C 1 0 0 0 0 0 1 0 0 0 0x000000
0 1 0 0 0 0 0 1 0 0 0 0x000000

# 2. INT_GATE = INT_REQ AND INT_EN

0 1 0 1 0 0 0 1 0 1 0 0x000000
0 1 0 0 0 0 0 1 0 0 0 0x000000
C 0 0 1 0 0 0 0 0 0 0 0x000000
0 0 0 1 0 0 0 0 0 0 0 0x000000
0 0 0 1 0 0 0 0 0 0 0 0x000000

# 3. Halt — HALTED=1, CLK_GATED=0 when CLK=1

C 1 1 0 0 0 0 1 1 0 0 0x000000
0 1 1 0 0 0 0 1 1 0 0 0x000000
1 1 1 0 0 0 0 1 1 0 0 0x000000

# 4. Release halt — two clocks to clear HALTED, then CLK_GATED=1

C 1 0 0 0 0 0 1 1 0 0 0x000000
0 1 0 0 0 0 0 1 1 0 0 0x000000
C 1 0 0 0 0 0 1 0 0 0 0x000000
0 1 0 0 0 0 0 1 0 0 0 0x000000
1 1 0 0 0 0 0 1 0 0 1 0x000000

# 5. INT_VECTOR encoding (bits 3–5 = vec × 8)

0 1 0 0 1 1 0 1 0 0 0 0x000018
0 1 0 0 1 1 1 1 0 0 0 0x000038
0 1 0 0 0 0 0 1 0 0 0 0x000000
0 1 0 0 1 0 0 1 0 0 0 0x000008
0 1 0 0 0 1 0 1 0 0 0 0x000010
0 1 0 0 0 0 1 1 0 0 0 0x000020

# 6. INT_EN clears on clock when INT_EN_IN=0

C 0 0 0 0 0 0 0 0 0 0 0x000000
0 0 0 0 0 0 0 0 0 0 0 0x000000
0 0 0 0 0 0 0 0 0 0 0 0x000000

# 7. HALT_IN sequence — set then clear HALTED

C 1 1 0 0 0 0 1 1 0 0 0x000000
0 1 1 0 0 0 0 1 1 0 0 0x000000
C 1 0 0 0 0 0 1 0 0 0 0x000000
0 1 0 0 0 0 0 1 0 0 0 0x000000
0 1 0 0 0 0 0 1 0 0 0 0x000000

# 8. Re-latch INT_EN=1 for INT_GATE checks

C 1 0 0 0 0 0 1 0 0 0 0x000000
0 1 0 0 0 0 0 1 0 0 0 0x000000
0 1 0 0 0 0 0 1 0 0 0 0x000000
0 1 0 1 0 0 0 1 0 1 0 0x000000

# 9. All 8 INT_VECTOR combinations (steady-state)

0 1 0 0 0 0 0 1 0 0 0 0x000000
0 1 0 0 1 0 0 1 0 0 0 0x000008
0 1 0 0 0 1 0 1 0 0 0 0x000010
0 1 0 0 1 1 0 1 0 0 0 0x000018
0 1 0 0 0 0 1 1 0 0 0 0x000020
0 1 0 0 1 0 1 1 0 0 0 0x000028
0 1 0 0 0 1 1 1 0 0 0 0x000030
0 1 0 0 1 1 1 1 0 0 0 0x000038

# 10. CLK_GATED low when CLK=0 (halt released)

C 1 0 0 0 0 0 1 0 0 0 0x000000
0 1 0 0 0 0 0 1 0 0 0 0x000000
0 1 0 0 0 0 0 1 0 0 0 0x000000
1 1 0 0 0 0 0 1 0 0 1 0x000000

# 11. Halt blocks gated clock even if CLK held high

C 1 1 0 0 0 0 1 x 0 0 0x000000
0 1 1 0 0 0 0 1 x 0 0 0x000000
1 1 1 0 0 0 0 1 1 0 0 0x000000

# 12. HALTED=1, INT_GATE and vector while halted

C 1 1 0 0 0 0 1 x 0 0 0x000000
0 1 1 0 0 0 0 1 x 0 0 0x000000
1 1 1 1 1 1 1 1 1 1 0 0x000038

# 13. Release halt then hold INT_EN across extra clocks

C 1 0 0 0 0 0 1 1 0 0 0x000000
0 1 0 0 0 0 0 1 1 0 0 0x000000
C 1 0 0 0 0 0 1 x 0 0 0x000000
0 1 0 0 0 0 0 1 x 0 0 0x000000
C 1 0 0 0 0 0 1 0 0 0 0x000000
0 1 0 0 0 0 0 1 0 0 0 0x000000
C 1 0 0 0 0 0 1 0 0 0 0x000000
0 1 0 0 0 0 0 1 0 0 0 0x000000
1 1 0 0 0 0 0 1 0 0 1 0x000000

# 14. Vector stable while toggling unrelated inputs

0 1 0 1 1 0 1 1 0 1 0 0x000028
0 0 1 0 1 0 1 1 0 0 0 0x000028

# 15. Exhaustive — all 4 latch input combinations (C pulse + CLK=1 verify)

C 0 0 0 0 0 0 x x 0 0 0x000000
1 0 0 0 0 0 0 0 0 0 1 0x000000
C 0 1 0 0 0 0 x x 0 0 0x000000
1 0 1 0 0 0 0 0 1 0 0 0x000000
C 1 0 0 0 0 0 x x 0 0 0x000000
1 1 0 0 0 0 0 1 0 0 1 0x000000
C 1 1 0 0 0 0 x x 0 0 0x000000
1 1 1 0 0 0 0 1 1 0 0 0x000000

# 16. Exhaustive — INT_GATE truth table at CLK=0

C 0 0 0 0 0 0 x x 0 0 0x000000
1 0 0 0 0 0 0 0 0 0 1 0x000000
0 0 0 0 0 0 0 x x 0 0 0x000000
0 0 0 1 0 0 0 x x 0 0 0x000000
C 1 0 0 0 0 0 x x 0 0 0x000000
1 1 0 0 0 0 0 1 0 0 1 0x000000
0 1 0 0 0 0 0 x x 0 0 0x000000
0 1 0 1 0 0 0 x x 1 0 0x000000

# 17. Exhaustive — CLK_GATED truth table (CLK × HALTED)

C 1 0 0 0 0 0 x x 0 0 0x000000
1 1 0 0 0 0 0 1 0 0 1 0x000000
0 1 0 0 0 0 0 x x 0 0 0x000000
1 1 0 0 0 0 0 x x 0 1 0x000000
C 1 1 0 0 0 0 x x 0 0 0x000000
1 1 1 0 0 0 0 1 1 0 0 0x000000
0 1 1 0 0 0 0 x x 0 0 0x000000
1 1 1 0 0 0 0 x x 0 0 0x000000

# 18. Exhaustive — INT_VECTOR all 8 encodings at CLK=0

C 1 0 0 0 0 0 x x 0 0 0x000000
1 1 0 0 0 0 0 1 0 0 1 0x000000
0 1 0 0 0 0 0 x x 0 0 0x000000
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*/
