// Digital circuit sc_flags_save.dig as structural Verilog
module sc_flags_save (
  input  INT_GATE,
  input  FLAG_N,
  input  FLAG_C,
  input  FLAG_Z,
  input  FLAG_O,
  output [3:0] FLAGS_SAVE
);

  _7474 _7474_1 (
    .pin1(1'b1), .pin2(FLAG_Z), .pin3(INT_GATE), .pin4(1'b1), .pin5(FLAGS_SAVE[0]), .pin7(1'b0),
    .pin9(FLAGS_SAVE[1]), .pin10(1'b1), .pin11(INT_GATE), .pin12(FLAG_C), .pin13(1'b1), .pin14(1'b1));  // open: pin6, pin8
  _7474 _7474_2 (
    .pin1(1'b1), .pin2(FLAG_N), .pin3(INT_GATE), .pin4(1'b1), .pin5(FLAGS_SAVE[2]), .pin7(1'b0),
    .pin9(FLAGS_SAVE[3]), .pin10(1'b1), .pin11(INT_GATE), .pin12(FLAG_O), .pin13(1'b1), .pin14(1'b1));  // open: pin6, pin8

  // Other names for the same wires on the sheet: FLAGS_SAVE_C = FLAGS_SAVE[1]; FLAGS_SAVE_N = FLAGS_SAVE[2];
  //   FLAGS_SAVE_O = FLAGS_SAVE[3]; FLAGS_SAVE_Z = FLAGS_SAVE[0]
endmodule
