// Digital circuit sc_mux24_2to1.dig as structural Verilog
module sc_mux24_2to1 (
  input  [23:0] B,
  input  [23:0] A,
  input  SEL,
  output [23:0] Y
);

  wire _74541_2_pin1, _74541_2_pin19, _74541_4_pin1, _74541_4_pin19, _74541_6_pin1, _74541_6_pin19;

  _74541 _74541_1 (
    .pin1(SEL), .pin2(A[0]), .pin3(A[1]), .pin4(A[2]), .pin5(A[3]), .pin6(A[4]), .pin7(A[5]), .pin8(A[6]),
    .pin9(A[7]), .pin10(1'b0), .pin11(Y[7]), .pin12(Y[6]), .pin13(Y[5]), .pin14(Y[4]), .pin15(Y[3]),
    .pin16(Y[2]), .pin17(Y[1]), .pin18(Y[0]), .pin19(SEL), .pin20(1'b1));
  _74541 _74541_2 (
    .pin1(_74541_2_pin1), .pin2(B[0]), .pin3(B[1]), .pin4(B[2]), .pin5(B[3]), .pin6(B[4]), .pin7(B[5]),
    .pin8(B[6]), .pin9(B[7]), .pin10(1'b0), .pin11(Y[7]), .pin12(Y[6]), .pin13(Y[5]), .pin14(Y[4]),
    .pin15(Y[3]), .pin16(Y[2]), .pin17(Y[1]), .pin18(Y[0]), .pin19(_74541_2_pin19), .pin20(1'b1));
  not not_1 (_74541_2_pin1, SEL);
  not not_2 (_74541_2_pin19, SEL);
  _74541 _74541_3 (
    .pin1(SEL), .pin2(A[8]), .pin3(A[9]), .pin4(A[10]), .pin5(A[11]), .pin6(A[12]), .pin7(A[13]),
    .pin8(A[14]), .pin9(A[15]), .pin10(1'b0), .pin11(Y[15]), .pin12(Y[14]), .pin13(Y[13]), .pin14(Y[12]),
    .pin15(Y[11]), .pin16(Y[10]), .pin17(Y[9]), .pin18(Y[8]), .pin19(SEL), .pin20(1'b1));
  _74541 _74541_4 (
    .pin1(_74541_4_pin1), .pin2(B[8]), .pin3(B[9]), .pin4(B[10]), .pin5(B[11]), .pin6(B[12]), .pin7(B[13]),
    .pin8(B[14]), .pin9(B[15]), .pin10(1'b0), .pin11(Y[15]), .pin12(Y[14]), .pin13(Y[13]), .pin14(Y[12]),
    .pin15(Y[11]), .pin16(Y[10]), .pin17(Y[9]), .pin18(Y[8]), .pin19(_74541_4_pin19), .pin20(1'b1));
  not not_3 (_74541_4_pin1, SEL);
  not not_4 (_74541_4_pin19, SEL);
  _74541 _74541_5 (
    .pin1(SEL), .pin2(A[16]), .pin3(A[17]), .pin4(A[18]), .pin5(A[19]), .pin6(A[20]), .pin7(A[21]),
    .pin8(A[22]), .pin9(A[23]), .pin10(1'b0), .pin11(Y[23]), .pin12(Y[22]), .pin13(Y[21]), .pin14(Y[20]),
    .pin15(Y[19]), .pin16(Y[18]), .pin17(Y[17]), .pin18(Y[16]), .pin19(SEL), .pin20(1'b1));
  _74541 _74541_6 (
    .pin1(_74541_6_pin1), .pin2(B[16]), .pin3(B[17]), .pin4(B[18]), .pin5(B[19]), .pin6(B[20]), .pin7(B[21]),
    .pin8(B[22]), .pin9(B[23]), .pin10(1'b0), .pin11(Y[23]), .pin12(Y[22]), .pin13(Y[21]), .pin14(Y[20]),
    .pin15(Y[19]), .pin16(Y[18]), .pin17(Y[17]), .pin18(Y[16]), .pin19(_74541_6_pin19), .pin20(1'b1));
  not not_5 (_74541_6_pin1, SEL);
  not not_6 (_74541_6_pin19, SEL);

  // Other names for the same wires on the sheet: A_0 = A[0]; A_1 = A[1]; A_2 = A[2]; A_3 = A[3]; A_4 = A[4];
  //   A_5 = A[5]; A_6 = A[6]; A_7 = A[7]; A_8 = A[8]; A_9 = A[9]; A_10 = A[10]; A_11 = A[11]; A_12 = A[12];
  //   A_13 = A[13]; A_14 = A[14]; A_15 = A[15]; A_16 = A[16]; A_17 = A[17]; A_18 = A[18]; A_19 = A[19]; A_20 = A[20];
  //   A_21 = A[21]; A_22 = A[22]; A_23 = A[23]; B_0 = B[0]; B_1 = B[1]; B_2 = B[2]; B_3 = B[3]; B_4 = B[4];
  //   B_5 = B[5]; B_6 = B[6]; B_7 = B[7]; B_8 = B[8]; B_9 = B[9]; B_10 = B[10]; B_11 = B[11]; B_12 = B[12];
  //   B_13 = B[13]; B_14 = B[14]; B_15 = B[15]; B_16 = B[16]; B_17 = B[17]; B_18 = B[18]; B_19 = B[19]; B_20 = B[20];
  //   B_21 = B[21]; B_22 = B[22]; B_23 = B[23]; Y_0 = Y[0]; Y_1 = Y[1]; Y_2 = Y[2]; Y_3 = Y[3]; Y_4 = Y[4];
  //   Y_5 = Y[5]; Y_6 = Y[6]; Y_7 = Y[7]; Y_8 = Y[8]; Y_9 = Y[9]; Y_10 = Y[10]; Y_11 = Y[11]; Y_12 = Y[12];
  //   Y_13 = Y[13]; Y_14 = Y[14]; Y_15 = Y[15]; Y_16 = Y[16]; Y_17 = Y[17]; Y_18 = Y[18]; Y_19 = Y[19]; Y_20 = Y[20];
  //   Y_21 = Y[21]; Y_22 = Y[22]; Y_23 = Y[23]

  // Notes on the sheet:
  //   B: default 99864
  //   A: default 6547
endmodule

/* Test case sc-mux24-tests:
SEL A B Y

# 24-bit 2:1 mux (6×74157), combinational — SEL=0 → A, SEL=1 → B


# 1. Plan milestone cases

0 0xaaaaaa 0x555555 0xaaaaaa
1 0xaaaaaa 0x555555 0x555555

# 2. Toggle SEL (combinational, no clock)

0 0x123456 0xfedcba 0x123456
1 0x123456 0xfedcba 0xfedcba
0 0x123456 0xfedcba 0x123456

# 3. Equal inputs — either select is valid

0 0x00ff00 0x00ff00 0x00ff00
1 0x00ff00 0x00ff00 0x00ff00
0 0xffffff 0xffffff 0xffffff
1 0xffffff 0xffffff 0xffffff

# 4. Zero / max extremes

0 0x000000 0xffffff 0x000000
1 0x000000 0xffffff 0xffffff
0 0xffffff 0x000000 0xffffff
1 0xffffff 0x000000 0x000000

# 5. Assembly-style address sources (layer 1 / layer 2)

0 0x001000 0x001010 0x001000
1 0x001000 0x001010 0x001010
0 0x001010 0x002000 0x001010
1 0x001010 0x002000 0x002000

# 6. Walking-one on A (B=0) — select A

0 0x000001 0x000000 0x000001
0 0x000002 0x000000 0x000002
0 0x000004 0x000000 0x000004
0 0x000008 0x000000 0x000008
0 0x000010 0x000000 0x000010
0 0x000020 0x000000 0x000020
0 0x000040 0x000000 0x000040
0 0x000080 0x000000 0x000080
0 0x000100 0x000000 0x000100
0 0x000200 0x000000 0x000200
0 0x000400 0x000000 0x000400
0 0x000800 0x000000 0x000800
0 0x001000 0x000000 0x001000
0 0x002000 0x000000 0x002000
0 0x004000 0x000000 0x004000
0 0x008000 0x000000 0x008000
0 0x010000 0x000000 0x010000
0 0x020000 0x000000 0x020000
0 0x040000 0x000000 0x040000
0 0x080000 0x000000 0x080000
0 0x100000 0x000000 0x100000
0 0x200000 0x000000 0x200000
0 0x400000 0x000000 0x400000
0 0x800000 0x000000 0x800000

# 7. Walking-one on B (A=0) — select B

1 0x000000 0x000001 0x000001
1 0x000000 0x000002 0x000002
1 0x000000 0x000004 0x000004
1 0x000000 0x000008 0x000008
1 0x000000 0x000010 0x000010
1 0x000000 0x000020 0x000020
1 0x000000 0x000040 0x000040
1 0x000000 0x000080 0x000080
1 0x000000 0x000100 0x000100
1 0x000000 0x000200 0x000200
1 0x000000 0x000400 0x000400
1 0x000000 0x000800 0x000800
1 0x000000 0x001000 0x001000
1 0x000000 0x002000 0x002000
1 0x000000 0x004000 0x004000
1 0x000000 0x008000 0x008000
1 0x000000 0x010000 0x010000
1 0x000000 0x020000 0x020000
1 0x000000 0x040000 0x040000
1 0x000000 0x080000 0x080000
1 0x000000 0x100000 0x100000
1 0x000000 0x200000 0x200000
1 0x000000 0x400000 0x400000
1 0x000000 0x800000 0x800000

# 8. Per-nibble independent patterns

0 0x00000a 0x000005 0x00000a
1 0x00000a 0x000005 0x000005
0 0x0000a0 0x000050 0x0000a0
1 0x0000a0 0x000050 0x000050
0 0x000a00 0x000500 0x000a00
1 0x000a00 0x000500 0x000500
0 0x00a000 0x005000 0x00a000
1 0x00a000 0x005000 0x005000
0 0x0a0000 0x050000 0x0a0000
1 0x0a0000 0x050000 0x050000
0 0xa00000 0x500000 0xa00000
1 0xa00000 0x500000 0x500000

# 9. Checkerboard and inverted checkerboard

0 0xaaaaaa 0x555555 0xaaaaaa
1 0xaaaaaa 0x555555 0x555555
0 0x555555 0xaaaaaa 0x555555
1 0x555555 0xaaaaaa 0xaaaaaa
0 0xf0f0f0 0x0f0f0f 0xf0f0f0
1 0xf0f0f0 0x0f0f0f 0x0f0f0f
0 0xff00ff 0x00ff00 0xff00ff
1 0xff00ff 0x00ff00 0x00ff00

# 10. Byte-lane isolation (single byte differs)

0 0xabcdef 0xabcd99 0xabcdef
1 0xabcdef 0xabcd99 0xabcd99
0 0xabcdef 0xab99ef 0xabcdef
1 0xabcdef 0xab99ef 0xab99ef
0 0xabcdef 0x99cdef 0xabcdef
1 0xabcdef 0x99cdef 0x99cdef
0 0xabcdef 0x99abcdef 0xabcdef
1 0xabcdef 0x99abcdef 0xabcdef
0 0xabcdef 0x9900abcdef 0xabcdef
1 0xabcdef 0x9900abcdef 0xabcdef
0 0xabcdef 0x990000abcdef 0xabcdef
1 0xabcdef 0x990000abcdef 0xabcdef

# 11. Systematic grid on low/mid/high 12-bit fields

0 0x000000 0x000000 0x000000
1 0x000000 0x000000 0x000000
0 0x000000 0x00000f 0x000000
1 0x000000 0x00000f 0x00000f
0 0x000000 0x0000f0 0x000000
1 0x000000 0x0000f0 0x0000f0
0 0x000000 0x000f00 0x000000
1 0x000000 0x000f00 0x000f00
0 0x000000 0x00f000 0x000000
1 0x000000 0x00f000 0x00f000
0 0x000000 0x0f0000 0x000000
1 0x000000 0x0f0000 0x0f0000
0 0x000000 0xffffff 0x000000
1 0x000000 0xffffff 0xffffff
0 0x00000f 0x000000 0x00000f
1 0x00000f 0x000000 0x000000
0 0x00000f 0x00000f 0x00000f
1 0x00000f 0x00000f 0x00000f
0 0x00000f 0x0000f0 0x00000f
1 0x00000f 0x0000f0 0x0000f0
0 0x00000f 0x000f00 0x00000f
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*/
