// Digital circuit sc_pc_counter.dig as structural Verilog
module sc_pc_counter (
  input  nSR,
  input  clk,
  input  nPE,
  input  [23:0] D,
  input  pc_en,
  output [23:0] Q
);

  wire tc1, tc2, tc3, tc4, tc5;

  _74163 U1 (
    .pin1(nSR), .pin2(clk), .pin3(D[0]), .pin4(D[1]), .pin5(D[2]), .pin6(D[3]), .pin7(pc_en), .pin8(1'b0),
    .pin9(nPE), .pin10(pc_en), .pin11(Q[3]), .pin12(Q[2]), .pin13(Q[1]), .pin14(Q[0]), .pin15(tc1),
    .pin16(1'b1));
  _74163 U4 (
    .pin1(nSR), .pin2(clk), .pin3(D[12]), .pin4(D[13]), .pin5(D[14]), .pin6(D[15]), .pin7(tc3), .pin8(1'b0),
    .pin9(nPE), .pin10(tc3), .pin11(Q[15]), .pin12(Q[14]), .pin13(Q[13]), .pin14(Q[12]), .pin15(tc4),
    .pin16(1'b1));
  _74163 U2 (
    .pin1(nSR), .pin2(clk), .pin3(D[4]), .pin4(D[5]), .pin5(D[6]), .pin6(D[7]), .pin7(tc1), .pin8(1'b0),
    .pin9(nPE), .pin10(tc1), .pin11(Q[7]), .pin12(Q[6]), .pin13(Q[5]), .pin14(Q[4]), .pin15(tc2), .pin16(1'b1));
  _74163 U5 (
    .pin1(nSR), .pin2(clk), .pin3(D[16]), .pin4(D[17]), .pin5(D[18]), .pin6(D[19]), .pin7(tc4), .pin8(1'b0),
    .pin9(nPE), .pin10(tc4), .pin11(Q[19]), .pin12(Q[18]), .pin13(Q[17]), .pin14(Q[16]), .pin15(tc5),
    .pin16(1'b1));
  _74163 U3 (
    .pin1(nSR), .pin2(clk), .pin3(D[8]), .pin4(D[9]), .pin5(D[10]), .pin6(D[11]), .pin7(tc2), .pin8(1'b0),
    .pin9(nPE), .pin10(tc2), .pin11(Q[11]), .pin12(Q[10]), .pin13(Q[9]), .pin14(Q[8]), .pin15(tc3),
    .pin16(1'b1));
  _74163 U6 (
    .pin1(nSR), .pin2(clk), .pin3(D[20]), .pin4(D[21]), .pin5(D[22]), .pin6(D[23]), .pin7(tc5), .pin8(1'b0),
    .pin9(nPE), .pin10(tc5), .pin11(Q[23]), .pin12(Q[22]), .pin13(Q[21]), .pin14(Q[20]), .pin16(1'b1));  // open: pin15

  // Other names for the same wires on the sheet: D_0 = D[0]; D_1 = D[1]; D_2 = D[2]; D_3 = D[3]; D_4 = D[4];
  //   D_5 = D[5]; D_6 = D[6]; D_7 = D[7]; D_8 = D[8]; D_9 = D[9]; D_10 = D[10]; D_11 = D[11]; D_12 = D[12];
  //   D_13 = D[13]; D_14 = D[14]; D_15 = D[15]; D_16 = D[16]; D_17 = D[17]; D_18 = D[18]; D_19 = D[19]; D_20 = D[20];
  //   D_21 = D[21]; D_22 = D[22]; D_23 = D[23]; Q_0 = Q[0]; Q_1 = Q[1]; Q_2 = Q[2]; Q_3 = Q[3]; Q_4 = Q[4];
  //   Q_5 = Q[5]; Q_6 = Q[6]; Q_7 = Q[7]; Q_8 = Q[8]; Q_9 = Q[9]; Q_10 = Q[10]; Q_11 = Q[11]; Q_12 = Q[12];
  //   Q_13 = Q[13]; Q_14 = Q[14]; Q_15 = Q[15]; Q_16 = Q[16]; Q_17 = Q[17]; Q_18 = Q[18]; Q_19 = Q[19]; Q_20 = Q[20];
  //   Q_21 = Q[21]; Q_22 = Q[22]; Q_23 = Q[23]
endmodule

/* Test case sc-pc-counter-tests:
clk ~SR ~PE D Q

# 24-bit synchronous counter (6×74163)
# ~PE=1 count, ~PE=0 parallel load from D; C = rising clock edge


# 1. Sync reset from unknown

0 1 1 0x000000 0x000000
C 0 1 0x000000 0x000000
0 1 1 0x000000 0x000000

# 2. Count 0 → 1 → 2

C 1 1 0x000000 0x000001
0 1 1 0x000000 0x000001
C 1 1 0x000000 0x000002
0 1 1 0x000000 0x000002

# 3. Nibble carry 0x0E → 0x0F → 0x10

C 1 1 0x000000 0x000003
0 1 1 0x000000 0x000003
C 1 1 0x000000 0x000004
0 1 1 0x000000 0x000004
C 1 1 0x000000 0x000005
0 1 1 0x000000 0x000005
C 1 1 0x000000 0x000006
0 1 1 0x000000 0x000006
C 1 1 0x000000 0x000007
0 1 1 0x000000 0x000007
C 1 1 0x000000 0x000008
0 1 1 0x000000 0x000008
C 1 1 0x000000 0x000009
0 1 1 0x000000 0x000009
C 1 1 0x000000 0x00000a
0 1 1 0x000000 0x00000a
C 1 1 0x000000 0x00000b
0 1 1 0x000000 0x00000b
C 1 1 0x000000 0x00000c
0 1 1 0x000000 0x00000c
C 1 1 0x000000 0x00000d
0 1 1 0x000000 0x00000d
C 1 1 0x000000 0x00000e
0 1 1 0x000000 0x00000e
C 1 1 0x000000 0x00000f
0 1 1 0x000000 0x00000f
C 1 1 0x000000 0x000010
0 1 1 0x000000 0x000010

# 4. Byte carry 0x00FE → 0x00FF → 0x0100

C 1 1 0x000000 0x000011
0 1 1 0x000000 0x000011
C 1 1 0x000000 0x000012
0 1 1 0x000000 0x000012
C 1 1 0x000000 0x000013
0 1 1 0x000000 0x000013
C 1 1 0x000000 0x000014
0 1 1 0x000000 0x000014
C 1 1 0x000000 0x000015
0 1 1 0x000000 0x000015
C 1 1 0x000000 0x000016
0 1 1 0x000000 0x000016
C 1 1 0x000000 0x000017
0 1 1 0x000000 0x000017
C 1 1 0x000000 0x000018
0 1 1 0x000000 0x000018
C 1 1 0x000000 0x000019
0 1 1 0x000000 0x000019
C 1 1 0x000000 0x00001a
0 1 1 0x000000 0x00001a
C 1 1 0x000000 0x00001b
0 1 1 0x000000 0x00001b
C 1 1 0x000000 0x00001c
0 1 1 0x000000 0x00001c
C 1 1 0x000000 0x00001d
0 1 1 0x000000 0x00001d
C 1 1 0x000000 0x00001e
0 1 1 0x000000 0x00001e
C 1 1 0x000000 0x00001f
0 1 1 0x000000 0x00001f
C 1 1 0x000000 0x000020
0 1 1 0x000000 0x000020
C 1 1 0x000000 0x000021
0 1 1 0x000000 0x000021
C 1 1 0x000000 0x000022
0 1 1 0x000000 0x000022
C 1 1 0x000000 0x000023
0 1 1 0x000000 0x000023
C 1 1 0x000000 0x000024
0 1 1 0x000000 0x000024
C 1 1 0x000000 0x000025
0 1 1 0x000000 0x000025
C 1 1 0x000000 0x000026
0 1 1 0x000000 0x000026
C 1 1 0x000000 0x000027
0 1 1 0x000000 0x000027
C 1 1 0x000000 0x000028
0 1 1 0x000000 0x000028
C 1 1 0x000000 0x000029
0 1 1 0x000000 0x000029
C 1 1 0x000000 0x00002a
0 1 1 0x000000 0x00002a
C 1 1 0x000000 0x00002b
0 1 1 0x000000 0x00002b
C 1 1 0x000000 0x00002c
0 1 1 0x000000 0x00002c
C 1 1 0x000000 0x00002d
0 1 1 0x000000 0x00002d
C 1 1 0x000000 0x00002e
0 1 1 0x000000 0x00002e
C 1 1 0x000000 0x00002f
0 1 1 0x000000 0x00002f
C 1 1 0x000000 0x000030
0 1 1 0x000000 0x000030
C 1 1 0x000000 0x000031
0 1 1 0x000000 0x000031
C 1 1 0x000000 0x000032
0 1 1 0x000000 0x000032
C 1 1 0x000000 0x000033
0 1 1 0x000000 0x000033
C 1 1 0x000000 0x000034
0 1 1 0x000000 0x000034
C 1 1 0x000000 0x000035
0 1 1 0x000000 0x000035
C 1 1 0x000000 0x000036
0 1 1 0x000000 0x000036
C 1 1 0x000000 0x000037
0 1 1 0x000000 0x000037
C 1 1 0x000000 0x000038
0 1 1 0x000000 0x000038
C 1 1 0x000000 0x000039
0 1 1 0x000000 0x000039
C 1 1 0x000000 0x00003a
0 1 1 0x000000 0x00003a
C 1 1 0x000000 0x00003b
0 1 1 0x000000 0x00003b
C 1 1 0x000000 0x00003c
0 1 1 0x000000 0x00003c
C 1 1 0x000000 0x00003d
0 1 1 0x000000 0x00003d
C 1 1 0x000000 0x00003e
0 1 1 0x000000 0x00003e
C 1 1 0x000000 0x00003f
0 1 1 0x000000 0x00003f
C 1 1 0x000000 0x000040
0 1 1 0x000000 0x000040
C 1 1 0x000000 0x000041
0 1 1 0x000000 0x000041
C 1 1 0x000000 0x000042
0 1 1 0x000000 0x000042
C 1 1 0x000000 0x000043
0 1 1 0x000000 0x000043
C 1 1 0x000000 0x000044
0 1 1 0x000000 0x000044
C 1 1 0x000000 0x000045
0 1 1 0x000000 0x000045
C 1 1 0x000000 0x000046
0 1 1 0x000000 0x000046
C 1 1 0x000000 0x000047
0 1 1 0x000000 0x000047
C 1 1 0x000000 0x000048
0 1 1 0x000000 0x000048
C 1 1 0x000000 0x000049
0 1 1 0x000000 0x000049
C 1 1 0x000000 0x00004a
0 1 1 0x000000 0x00004a
C 1 1 0x000000 0x00004b
0 1 1 0x000000 0x00004b
C 1 1 0x000000 0x00004c
0 1 1 0x000000 0x00004c
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*/
