// Digital circuit sequencer.dig as structural Verilog
module sequencer (
  input  reset,
  input  [1:0] cycles,
  input  CLK,
  output FETCH,
  output EXECUTE,
  output MEM_WAIT
);

  wire CYC_DONE, CYC_MATCH_0, CYC_MATCH_1, nclk, NOT_CYC_DONE, NOT_RST, RESET_N, rst, SEQ_Q0, SEQ_Q0_N,
       SEQ_Q1, SEQ_Q1_N, SEQ_TC, UNUSED_Q2, UNUSED_Q3;

  not not_1 (nclk, CLK);
  _74163 _74163_1 (
    .pin1(RESET_N), .pin2(nclk), .pin3(1'b0), .pin4(1'b0), .pin5(1'b0), .pin6(1'b0), .pin7(1'b1),
    .pin8(1'b0), .pin9(1'b1), .pin10(1'b1), .pin11(UNUSED_Q3), .pin12(UNUSED_Q2), .pin13(SEQ_Q1),
    .pin14(SEQ_Q0), .pin15(SEQ_TC), .pin16(1'b1));
  not not_2 (NOT_RST, rst);
  not not_3 (NOT_CYC_DONE, CYC_DONE);
  and and_1 (RESET_N, NOT_RST, NOT_CYC_DONE);
  not not_4 (rst, reset);
  not not_5 (SEQ_Q0_N, SEQ_Q0);
  and and_2 (FETCH, SEQ_Q0_N, SEQ_Q1_N);
  not not_6 (SEQ_Q1_N, SEQ_Q1);
  and and_3 (MEM_WAIT, SEQ_Q0_N, SEQ_Q1);
  and and_4 (EXECUTE, SEQ_Q0, SEQ_Q1_N);
  and and_5 (CYC_DONE, CYC_MATCH_0, CYC_MATCH_1);
  xnor xnor_1 (CYC_MATCH_0, SEQ_Q0, cycles[0]);
  xnor xnor_2 (CYC_MATCH_1, SEQ_Q1, cycles[1]);

  // Other names for the same wires on the sheet: CYC0 = cycles[0]; CYC1 = cycles[1]
endmodule

/* Test case Sequencer Exhaustive:
reset cycles CLK FETCH EXECUTE MEM_WAIT

# Hold (reset=0): counter cleared — FETCH
0 0 0 1 0 0
0 0 C 1 0 0

# Release run (reset=1), cycles=0: single-phase (FETCH only)
1 0 0 1 0 0
1 0 C 1 0 0
1 0 C 1 0 0

# cycles=1: FETCH -> EXECUTE -> FETCH (2 phases)
1 1 0 1 0 0
1 1 C 0 1 0
1 1 C 1 0 0
1 1 C 0 1 0
1 1 C 1 0 0

# cycles=2: FETCH -> EXECUTE -> MEM_WAIT -> FETCH (3 phases)
1 2 0 1 0 0
1 2 C 0 1 0
1 2 C 0 0 1
1 2 C 1 0 0
1 2 C 0 1 0
1 2 C 0 0 1
1 2 C 1 0 0

# cycles=3: four counter steps (through RESERVED) — terminal reload at 11
1 3 0 1 0 0
1 3 C 0 1 0
1 3 C 0 0 1
1 3 C 0 0 0
1 3 C 1 0 0

# Run hold: reset=0 clears counter (FETCH); stays until run=1
1 2 C 0 1 0
0 2 0 0 1 0
0 2 C 1 0 0
1 2 C 0 1 0

# Mid-flight cycles change: was 2-phase (cy=1), switch to cy=2 at EXECUTE
0 0 C 1 0 0
1 1 C 0 1 0
1 2 0 0 1 0
1 2 C 0 0 1
1 2 C 1 0 0

# cycles=0 lock: never leaves FETCH (unused in ROM)
0 0 C 1 0 0
1 0 C 1 0 0
1 0 C 1 0 0
1 0 C 1 0 0
*/
