// Digital circuit shift-mul-control.dig as structural Verilog
module shift_mul_control (
  input  [8:0] op,
  output [1:0] shift_op,
  output mul_div_en,
  output pc_enc
);

  wire [7:4] shift_mul_control_d;

  ROM #(.bigEndian("true"), .AddrBits(9), .Bits(8)) shift_mul_control (
    .A(op), .sel(1'b1), .D({shift_mul_control_d, pc_enc, mul_div_en, shift_op}));

  // Other names for the same wires on the sheet: ir_opcode[8:0] = op

  // Notes on the sheet:
  //   op: default 48
  //   contents of shift_mul_control (hex, n*v repeats v):
  //   0,0,0,0,0,0,0,0,0,0,0,0,0,0,0,0,0,0,0,0,0,0,0,0,0,0,0,0,0,0,0,0,0,0,0,0,0,0,0,0,0,0,0,0,0,0,
  //   0,0,0,0,0,0,0,0,0,0,0,0,0,0,0,0,0,0,0,1,2,0,0,0,0,0,0,0,0,0,0,0,0,0,0,0,0,0,0,0,0,0,0,0,0,0,
  //   0,0,0,0,0,0,0,0,0,0,0,0,0,0,0,0,0,0,0,0,0,0,0,0,0,0,0,0,0,0,0,0,0,0,0,0,0,0,0,0,0,0,0,0,0,0,
  //   0,0,0,0,0,0,0,0,0,0,0,0,0,0,0,0,0,0,0,0,0,0,0,0,0,0,0,0,0,0,0,0,0,0,0,0,0,0,0,0,0,0,0,0,0,0,
  //   0,0,0,0,0,0,0,0,0,0,0,0,0,0,0,0,0,0,0,0,0,0,0,0,0,0,0,0,0,0,0,0,0,0,0,0,0,0,0,0,0,0,0,0,0,0,
  //   0,0,0,0,0,0,0,0,0,0,0,0,0,0,0,0,0,0,0,0,0,0,0,0,0,0,0,0,0,0,0,0,0,0,0,0,0,0,0,0,0,0,0,0,0,0,
  //   0,0,0,0,0,0,0,0,0,0,0,0,0,0,0,0,0,0,0,0,0,0,0,0,0,0,0,0,0,0,0,0,0,0,0,0,0,0,0,0,0,0,0,0,0,0,
  //   0,0,0,0,0,0,0,0,0,0,0,0,0,0,0,0,0,0,0,0,0,0,0,0,0,0,0,0,0,0,0,0,0,0,0,0,0,0,0,0,0,0,0,0,0,0,
  //   0,0,0,0,0,0,0,0,0,0,0,0,0,0,0,0,0,0,0,0,0,0,0,0,0,0,0,0,0,0,0,0,0,0,0,0,0,0,0,0,0,0,0,0,0,0,
  //   0,0,0,0,0,0,0,0,0,0,0,0,0,0,0,0,0,0,0,0,0,0,0,0,0,0,0,0,0,0,0,0,0,0,0,0,0,0,0,0,0,0,0,0,0,0,
  //   0,0,0,0,0,0,0,0,0,0,0,0,0,0,0,0,0,0,0,0,0,0,0,0,0,0,0,0,0,0,0,0,0,0,0,0,0,0,0,0,0,0,0,0,0,0,
  //   0,0,0,0,0,0
endmodule

/* Test case tomato-v1-burn:
op shift_op mul_div_en pc_enc
# NOP
0 0 0 0
# ADD
1 0 0 0
# SUB
2 0 0 0
# AND
3 0 0 0
# OR
4 0 0 0
# XOR
5 0 0 0
# MOV
6 0 0 0
# CMP
7 0 0 0
# ADDI
32 0 0 0
# ANDI
33 0 0 0
# ORI
34 0 0 0
# XORI
35 0 0 0
# LUI
36 0 0 0
# LSL
64 0 0 0
# LSR
65 1 0 0
# ASR
66 2 0 0
# LW
96 0 0 0
# LB
97 0 0 0
# SW
104 0 0 0
# SB
105 0 0 0
# BEQ
128 0 0 0
# BNE
129 0 0 0
# BLT
130 0 0 0
# JMP
160 0 0 0
# JAL
161 0 0 0
# RET
162 0 0 0
# JR
163 0 0 0
# HALT
255 0 0 0
*/
