// Digital circuit shift.dig as structural Verilog
module shift (
  input  [31:0] A,
  input  [1:0] mode,
  input  [4:0] B,
  output [31:0] Out
);

  wire ASR, fill, LSL, MODE0, not_1_out, not_2_out, not_3_out, stg0_b00, stg0_b01, stg0_b02, stg0_b03,
       stg0_b04, stg0_b05, stg0_b06, stg0_b07, stg0_b08, stg0_b09, stg0_b10, stg0_b11, stg0_b12, stg0_b13,
       stg0_b14, stg0_b15, stg0_b16, stg0_b17, stg0_b18, stg0_b19, stg0_b20, stg0_b21, stg0_b22, stg0_b23,
       stg0_b24, stg0_b25, stg0_b26, stg0_b27, stg0_b28, stg0_b29, stg0_b30, stg0_b31, stg1_b00, stg1_b01,
       stg1_b02, stg1_b03, stg1_b04, stg1_b05, stg1_b06, stg1_b07, stg1_b08, stg1_b09, stg1_b10, stg1_b11,
       stg1_b12, stg1_b13, stg1_b14, stg1_b15, stg1_b16, stg1_b17, stg1_b18, stg1_b19, stg1_b20, stg1_b21,
       stg1_b22, stg1_b23, stg1_b24, stg1_b25, stg1_b26, stg1_b27, stg1_b28, stg1_b29, stg1_b30, stg1_b31,
       stg2_b00, stg2_b01, stg2_b02, stg2_b03, stg2_b04, stg2_b05, stg2_b06, stg2_b07, stg2_b08, stg2_b09,
       stg2_b10, stg2_b11, stg2_b12, stg2_b13, stg2_b14, stg2_b15, stg2_b16, stg2_b17, stg2_b18, stg2_b19,
       stg2_b20, stg2_b21, stg2_b22, stg2_b23, stg2_b24, stg2_b25, stg2_b26, stg2_b27, stg2_b28, stg2_b29,
       stg2_b30, stg2_b31, stg3_b00, stg3_b01, stg3_b02, stg3_b03, stg3_b04, stg3_b05, stg3_b06, stg3_b07,
       stg3_b08, stg3_b09, stg3_b10, stg3_b11, stg3_b12, stg3_b13, stg3_b14, stg3_b15, stg3_b16, stg3_b17,
       stg3_b18, stg3_b19, stg3_b20, stg3_b21, stg3_b22, stg3_b23, stg3_b24, stg3_b25, stg3_b26, stg3_b27,
       stg3_b28, stg3_b29, stg3_b30, stg3_b31, stg4_b00, stg4_b01, stg4_b02, stg4_b03, stg4_b04, stg4_b05,
       stg4_b06, stg4_b07, stg4_b08, stg4_b09, stg4_b10, stg4_b11, stg4_b12, stg4_b13, stg4_b14, stg4_b15,
       stg4_b16, stg4_b17, stg4_b18, stg4_b19, stg4_b20, stg4_b21, stg4_b22, stg4_b23, stg4_b24, stg4_b25,
       stg4_b26, stg4_b27, stg4_b28, stg4_b29, stg4_b30, stg4_b31, stg5_b00, stg5_b01, stg5_b02, stg5_b03,
       stg5_b04, stg5_b05, stg5_b06, stg5_b07, stg5_b08, stg5_b09, stg5_b10, stg5_b11, stg5_b12, stg5_b13,
       stg5_b14, stg5_b15, stg5_b16, stg5_b17, stg5_b18, stg5_b19, stg5_b20, stg5_b21, stg5_b22, stg5_b23,
       stg5_b24, stg5_b25, stg5_b26, stg5_b27, stg5_b28, stg5_b29, stg5_b30, stg5_b31;

  not not_1 (not_1_out, MODE0);
  not not_2 (not_2_out, mode[1]);
  and and_1 (ASR, mode[1], not_1_out);
  and and_2 (LSL, MODE0, not_2_out);
  and and_3 (fill, ASR, A[31]);
  not not_3 (not_3_out, mode[1]);
  xor xor_1 (MODE0, mode[0], not_3_out);
  _74157 _74157_1 (
    .pin1(LSL), .pin2(A[0]), .pin3(A[31]), .pin4(stg0_b00), .pin5(A[1]), .pin6(A[30]), .pin7(stg0_b01),
    .pin8(1'b0), .pin9(stg0_b02), .pin10(A[29]), .pin11(A[2]), .pin12(stg0_b03), .pin13(A[28]), .pin14(A[3]),
    .pin15(1'b0), .pin16(1'b1));
  _74157 _74157_2 (
    .pin1(B[0]), .pin2(stg0_b00), .pin3(stg0_b01), .pin4(stg1_b00), .pin5(stg0_b01), .pin6(stg0_b02),
    .pin7(stg1_b01), .pin8(1'b0), .pin9(stg1_b02), .pin10(stg0_b03), .pin11(stg0_b02), .pin12(stg1_b03),
    .pin13(stg0_b04), .pin14(stg0_b03), .pin15(1'b0), .pin16(1'b1));
  _74157 _74157_3 (
    .pin1(B[1]), .pin2(stg1_b00), .pin3(stg1_b02), .pin4(stg2_b00), .pin5(stg1_b01), .pin6(stg1_b03),
    .pin7(stg2_b01), .pin8(1'b0), .pin9(stg2_b02), .pin10(stg1_b04), .pin11(stg1_b02), .pin12(stg2_b03),
    .pin13(stg1_b05), .pin14(stg1_b03), .pin15(1'b0), .pin16(1'b1));
  _74157 _74157_4 (
    .pin1(B[2]), .pin2(stg2_b00), .pin3(stg2_b04), .pin4(stg3_b00), .pin5(stg2_b01), .pin6(stg2_b05),
    .pin7(stg3_b01), .pin8(1'b0), .pin9(stg3_b02), .pin10(stg2_b06), .pin11(stg2_b02), .pin12(stg3_b03),
    .pin13(stg2_b07), .pin14(stg2_b03), .pin15(1'b0), .pin16(1'b1));
  _74157 _74157_5 (
    .pin1(B[3]), .pin2(stg3_b00), .pin3(stg3_b08), .pin4(stg4_b00), .pin5(stg3_b01), .pin6(stg3_b09),
    .pin7(stg4_b01), .pin8(1'b0), .pin9(stg4_b02), .pin10(stg3_b10), .pin11(stg3_b02), .pin12(stg4_b03),
    .pin13(stg3_b11), .pin14(stg3_b03), .pin15(1'b0), .pin16(1'b1));
  _74157 _74157_6 (
    .pin1(B[4]), .pin2(stg4_b00), .pin3(stg4_b16), .pin4(stg5_b00), .pin5(stg4_b01), .pin6(stg4_b17),
    .pin7(stg5_b01), .pin8(1'b0), .pin9(stg5_b02), .pin10(stg4_b18), .pin11(stg4_b02), .pin12(stg5_b03),
    .pin13(stg4_b19), .pin14(stg4_b03), .pin15(1'b0), .pin16(1'b1));
  _74157 _74157_7 (
    .pin1(LSL), .pin2(stg5_b00), .pin3(stg5_b31), .pin4(Out[0]), .pin5(stg5_b01), .pin6(stg5_b30),
    .pin7(Out[1]), .pin8(1'b0), .pin9(Out[2]), .pin10(stg5_b29), .pin11(stg5_b02), .pin12(Out[3]),
    .pin13(stg5_b28), .pin14(stg5_b03), .pin15(1'b0), .pin16(1'b1));
  _74157 _74157_8 (
    .pin1(LSL), .pin2(A[4]), .pin3(A[27]), .pin4(stg0_b04), .pin5(A[5]), .pin6(A[26]), .pin7(stg0_b05),
    .pin8(1'b0), .pin9(stg0_b06), .pin10(A[25]), .pin11(A[6]), .pin12(stg0_b07), .pin13(A[24]), .pin14(A[7]),
    .pin15(1'b0), .pin16(1'b1));
  _74157 _74157_9 (
    .pin1(B[0]), .pin2(stg0_b04), .pin3(stg0_b05), .pin4(stg1_b04), .pin5(stg0_b05), .pin6(stg0_b06),
    .pin7(stg1_b05), .pin8(1'b0), .pin9(stg1_b06), .pin10(stg0_b07), .pin11(stg0_b06), .pin12(stg1_b07),
    .pin13(stg0_b08), .pin14(stg0_b07), .pin15(1'b0), .pin16(1'b1));
  _74157 _74157_10 (
    .pin1(B[1]), .pin2(stg1_b04), .pin3(stg1_b06), .pin4(stg2_b04), .pin5(stg1_b05), .pin6(stg1_b07),
    .pin7(stg2_b05), .pin8(1'b0), .pin9(stg2_b06), .pin10(stg1_b08), .pin11(stg1_b06), .pin12(stg2_b07),
    .pin13(stg1_b09), .pin14(stg1_b07), .pin15(1'b0), .pin16(1'b1));
  _74157 _74157_11 (
    .pin1(B[2]), .pin2(stg2_b04), .pin3(stg2_b08), .pin4(stg3_b04), .pin5(stg2_b05), .pin6(stg2_b09),
    .pin7(stg3_b05), .pin8(1'b0), .pin9(stg3_b06), .pin10(stg2_b10), .pin11(stg2_b06), .pin12(stg3_b07),
    .pin13(stg2_b11), .pin14(stg2_b07), .pin15(1'b0), .pin16(1'b1));
  _74157 _74157_12 (
    .pin1(B[3]), .pin2(stg3_b04), .pin3(stg3_b12), .pin4(stg4_b04), .pin5(stg3_b05), .pin6(stg3_b13),
    .pin7(stg4_b05), .pin8(1'b0), .pin9(stg4_b06), .pin10(stg3_b14), .pin11(stg3_b06), .pin12(stg4_b07),
    .pin13(stg3_b15), .pin14(stg3_b07), .pin15(1'b0), .pin16(1'b1));
  _74157 _74157_13 (
    .pin1(B[4]), .pin2(stg4_b04), .pin3(stg4_b20), .pin4(stg5_b04), .pin5(stg4_b05), .pin6(stg4_b21),
    .pin7(stg5_b05), .pin8(1'b0), .pin9(stg5_b06), .pin10(stg4_b22), .pin11(stg4_b06), .pin12(stg5_b07),
    .pin13(stg4_b23), .pin14(stg4_b07), .pin15(1'b0), .pin16(1'b1));
  _74157 _74157_14 (
    .pin1(LSL), .pin2(stg5_b04), .pin3(stg5_b27), .pin4(Out[4]), .pin5(stg5_b05), .pin6(stg5_b26),
    .pin7(Out[5]), .pin8(1'b0), .pin9(Out[6]), .pin10(stg5_b25), .pin11(stg5_b06), .pin12(Out[7]),
    .pin13(stg5_b24), .pin14(stg5_b07), .pin15(1'b0), .pin16(1'b1));
  _74157 _74157_15 (
    .pin1(LSL), .pin2(A[8]), .pin3(A[23]), .pin4(stg0_b08), .pin5(A[9]), .pin6(A[22]), .pin7(stg0_b09),
    .pin8(1'b0), .pin9(stg0_b10), .pin10(A[21]), .pin11(A[10]), .pin12(stg0_b11), .pin13(A[20]),
    .pin14(A[11]), .pin15(1'b0), .pin16(1'b1));
  _74157 _74157_16 (
    .pin1(B[0]), .pin2(stg0_b08), .pin3(stg0_b09), .pin4(stg1_b08), .pin5(stg0_b09), .pin6(stg0_b10),
    .pin7(stg1_b09), .pin8(1'b0), .pin9(stg1_b10), .pin10(stg0_b11), .pin11(stg0_b10), .pin12(stg1_b11),
    .pin13(stg0_b12), .pin14(stg0_b11), .pin15(1'b0), .pin16(1'b1));
  _74157 _74157_17 (
    .pin1(B[1]), .pin2(stg1_b08), .pin3(stg1_b10), .pin4(stg2_b08), .pin5(stg1_b09), .pin6(stg1_b11),
    .pin7(stg2_b09), .pin8(1'b0), .pin9(stg2_b10), .pin10(stg1_b12), .pin11(stg1_b10), .pin12(stg2_b11),
    .pin13(stg1_b13), .pin14(stg1_b11), .pin15(1'b0), .pin16(1'b1));
  _74157 _74157_18 (
    .pin1(B[2]), .pin2(stg2_b08), .pin3(stg2_b12), .pin4(stg3_b08), .pin5(stg2_b09), .pin6(stg2_b13),
    .pin7(stg3_b09), .pin8(1'b0), .pin9(stg3_b10), .pin10(stg2_b14), .pin11(stg2_b10), .pin12(stg3_b11),
    .pin13(stg2_b15), .pin14(stg2_b11), .pin15(1'b0), .pin16(1'b1));
  _74157 _74157_19 (
    .pin1(B[3]), .pin2(stg3_b08), .pin3(stg3_b16), .pin4(stg4_b08), .pin5(stg3_b09), .pin6(stg3_b17),
    .pin7(stg4_b09), .pin8(1'b0), .pin9(stg4_b10), .pin10(stg3_b18), .pin11(stg3_b10), .pin12(stg4_b11),
    .pin13(stg3_b19), .pin14(stg3_b11), .pin15(1'b0), .pin16(1'b1));
  _74157 _74157_20 (
    .pin1(B[4]), .pin2(stg4_b08), .pin3(stg4_b24), .pin4(stg5_b08), .pin5(stg4_b09), .pin6(stg4_b25),
    .pin7(stg5_b09), .pin8(1'b0), .pin9(stg5_b10), .pin10(stg4_b26), .pin11(stg4_b10), .pin12(stg5_b11),
    .pin13(stg4_b27), .pin14(stg4_b11), .pin15(1'b0), .pin16(1'b1));
  _74157 _74157_21 (
    .pin1(LSL), .pin2(stg5_b08), .pin3(stg5_b23), .pin4(Out[8]), .pin5(stg5_b09), .pin6(stg5_b22),
    .pin7(Out[9]), .pin8(1'b0), .pin9(Out[10]), .pin10(stg5_b21), .pin11(stg5_b10), .pin12(Out[11]),
    .pin13(stg5_b20), .pin14(stg5_b11), .pin15(1'b0), .pin16(1'b1));
  _74157 _74157_22 (
    .pin1(LSL), .pin2(A[12]), .pin3(A[19]), .pin4(stg0_b12), .pin5(A[13]), .pin6(A[18]), .pin7(stg0_b13),
    .pin8(1'b0), .pin9(stg0_b14), .pin10(A[17]), .pin11(A[14]), .pin12(stg0_b15), .pin13(A[16]),
    .pin14(A[15]), .pin15(1'b0), .pin16(1'b1));
  _74157 _74157_23 (
    .pin1(B[0]), .pin2(stg0_b12), .pin3(stg0_b13), .pin4(stg1_b12), .pin5(stg0_b13), .pin6(stg0_b14),
    .pin7(stg1_b13), .pin8(1'b0), .pin9(stg1_b14), .pin10(stg0_b15), .pin11(stg0_b14), .pin12(stg1_b15),
    .pin13(stg0_b16), .pin14(stg0_b15), .pin15(1'b0), .pin16(1'b1));
  _74157 _74157_24 (
    .pin1(B[1]), .pin2(stg1_b12), .pin3(stg1_b14), .pin4(stg2_b12), .pin5(stg1_b13), .pin6(stg1_b15),
    .pin7(stg2_b13), .pin8(1'b0), .pin9(stg2_b14), .pin10(stg1_b16), .pin11(stg1_b14), .pin12(stg2_b15),
    .pin13(stg1_b17), .pin14(stg1_b15), .pin15(1'b0), .pin16(1'b1));
  _74157 _74157_25 (
    .pin1(B[2]), .pin2(stg2_b12), .pin3(stg2_b16), .pin4(stg3_b12), .pin5(stg2_b13), .pin6(stg2_b17),
    .pin7(stg3_b13), .pin8(1'b0), .pin9(stg3_b14), .pin10(stg2_b18), .pin11(stg2_b14), .pin12(stg3_b15),
    .pin13(stg2_b19), .pin14(stg2_b15), .pin15(1'b0), .pin16(1'b1));
  _74157 _74157_26 (
    .pin1(B[3]), .pin2(stg3_b12), .pin3(stg3_b20), .pin4(stg4_b12), .pin5(stg3_b13), .pin6(stg3_b21),
    .pin7(stg4_b13), .pin8(1'b0), .pin9(stg4_b14), .pin10(stg3_b22), .pin11(stg3_b14), .pin12(stg4_b15),
    .pin13(stg3_b23), .pin14(stg3_b15), .pin15(1'b0), .pin16(1'b1));
  _74157 _74157_27 (
    .pin1(B[4]), .pin2(stg4_b12), .pin3(stg4_b28), .pin4(stg5_b12), .pin5(stg4_b13), .pin6(stg4_b29),
    .pin7(stg5_b13), .pin8(1'b0), .pin9(stg5_b14), .pin10(stg4_b30), .pin11(stg4_b14), .pin12(stg5_b15),
    .pin13(stg4_b31), .pin14(stg4_b15), .pin15(1'b0), .pin16(1'b1));
  _74157 _74157_28 (
    .pin1(LSL), .pin2(stg5_b12), .pin3(stg5_b19), .pin4(Out[12]), .pin5(stg5_b13), .pin6(stg5_b18),
    .pin7(Out[13]), .pin8(1'b0), .pin9(Out[14]), .pin10(stg5_b17), .pin11(stg5_b14), .pin12(Out[15]),
    .pin13(stg5_b16), .pin14(stg5_b15), .pin15(1'b0), .pin16(1'b1));
  _74157 _74157_29 (
    .pin1(LSL), .pin2(A[16]), .pin3(A[15]), .pin4(stg0_b16), .pin5(A[17]), .pin6(A[14]), .pin7(stg0_b17),
    .pin8(1'b0), .pin9(stg0_b18), .pin10(A[13]), .pin11(A[18]), .pin12(stg0_b19), .pin13(A[12]),
    .pin14(A[19]), .pin15(1'b0), .pin16(1'b1));
  _74157 _74157_30 (
    .pin1(B[0]), .pin2(stg0_b16), .pin3(stg0_b17), .pin4(stg1_b16), .pin5(stg0_b17), .pin6(stg0_b18),
    .pin7(stg1_b17), .pin8(1'b0), .pin9(stg1_b18), .pin10(stg0_b19), .pin11(stg0_b18), .pin12(stg1_b19),
    .pin13(stg0_b20), .pin14(stg0_b19), .pin15(1'b0), .pin16(1'b1));
  _74157 _74157_31 (
    .pin1(B[1]), .pin2(stg1_b16), .pin3(stg1_b18), .pin4(stg2_b16), .pin5(stg1_b17), .pin6(stg1_b19),
    .pin7(stg2_b17), .pin8(1'b0), .pin9(stg2_b18), .pin10(stg1_b20), .pin11(stg1_b18), .pin12(stg2_b19),
    .pin13(stg1_b21), .pin14(stg1_b19), .pin15(1'b0), .pin16(1'b1));
  _74157 _74157_32 (
    .pin1(B[2]), .pin2(stg2_b16), .pin3(stg2_b20), .pin4(stg3_b16), .pin5(stg2_b17), .pin6(stg2_b21),
    .pin7(stg3_b17), .pin8(1'b0), .pin9(stg3_b18), .pin10(stg2_b22), .pin11(stg2_b18), .pin12(stg3_b19),
    .pin13(stg2_b23), .pin14(stg2_b19), .pin15(1'b0), .pin16(1'b1));
  _74157 _74157_33 (
    .pin1(B[3]), .pin2(stg3_b16), .pin3(stg3_b24), .pin4(stg4_b16), .pin5(stg3_b17), .pin6(stg3_b25),
    .pin7(stg4_b17), .pin8(1'b0), .pin9(stg4_b18), .pin10(stg3_b26), .pin11(stg3_b18), .pin12(stg4_b19),
    .pin13(stg3_b27), .pin14(stg3_b19), .pin15(1'b0), .pin16(1'b1));
  _74157 _74157_34 (
    .pin1(B[4]), .pin2(stg4_b16), .pin3(fill), .pin4(stg5_b16), .pin5(stg4_b17), .pin6(fill),
    .pin7(stg5_b17), .pin8(1'b0), .pin9(stg5_b18), .pin10(fill), .pin11(stg4_b18), .pin12(stg5_b19),
    .pin13(fill), .pin14(stg4_b19), .pin15(1'b0), .pin16(1'b1));
  _74157 _74157_35 (
    .pin1(LSL), .pin2(stg5_b16), .pin3(stg5_b15), .pin4(Out[16]), .pin5(stg5_b17), .pin6(stg5_b14),
    .pin7(Out[17]), .pin8(1'b0), .pin9(Out[18]), .pin10(stg5_b13), .pin11(stg5_b18), .pin12(Out[19]),
    .pin13(stg5_b12), .pin14(stg5_b19), .pin15(1'b0), .pin16(1'b1));
  _74157 _74157_36 (
    .pin1(LSL), .pin2(A[20]), .pin3(A[11]), .pin4(stg0_b20), .pin5(A[21]), .pin6(A[10]), .pin7(stg0_b21),
    .pin8(1'b0), .pin9(stg0_b22), .pin10(A[9]), .pin11(A[22]), .pin12(stg0_b23), .pin13(A[8]), .pin14(A[23]),
    .pin15(1'b0), .pin16(1'b1));
  _74157 _74157_37 (
    .pin1(B[0]), .pin2(stg0_b20), .pin3(stg0_b21), .pin4(stg1_b20), .pin5(stg0_b21), .pin6(stg0_b22),
    .pin7(stg1_b21), .pin8(1'b0), .pin9(stg1_b22), .pin10(stg0_b23), .pin11(stg0_b22), .pin12(stg1_b23),
    .pin13(stg0_b24), .pin14(stg0_b23), .pin15(1'b0), .pin16(1'b1));
  _74157 _74157_38 (
    .pin1(B[1]), .pin2(stg1_b20), .pin3(stg1_b22), .pin4(stg2_b20), .pin5(stg1_b21), .pin6(stg1_b23),
    .pin7(stg2_b21), .pin8(1'b0), .pin9(stg2_b22), .pin10(stg1_b24), .pin11(stg1_b22), .pin12(stg2_b23),
    .pin13(stg1_b25), .pin14(stg1_b23), .pin15(1'b0), .pin16(1'b1));
  _74157 _74157_39 (
    .pin1(B[2]), .pin2(stg2_b20), .pin3(stg2_b24), .pin4(stg3_b20), .pin5(stg2_b21), .pin6(stg2_b25),
    .pin7(stg3_b21), .pin8(1'b0), .pin9(stg3_b22), .pin10(stg2_b26), .pin11(stg2_b22), .pin12(stg3_b23),
    .pin13(stg2_b27), .pin14(stg2_b23), .pin15(1'b0), .pin16(1'b1));
  _74157 _74157_40 (
    .pin1(B[3]), .pin2(stg3_b20), .pin3(stg3_b28), .pin4(stg4_b20), .pin5(stg3_b21), .pin6(stg3_b29),
    .pin7(stg4_b21), .pin8(1'b0), .pin9(stg4_b22), .pin10(stg3_b30), .pin11(stg3_b22), .pin12(stg4_b23),
    .pin13(stg3_b31), .pin14(stg3_b23), .pin15(1'b0), .pin16(1'b1));
  _74157 _74157_41 (
    .pin1(B[4]), .pin2(stg4_b20), .pin3(fill), .pin4(stg5_b20), .pin5(stg4_b21), .pin6(fill),
    .pin7(stg5_b21), .pin8(1'b0), .pin9(stg5_b22), .pin10(fill), .pin11(stg4_b22), .pin12(stg5_b23),
    .pin13(fill), .pin14(stg4_b23), .pin15(1'b0), .pin16(1'b1));
  _74157 _74157_42 (
    .pin1(LSL), .pin2(stg5_b20), .pin3(stg5_b11), .pin4(Out[20]), .pin5(stg5_b21), .pin6(stg5_b10),
    .pin7(Out[21]), .pin8(1'b0), .pin9(Out[22]), .pin10(stg5_b09), .pin11(stg5_b22), .pin12(Out[23]),
    .pin13(stg5_b08), .pin14(stg5_b23), .pin15(1'b0), .pin16(1'b1));
  _74157 _74157_43 (
    .pin1(LSL), .pin2(A[24]), .pin3(A[7]), .pin4(stg0_b24), .pin5(A[25]), .pin6(A[6]), .pin7(stg0_b25),
    .pin8(1'b0), .pin9(stg0_b26), .pin10(A[5]), .pin11(A[26]), .pin12(stg0_b27), .pin13(A[4]), .pin14(A[27]),
    .pin15(1'b0), .pin16(1'b1));
  _74157 _74157_44 (
    .pin1(B[0]), .pin2(stg0_b24), .pin3(stg0_b25), .pin4(stg1_b24), .pin5(stg0_b25), .pin6(stg0_b26),
    .pin7(stg1_b25), .pin8(1'b0), .pin9(stg1_b26), .pin10(stg0_b27), .pin11(stg0_b26), .pin12(stg1_b27),
    .pin13(stg0_b28), .pin14(stg0_b27), .pin15(1'b0), .pin16(1'b1));
  _74157 _74157_45 (
    .pin1(B[1]), .pin2(stg1_b24), .pin3(stg1_b26), .pin4(stg2_b24), .pin5(stg1_b25), .pin6(stg1_b27),
    .pin7(stg2_b25), .pin8(1'b0), .pin9(stg2_b26), .pin10(stg1_b28), .pin11(stg1_b26), .pin12(stg2_b27),
    .pin13(stg1_b29), .pin14(stg1_b27), .pin15(1'b0), .pin16(1'b1));
  _74157 _74157_46 (
    .pin1(B[2]), .pin2(stg2_b24), .pin3(stg2_b28), .pin4(stg3_b24), .pin5(stg2_b25), .pin6(stg2_b29),
    .pin7(stg3_b25), .pin8(1'b0), .pin9(stg3_b26), .pin10(stg2_b30), .pin11(stg2_b26), .pin12(stg3_b27),
    .pin13(stg2_b31), .pin14(stg2_b27), .pin15(1'b0), .pin16(1'b1));
  _74157 _74157_47 (
    .pin1(B[3]), .pin2(stg3_b24), .pin3(fill), .pin4(stg4_b24), .pin5(stg3_b25), .pin6(fill),
    .pin7(stg4_b25), .pin8(1'b0), .pin9(stg4_b26), .pin10(fill), .pin11(stg3_b26), .pin12(stg4_b27),
    .pin13(fill), .pin14(stg3_b27), .pin15(1'b0), .pin16(1'b1));
  _74157 _74157_48 (
    .pin1(B[4]), .pin2(stg4_b24), .pin3(fill), .pin4(stg5_b24), .pin5(stg4_b25), .pin6(fill),
    .pin7(stg5_b25), .pin8(1'b0), .pin9(stg5_b26), .pin10(fill), .pin11(stg4_b26), .pin12(stg5_b27),
    .pin13(fill), .pin14(stg4_b27), .pin15(1'b0), .pin16(1'b1));
  _74157 _74157_49 (
    .pin1(LSL), .pin2(stg5_b24), .pin3(stg5_b07), .pin4(Out[24]), .pin5(stg5_b25), .pin6(stg5_b06),
    .pin7(Out[25]), .pin8(1'b0), .pin9(Out[26]), .pin10(stg5_b05), .pin11(stg5_b26), .pin12(Out[27]),
    .pin13(stg5_b04), .pin14(stg5_b27), .pin15(1'b0), .pin16(1'b1));
  _74157 _74157_50 (
    .pin1(LSL), .pin2(A[28]), .pin3(A[3]), .pin4(stg0_b28), .pin5(A[29]), .pin6(A[2]), .pin7(stg0_b29),
    .pin8(1'b0), .pin9(stg0_b30), .pin10(A[1]), .pin11(A[30]), .pin12(stg0_b31), .pin13(A[0]), .pin14(A[31]),
    .pin15(1'b0), .pin16(1'b1));
  _74157 _74157_51 (
    .pin1(B[0]), .pin2(stg0_b28), .pin3(stg0_b29), .pin4(stg1_b28), .pin5(stg0_b29), .pin6(stg0_b30),
    .pin7(stg1_b29), .pin8(1'b0), .pin9(stg1_b30), .pin10(stg0_b31), .pin11(stg0_b30), .pin12(stg1_b31),
    .pin13(fill), .pin14(stg0_b31), .pin15(1'b0), .pin16(1'b1));
  _74157 _74157_52 (
    .pin1(B[1]), .pin2(stg1_b28), .pin3(stg1_b30), .pin4(stg2_b28), .pin5(stg1_b29), .pin6(stg1_b31),
    .pin7(stg2_b29), .pin8(1'b0), .pin9(stg2_b30), .pin10(fill), .pin11(stg1_b30), .pin12(stg2_b31),
    .pin13(fill), .pin14(stg1_b31), .pin15(1'b0), .pin16(1'b1));
  _74157 _74157_53 (
    .pin1(B[2]), .pin2(stg2_b28), .pin3(fill), .pin4(stg3_b28), .pin5(stg2_b29), .pin6(fill),
    .pin7(stg3_b29), .pin8(1'b0), .pin9(stg3_b30), .pin10(fill), .pin11(stg2_b30), .pin12(stg3_b31),
    .pin13(fill), .pin14(stg2_b31), .pin15(1'b0), .pin16(1'b1));
  _74157 _74157_54 (
    .pin1(B[3]), .pin2(stg3_b28), .pin3(fill), .pin4(stg4_b28), .pin5(stg3_b29), .pin6(fill),
    .pin7(stg4_b29), .pin8(1'b0), .pin9(stg4_b30), .pin10(fill), .pin11(stg3_b30), .pin12(stg4_b31),
    .pin13(fill), .pin14(stg3_b31), .pin15(1'b0), .pin16(1'b1));
  _74157 _74157_55 (
    .pin1(B[4]), .pin2(stg4_b28), .pin3(fill), .pin4(stg5_b28), .pin5(stg4_b29), .pin6(fill),
    .pin7(stg5_b29), .pin8(1'b0), .pin9(stg5_b30), .pin10(fill), .pin11(stg4_b30), .pin12(stg5_b31),
    .pin13(fill), .pin14(stg4_b31), .pin15(1'b0), .pin16(1'b1));
  _74157 _74157_56 (
    .pin1(LSL), .pin2(stg5_b28), .pin3(stg5_b03), .pin4(Out[28]), .pin5(stg5_b29), .pin6(stg5_b02),
    .pin7(Out[29]), .pin8(1'b0), .pin9(Out[30]), .pin10(stg5_b01), .pin11(stg5_b30), .pin12(Out[31]),
    .pin13(stg5_b00), .pin14(stg5_b31), .pin15(1'b0), .pin16(1'b1));

  // Other names for the same wires on the sheet: ain[31:0] = A; in_b00 = A[0]; in_b01 = A[1]; in_b02 = A[2];
  //   in_b03 = A[3]; in_b04 = A[4]; in_b05 = A[5]; in_b06 = A[6]; in_b07 = A[7]; in_b08 = A[8]; in_b09 = A[9];
  //   in_b10 = A[10]; in_b11 = A[11]; in_b12 = A[12]; in_b13 = A[13]; in_b14 = A[14]; in_b15 = A[15]; in_b16 = A[16];
  //   in_b17 = A[17]; in_b18 = A[18]; in_b19 = A[19]; in_b20 = A[20]; in_b21 = A[21]; in_b22 = A[22]; in_b23 = A[23];
  //   in_b24 = A[24]; in_b25 = A[25]; in_b26 = A[26]; in_b27 = A[27]; in_b28 = A[28]; in_b29 = A[29]; in_b30 = A[30];
  //   in_b31 = A[31]; bin[4:0] = B; bin0 = B[0]; bin1 = B[1]; bin2 = B[2]; bin3 = B[3]; bin4 = B[4];
  //   mode0_t = mode[0]; out_b00 = Out[0]; result[31:0] = Out; out_b01 = Out[1]; out_b02 = Out[2]; out_b03 = Out[3];
  //   out_b04 = Out[4]; out_b05 = Out[5]; out_b06 = Out[6]; out_b07 = Out[7]; out_b08 = Out[8]; out_b09 = Out[9];
  //   out_b10 = Out[10]; out_b11 = Out[11]; out_b12 = Out[12]; out_b13 = Out[13]; out_b14 = Out[14];
  //   out_b15 = Out[15]; out_b16 = Out[16]; out_b17 = Out[17]; out_b18 = Out[18]; out_b19 = Out[19];
  //   out_b20 = Out[20]; out_b21 = Out[21]; out_b22 = Out[22]; out_b23 = Out[23]; out_b24 = Out[24];
  //   out_b25 = Out[25]; out_b26 = Out[26]; out_b27 = Out[27]; out_b28 = Out[28]; out_b29 = Out[29];
  //   out_b30 = Out[30]; out_b31 = Out[31]

  // Notes on the sheet:
  //   A: default 3437240336
endmodule

/* Test case shift exhaustive:
A mode B Out
# mode 0/3 LSR, 1 LSL, 2 ASR — all B[4:0]
# A=0x00000000
0x00000000 0 0 0x00000000
0x00000000 0 1 0x00000000
0x00000000 0 2 0x00000000
0x00000000 0 3 0x00000000
0x00000000 0 4 0x00000000
0x00000000 0 5 0x00000000
0x00000000 0 6 0x00000000
0x00000000 0 7 0x00000000
0x00000000 0 8 0x00000000
0x00000000 0 9 0x00000000
0x00000000 0 10 0x00000000
0x00000000 0 11 0x00000000
0x00000000 0 12 0x00000000
0x00000000 0 13 0x00000000
0x00000000 0 14 0x00000000
0x00000000 0 15 0x00000000
0x00000000 0 16 0x00000000
0x00000000 0 17 0x00000000
0x00000000 0 18 0x00000000
0x00000000 0 19 0x00000000
0x00000000 0 20 0x00000000
0x00000000 0 21 0x00000000
0x00000000 0 22 0x00000000
0x00000000 0 23 0x00000000
0x00000000 0 24 0x00000000
0x00000000 0 25 0x00000000
0x00000000 0 26 0x00000000
0x00000000 0 27 0x00000000
0x00000000 0 28 0x00000000
0x00000000 0 29 0x00000000
0x00000000 0 30 0x00000000
0x00000000 0 31 0x00000000
0x00000000 1 0 0x00000000
0x00000000 1 1 0x00000000
0x00000000 1 2 0x00000000
0x00000000 1 3 0x00000000
0x00000000 1 4 0x00000000
0x00000000 1 5 0x00000000
0x00000000 1 6 0x00000000
0x00000000 1 7 0x00000000
0x00000000 1 8 0x00000000
0x00000000 1 9 0x00000000
0x00000000 1 10 0x00000000
0x00000000 1 11 0x00000000
0x00000000 1 12 0x00000000
0x00000000 1 13 0x00000000
0x00000000 1 14 0x00000000
0x00000000 1 15 0x00000000
0x00000000 1 16 0x00000000
0x00000000 1 17 0x00000000
0x00000000 1 18 0x00000000
0x00000000 1 19 0x00000000
0x00000000 1 20 0x00000000
0x00000000 1 21 0x00000000
0x00000000 1 22 0x00000000
0x00000000 1 23 0x00000000
0x00000000 1 24 0x00000000
0x00000000 1 25 0x00000000
0x00000000 1 26 0x00000000
0x00000000 1 27 0x00000000
0x00000000 1 28 0x00000000
0x00000000 1 29 0x00000000
0x00000000 1 30 0x00000000
0x00000000 1 31 0x00000000
0x00000000 2 0 0x00000000
0x00000000 2 1 0x00000000
0x00000000 2 2 0x00000000
0x00000000 2 3 0x00000000
0x00000000 2 4 0x00000000
0x00000000 2 5 0x00000000
0x00000000 2 6 0x00000000
0x00000000 2 7 0x00000000
0x00000000 2 8 0x00000000
0x00000000 2 9 0x00000000
0x00000000 2 10 0x00000000
0x00000000 2 11 0x00000000
0x00000000 2 12 0x00000000
0x00000000 2 13 0x00000000
0x00000000 2 14 0x00000000
0x00000000 2 15 0x00000000
0x00000000 2 16 0x00000000
0x00000000 2 17 0x00000000
0x00000000 2 18 0x00000000
0x00000000 2 19 0x00000000
0x00000000 2 20 0x00000000
0x00000000 2 21 0x00000000
0x00000000 2 22 0x00000000
0x00000000 2 23 0x00000000
0x00000000 2 24 0x00000000
0x00000000 2 25 0x00000000
0x00000000 2 26 0x00000000
0x00000000 2 27 0x00000000
0x00000000 2 28 0x00000000
0x00000000 2 29 0x00000000
0x00000000 2 30 0x00000000
0x00000000 2 31 0x00000000
0x00000000 3 0 0x00000000
0x00000000 3 1 0x00000000
0x00000000 3 2 0x00000000
0x00000000 3 3 0x00000000
0x00000000 3 4 0x00000000
0x00000000 3 5 0x00000000
0x00000000 3 6 0x00000000
0x00000000 3 7 0x00000000
0x00000000 3 8 0x00000000
0x00000000 3 9 0x00000000
0x00000000 3 10 0x00000000
0x00000000 3 11 0x00000000
0x00000000 3 12 0x00000000
0x00000000 3 13 0x00000000
0x00000000 3 14 0x00000000
0x00000000 3 15 0x00000000
0x00000000 3 16 0x00000000
0x00000000 3 17 0x00000000
0x00000000 3 18 0x00000000
0x00000000 3 19 0x00000000
0x00000000 3 20 0x00000000
0x00000000 3 21 0x00000000
0x00000000 3 22 0x00000000
0x00000000 3 23 0x00000000
0x00000000 3 24 0x00000000
0x00000000 3 25 0x00000000
0x00000000 3 26 0x00000000
0x00000000 3 27 0x00000000
0x00000000 3 28 0x00000000
0x00000000 3 29 0x00000000
0x00000000 3 30 0x00000000
0x00000000 3 31 0x00000000
# A=0x00000001
0x00000001 0 0 0x00000001
0x00000001 0 1 0x00000000
0x00000001 0 2 0x00000000
0x00000001 0 3 0x00000000
0x00000001 0 4 0x00000000
0x00000001 0 5 0x00000000
0x00000001 0 6 0x00000000
0x00000001 0 7 0x00000000
0x00000001 0 8 0x00000000
0x00000001 0 9 0x00000000
0x00000001 0 10 0x00000000
0x00000001 0 11 0x00000000
0x00000001 0 12 0x00000000
0x00000001 0 13 0x00000000
0x00000001 0 14 0x00000000
0x00000001 0 15 0x00000000
0x00000001 0 16 0x00000000
0x00000001 0 17 0x00000000
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*/
