// Digital circuit sp.dig as structural Verilog
module sp (
  input  [1:0] sp_op,
  input  CLK,
  input  Reset,
  input  [39:0] sp_load_in,
  input  seq_exec,
  output [23:0] sp_out
);

  wire and_3_out, not_1_out, or_1_out, reg_en, sp_addr_sel;
  wire [0:0] and_2_out;
  wire [23:0] sp_delta, sp_next, sp_out_reg, sp_reg_d;

  and and_1 (sp_addr_sel, not_1_out, sp_op[1]);
  not not_1 (not_1_out, sp_op[0]);
  or or_1 (or_1_out, sp_op[1], sp_op[0]);
  and and_2 (and_2_out[0], sp_op[1], sp_op[0]);
  and and_3 (and_3_out, or_1_out, seq_exec);
  Multiplexer #(.Selector_Bits(2), .Bits(24)) multiplexer_1 (
    .sel(sp_op), .in_0({24{1'b0}}), .in_1(24'h4), .in_2(24'hfffffc), .in_3({24{1'b0}}), .out(sp_delta));
  Multiplexer #(.Selector_Bits(2), .Bits(24)) multiplexer_2 (
    .sel({Reset, and_2_out[0]}), .in_0(sp_next), .in_1(sp_load_in[23:0]), .in_2(24'h10000), .in_3(24'h10000),
    .out(sp_reg_d));
  or or_2 (reg_en, and_3_out, Reset);
  Add #(.Bits(24)) add_1 (.a(sp_out_reg), .b(sp_delta), .c_i(1'b0), .s(sp_next));  // open: c_o
  Register #(.Bits(24)) register_1 (.D(sp_reg_d), .C(CLK), .en(reg_en), .Q(sp_out_reg));
  Multiplexer #(.Bits(24)) multiplexer_3 (.sel(sp_addr_sel), .in_0(sp_out_reg), .in_1(sp_next), .out(sp_out));

  // Other names for the same wires on the sheet: sp_load[23:0] = sp_load_in[23:0]

  // Notes on the sheet:
  //   sp_load_in: default 456
endmodule

/* Test case sp-reset-init:
sp-op Reset seq-exec sp-load-in CLK sp-out

# Reset=1 loads SP_INIT (0x010000). Reset=0 = run.

0 1 0 0 0 x
0 1 0 0 C 0x010000
0 1 0 0 0 0x010000
*/

/* Test case sp-push-pop:
sp-op Reset seq-exec sp-load-in CLK sp-out

# Init then PUSH (-4) then POP (+4). Tomato32 native 0x70 / 0x71.
# After PUSH clock, drop sp-op to HOLD before checking sp-out (addr mux = sp_next while PUSH).

0 1 0 0 0 x
0 1 0 0 C 0x010000
0 0 0 0 0 0x010000
2 0 0 0 0 0x00FFFC
2 0 1 0 C x
0 0 0 0 0 0x00FFFC
1 0 0 0 0 0x00FFFC
1 0 1 0 C x
0 0 0 0 0 0x010000
*/

/* Test case sp-seq-gate:
sp-op Reset seq-exec sp-load-in CLK sp-out

# reg_en = (|sp-op & seq-exec) | Reset — no SP register change without seq-exec.

0 1 0 0 C 0x010000
0 0 0 0 0 0x010000
2 0 0 0 C x
0 0 0 0 0 0x010000
0 0 1 0 C 0x010000
0 0 1 0 0 0x010000
2 0 0 0 0 x
0 0 0 0 0 0x010000
*/

/* Test case sp-addr-mux:
sp-op Reset seq-exec sp-load-in CLK sp-out

# PUSH (sp-op=2) drives sp_next on sp-out; POP (sp-op=1) drives registered top.
# Combinatorial only — no EXEC clock (PUSH+seq-exec after edge re-exposes decremented sp_next).

0 1 0 0 C 0x010000
0 0 0 0 0 0x010000
2 0 0 0 0 0x00FFFC
1 0 0 0 0 0x010000
0 0 0 0 0 0x010000
*/
