// Digital circuit store-mux.dig as structural Verilog
module store_mux (
  input  [31:0] reg_a,
  input  [31:0] alu_out,
  input  [23:0] pc_save,
  input  [31:0] reg_b,
  input  [1:0] mem_sel,
  output [31:0] mem_mux
);

  Multiplexer #(.Selector_Bits(2), .Bits(32)) multiplexer_1 (
    .sel(mem_sel), .in_0(reg_a), .in_1(reg_b), .in_2({{8{1'b0}}, pc_save}), .in_3(alu_out), .out(mem_mux));

  // Other names for the same wires on the sheet: pc_save_24[23:0] = pc_save; pc_save_32[23:0] = pc_save
endmodule

/* Test case store-mux-select:
reg_a reg_b alu_out pc_save mem-sel mem-mux
# mem-sel: 0=reg_a 1=reg_b 2=pc_save (zero-ext) 3=alu_out
# 1. One row per select — distinct sources
0x11111111 0x22222222 0x33333333 0x001234 0 0x11111111
0x11111111 0x22222222 0x33333333 0x001234 1 0x22222222
0x11111111 0x22222222 0x33333333 0x001234 2 0x00001234
0x11111111 0x22222222 0x33333333 0x001234 3 0x33333333
# 2. pc_save zero-extension (upper 8 bits forced to 0)
0xAAAAAAAA 0xBBBBBBBB 0xCCCCCCCC 0xFEDCBA 2 0x00FEDCBA
0xAAAAAAAA 0xBBBBBBBB 0xCCCCCCCC 0xFFFFFF 2 0x00FFFFFF
0xAAAAAAAA 0xBBBBBBBB 0xCCCCCCCC 0 2 0x00000000
# 3. Cross-talk — only selected input matters
0xDEADBEEF 0xCAFEBABE 0x13572468 0xABCDEF 0 0xDEADBEEF
0xDEADBEEF 0xCAFEBABE 0x13572468 0xABCDEF 1 0xCAFEBABE
0xDEADBEEF 0xCAFEBABE 0x13572468 0xABCDEF 2 0x00ABCDEF
0xDEADBEEF 0xCAFEBABE 0x13572468 0xABCDEF 3 0x13572468
# 4. All-zero / all-one inputs
0 0 0 0 0 0
0 0 0 0 1 0
0 0 0 0 2 0
0 0 0 0 3 0
0xFFFFFFFF 0xFFFFFFFF 0xFFFFFFFF 0xFFFFFF 0 0xFFFFFFFF
0xFFFFFFFF 0xFFFFFFFF 0xFFFFFFFF 0xFFFFFF 1 0xFFFFFFFF
0xFFFFFFFF 0xFFFFFFFF 0xFFFFFFFF 0xFFFFFF 2 0x00FFFFFF
0xFFFFFFFF 0xFFFFFFFF 0xFFFFFFFF 0xFFFFFF 3 0xFFFFFFFF
*/
