// Digital circuit test2.dig as structural Verilog
module test2 (
  input  CLK,
  input  [31:0] A,
  input  [31:0] B,
  input  [31:0] C,
  input  cin,
  input  [31:0] Test,
  output [7:0] lutB,
  output [7:0] lutA,
  output [31:0] Out
);

  wire aeff31, beff31, clk_t, counter_1_ovf, COUT, cout0, cout1, cout2, cout3, cout4, cout5, cout6, found,
       not_1_out, not_2_out, ovf, sum31;
  wire [15:0] sub_1_s, sub_1_s_2;

  not not_1 (not_1_out, ovf);
  not not_2 (not_2_out, found);
  Counter #(.Bits(8)) counter_1 (.en(1'b1), .C(clk_t), .clr(1'b0), .out(lutA), .ovf(counter_1_ovf));
  and and_1 (clk_t, CLK, not_1_out, not_2_out);
  Sub #(.Bits(32)) sub_1 (.a(Out), .b(Test), .c_i(1'b0), .s({sub_1_s_2, sub_1_s}));  // open: c_o
  Counter #(.Bits(8)) counter_2 (.en(counter_1_ovf), .C(clk_t), .clr(1'b0), .out(lutB), .ovf(ovf));
  nor nor_1 (found, sub_1_s_2[15], sub_1_s_2[14], sub_1_s_2[13], sub_1_s_2[12], sub_1_s_2[11], sub_1_s_2[10], sub_1_s_2[9], sub_1_s_2[8], sub_1_s_2[7], sub_1_s_2[6], sub_1_s_2[5], sub_1_s_2[4], sub_1_s_2[3], sub_1_s_2[2], sub_1_s_2[1], sub_1_s_2[0], sub_1_s[0], sub_1_s[1], sub_1_s[2], sub_1_s[3], sub_1_s[4], sub_1_s[5], sub_1_s[6], sub_1_s[7], sub_1_s[8], sub_1_s[9], sub_1_s[10], sub_1_s[11], sub_1_s[12], sub_1_s[13], sub_1_s[14], sub_1_s[15]);
  // alu_4b_final alu_4b_final_1: pin names not known; wires that end beside it: A[3:0], B[3:0], lutA, C[3:0], cin, lutB, Out[3:0], cout0
  // alu_4b_final alu_4b_final_2: pin names not known; wires that end beside it: A[19:16], B[19:16], lutA, C[19:16], cout3, lutB, Out[19:16], cout4
  // alu_4b_final alu_4b_final_3: pin names not known; wires that end beside it: A[7:4], B[7:4], lutA, C[7:4], cout0, lutB, Out[7:4], cout1
  // alu_4b_final alu_4b_final_4: pin names not known; wires that end beside it: A[23:20], B[23:20], lutA, C[23:20], cout4, lutB, Out[23:20], cout5
  // alu_4b_final alu_4b_final_5: pin names not known; wires that end beside it: A[11:8], B[11:8], lutA, C[11:8], cout1, lutB, Out[11:8], cout2
  // alu_4b_final alu_4b_final_6: pin names not known; wires that end beside it: A[27:24], B[27:24], lutA, C[27:24], cout5, lutB, Out[27:24], cout6
  alu_4b_final alu_4b_final_7 (
    .A(A[15:12]), .B(B[15:12]), .lutA(lutA), .C(C[15:12]), .cin(cout2), .lutB(lutB), .Out(Out[15:12]),
    .cout(cout3));  // open: sum3, aeff3, beff3
  alu_4b_final alu_4b_final_8 (
    .A(A[31:28]), .B(B[31:28]), .lutA(lutA), .C(C[31:28]), .cin(cout6), .lutB(lutB), .Out(Out[31:28]),
    .cout(COUT), .sum3(sum31), .aeff3(aeff31), .beff3(beff31));

  // Other names for the same wires on the sheet: a4[3:0] = A[3:0]; a8[3:0] = A[7:4]; a12[3:0] = A[11:8];
  //   a16[3:0] = A[15:12]; a20[3:0] = A[19:16]; a24[3:0] = A[23:20]; a28[3:0] = A[27:24]; a32[3:0] = A[31:28];
  //   b4[3:0] = B[3:0]; b8[3:0] = B[7:4]; b12[3:0] = B[11:8]; b16[3:0] = B[15:12]; b20[3:0] = B[19:16];
  //   b24[3:0] = B[23:20]; b28[3:0] = B[27:24]; b32[3:0] = B[31:28]; c4[3:0] = C[3:0]; c8[3:0] = C[7:4];
  //   c12[3:0] = C[11:8]; c16[3:0] = C[15:12]; c20[3:0] = C[19:16]; c24[3:0] = C[23:20]; c28[3:0] = C[27:24];
  //   c32[3:0] = C[31:28]; OUT4[3:0] = Out[3:0]; OUT8[3:0] = Out[7:4]; OUT12[3:0] = Out[11:8];
  //   OUT16[3:0] = Out[15:12]; OUT20[3:0] = Out[19:16]; OUT24[3:0] = Out[23:20]; OUT28[3:0] = Out[27:24];
  //   OUT32[3:0] = Out[31:28]

  // Notes on the sheet:
  //   CLK: Hz: 10000
  //   A: default 2781028222
  //   B: default 1000219752
  //   C: default 2115866819
  //   Test: default 2160154409
endmodule
