// Digital circuit vga.dig as structural Verilog
module vga (
);

  wire BUS_DIR, BUS_OE, CLK, CPU_ADDR_0, CPU_ADDR_1, CPU_DATA_0, CPU_DATA_1, CPU_DATA_2, CPU_DATA_3,
       CPU_DATA_4, CPU_DATA_5, CPU_DATA_6, CPU_DATA_7, CPU_RDATA_0, CPU_RDATA_1, CPU_RDATA_2, CPU_RDATA_3,
       CPU_RDATA_4, CPU_RDATA_5, CPU_RDATA_6, CPU_RDATA_7, CPU_RE, CPU_WE, INT_ACK, INT_LATCHED, INT_RAW,
       IO_SEL, V9958_CSR, V9958_CSW, V9958_MODE0, V9958_MODE1, VGA_INT;

  _7474 _7474_1 (
    .pin1(CLK), .pin2(INT_LATCHED), .pin3(INT_ACK), .pin4(VGA_INT), .pin5(INT_LATCHED), .pin6(INT_RAW),
    .pin7(1'b0), .pin8(INT_RAW), .pin9(INT_RAW), .pin10(INT_RAW), .pin11(CLK), .pin12(INT_RAW), .pin13(CLK),
    .pin14(1'b1));
  _74245 _74245_1 (
    .pin1(CPU_RDATA_0), .pin2(CPU_RDATA_1), .pin3(CPU_RDATA_2), .pin4(CPU_RDATA_3), .pin5(CPU_RDATA_4),
    .pin6(CPU_RDATA_5), .pin7(CPU_RDATA_6), .pin8(CPU_RDATA_7), .pin9(BUS_OE), .pin10(1'b0),
    .pin11(CPU_DATA_7), .pin12(CPU_DATA_6), .pin13(CPU_DATA_5), .pin14(CPU_DATA_4), .pin15(CPU_DATA_3),
    .pin16(CPU_DATA_2), .pin17(CPU_DATA_1), .pin18(CPU_DATA_0), .pin19(BUS_DIR), .pin20(1'b1));
  _74245 _74245_2 (
    .pin1(CPU_RDATA_0), .pin2(CPU_RDATA_1), .pin3(CPU_RDATA_2), .pin4(CPU_RDATA_3), .pin5(CPU_RDATA_4),
    .pin6(CPU_RDATA_5), .pin7(CPU_RDATA_6), .pin8(CPU_RDATA_7), .pin9(BUS_OE), .pin10(1'b0),
    .pin11(CPU_DATA_7), .pin12(CPU_DATA_6), .pin13(CPU_DATA_5), .pin14(CPU_DATA_4), .pin15(CPU_DATA_3),
    .pin16(CPU_DATA_2), .pin17(CPU_DATA_1), .pin18(CPU_DATA_0), .pin19(BUS_DIR), .pin20(1'b1));
  _74138 _74138_1 (
    .pin1(CPU_RE), .pin2(V9958_MODE1), .pin3(V9958_MODE0), .pin4(V9958_CSR), .pin5(V9958_CSW), .pin6(1'b0),
    .pin7(1'b0), .pin8(1'b0), .pin9(CPU_WE), .pin10(1'b0), .pin11(1'b0), .pin12(CPU_WE), .pin13(IO_SEL),
    .pin14(CPU_ADDR_1), .pin15(CPU_ADDR_0), .pin16(1'b1));

  // Notes on the sheet:
  //   V9958
  //   R-2R DAC
  //   GBS-Control
  //   V4C16258 VRAM
endmodule
