// Digital circuit alu-1b.dig as structural Verilog
module alu_1b (
  input  [7:0] Opcode,
  input  A,
  input  B,
  input  cin,
  output out,
  output cout
);

  wire multiplexer_1_out, multiplexer_2_out;

  Multiplexer #(.Selector_Bits(2)) multiplexer_1 (
    .sel({B, A}), .in_0(Opcode[0]), .in_1(Opcode[1]), .in_2(Opcode[2]), .in_3(Opcode[3]),
    .out(multiplexer_1_out));
  Multiplexer #(.Selector_Bits(2)) multiplexer_2 (
    .sel({B, A}), .in_0(Opcode[4]), .in_1(Opcode[5]), .in_2(Opcode[6]), .in_3(Opcode[7]),
    .out(multiplexer_2_out));
  Add add_1 (.a(multiplexer_1_out), .b(multiplexer_2_out), .c_i(cin), .s(out), .c_o(cout));

  // Other names for the same wires on the sheet: lutA[3:0] = Opcode[3:0]; lutB[3:0] = Opcode[7:4]
endmodule
