// Digital circuit alu-8b.dig as structural Verilog
module alu_8b (
  input  [7:0] opcode,
  input  [7:0] A,
  input  [7:0] B,
  input  C,
  output [7:0] OUT
);

  wire cout0, cout1, cout2, cout3, cout4, cout5, cout6, cout7;

  alu_1b alu_1b_1 (.Opcode(opcode), .A(A[0]), .B(B[0]), .cin(C), .out(OUT[0]), .cout(cout0));
  alu_1b alu_1b_2 (.Opcode(opcode), .A(A[1]), .B(B[1]), .cin(cout0), .out(OUT[1]), .cout(cout1));
  alu_1b alu_1b_3 (.Opcode(opcode), .A(A[2]), .B(B[2]), .cin(cout1), .out(OUT[2]), .cout(cout2));
  alu_1b alu_1b_4 (.Opcode(opcode), .A(A[3]), .B(B[3]), .cin(cout2), .out(OUT[3]), .cout(cout3));
  alu_1b alu_1b_5 (.Opcode(opcode), .A(A[4]), .B(B[4]), .cin(cout3), .out(OUT[4]), .cout(cout4));
  alu_1b alu_1b_6 (.Opcode(opcode), .A(A[5]), .B(B[5]), .cin(cout4), .out(OUT[5]), .cout(cout5));
  alu_1b alu_1b_7 (.Opcode(opcode), .A(A[6]), .B(B[6]), .cin(cout5), .out(OUT[6]), .cout(cout6));
  alu_1b alu_1b_8 (.Opcode(opcode), .A(A[7]), .B(B[7]), .cin(cout6), .out(OUT[7]), .cout(cout7));

  // Other names for the same wires on the sheet: cin = C; Op[7:0] = opcode; s0 = OUT[0]; s_out[7:0] = OUT;
  //   s1 = OUT[1]; s2 = OUT[2]; s3 = OUT[3]; s4 = OUT[4]; s5 = OUT[5]; s6 = OUT[6]; s7 = OUT[7]
endmodule
